// Logisim project accumulator_4bit.circ as structural Verilog
module accumulator_4bit (
  input  RST,
  input  GND,
  input  A0,
  input  A1,
  input  A2,
  input  A3,
  output Q0,
  output Q1,
  output Q2,
  output Q3
);

  wire AA1_out, AA2_out, AA3_out, AA4_out, AB1_out, AB2_out, AB3_out, AB4_out, AG1_out, AG2_out, AG3_out,
       AO1_out, AO2_out, AO3_out, AO4_out, AS1_out, AS2_out, AS3_out, AS4_out, AX1_out, AX2_out, AX3_out,
       AX4_out, CLK_out;

  Clock CLK (.out(CLK_out));
  D_Flip_Flop U1 (.D(AS1_out), .clk(CLK_out), .Q(Q0), .preset(RST), .reset(RST));  // open: Qn
  D_Flip_Flop U2 (.D(AS2_out), .clk(CLK_out), .Q(Q1), .preset(RST), .reset(RST));  // open: Qn
  D_Flip_Flop U3 (.D(AS3_out), .clk(CLK_out), .Q(Q2), .preset(RST), .reset(RST));  // open: Qn
  D_Flip_Flop U4 (.D(AS4_out), .clk(CLK_out), .Q(Q3), .preset(RST), .reset(RST));  // open: Qn
  xor AX1 (AX1_out, A0, Q0);
  xor AS1 (AS1_out, AX1_out, GND);
  and AA1 (AA1_out, A0, Q0);
  and AB1 (AB1_out, GND, AX1_out);
  or AO1 (AO1_out, AA1_out, AB1_out);
  or AG1 (AG1_out, AO1_out, GND);
  xor AX2 (AX2_out, A1, Q1);
  xor AS2 (AS2_out, AX2_out, AG1_out);
  and AA2 (AA2_out, A1, Q1);
  and AB2 (AB2_out, AG1_out, AX2_out);
  or AO2 (AO2_out, AA2_out, AB2_out);
  or AG2 (AG2_out, AO2_out, GND);
  xor AX3 (AX3_out, A2, Q2);
  xor AS3 (AS3_out, AX3_out, AG2_out);
  and AA3 (AA3_out, A2, Q2);
  and AB3 (AB3_out, AG2_out, AX3_out);
  or AO3 (AO3_out, AA3_out, AB3_out);
  or AG3 (AG3_out, AO3_out, GND);
  xor AX4 (AX4_out, A3, Q3);
  xor AS4 (AS4_out, AX4_out, AG3_out);
  and AA4 (AA4_out, A3, Q3);
  and AB4 (AB4_out, AG3_out, AX4_out);
  or AO4 (AO4_out, AA4_out, AB4_out);
  // OR_Gate AG4 has open pins: in0=AO4_out, in1=GND, out=open
endmodule
