// Logisim project adder_4bit.circ as structural Verilog
module adder_4bit (
  input  A0,
  input  B0,
  input  A1,
  input  B1,
  input  A2,
  input  B2,
  input  A3,
  input  B3,
  input  Cin,
  output S0,
  output S1,
  output S2,
  output S3,
  output Cout
);

  wire FA0G1_out, FA0G2_out, FA0G3_out, FA0O1_out, FA0O2_out, FA0X1_out, FA1G1_out, FA1G2_out, FA1G3_out,
       FA1O1_out, FA1O2_out, FA1X1_out, FA2G1_out, FA2G2_out, FA2G3_out, FA2O1_out, FA2O2_out, FA2X1_out,
       FA3G1_out, FA3G2_out, FA3G3_out, FA3O1_out, FA3X1_out;

  xor FA0X1 (FA0X1_out, A0, B0);
  xor FA0X2 (S0, FA0X1_out, Cin);
  and FA0G1 (FA0G1_out, B0, A0);
  and FA0G2 (FA0G2_out, A0, Cin);
  and FA0G3 (FA0G3_out, Cin, B0);
  or FA0O1 (FA0O1_out, FA0G1_out, FA0G2_out);
  or FA0O2 (FA0O2_out, FA0O1_out, FA0G3_out);
  xor FA1X1 (FA1X1_out, A1, B1);
  xor FA1X2 (S1, FA1X1_out, FA0O2_out);
  and FA1G1 (FA1G1_out, B1, A1);
  and FA1G2 (FA1G2_out, A1, FA0O2_out);
  and FA1G3 (FA1G3_out, FA0O2_out, B1);
  or FA1O1 (FA1O1_out, FA1G1_out, FA1G2_out);
  or FA1O2 (FA1O2_out, FA1O1_out, FA1G3_out);
  xor FA2X1 (FA2X1_out, A2, B2);
  xor FA2X2 (S2, FA2X1_out, FA1O2_out);
  and FA2G1 (FA2G1_out, B2, A2);
  and FA2G2 (FA2G2_out, A2, FA1O2_out);
  and FA2G3 (FA2G3_out, FA1O2_out, B2);
  or FA2O1 (FA2O1_out, FA2G1_out, FA2G2_out);
  or FA2O2 (FA2O2_out, FA2O1_out, FA2G3_out);
  xor FA3X1 (FA3X1_out, A3, B3);
  xor FA3X2 (S3, FA3X1_out, FA2O2_out);
  and FA3G1 (FA3G1_out, B3, A3);
  and FA3G2 (FA3G2_out, A3, FA2O2_out);
  and FA3G3 (FA3G3_out, FA2O2_out, B3);
  or FA3O1 (FA3O1_out, FA3G1_out, FA3G2_out);
  or FA3O2 (Cout, FA3O1_out, FA3G3_out);
endmodule
