// Logisim project adder_8bit.circ as structural Verilog
module adder_8bit (
  input  A0,
  input  B0,
  input  A1,
  input  B1,
  input  A2,
  input  B2,
  input  A3,
  input  B3,
  input  A4,
  input  B4,
  input  A5,
  input  B5,
  input  A6,
  input  B6,
  input  A7,
  input  B7,
  input  Cin,
  output S0,
  output S1,
  output S2,
  output S3,
  output S4,
  output S5,
  output S6,
  output S7,
  output Cout
);

  wire TQ1b, TQ1c, TQ1d, TQ1e, TQ1f, TQ1g, TQ1i, TQ1j, TQ1k, TQ1l, TQ1m, TQ1n, TQ1p, TQ1q, TQ1r, TQ1s, TQ1t,
       TQ1u, TQ1w, TQ1x, TQ1y, TQ1z, TQ10, TQ11, TQ12, TQ14, TQ15, TQ16, TQ17, TQ18, TQ19, TQh, TQj, TQk,
       TQl, TQm, TQn, TQo, TQq, TQr, TQs, TQt, TQu, TQv, TQx, TQy, TQz;

  xor FA0X1 (TQh, A0, B0);
  or FA1O1 (TQt, TQq, TQr);
  and FA3G2 (TQ15, A3, TQ11);
  xor FA5X2 (S5, TQ1g, TQ1f);
  or FA6O2 (TQ1t, TQ1s, TQ1r);
  xor FA0X2 (S0, TQh, Cin);
  or FA1O2 (TQu, TQt, TQs);
  and FA3G3 (TQ16, TQ11, B3);
  and FA5G1 (TQ1i, B5, A5);
  xor FA7X1 (TQ1u, A7, B7);
  and FA0G1 (TQj, B0, A0);
  xor FA2X1 (TQv, A2, B2);
  or FA3O1 (TQ17, TQ14, TQ15);
  and FA5G2 (TQ1j, A5, TQ1f);
  xor FA7X2 (S7, TQ1u, TQ1t);
  and FA0G2 (TQk, A0, Cin);
  xor FA2X2 (S2, TQv, TQu);
  or FA3O2 (TQ18, TQ17, TQ16);
  and FA5G3 (TQ1k, TQ1f, B5);
  and FA7G1 (TQ1w, B7, A7);
  and FA0G3 (TQl, Cin, B0);
  and FA2G1 (TQx, B2, A2);
  xor FA4X1 (TQ19, A4, B4);
  or FA5O1 (TQ1l, TQ1i, TQ1j);
  and FA7G2 (TQ1x, A7, TQ1t);
  or FA0O1 (TQm, TQj, TQk);
  and FA2G2 (TQy, A2, TQu);
  xor FA4X2 (S4, TQ19, TQ18);
  or FA5O2 (TQ1m, TQ1l, TQ1k);
  and FA7G3 (TQ1y, TQ1t, B7);
  or FA0O2 (TQn, TQm, TQl);
  and FA2G3 (TQz, TQu, B2);
  and FA4G1 (TQ1b, B4, A4);
  xor FA6X1 (TQ1n, A6, B6);
  or FA7O1 (TQ1z, TQ1w, TQ1x);
  xor FA1X1 (TQo, A1, B1);
  or FA2O1 (TQ10, TQx, TQy);
  and FA4G2 (TQ1c, A4, TQ18);
  xor FA6X2 (S6, TQ1n, TQ1m);
  or FA7O2 (Cout, TQ1z, TQ1y);
  xor FA1X2 (S1, TQo, TQn);
  or FA2O2 (TQ11, TQ10, TQz);
  and FA4G3 (TQ1d, TQ18, B4);
  and FA6G1 (TQ1p, B6, A6);
  and FA1G1 (TQq, B1, A1);
  xor FA3X1 (TQ12, A3, B3);
  or FA4O1 (TQ1e, TQ1b, TQ1c);
  and FA6G2 (TQ1q, A6, TQ1m);
  and FA1G2 (TQr, A1, TQn);
  xor FA3X2 (S3, TQ12, TQ11);
  or FA4O2 (TQ1f, TQ1e, TQ1d);
  and FA6G3 (TQ1r, TQ1m, B6);
  and FA1G3 (TQs, TQn, B1);
  and FA3G1 (TQ14, B3, A3);
  xor FA5X1 (TQ1g, A5, B5);
  or FA6O1 (TQ1s, TQ1p, TQ1q);

  // Other names for the same wires on the sheet: TQ0 = A0; TQ1 = B0; TQ1a = S4; TQ1h = S5; TQ1o = S6; TQ1v = S7;
  //   TQ2 = A1; TQ3 = B1; TQ4 = A2; TQ5 = B2; TQ6 = A3; TQ7 = B3; TQ8 = A4; TQ9 = B4; TQ13 = S3; TQ20 = Cout;
  //   TQa = A5; TQb = B5; TQc = A6; TQd = B6; TQe = A7; TQf = B7; TQg = Cin; TQi = S0; TQp = S1; TQw = S2
endmodule
