// Logisim project alu_1bit.circ as structural Verilog
module alu_1bit (
  input  A0,
  input  B0,
  input  S1,
  input  S0,
  input  Cin,
  output R0,
  output Cout,
  output Z
);

  wire ALU0A_out, ALU0BX_out, ALU0C1_out, ALU0CS_out, ALU0CSN_out, ALU0CSO_out, ALU0G1_out, ALU0G2_out,
       ALU0G3_out, ALU0M1_out, ALU0M1A_out, ALU0M2_out, ALU0M2A_out, ALU0M3_out, ALU0MO1_out, ALU0N1_out,
       ALU0N2_out, ALU0O_out, ALU0SS_out, ALU0X1_out, ALU0X2_out;

  and ALU0A (ALU0A_out, A0, B0);
  or ALU0O (ALU0O_out, B0, A0);
  xor ALU0X1 (ALU0X1_out, A0, ALU0BX_out);
  xor ALU0X2 (ALU0X2_out, ALU0X1_out, ALU0CSO_out);
  and ALU0G1 (ALU0G1_out, A0, ALU0BX_out);
  and ALU0G2 (ALU0G2_out, A0, ALU0CSO_out);
  and ALU0G3 (ALU0G3_out, ALU0X1_out, ALU0CSO_out);
  or ALU0C1 (ALU0C1_out, ALU0G1_out, ALU0G2_out);
  or ALU0C2 (Cout, ALU0C1_out, ALU0G3_out);
  and ALU0SS (ALU0SS_out, S1, S0);
  xor ALU0BX (ALU0BX_out, ALU0SS_out, B0);
  not ALU0N1 (ALU0N1_out, S1);
  not ALU0N2 (ALU0N2_out, S0);
  and ALU0M1A (ALU0M1A_out, ALU0A_out, ALU0N1_out);
  and ALU0M2A (ALU0M2A_out, ALU0O_out, ALU0N1_out);
  and ALU0M1 (ALU0M1_out, ALU0M1A_out, ALU0N2_out);
  and ALU0M2 (ALU0M2_out, ALU0M2A_out, S0);
  and ALU0M3 (ALU0M3_out, ALU0X2_out, S1);
  or ALU0MO1 (ALU0MO1_out, ALU0M1_out, ALU0M2_out);
  or ALU0MO2 (R0, ALU0MO1_out, ALU0M3_out);
  and ALU0CS (ALU0CS_out, ALU0CSN_out, Cin);
  not ALU0CSN (ALU0CSN_out, ALU0SS_out);
  or ALU0CSO (ALU0CSO_out, ALU0CS_out, ALU0SS_out);
  not ALU0ZO (Z, R0);
endmodule
