// Logisim project alu_2bit.circ as structural Verilog
module alu_2bit (
  input  A0,
  input  B0,
  input  A1,
  input  B1,
  input  S1,
  input  S0,
  input  Cin,
  output R0,
  output R1,
  output Cout,
  output Z
);

  wire ALU0A_out, ALU0BX_out, ALU0C1_out, ALU0C2_out, ALU0CS_out, ALU0CSN_out, ALU0CSO_out, ALU0G1_out,
       ALU0G2_out, ALU0G3_out, ALU0M1_out, ALU0M1A_out, ALU0M2_out, ALU0M2A_out, ALU0M3_out, ALU0MO1_out,
       ALU0N1_out, ALU0N2_out, ALU0O_out, ALU0SS_out, ALU0X1_out, ALU0X2_out, ALU0ZO_out, ALU1A_out,
       ALU1BX_out, ALU1C1_out, ALU1C2_out, ALU1G1_out, ALU1G2_out, ALU1G3_out, ALU1M1_out, ALU1M1A_out,
       ALU1M2_out, ALU1M2A_out, ALU1M3_out, ALU1MO1_out, ALU1N1_out, ALU1N2_out, ALU1O_out, ALU1SS_out,
       ALU1X1_out, ALU1X2_out, ALU1ZO_out, ALUCX_out, ALUF_out;

  and ALU0A (ALU0A_out, A0, B0);
  or ALU0O (ALU0O_out, B0, A0);
  xor ALU0X1 (ALU0X1_out, A0, ALU0BX_out);
  xor ALU0X2 (ALU0X2_out, ALU0X1_out, ALU0CSO_out);
  and ALU0G1 (ALU0G1_out, A0, ALU0BX_out);
  and ALU0G2 (ALU0G2_out, A0, ALU0CSO_out);
  and ALU0G3 (ALU0G3_out, ALU0X1_out, ALU0CSO_out);
  or ALU0C1 (ALU0C1_out, ALU0G1_out, ALU0G2_out);
  or ALU0C2 (ALU0C2_out, ALU0C1_out, ALU0G3_out);
  and ALU0SS (ALU0SS_out, S1, S0);
  xor ALU0BX (ALU0BX_out, ALU0SS_out, B0);
  not ALU0N1 (ALU0N1_out, S1);
  not ALU0N2 (ALU0N2_out, S0);
  and ALU0M1A (ALU0M1A_out, ALU0A_out, ALU0N1_out);
  and ALU0M2A (ALU0M2A_out, ALU0O_out, ALU0N1_out);
  and ALU0M1 (ALU0M1_out, ALU0M1A_out, ALU0N2_out);
  and ALU0M2 (ALU0M2_out, ALU0M2A_out, S0);
  and ALU0M3 (ALU0M3_out, ALU0X2_out, S1);
  or ALU0MO1 (ALU0MO1_out, ALU0M1_out, ALU0M2_out);
  or ALU0MO2 (R0, ALU0MO1_out, ALU0M3_out);
  and ALU0CS (ALU0CS_out, ALU0CSN_out, Cin);
  not ALU0CSN (ALU0CSN_out, ALU0SS_out);
  or ALU0CSO (ALU0CSO_out, ALU0CS_out, ALU0SS_out);
  or ALU0ZO (ALU0ZO_out, R0, R1);
  and ALU1A (ALU1A_out, A1, B1);
  or ALU1O (ALU1O_out, B1, A1);
  xor ALU1X1 (ALU1X1_out, A1, ALU1BX_out);
  xor ALU1X2 (ALU1X2_out, ALU1X1_out, ALU0C2_out);
  and ALU1G1 (ALU1G1_out, A1, ALU1BX_out);
  and ALU1G2 (ALU1G2_out, A1, ALU0C2_out);
  and ALU1G3 (ALU1G3_out, ALU1X1_out, ALU0C2_out);
  or ALU1C1 (ALU1C1_out, ALU1G1_out, ALU1G2_out);
  or ALU1C2 (ALU1C2_out, ALU1C1_out, ALU1G3_out);
  and ALU1SS (ALU1SS_out, S1, S0);
  xor ALU1BX (ALU1BX_out, ALU1SS_out, B1);
  not ALU1N1 (ALU1N1_out, S1);
  not ALU1N2 (ALU1N2_out, S0);
  and ALU1M1A (ALU1M1A_out, ALU1A_out, ALU1N1_out);
  and ALU1M2A (ALU1M2A_out, ALU1O_out, ALU1N1_out);
  and ALU1M1 (ALU1M1_out, ALU1M1A_out, ALU1N2_out);
  and ALU1M2 (ALU1M2_out, ALU1M2A_out, S0);
  and ALU1M3 (ALU1M3_out, ALU1X2_out, S1);
  or ALU1MO1 (ALU1MO1_out, ALU1M1_out, ALU1M2_out);
  or ALU1MO2 (R1, ALU1MO1_out, ALU1M3_out);
  or ALU1ZO (ALU1ZO_out, R1, ALU0ZO_out);
  not ALUZ (Z, ALU1ZO_out);
  and ALUF (ALUF_out, S1, S0);
  xor ALUCX (ALUCX_out, ALU1C2_out, ALUF_out);
  and ALUCG (Cout, ALUCX_out, S1);
endmodule
