// Logisim project alu_4bit.circ as structural Verilog
module alu_4bit (
  input  A0,
  input  B0,
  input  A1,
  input  B1,
  input  A2,
  input  B2,
  input  A3,
  input  B3,
  input  S1,
  input  S0,
  input  Cin,
  output R0,
  output R1,
  output R2,
  output R3,
  output Cout,
  output Z
);

  wire ALU3M1_out, ALU3M1A_out, ALU3M2_out, ALU3M2A_out, ALU3M3_out, ALU3MO1_out, ALU3N1_out, ALU3N2_out,
       ALU3ZO_out, ALUCX_out, ALUF_out, TQ1b, TQ1e, TQ1f, TQ1g, TQ1h, TQ1i, TQ1j, TQ1k, TQ1l, TQ1m, TQ1n,
       TQ1o, TQ1p, TQ1q, TQ1r, TQ1s, TQ1t, TQ1u, TQ1v, TQ1w, TQ1y, TQ2, TQ2a, TQ2b, TQ2d, TQ2g, TQ4, TQ5,
       TQ6, TQ7, TQ8, TQ9, TQ10, TQ11, TQ12, TQ13, TQ14, TQ15, TQ16, TQ17, TQ18, TQ19, TQ21, TQ22, TQ23,
       TQ24, TQ25, TQ26, TQ27, TQ28, TQ29, TQa, TQb, TQc, TQd, TQe, TQf, TQg, TQh, TQi, TQj, TQk, TQl, TQm,
       TQn, TQr, TQs, TQt, TQu, TQv, TQw, TQx, TQy, TQz;

  and ALU0A (TQe, A0, B0);
  or ALU0O (TQh, B0, A0);
  xor ALU0X1 (TQ5, A0, TQc);
  xor ALU0X2 (TQd, TQ5, TQ6);
  and ALU0G1 (TQ7, A0, TQc);
  and ALU0G2 (TQ8, A0, TQ6);
  and ALU0G3 (TQ9, TQ5, TQ6);
  or ALU0C1 (TQa, TQ7, TQ8);
  or ALU0C2 (TQs, TQa, TQ9);
  and ALU0SS (TQb, S1, S0);
  xor ALU0BX (TQc, TQb, B0);
  not ALU0N1 (TQi, S1);
  not ALU0N2 (TQg, S0);
  and ALU0M1A (TQf, TQe, TQi);
  and ALU0M2A (TQj, TQh, TQi);
  and ALU0M1 (TQk, TQf, TQg);
  and ALU0M2 (TQl, TQj, S0);
  and ALU0M3 (TQn, TQd, S1);
  or ALU0MO1 (TQm, TQk, TQl);
  or ALU0MO2 (R0, TQm, TQn);
  and ALU0CS (TQ4, TQ2, Cin);
  not ALU0CSN (TQ2, TQb);
  or ALU0CSO (TQ6, TQ4, TQb);
  or ALU0ZO (TQ1b, R0, R1);
  and ALU1A (TQ10, A1, B1);
  or ALU1O (TQ13, B1, A1);
  xor ALU1X1 (TQr, A1, TQy);
  xor ALU1X2 (TQz, TQr, TQs);
  and ALU1G1 (TQt, A1, TQy);
  and ALU1G2 (TQu, A1, TQs);
  and ALU1G3 (TQv, TQr, TQs);
  or ALU1C1 (TQw, TQt, TQu);
  or ALU1C2 (TQ1f, TQw, TQv);
  and ALU1SS (TQx, S1, S0);
  xor ALU1BX (TQy, TQx, B1);
  not ALU1N1 (TQ14, S1);
  not ALU1N2 (TQ12, S0);
  and ALU1M1A (TQ11, TQ10, TQ14);
  and ALU1M2A (TQ15, TQ13, TQ14);
  and ALU1M1 (TQ16, TQ11, TQ12);
  and ALU1M2 (TQ17, TQ15, S0);
  and ALU1M3 (TQ19, TQz, S1);
  or ALU1MO1 (TQ18, TQ16, TQ17);
  or ALU1MO2 (R1, TQ18, TQ19);
  or ALU1ZO (TQ1y, R1, TQ1b);
  and ALU2A (TQ1n, A2, B2);
  or ALU2O (TQ1q, B2, A2);
  xor ALU2X1 (TQ1e, A2, TQ1l);
  xor ALU2X2 (TQ1m, TQ1e, TQ1f);
  and ALU2G1 (TQ1g, A2, TQ1l);
  and ALU2G2 (TQ1h, A2, TQ1f);
  and ALU2G3 (TQ1i, TQ1e, TQ1f);
  or ALU2C1 (TQ1j, TQ1g, TQ1h);
  or ALU2C2 (TQ22, TQ1j, TQ1i);
  and ALU2SS (TQ1k, S1, S0);
  xor ALU2BX (TQ1l, TQ1k, B2);
  not ALU2N1 (TQ1r, S1);
  not ALU2N2 (TQ1p, S0);
  and ALU2M1A (TQ1o, TQ1n, TQ1r);
  and ALU2M2A (TQ1s, TQ1q, TQ1r);
  and ALU2M1 (TQ1t, TQ1o, TQ1p);
  and ALU2M2 (TQ1u, TQ1s, S0);
  and ALU2M3 (TQ1w, TQ1m, S1);
  or ALU2MO1 (TQ1v, TQ1t, TQ1u);
  or ALU2MO2 (R2, TQ1v, TQ1w);
  or ALU2ZO (TQ2d, R2, TQ1y);
  and ALU3A (TQ2a, A3, B3);
  or ALU3O (TQ2b, B3, A3);
  xor ALU3X1 (TQ21, A3, TQ28);
  xor ALU3X2 (TQ29, TQ21, TQ22);
  and ALU3G1 (TQ23, A3, TQ28);
  and ALU3G2 (TQ24, A3, TQ22);
  and ALU3G3 (TQ25, TQ21, TQ22);
  or ALU3C1 (TQ26, TQ23, TQ24);
  or ALU3C2 (TQ2g, TQ26, TQ25);
  and ALU3SS (TQ27, S1, S0);
  xor ALU3BX (TQ28, TQ27, B3);
  not ALU3N1 (ALU3N1_out, S1);
  not ALU3N2 (ALU3N2_out, S0);
  and ALU3M1A (ALU3M1A_out, TQ2a, ALU3N1_out);
  and ALU3M2A (ALU3M2A_out, TQ2b, ALU3N1_out);
  and ALU3M1 (ALU3M1_out, ALU3M1A_out, ALU3N2_out);
  and ALU3M2 (ALU3M2_out, ALU3M2A_out, S0);
  and ALU3M3 (ALU3M3_out, TQ29, S1);
  or ALU3MO1 (ALU3MO1_out, ALU3M1_out, ALU3M2_out);
  or ALU3MO2 (R3, ALU3MO1_out, ALU3M3_out);
  or ALU3ZO (ALU3ZO_out, R3, TQ2d);
  not ALUZ (Z, ALU3ZO_out);
  and ALUF (ALUF_out, S1, S0);
  xor ALUCX (ALUCX_out, TQ2g, ALUF_out);
  and ALUCG (Cout, ALUCX_out, S1);

  // Other names for the same wires on the sheet: TQ0 = A0; TQ1 = B0; TQ1a = R1; TQ1c = A2; TQ1d = B2; TQ1x = R2;
  //   TQ1z = A3; TQ2c = R3; TQ2e = Z; TQ2f = S0; TQ2h = S1; TQ2i = Cout; TQ3 = Cin; TQ20 = B3; TQo = R0; TQp = A1;
  //   TQq = B1
endmodule
