// Logisim project alu_8bit.circ as structural Verilog
module alu_8bit (
  input  A0,
  input  B0,
  input  A1,
  input  B1,
  input  A2,
  input  B2,
  input  A3,
  input  B3,
  input  A4,
  input  B4,
  input  A5,
  input  B5,
  input  A6,
  input  B6,
  input  A7,
  input  B7,
  input  S1,
  input  S0,
  input  Cin,
  output R0,
  output R1,
  output R2,
  output R3,
  output R4,
  output R5,
  output R6,
  output R7,
  output Cout,
  output Z
);

  wire ALU0A_out, ALU0BX_out, ALU0C1_out, ALU0C2_out, ALU0CS_out, ALU0CSN_out, ALU0CSO_out, ALU0G1_out,
       ALU0G2_out, ALU0G3_out, ALU0M1_out, ALU0M1A_out, ALU0M2_out, ALU0M2A_out, ALU0M3_out, ALU0MO1_out,
       ALU0N1_out, ALU0N2_out, ALU0O_out, ALU0SS_out, ALU0X1_out, ALU0X2_out, ALU0ZO_out, ALU1A_out,
       ALU1BX_out, ALU1C1_out, ALU1C2_out, ALU1G1_out, ALU1G2_out, ALU1G3_out, ALU1M1_out, ALU1M1A_out,
       ALU1M2_out, ALU1M2A_out, ALU1M3_out, ALU1MO1_out, ALU1N1_out, ALU1N2_out, ALU1O_out, ALU1SS_out,
       ALU1X1_out, ALU1X2_out, ALU1ZO_out, ALU2A_out, ALU2BX_out, ALU2C1_out, ALU2C2_out, ALU2G1_out,
       ALU2G2_out, ALU2G3_out, ALU2M1_out, ALU2M1A_out, ALU2M2_out, ALU2M2A_out, ALU2M3_out, ALU2MO1_out,
       ALU2N1_out, ALU2N2_out, ALU2O_out, ALU2SS_out, ALU2X1_out, ALU2X2_out, ALU2ZO_out, ALU3A_out,
       ALU3BX_out, ALU3C1_out, ALU3C2_out, ALU3G1_out, ALU3G2_out, ALU3G3_out, ALU3M1_out, ALU3M1A_out,
       ALU3M2_out, ALU3M2A_out, ALU3M3_out, ALU3MO1_out, ALU3N1_out, ALU3N2_out, ALU3O_out, ALU3SS_out,
       ALU3X1_out, ALU3X2_out, ALU3ZO_out, ALU4A_out, ALU4BX_out, ALU4C1_out, ALU4C2_out, ALU4G1_out,
       ALU4G2_out, ALU4G3_out, ALU4M1_out, ALU4M1A_out, ALU4M2_out, ALU4M2A_out, ALU4M3_out, ALU4MO1_out,
       ALU4N1_out, ALU4N2_out, ALU4O_out, ALU4SS_out, ALU4X1_out, ALU4X2_out, ALU4ZO_out, ALU5A_out,
       ALU5BX_out, ALU5C1_out, ALU5C2_out, ALU5G1_out, ALU5G2_out, ALU5G3_out, ALU5M1_out, ALU5M1A_out,
       ALU5M2_out, ALU5M2A_out, ALU5M3_out, ALU5MO1_out, ALU5N1_out, ALU5N2_out, ALU5O_out, ALU5SS_out,
       ALU5X1_out, ALU5X2_out, ALU5ZO_out, ALU6A_out, ALU6BX_out, ALU6C1_out, ALU6C2_out, ALU6G1_out,
       ALU6G2_out, ALU6G3_out, ALU6M1_out, ALU6M1A_out, ALU6M2_out, ALU6M2A_out, ALU6M3_out, ALU6MO1_out,
       ALU6N1_out, ALU6N2_out, ALU6O_out, ALU6SS_out, ALU6X1_out, ALU6X2_out, ALU6ZO_out, ALU7A_out,
       ALU7BX_out, ALU7C1_out, ALU7C2_out, ALU7G1_out, ALU7G2_out, ALU7G3_out, ALU7M1_out, ALU7M1A_out,
       ALU7M2_out, ALU7M2A_out, ALU7M3_out, ALU7MO1_out, ALU7N1_out, ALU7N2_out, ALU7O_out, ALU7SS_out,
       ALU7X1_out, ALU7X2_out, ALU7ZO_out, ALUCX_out, ALUF_out;

  and ALU0A (ALU0A_out, A0, B0);
  or ALU0O (ALU0O_out, B0, A0);
  xor ALU0X1 (ALU0X1_out, A0, ALU0BX_out);
  xor ALU0X2 (ALU0X2_out, ALU0X1_out, ALU0CSO_out);
  and ALU0G1 (ALU0G1_out, A0, ALU0BX_out);
  and ALU0G2 (ALU0G2_out, A0, ALU0CSO_out);
  and ALU0G3 (ALU0G3_out, ALU0X1_out, ALU0CSO_out);
  or ALU0C1 (ALU0C1_out, ALU0G1_out, ALU0G2_out);
  or ALU0C2 (ALU0C2_out, ALU0C1_out, ALU0G3_out);
  and ALU0SS (ALU0SS_out, S1, S0);
  xor ALU0BX (ALU0BX_out, ALU0SS_out, B0);
  not ALU0N1 (ALU0N1_out, S1);
  not ALU0N2 (ALU0N2_out, S0);
  and ALU0M1A (ALU0M1A_out, ALU0A_out, ALU0N1_out);
  and ALU0M2A (ALU0M2A_out, ALU0O_out, ALU0N1_out);
  and ALU0M1 (ALU0M1_out, ALU0M1A_out, ALU0N2_out);
  and ALU0M2 (ALU0M2_out, ALU0M2A_out, S0);
  and ALU0M3 (ALU0M3_out, ALU0X2_out, S1);
  or ALU0MO1 (ALU0MO1_out, ALU0M1_out, ALU0M2_out);
  or ALU0MO2 (R0, ALU0MO1_out, ALU0M3_out);
  and ALU0CS (ALU0CS_out, ALU0CSN_out, Cin);
  not ALU0CSN (ALU0CSN_out, ALU0SS_out);
  or ALU0CSO (ALU0CSO_out, ALU0CS_out, ALU0SS_out);
  or ALU0ZO (ALU0ZO_out, R0, R1);
  and ALU1A (ALU1A_out, A1, B1);
  or ALU1O (ALU1O_out, B1, A1);
  xor ALU1X1 (ALU1X1_out, A1, ALU1BX_out);
  xor ALU1X2 (ALU1X2_out, ALU1X1_out, ALU0C2_out);
  and ALU1G1 (ALU1G1_out, A1, ALU1BX_out);
  and ALU1G2 (ALU1G2_out, A1, ALU0C2_out);
  and ALU1G3 (ALU1G3_out, ALU1X1_out, ALU0C2_out);
  or ALU1C1 (ALU1C1_out, ALU1G1_out, ALU1G2_out);
  or ALU1C2 (ALU1C2_out, ALU1C1_out, ALU1G3_out);
  and ALU1SS (ALU1SS_out, S1, S0);
  xor ALU1BX (ALU1BX_out, ALU1SS_out, B1);
  not ALU1N1 (ALU1N1_out, S1);
  not ALU1N2 (ALU1N2_out, S0);
  and ALU1M1A (ALU1M1A_out, ALU1A_out, ALU1N1_out);
  and ALU1M2A (ALU1M2A_out, ALU1O_out, ALU1N1_out);
  and ALU1M1 (ALU1M1_out, ALU1M1A_out, ALU1N2_out);
  and ALU1M2 (ALU1M2_out, ALU1M2A_out, S0);
  and ALU1M3 (ALU1M3_out, ALU1X2_out, S1);
  or ALU1MO1 (ALU1MO1_out, ALU1M1_out, ALU1M2_out);
  or ALU1MO2 (R1, ALU1MO1_out, ALU1M3_out);
  or ALU1ZO (ALU1ZO_out, R1, ALU0ZO_out);
  and ALU2A (ALU2A_out, A2, B2);
  or ALU2O (ALU2O_out, B2, A2);
  xor ALU2X1 (ALU2X1_out, A2, ALU2BX_out);
  xor ALU2X2 (ALU2X2_out, ALU2X1_out, ALU1C2_out);
  and ALU2G1 (ALU2G1_out, A2, ALU2BX_out);
  and ALU2G2 (ALU2G2_out, A2, ALU1C2_out);
  and ALU2G3 (ALU2G3_out, ALU2X1_out, ALU1C2_out);
  or ALU2C1 (ALU2C1_out, ALU2G1_out, ALU2G2_out);
  or ALU2C2 (ALU2C2_out, ALU2C1_out, ALU2G3_out);
  and ALU2SS (ALU2SS_out, S1, S0);
  xor ALU2BX (ALU2BX_out, ALU2SS_out, B2);
  not ALU2N1 (ALU2N1_out, S1);
  not ALU2N2 (ALU2N2_out, S0);
  and ALU2M1A (ALU2M1A_out, ALU2A_out, ALU2N1_out);
  and ALU2M2A (ALU2M2A_out, ALU2O_out, ALU2N1_out);
  and ALU2M1 (ALU2M1_out, ALU2M1A_out, ALU2N2_out);
  and ALU2M2 (ALU2M2_out, ALU2M2A_out, S0);
  and ALU2M3 (ALU2M3_out, ALU2X2_out, S1);
  or ALU2MO1 (ALU2MO1_out, ALU2M1_out, ALU2M2_out);
  or ALU2MO2 (R2, ALU2MO1_out, ALU2M3_out);
  or ALU2ZO (ALU2ZO_out, R2, ALU1ZO_out);
  and ALU3A (ALU3A_out, A3, B3);
  or ALU3O (ALU3O_out, B3, A3);
  xor ALU3X1 (ALU3X1_out, A3, ALU3BX_out);
  xor ALU3X2 (ALU3X2_out, ALU3X1_out, ALU2C2_out);
  and ALU3G1 (ALU3G1_out, A3, ALU3BX_out);
  and ALU3G2 (ALU3G2_out, A3, ALU2C2_out);
  and ALU3G3 (ALU3G3_out, ALU3X1_out, ALU2C2_out);
  or ALU3C1 (ALU3C1_out, ALU3G1_out, ALU3G2_out);
  or ALU3C2 (ALU3C2_out, ALU3C1_out, ALU3G3_out);
  and ALU3SS (ALU3SS_out, S1, S0);
  xor ALU3BX (ALU3BX_out, ALU3SS_out, B3);
  not ALU3N1 (ALU3N1_out, S1);
  not ALU3N2 (ALU3N2_out, S0);
  and ALU3M1A (ALU3M1A_out, ALU3A_out, ALU3N1_out);
  and ALU3M2A (ALU3M2A_out, ALU3O_out, ALU3N1_out);
  and ALU3M1 (ALU3M1_out, ALU3M1A_out, ALU3N2_out);
  and ALU3M2 (ALU3M2_out, ALU3M2A_out, S0);
  and ALU3M3 (ALU3M3_out, ALU3X2_out, S1);
  or ALU3MO1 (ALU3MO1_out, ALU3M1_out, ALU3M2_out);
  or ALU3MO2 (R3, ALU3MO1_out, ALU3M3_out);
  or ALU3ZO (ALU3ZO_out, R3, ALU2ZO_out);
  and ALU4A (ALU4A_out, A4, B4);
  or ALU4O (ALU4O_out, B4, A4);
  xor ALU4X1 (ALU4X1_out, A4, ALU4BX_out);
  xor ALU4X2 (ALU4X2_out, ALU4X1_out, ALU3C2_out);
  and ALU4G1 (ALU4G1_out, A4, ALU4BX_out);
  and ALU4G2 (ALU4G2_out, A4, ALU3C2_out);
  and ALU4G3 (ALU4G3_out, ALU4X1_out, ALU3C2_out);
  or ALU4C1 (ALU4C1_out, ALU4G1_out, ALU4G2_out);
  or ALU4C2 (ALU4C2_out, ALU4C1_out, ALU4G3_out);
  and ALU4SS (ALU4SS_out, S1, S0);
  xor ALU4BX (ALU4BX_out, ALU4SS_out, B4);
  not ALU4N1 (ALU4N1_out, S1);
  not ALU4N2 (ALU4N2_out, S0);
  and ALU4M1A (ALU4M1A_out, ALU4A_out, ALU4N1_out);
  and ALU4M2A (ALU4M2A_out, ALU4O_out, ALU4N1_out);
  and ALU4M1 (ALU4M1_out, ALU4M1A_out, ALU4N2_out);
  and ALU4M2 (ALU4M2_out, ALU4M2A_out, S0);
  and ALU4M3 (ALU4M3_out, ALU4X2_out, S1);
  or ALU4MO1 (ALU4MO1_out, ALU4M1_out, ALU4M2_out);
  or ALU4MO2 (R4, ALU4MO1_out, ALU4M3_out);
  or ALU4ZO (ALU4ZO_out, R4, ALU3ZO_out);
  and ALU5A (ALU5A_out, A5, B5);
  or ALU5O (ALU5O_out, B5, A5);
  xor ALU5X1 (ALU5X1_out, A5, ALU5BX_out);
  xor ALU5X2 (ALU5X2_out, ALU5X1_out, ALU4C2_out);
  and ALU5G1 (ALU5G1_out, A5, ALU5BX_out);
  and ALU5G2 (ALU5G2_out, A5, ALU4C2_out);
  and ALU5G3 (ALU5G3_out, ALU5X1_out, ALU4C2_out);
  or ALU5C1 (ALU5C1_out, ALU5G1_out, ALU5G2_out);
  or ALU5C2 (ALU5C2_out, ALU5C1_out, ALU5G3_out);
  and ALU5SS (ALU5SS_out, S1, S0);
  xor ALU5BX (ALU5BX_out, ALU5SS_out, B5);
  not ALU5N1 (ALU5N1_out, S1);
  not ALU5N2 (ALU5N2_out, S0);
  and ALU5M1A (ALU5M1A_out, ALU5A_out, ALU5N1_out);
  and ALU5M2A (ALU5M2A_out, ALU5O_out, ALU5N1_out);
  and ALU5M1 (ALU5M1_out, ALU5M1A_out, ALU5N2_out);
  and ALU5M2 (ALU5M2_out, ALU5M2A_out, S0);
  and ALU5M3 (ALU5M3_out, ALU5X2_out, S1);
  or ALU5MO1 (ALU5MO1_out, ALU5M1_out, ALU5M2_out);
  or ALU5MO2 (R5, ALU5MO1_out, ALU5M3_out);
  or ALU5ZO (ALU5ZO_out, R5, ALU4ZO_out);
  and ALU6A (ALU6A_out, A6, B6);
  or ALU6O (ALU6O_out, B6, A6);
  xor ALU6X1 (ALU6X1_out, A6, ALU6BX_out);
  xor ALU6X2 (ALU6X2_out, ALU6X1_out, ALU5C2_out);
  and ALU6G1 (ALU6G1_out, A6, ALU6BX_out);
  and ALU6G2 (ALU6G2_out, A6, ALU5C2_out);
  and ALU6G3 (ALU6G3_out, ALU6X1_out, ALU5C2_out);
  or ALU6C1 (ALU6C1_out, ALU6G1_out, ALU6G2_out);
  or ALU6C2 (ALU6C2_out, ALU6C1_out, ALU6G3_out);
  and ALU6SS (ALU6SS_out, S1, S0);
  xor ALU6BX (ALU6BX_out, ALU6SS_out, B6);
  not ALU6N1 (ALU6N1_out, S1);
  not ALU6N2 (ALU6N2_out, S0);
  and ALU6M1A (ALU6M1A_out, ALU6A_out, ALU6N1_out);
  and ALU6M2A (ALU6M2A_out, ALU6O_out, ALU6N1_out);
  and ALU6M1 (ALU6M1_out, ALU6M1A_out, ALU6N2_out);
  and ALU6M2 (ALU6M2_out, ALU6M2A_out, S0);
  and ALU6M3 (ALU6M3_out, ALU6X2_out, S1);
  or ALU6MO1 (ALU6MO1_out, ALU6M1_out, ALU6M2_out);
  or ALU6MO2 (R6, ALU6MO1_out, ALU6M3_out);
  or ALU6ZO (ALU6ZO_out, R6, ALU5ZO_out);
  and ALU7A (ALU7A_out, A7, B7);
  or ALU7O (ALU7O_out, B7, A7);
  xor ALU7X1 (ALU7X1_out, A7, ALU7BX_out);
  xor ALU7X2 (ALU7X2_out, ALU7X1_out, ALU6C2_out);
  and ALU7G1 (ALU7G1_out, A7, ALU7BX_out);
  and ALU7G2 (ALU7G2_out, A7, ALU6C2_out);
  and ALU7G3 (ALU7G3_out, ALU7X1_out, ALU6C2_out);
  or ALU7C1 (ALU7C1_out, ALU7G1_out, ALU7G2_out);
  or ALU7C2 (ALU7C2_out, ALU7C1_out, ALU7G3_out);
  and ALU7SS (ALU7SS_out, S1, S0);
  xor ALU7BX (ALU7BX_out, ALU7SS_out, B7);
  not ALU7N1 (ALU7N1_out, S1);
  not ALU7N2 (ALU7N2_out, S0);
  and ALU7M1A (ALU7M1A_out, ALU7A_out, ALU7N1_out);
  and ALU7M2A (ALU7M2A_out, ALU7O_out, ALU7N1_out);
  and ALU7M1 (ALU7M1_out, ALU7M1A_out, ALU7N2_out);
  and ALU7M2 (ALU7M2_out, ALU7M2A_out, S0);
  and ALU7M3 (ALU7M3_out, ALU7X2_out, S1);
  or ALU7MO1 (ALU7MO1_out, ALU7M1_out, ALU7M2_out);
  or ALU7MO2 (R7, ALU7MO1_out, ALU7M3_out);
  or ALU7ZO (ALU7ZO_out, R7, ALU6ZO_out);
  not ALUZ (Z, ALU7ZO_out);
  and ALUF (ALUF_out, S1, S0);
  xor ALUCX (ALUCX_out, ALU7C2_out, ALUF_out);
  and ALUCG (Cout, ALUCX_out, S1);
endmodule
