// Logisim project automatic_door.circ as structural Verilog
module automatic_door (
  input  RST,
  input  SENSOR,
  input  LIM,
  input  CLOSED,
  output OPENV,
  output HOLD,
  output CLOSEV
);

  wire A21_out, A22_out, A23_out, AH0_out, AH1_out, NC0_out, NC1_out, O24_out, O25_out, O26_out, O28_out,
       O29_out, O30_out, TQ0, TQ1, TQ3, TQ4, TQ5, TQ6, TQ7, TQ8, TQ9, TQa, TQb, TQd, TQg, TQh, TQi, TQj, TQl,
       TQm, TQn, TQo, TQp, TQr, TQs, TQt, TQu, TQv, TQx;

  Clock CLK (.out(TQ1));
  D_Flip_Flop U1 (.D(TQ3), .clk(TQ1), .Q(TQ0), .reset(RST));  // open: Qn, preset
  D_Flip_Flop U2 (.D(TQb), .clk(TQ1), .Q(TQ8), .reset(RST));  // open: Qn, preset
  not N1 (TQl, TQ0);
  not N2 (TQg, TQ8);
  not NIsensor (TQs, SENSOR);
  not NIlim (TQx, LIM);
  not NIclosed (TQv, CLOSED);
  // AND_Gate M0 has open pins: in0=TQl, in1=TQg, out=open
  and A1 (TQ9, TQl, TQg);
  and A2 (TQa, TQ9, TQv);
  and A3 (TQd, TQa, SENSOR);
  and A4 (TQ6, TQd, TQx);
  and M5 (OPENV, TQ0, TQg);
  and A6 (TQh, TQ0, TQg);
  and A7 (TQi, TQh, TQv);
  and A8 (TQj, TQi, TQs);
  and A9 (TQ4, TQj, LIM);
  and M10 (HOLD, TQl, TQ8);
  and A11 (TQm, TQl, TQ8);
  and A12 (TQn, TQm, TQv);
  and A13 (TQo, TQn, TQs);
  and A14 (TQ5, TQo, TQx);
  and M15 (CLOSEV, TQ0, TQ8);
  and A16 (TQp, TQ0, TQ8);
  and A17 (TQr, TQp, CLOSED);
  and A18 (TQt, TQr, TQs);
  and A19 (TQ7, TQt, TQx);
  and A20 (TQu, TQ0, TQ8);
  and A21 (A21_out, TQu, TQv);
  and A22 (A22_out, A21_out, SENSOR);
  and A23 (A23_out, A22_out, TQx);
  or O24 (O24_out, TQ6, A23_out);
  or O25 (O25_out, O24_out, TQ5);
  or O26 (O26_out, TQ4, TQ7);
  not NC0 (NC0_out, O26_out);
  and AH0 (AH0_out, TQ0, NC0_out);
  or O27 (TQ3, O25_out, AH0_out);
  or O28 (O28_out, TQ4, TQ5);
  or O29 (O29_out, TQ6, A23_out);
  or O30 (O30_out, O29_out, TQ7);
  not NC1 (NC1_out, O30_out);
  and AH1 (AH1_out, TQ8, NC1_out);
  or O31 (TQb, O28_out, AH1_out);

  // Other names for the same wires on the sheet: TQ2 = RST; TQc = OPENV; TQe = HOLD; TQf = CLOSEV; TQk = LIM;
  //   TQq = CLOSED; TQw = SENSOR
endmodule
