// Logisim project barrel_shifter_2bit.circ as structural Verilog
module barrel_shifter_2bit (
  input  D0,
  input  D1,
  input  SH0,
  input  GND,
  output Y0,
  output Y1
);

  wire NS1_out, SA1_out, SA2_out, SA4_out, SA5_out;

  not NS1 (NS1_out, SH0);
  and SA1 (SA1_out, D0, NS1_out);
  and SA2 (SA2_out, GND, SH0);
  or MO3 (Y0, SA1_out, SA2_out);
  and SA4 (SA4_out, D1, NS1_out);
  and SA5 (SA5_out, D0, SH0);
  or MO6 (Y1, SA4_out, SA5_out);

  // Other names for the same wires on the sheet: TQ0 = GND; TQ1 = Y0; TQ2 = D1; TQ3 = D0; TQ4 = SH0; TQ5 = Y1
endmodule
