// Logisim project barrel_shifter_4bit.circ as structural Verilog
module barrel_shifter_4bit (
  input  D0,
  input  D1,
  input  D2,
  input  D3,
  input  SH0,
  input  SH1,
  input  GND,
  output Y0,
  output Y1,
  output Y2,
  output Y3
);

  wire MO9_out, MO10_out, MO20_out, MO21_out, MO31_out, MO32_out, MO42_out, MO43_out, NS1_out, NS2_out,
       SA1_out, SA3_out, SA5_out, SA7_out, SA12_out, SA14_out, SA16_out, SA18_out, SA23_out, SA25_out,
       SA27_out, SA29_out, SA34_out, SA36_out, SA38_out, SA40_out, SB2_out, SB4_out, SB6_out, SB8_out,
       SB13_out, SB15_out, SB17_out, SB19_out, SB24_out, SB26_out, SB28_out, SB30_out, SB35_out, SB37_out,
       SB39_out, SB41_out;

  not NS1 (NS1_out, SH0);
  not NS2 (NS2_out, SH1);
  and SA1 (SA1_out, D0, NS1_out);
  and SB2 (SB2_out, SA1_out, NS2_out);
  and SA3 (SA3_out, GND, SH0);
  and SB4 (SB4_out, SA3_out, NS2_out);
  and SA5 (SA5_out, GND, NS1_out);
  and SB6 (SB6_out, SA5_out, SH1);
  and SA7 (SA7_out, GND, SH0);
  and SB8 (SB8_out, SA7_out, SH1);
  or MO9 (MO9_out, SB2_out, SB4_out);
  or MO10 (MO10_out, MO9_out, SB6_out);
  or MO11 (Y0, MO10_out, SB8_out);
  and SA12 (SA12_out, D1, NS1_out);
  and SB13 (SB13_out, SA12_out, NS2_out);
  and SA14 (SA14_out, D0, SH0);
  and SB15 (SB15_out, SA14_out, NS2_out);
  and SA16 (SA16_out, GND, NS1_out);
  and SB17 (SB17_out, SA16_out, SH1);
  and SA18 (SA18_out, GND, SH0);
  and SB19 (SB19_out, SA18_out, SH1);
  or MO20 (MO20_out, SB13_out, SB15_out);
  or MO21 (MO21_out, MO20_out, SB17_out);
  or MO22 (Y1, MO21_out, SB19_out);
  and SA23 (SA23_out, D2, NS1_out);
  and SB24 (SB24_out, SA23_out, NS2_out);
  and SA25 (SA25_out, D1, SH0);
  and SB26 (SB26_out, SA25_out, NS2_out);
  and SA27 (SA27_out, D0, NS1_out);
  and SB28 (SB28_out, SA27_out, SH1);
  and SA29 (SA29_out, GND, SH0);
  and SB30 (SB30_out, SA29_out, SH1);
  or MO31 (MO31_out, SB24_out, SB26_out);
  or MO32 (MO32_out, MO31_out, SB28_out);
  or MO33 (Y2, MO32_out, SB30_out);
  and SA34 (SA34_out, D3, NS1_out);
  and SB35 (SB35_out, SA34_out, NS2_out);
  and SA36 (SA36_out, D2, SH0);
  and SB37 (SB37_out, SA36_out, NS2_out);
  and SA38 (SA38_out, D1, NS1_out);
  and SB39 (SB39_out, SA38_out, SH1);
  and SA40 (SA40_out, D0, SH0);
  and SB41 (SB41_out, SA40_out, SH1);
  or MO42 (MO42_out, SB35_out, SB37_out);
  or MO43 (MO43_out, MO42_out, SB39_out);
  or MO44 (Y3, MO43_out, SB41_out);
endmodule
