// Logisim project barrel_shifter_8bit.circ as structural Verilog
module barrel_shifter_8bit (
  input  D0,
  input  D1,
  input  D2,
  input  D3,
  input  D4,
  input  D5,
  input  D6,
  input  D7,
  input  SH0,
  input  SH1,
  input  SH2,
  input  GND,
  output Y0,
  output Y1,
  output Y2,
  output Y3,
  output Y4,
  output Y5,
  output Y6,
  output Y7
);

  wire MO242_out, MO243_out, MO244_out, MO245_out, MO246_out, MO247_out, SA236_out, SA239_out, SB234_out,
       SB235_out, SB237_out, SB238_out, SB240_out, SB241_out, TQ0, TQ1, TQ1a, TQ1b, TQ1c, TQ1d, TQ1e, TQ1f,
       TQ1g, TQ1h, TQ1i, TQ1j, TQ1k, TQ1l, TQ1m, TQ1n, TQ1o, TQ1q, TQ1r, TQ1s, TQ1t, TQ1u, TQ1v, TQ1w, TQ1x,
       TQ1y, TQ1z, TQ2, TQ2a, TQ2b, TQ2c, TQ2d, TQ2e, TQ2f, TQ2g, TQ2h, TQ2i, TQ2j, TQ2l, TQ2m, TQ2n, TQ2o,
       TQ2p, TQ2q, TQ2r, TQ2s, TQ2t, TQ2u, TQ2v, TQ2w, TQ2x, TQ2y, TQ2z, TQ3, TQ3a, TQ3b, TQ3c, TQ3d, TQ3e,
       TQ3g, TQ3h, TQ3i, TQ3j, TQ3k, TQ3l, TQ3m, TQ3n, TQ3o, TQ3p, TQ3q, TQ3r, TQ3s, TQ3t, TQ3u, TQ3v, TQ3w,
       TQ3x, TQ3y, TQ3z, TQ4, TQ4b, TQ4c, TQ4d, TQ4e, TQ4f, TQ4g, TQ4h, TQ4i, TQ4j, TQ4k, TQ4l, TQ4m, TQ4n,
       TQ4o, TQ4p, TQ4q, TQ4r, TQ4s, TQ4t, TQ4u, TQ4v, TQ4w, TQ4x, TQ4y, TQ4z, TQ5, TQ5a, TQ5b, TQ5c, TQ5d,
       TQ5e, TQ5f, TQ5g, TQ5h, TQ5i, TQ5j, TQ5l, TQ5m, TQ5n, TQ5o, TQ5p, TQ5q, TQ5r, TQ5s, TQ5t, TQ5u, TQ5v,
       TQ5w, TQ5x, TQ5y, TQ5z, TQ6, TQ6a, TQ6c, TQ6d, TQ6e, TQ6g, TQ6h, TQ6j, TQ6k, TQ6m, TQ6r, TQ6s, TQ6t,
       TQ6u, TQ6v, TQ7, TQ8, TQ9, TQ10, TQ11, TQ12, TQ13, TQ14, TQ15, TQ16, TQ17, TQ18, TQ19, TQ20, TQ21,
       TQ22, TQ23, TQ24, TQ25, TQ26, TQ27, TQ28, TQ29, TQ30, TQ31, TQ32, TQ33, TQ34, TQ35, TQ36, TQ37, TQ38,
       TQ39, TQ40, TQ41, TQ42, TQ43, TQ44, TQ45, TQ46, TQ47, TQ48, TQ49, TQ50, TQ51, TQ52, TQ53, TQ54, TQ56,
       TQ57, TQ58, TQ59, TQ60, TQ63, TQ64, TQ66, TQ67, TQ69, TQa, TQb, TQc, TQd, TQe, TQf, TQg, TQh, TQi,
       TQj, TQk, TQl, TQm, TQn, TQo, TQp, TQq, TQr, TQs, TQt, TQv, TQw, TQx, TQy, TQz;

  not NS1 (TQ6m, SH0);
  not NS2 (TQ6k, SH1);
  not NS3 (TQ6e, SH2);
  and SA1 (TQ0, D0, TQ6m);
  and SB2 (TQ1, TQ0, TQ6k);
  and SB3 (TQg, TQ1, TQ6e);
  and SA4 (TQ2, GND, SH0);
  and SB5 (TQ3, TQ2, TQ6k);
  and SB6 (TQh, TQ3, TQ6e);
  and SA7 (TQ4, GND, TQ6m);
  and SB8 (TQ5, TQ4, SH1);
  and SB9 (TQj, TQ5, TQ6e);
  and SA10 (TQ6, GND, SH0);
  and SB11 (TQ7, TQ6, SH1);
  and SB12 (TQl, TQ7, TQ6e);
  and SA13 (TQ8, GND, TQ6m);
  and SB14 (TQ9, TQ8, TQ6k);
  and SB15 (TQn, TQ9, SH2);
  and SA16 (TQa, GND, SH0);
  and SB17 (TQb, TQa, TQ6k);
  and SB18 (TQp, TQb, SH2);
  and SA19 (TQc, GND, TQ6m);
  and SB20 (TQd, TQc, SH1);
  and SB21 (TQr, TQd, SH2);
  and SA22 (TQe, GND, SH0);
  and SB23 (TQf, TQe, SH1);
  and SB24 (TQt, TQf, SH2);
  or MO25 (TQi, TQg, TQh);
  or MO26 (TQk, TQi, TQj);
  or MO27 (TQm, TQk, TQl);
  or MO28 (TQo, TQm, TQn);
  or MO29 (TQq, TQo, TQp);
  or MO30 (TQs, TQq, TQr);
  or MO31 (Y0, TQs, TQt);
  and SA32 (TQv, D1, TQ6m);
  and SB33 (TQw, TQv, TQ6k);
  and SB34 (TQ1b, TQw, TQ6e);
  and SA35 (TQx, D0, SH0);
  and SB36 (TQy, TQx, TQ6k);
  and SB37 (TQ1c, TQy, TQ6e);
  and SA38 (TQz, GND, TQ6m);
  and SB39 (TQ10, TQz, SH1);
  and SB40 (TQ1e, TQ10, TQ6e);
  and SA41 (TQ11, GND, SH0);
  and SB42 (TQ12, TQ11, SH1);
  and SB43 (TQ1g, TQ12, TQ6e);
  and SA44 (TQ13, GND, TQ6m);
  and SB45 (TQ14, TQ13, TQ6k);
  and SB46 (TQ1i, TQ14, SH2);
  and SA47 (TQ15, GND, SH0);
  and SB48 (TQ16, TQ15, TQ6k);
  and SB49 (TQ1k, TQ16, SH2);
  and SA50 (TQ17, GND, TQ6m);
  and SB51 (TQ18, TQ17, SH1);
  and SB52 (TQ1m, TQ18, SH2);
  and SA53 (TQ19, GND, SH0);
  and SB54 (TQ1a, TQ19, SH1);
  and SB55 (TQ1o, TQ1a, SH2);
  or MO56 (TQ1d, TQ1b, TQ1c);
  or MO57 (TQ1f, TQ1d, TQ1e);
  or MO58 (TQ1h, TQ1f, TQ1g);
  or MO59 (TQ1j, TQ1h, TQ1i);
  or MO60 (TQ1l, TQ1j, TQ1k);
  or MO61 (TQ1n, TQ1l, TQ1m);
  or MO62 (Y1, TQ1n, TQ1o);
  and SA63 (TQ1q, D2, TQ6m);
  and SB64 (TQ1r, TQ1q, TQ6k);
  and SB65 (TQ26, TQ1r, TQ6e);
  and SA66 (TQ1s, D1, SH0);
  and SB67 (TQ1t, TQ1s, TQ6k);
  and SB68 (TQ27, TQ1t, TQ6e);
  and SA69 (TQ1u, D0, TQ6m);
  and SB70 (TQ1v, TQ1u, SH1);
  and SB71 (TQ29, TQ1v, TQ6e);
  and SA72 (TQ1w, GND, SH0);
  and SB73 (TQ1x, TQ1w, SH1);
  and SB74 (TQ2b, TQ1x, TQ6e);
  and SA75 (TQ1y, GND, TQ6m);
  and SB76 (TQ1z, TQ1y, TQ6k);
  and SB77 (TQ2d, TQ1z, SH2);
  and SA78 (TQ20, GND, SH0);
  and SB79 (TQ21, TQ20, TQ6k);
  and SB80 (TQ2f, TQ21, SH2);
  and SA81 (TQ22, GND, TQ6m);
  and SB82 (TQ23, TQ22, SH1);
  and SB83 (TQ2h, TQ23, SH2);
  and SA84 (TQ24, GND, SH0);
  and SB85 (TQ25, TQ24, SH1);
  and SB86 (TQ2j, TQ25, SH2);
  or MO87 (TQ28, TQ26, TQ27);
  or MO88 (TQ2a, TQ28, TQ29);
  or MO89 (TQ2c, TQ2a, TQ2b);
  or MO90 (TQ2e, TQ2c, TQ2d);
  or MO91 (TQ2g, TQ2e, TQ2f);
  or MO92 (TQ2i, TQ2g, TQ2h);
  or MO93 (Y2, TQ2i, TQ2j);
  and SA94 (TQ2l, D3, TQ6m);
  and SB95 (TQ2m, TQ2l, TQ6k);
  and SB96 (TQ31, TQ2m, TQ6e);
  and SA97 (TQ2n, D2, SH0);
  and SB98 (TQ2o, TQ2n, TQ6k);
  and SB99 (TQ32, TQ2o, TQ6e);
  and SA100 (TQ2p, D1, TQ6m);
  and SB101 (TQ2q, TQ2p, SH1);
  and SB102 (TQ34, TQ2q, TQ6e);
  and SA103 (TQ2r, D0, SH0);
  and SB104 (TQ2s, TQ2r, SH1);
  and SB105 (TQ36, TQ2s, TQ6e);
  and SA106 (TQ2t, GND, TQ6m);
  and SB107 (TQ2u, TQ2t, TQ6k);
  and SB108 (TQ38, TQ2u, SH2);
  and SA109 (TQ2v, GND, SH0);
  and SB110 (TQ2w, TQ2v, TQ6k);
  and SB111 (TQ3a, TQ2w, SH2);
  and SA112 (TQ2x, GND, TQ6m);
  and SB113 (TQ2y, TQ2x, SH1);
  and SB114 (TQ3c, TQ2y, SH2);
  and SA115 (TQ2z, GND, SH0);
  and SB116 (TQ30, TQ2z, SH1);
  and SB117 (TQ3e, TQ30, SH2);
  or MO118 (TQ33, TQ31, TQ32);
  or MO119 (TQ35, TQ33, TQ34);
  or MO120 (TQ37, TQ35, TQ36);
  or MO121 (TQ39, TQ37, TQ38);
  or MO122 (TQ3b, TQ39, TQ3a);
  or MO123 (TQ3d, TQ3b, TQ3c);
  or MO124 (Y3, TQ3d, TQ3e);
  and SA125 (TQ3g, D4, TQ6m);
  and SB126 (TQ3h, TQ3g, TQ6k);
  and SB127 (TQ3w, TQ3h, TQ6e);
  and SA128 (TQ3i, D3, SH0);
  and SB129 (TQ3j, TQ3i, TQ6k);
  and SB130 (TQ3x, TQ3j, TQ6e);
  and SA131 (TQ3k, D2, TQ6m);
  and SB132 (TQ3l, TQ3k, SH1);
  and SB133 (TQ3z, TQ3l, TQ6e);
  and SA134 (TQ3m, D1, SH0);
  and SB135 (TQ3n, TQ3m, SH1);
  and SB136 (TQ41, TQ3n, TQ6e);
  and SA137 (TQ3o, D0, TQ6m);
  and SB138 (TQ3p, TQ3o, TQ6k);
  and SB139 (TQ43, TQ3p, SH2);
  and SA140 (TQ3q, GND, SH0);
  and SB141 (TQ3r, TQ3q, TQ6k);
  and SB142 (TQ45, TQ3r, SH2);
  and SA143 (TQ3s, GND, TQ6m);
  and SB144 (TQ3t, TQ3s, SH1);
  and SB145 (TQ47, TQ3t, SH2);
  and SA146 (TQ3u, GND, SH0);
  and SB147 (TQ3v, TQ3u, SH1);
  and SB148 (TQ49, TQ3v, SH2);
  or MO149 (TQ3y, TQ3w, TQ3x);
  or MO150 (TQ40, TQ3y, TQ3z);
  or MO151 (TQ42, TQ40, TQ41);
  or MO152 (TQ44, TQ42, TQ43);
  or MO153 (TQ46, TQ44, TQ45);
  or MO154 (TQ48, TQ46, TQ47);
  or MO155 (Y4, TQ48, TQ49);
  and SA156 (TQ4b, D5, TQ6m);
  and SB157 (TQ4c, TQ4b, TQ6k);
  and SB158 (TQ4r, TQ4c, TQ6e);
  and SA159 (TQ4d, D4, SH0);
  and SB160 (TQ4e, TQ4d, TQ6k);
  and SB161 (TQ4s, TQ4e, TQ6e);
  and SA162 (TQ4f, D3, TQ6m);
  and SB163 (TQ4g, TQ4f, SH1);
  and SB164 (TQ4u, TQ4g, TQ6e);
  and SA165 (TQ4h, D2, SH0);
  and SB166 (TQ4i, TQ4h, SH1);
  and SB167 (TQ4w, TQ4i, TQ6e);
  and SA168 (TQ4j, D1, TQ6m);
  and SB169 (TQ4k, TQ4j, TQ6k);
  and SB170 (TQ4y, TQ4k, SH2);
  and SA171 (TQ4l, D0, SH0);
  and SB172 (TQ4m, TQ4l, TQ6k);
  and SB173 (TQ50, TQ4m, SH2);
  and SA174 (TQ4n, GND, TQ6m);
  and SB175 (TQ4o, TQ4n, SH1);
  and SB176 (TQ52, TQ4o, SH2);
  and SA177 (TQ4p, GND, SH0);
  and SB178 (TQ4q, TQ4p, SH1);
  and SB179 (TQ54, TQ4q, SH2);
  or MO180 (TQ4t, TQ4r, TQ4s);
  or MO181 (TQ4v, TQ4t, TQ4u);
  or MO182 (TQ4x, TQ4v, TQ4w);
  or MO183 (TQ4z, TQ4x, TQ4y);
  or MO184 (TQ51, TQ4z, TQ50);
  or MO185 (TQ53, TQ51, TQ52);
  or MO186 (Y5, TQ53, TQ54);
  and SA187 (TQ56, D6, TQ6m);
  and SB188 (TQ57, TQ56, TQ6k);
  and SB189 (TQ5n, TQ57, TQ6e);
  and SA190 (TQ58, D5, SH0);
  and SB191 (TQ59, TQ58, TQ6k);
  and SB192 (TQ5o, TQ59, TQ6e);
  and SA193 (TQ5a, D4, TQ6m);
  and SB194 (TQ5b, TQ5a, SH1);
  and SB195 (TQ5q, TQ5b, TQ6e);
  and SA196 (TQ5c, D3, SH0);
  and SB197 (TQ5d, TQ5c, SH1);
  and SB198 (TQ5s, TQ5d, TQ6e);
  and SA199 (TQ5e, D2, TQ6m);
  and SB200 (TQ5f, TQ5e, TQ6k);
  and SB201 (TQ5u, TQ5f, SH2);
  and SA202 (TQ5g, D1, SH0);
  and SB203 (TQ5h, TQ5g, TQ6k);
  and SB204 (TQ5w, TQ5h, SH2);
  and SA205 (TQ5i, D0, TQ6m);
  and SB206 (TQ5j, TQ5i, SH1);
  and SB207 (TQ5y, TQ5j, SH2);
  and SA208 (TQ5l, GND, SH0);
  and SB209 (TQ5m, TQ5l, SH1);
  and SB210 (TQ60, TQ5m, SH2);
  or MO211 (TQ5p, TQ5n, TQ5o);
  or MO212 (TQ5r, TQ5p, TQ5q);
  or MO213 (TQ5t, TQ5r, TQ5s);
  or MO214 (TQ5v, TQ5t, TQ5u);
  or MO215 (TQ5x, TQ5v, TQ5w);
  or MO216 (TQ5z, TQ5x, TQ5y);
  or MO217 (Y6, TQ5z, TQ60);
  and SA218 (TQ63, D7, TQ6m);
  and SB219 (TQ64, TQ63, TQ6k);
  and SB220 (TQ6r, TQ64, TQ6e);
  and SA221 (TQ66, D6, SH0);
  and SB222 (TQ67, TQ66, TQ6k);
  and SB223 (TQ6s, TQ67, TQ6e);
  and SA224 (TQ69, D5, TQ6m);
  and SB225 (TQ6a, TQ69, SH1);
  and SB226 (TQ6t, TQ6a, TQ6e);
  and SA227 (TQ6c, D4, SH0);
  and SB228 (TQ6d, TQ6c, SH1);
  and SB229 (TQ6u, TQ6d, TQ6e);
  and SA230 (TQ6g, D3, TQ6m);
  and SB231 (TQ6h, TQ6g, TQ6k);
  and SB232 (TQ6v, TQ6h, SH2);
  and SA233 (TQ6j, D2, SH0);
  and SB234 (SB234_out, TQ6j, TQ6k);
  and SB235 (SB235_out, SB234_out, SH2);
  and SA236 (SA236_out, D1, TQ6m);
  and SB237 (SB237_out, SA236_out, SH1);
  and SB238 (SB238_out, SB237_out, SH2);
  and SA239 (SA239_out, D0, SH0);
  and SB240 (SB240_out, SA239_out, SH1);
  and SB241 (SB241_out, SB240_out, SH2);
  or MO242 (MO242_out, TQ6r, TQ6s);
  or MO243 (MO243_out, MO242_out, TQ6t);
  or MO244 (MO244_out, MO243_out, TQ6u);
  or MO245 (MO245_out, MO244_out, TQ6v);
  or MO246 (MO246_out, MO245_out, SB235_out);
  or MO247 (MO247_out, MO246_out, SB238_out);
  or MO248 (Y7, MO247_out, SB241_out);

  // Other names for the same wires on the sheet: TQ1p = Y1; TQ2k = Y2; TQ3f = Y3; TQ4a = Y4; TQ5k = GND; TQ6b = D4;
  //   TQ6f = D3; TQ6i = D2; TQ6l = D1; TQ6n = D0; TQ6o = SH0; TQ6p = SH1; TQ6q = SH2; TQ6w = Y7; TQ55 = Y5; TQ61 = Y6;
  //   TQ62 = D7; TQ65 = D6; TQ68 = D5; TQu = Y0
endmodule
