// Logisim project bcd2bin_2digit.circ as structural Verilog
module bcd2bin_2digit (
  input  T0,
  input  T1,
  input  T2,
  input  T3,
  input  U0,
  input  U1,
  input  U2,
  input  U3,
  output B0,
  output B1,
  output B2,
  output B3,
  output B4,
  output B5,
  output B6
);

  wire B2A_out, B2C_out, B2D_out, B2O_out, B3A_out, B3C_out, B3D_out, B3O_out, B4A_out, B5A_out, TQ0, TQ1,
       TQ2, TQ3, TQ5, TQ7, TQe, TQg, TQj, TQl, TQn;

  xor S3X (TQg, T0, T2);
  and S3A (TQ0, T0, T2);
  xor S4A (TQ1, T1, T3);
  xor S4B (TQj, TQ1, TQ0);
  and S4C (TQ2, T1, T3);
  and S4D (TQ3, TQ0, TQ1);
  or S4O (TQ5, TQ2, TQ3);
  xor S5X (TQl, T2, TQ5);
  and S5A (TQ7, T2, TQ5);
  xor S6X (TQn, T3, TQ7);
  xor B1X (B1, T0, U1);
  and B1A (TQe, T0, U1);
  xor B2A (B2A_out, T1, U2);
  xor B2B (B2, B2A_out, TQe);
  and B2C (B2C_out, T1, U2);
  and B2D (B2D_out, TQe, B2A_out);
  or B2O (B2O_out, B2C_out, B2D_out);
  xor B3A (B3A_out, TQg, U3);
  xor B3B (B3, B3A_out, B2O_out);
  and B3C (B3C_out, TQg, U3);
  and B3D (B3D_out, B2O_out, B3A_out);
  or B3O (B3O_out, B3C_out, B3D_out);
  xor B4X (B4, TQj, B3O_out);
  and B4A (B4A_out, TQj, B3O_out);
  xor B5X (B5, TQl, B4A_out);
  and B5A (B5A_out, TQl, B4A_out);
  xor B6X (B6, TQn, B5A_out);

  assign B0 = U0;

  // Other names for the same wires on the sheet: TQ4 = T2; TQ6 = T3; TQ8 = U0; TQ9 = T0; TQa = U1; TQb = B1; TQc = T1;
  //   TQd = U2; TQf = B2; TQh = U3; TQi = B3; TQk = B4; TQm = B5; TQo = B6
endmodule
