// Logisim project bcd7seg.circ as structural Verilog
module bcd7seg (
  input  B0,
  input  B1,
  input  B2,
  input  B3,
  output a,
  output b,
  output c,
  output d,
  output e,
  output f,
  output g
);

  wire B7N1_out, B7N2_out, B7N3_out, B7N4_out, B7O7_out, B7O11_out, B7O15_out, B7O19_out, B7O23_out,
       B7O27_out, B7O38_out, B7O42_out, B7O46_out, B7O50_out, B7O54_out, B7O58_out, B7O69_out, B7O73_out,
       B7O77_out, B7O81_out, B7O85_out, B7O89_out, B7O93_out, B7O104_out, B7O108_out, B7O112_out, B7O116_out,
       B7O120_out, B7O131_out, B7O135_out, B7O146_out, B7O150_out, B7O154_out, B7O158_out, B7O169_out,
       B7O173_out, B7O177_out, B7O181_out, B7O185_out, B7P1_out, B7P2_out, B7P3_out, B7P4_out, B7P5_out,
       B7P6_out, B7P8_out, B7P9_out, B7P10_out, B7P12_out, B7P13_out, B7P14_out, B7P16_out, B7P17_out,
       B7P18_out, B7P20_out, B7P21_out, B7P22_out, B7P24_out, B7P25_out, B7P26_out, B7P28_out, B7P29_out,
       B7P30_out, B7P32_out, B7P33_out, B7P34_out, B7P35_out, B7P36_out, B7P37_out, B7P39_out, B7P40_out,
       B7P41_out, B7P43_out, B7P44_out, B7P45_out, B7P47_out, B7P48_out, B7P49_out, B7P51_out, B7P52_out,
       B7P53_out, B7P55_out, B7P56_out, B7P57_out, B7P59_out, B7P60_out, B7P61_out, B7P63_out, B7P64_out,
       B7P65_out, B7P66_out, B7P67_out, B7P68_out, B7P70_out, B7P71_out, B7P72_out, B7P74_out, B7P75_out,
       B7P76_out, B7P78_out, B7P79_out, B7P80_out, B7P82_out, B7P83_out, B7P84_out, B7P86_out, B7P87_out,
       B7P88_out, B7P90_out, B7P91_out, B7P92_out, B7P94_out, B7P95_out, B7P96_out, B7P98_out, B7P99_out,
       B7P100_out, B7P101_out, B7P102_out, B7P103_out, B7P105_out, B7P106_out, B7P107_out, B7P109_out,
       B7P110_out, B7P111_out, B7P113_out, B7P114_out, B7P115_out, B7P117_out, B7P118_out, B7P119_out,
       B7P121_out, B7P122_out, B7P123_out, B7P125_out, B7P126_out, B7P127_out, B7P128_out, B7P129_out,
       B7P130_out, B7P132_out, B7P133_out, B7P134_out, B7P136_out, B7P137_out, B7P138_out, B7P140_out,
       B7P141_out, B7P142_out, B7P143_out, B7P144_out, B7P145_out, B7P147_out, B7P148_out, B7P149_out,
       B7P151_out, B7P152_out, B7P153_out, B7P155_out, B7P156_out, B7P157_out, B7P159_out, B7P160_out,
       B7P161_out, B7P163_out, B7P164_out, B7P165_out, B7P166_out, B7P167_out, B7P168_out, B7P170_out,
       B7P171_out, B7P172_out, B7P174_out, B7P175_out, B7P176_out, B7P178_out, B7P179_out, B7P180_out,
       B7P182_out, B7P183_out, B7P184_out, B7P186_out, B7P187_out, B7P188_out;

  not B7N1 (B7N1_out, B0);
  not B7N2 (B7N2_out, B1);
  not B7N3 (B7N3_out, B2);
  not B7N4 (B7N4_out, B3);
  and B7P1 (B7P1_out, B7N1_out, B7N2_out);
  and B7P2 (B7P2_out, B7P1_out, B7N3_out);
  and B7P3 (B7P3_out, B7P2_out, B7N4_out);
  and B7P4 (B7P4_out, B7N1_out, B1);
  and B7P5 (B7P5_out, B7P4_out, B7N3_out);
  and B7P6 (B7P6_out, B7P5_out, B7N4_out);
  or B7O7 (B7O7_out, B7P3_out, B7P6_out);
  and B7P8 (B7P8_out, B0, B1);
  and B7P9 (B7P9_out, B7P8_out, B7N3_out);
  and B7P10 (B7P10_out, B7P9_out, B7N4_out);
  or B7O11 (B7O11_out, B7O7_out, B7P10_out);
  and B7P12 (B7P12_out, B0, B7N2_out);
  and B7P13 (B7P13_out, B7P12_out, B2);
  and B7P14 (B7P14_out, B7P13_out, B7N4_out);
  or B7O15 (B7O15_out, B7O11_out, B7P14_out);
  and B7P16 (B7P16_out, B7N1_out, B1);
  and B7P17 (B7P17_out, B7P16_out, B2);
  and B7P18 (B7P18_out, B7P17_out, B7N4_out);
  or B7O19 (B7O19_out, B7O15_out, B7P18_out);
  and B7P20 (B7P20_out, B0, B1);
  and B7P21 (B7P21_out, B7P20_out, B2);
  and B7P22 (B7P22_out, B7P21_out, B7N4_out);
  or B7O23 (B7O23_out, B7O19_out, B7P22_out);
  and B7P24 (B7P24_out, B7N1_out, B7N2_out);
  and B7P25 (B7P25_out, B7P24_out, B7N3_out);
  and B7P26 (B7P26_out, B7P25_out, B3);
  or B7O27 (B7O27_out, B7O23_out, B7P26_out);
  and B7P28 (B7P28_out, B0, B7N2_out);
  and B7P29 (B7P29_out, B7P28_out, B7N3_out);
  and B7P30 (B7P30_out, B7P29_out, B3);
  or B7O31 (a, B7O27_out, B7P30_out);
  and B7P32 (B7P32_out, B7N1_out, B7N2_out);
  and B7P33 (B7P33_out, B7P32_out, B7N3_out);
  and B7P34 (B7P34_out, B7P33_out, B7N4_out);
  and B7P35 (B7P35_out, B0, B7N2_out);
  and B7P36 (B7P36_out, B7P35_out, B7N3_out);
  and B7P37 (B7P37_out, B7P36_out, B7N4_out);
  or B7O38 (B7O38_out, B7P34_out, B7P37_out);
  and B7P39 (B7P39_out, B7N1_out, B1);
  and B7P40 (B7P40_out, B7P39_out, B7N3_out);
  and B7P41 (B7P41_out, B7P40_out, B7N4_out);
  or B7O42 (B7O42_out, B7O38_out, B7P41_out);
  and B7P43 (B7P43_out, B0, B1);
  and B7P44 (B7P44_out, B7P43_out, B7N3_out);
  and B7P45 (B7P45_out, B7P44_out, B7N4_out);
  or B7O46 (B7O46_out, B7O42_out, B7P45_out);
  and B7P47 (B7P47_out, B7N1_out, B7N2_out);
  and B7P48 (B7P48_out, B7P47_out, B2);
  and B7P49 (B7P49_out, B7P48_out, B7N4_out);
  or B7O50 (B7O50_out, B7O46_out, B7P49_out);
  and B7P51 (B7P51_out, B0, B1);
  and B7P52 (B7P52_out, B7P51_out, B2);
  and B7P53 (B7P53_out, B7P52_out, B7N4_out);
  or B7O54 (B7O54_out, B7O50_out, B7P53_out);
  and B7P55 (B7P55_out, B7N1_out, B7N2_out);
  and B7P56 (B7P56_out, B7P55_out, B7N3_out);
  and B7P57 (B7P57_out, B7P56_out, B3);
  or B7O58 (B7O58_out, B7O54_out, B7P57_out);
  and B7P59 (B7P59_out, B0, B7N2_out);
  and B7P60 (B7P60_out, B7P59_out, B7N3_out);
  and B7P61 (B7P61_out, B7P60_out, B3);
  or B7O62 (b, B7O58_out, B7P61_out);
  and B7P63 (B7P63_out, B7N1_out, B7N2_out);
  and B7P64 (B7P64_out, B7P63_out, B7N3_out);
  and B7P65 (B7P65_out, B7P64_out, B7N4_out);
  and B7P66 (B7P66_out, B0, B7N2_out);
  and B7P67 (B7P67_out, B7P66_out, B7N3_out);
  and B7P68 (B7P68_out, B7P67_out, B7N4_out);
  or B7O69 (B7O69_out, B7P65_out, B7P68_out);
  and B7P70 (B7P70_out, B0, B1);
  and B7P71 (B7P71_out, B7P70_out, B7N3_out);
  and B7P72 (B7P72_out, B7P71_out, B7N4_out);
  or B7O73 (B7O73_out, B7O69_out, B7P72_out);
  and B7P74 (B7P74_out, B7N1_out, B7N2_out);
  and B7P75 (B7P75_out, B7P74_out, B2);
  and B7P76 (B7P76_out, B7P75_out, B7N4_out);
  or B7O77 (B7O77_out, B7O73_out, B7P76_out);
  and B7P78 (B7P78_out, B0, B7N2_out);
  and B7P79 (B7P79_out, B7P78_out, B2);
  and B7P80 (B7P80_out, B7P79_out, B7N4_out);
  or B7O81 (B7O81_out, B7O77_out, B7P80_out);
  and B7P82 (B7P82_out, B7N1_out, B1);
  and B7P83 (B7P83_out, B7P82_out, B2);
  and B7P84 (B7P84_out, B7P83_out, B7N4_out);
  or B7O85 (B7O85_out, B7O81_out, B7P84_out);
  and B7P86 (B7P86_out, B0, B1);
  and B7P87 (B7P87_out, B7P86_out, B2);
  and B7P88 (B7P88_out, B7P87_out, B7N4_out);
  or B7O89 (B7O89_out, B7O85_out, B7P88_out);
  and B7P90 (B7P90_out, B7N1_out, B7N2_out);
  and B7P91 (B7P91_out, B7P90_out, B7N3_out);
  and B7P92 (B7P92_out, B7P91_out, B3);
  or B7O93 (B7O93_out, B7O89_out, B7P92_out);
  and B7P94 (B7P94_out, B0, B7N2_out);
  and B7P95 (B7P95_out, B7P94_out, B7N3_out);
  and B7P96 (B7P96_out, B7P95_out, B3);
  or B7O97 (c, B7O93_out, B7P96_out);
  and B7P98 (B7P98_out, B7N1_out, B7N2_out);
  and B7P99 (B7P99_out, B7P98_out, B7N3_out);
  and B7P100 (B7P100_out, B7P99_out, B7N4_out);
  and B7P101 (B7P101_out, B7N1_out, B1);
  and B7P102 (B7P102_out, B7P101_out, B7N3_out);
  and B7P103 (B7P103_out, B7P102_out, B7N4_out);
  or B7O104 (B7O104_out, B7P100_out, B7P103_out);
  and B7P105 (B7P105_out, B0, B1);
  and B7P106 (B7P106_out, B7P105_out, B7N3_out);
  and B7P107 (B7P107_out, B7P106_out, B7N4_out);
  or B7O108 (B7O108_out, B7O104_out, B7P107_out);
  and B7P109 (B7P109_out, B0, B7N2_out);
  and B7P110 (B7P110_out, B7P109_out, B2);
  and B7P111 (B7P111_out, B7P110_out, B7N4_out);
  or B7O112 (B7O112_out, B7O108_out, B7P111_out);
  and B7P113 (B7P113_out, B7N1_out, B1);
  and B7P114 (B7P114_out, B7P113_out, B2);
  and B7P115 (B7P115_out, B7P114_out, B7N4_out);
  or B7O116 (B7O116_out, B7O112_out, B7P115_out);
  and B7P117 (B7P117_out, B7N1_out, B7N2_out);
  and B7P118 (B7P118_out, B7P117_out, B7N3_out);
  and B7P119 (B7P119_out, B7P118_out, B3);
  or B7O120 (B7O120_out, B7O116_out, B7P119_out);
  and B7P121 (B7P121_out, B0, B7N2_out);
  and B7P122 (B7P122_out, B7P121_out, B7N3_out);
  and B7P123 (B7P123_out, B7P122_out, B3);
  or B7O124 (d, B7O120_out, B7P123_out);
  and B7P125 (B7P125_out, B7N1_out, B7N2_out);
  and B7P126 (B7P126_out, B7P125_out, B7N3_out);
  and B7P127 (B7P127_out, B7P126_out, B7N4_out);
  and B7P128 (B7P128_out, B7N1_out, B1);
  and B7P129 (B7P129_out, B7P128_out, B7N3_out);
  and B7P130 (B7P130_out, B7P129_out, B7N4_out);
  or B7O131 (B7O131_out, B7P127_out, B7P130_out);
  and B7P132 (B7P132_out, B7N1_out, B1);
  and B7P133 (B7P133_out, B7P132_out, B2);
  and B7P134 (B7P134_out, B7P133_out, B7N4_out);
  or B7O135 (B7O135_out, B7O131_out, B7P134_out);
  and B7P136 (B7P136_out, B7N1_out, B7N2_out);
  and B7P137 (B7P137_out, B7P136_out, B7N3_out);
  and B7P138 (B7P138_out, B7P137_out, B3);
  or B7O139 (e, B7O135_out, B7P138_out);
  and B7P140 (B7P140_out, B7N1_out, B7N2_out);
  and B7P141 (B7P141_out, B7P140_out, B7N3_out);
  and B7P142 (B7P142_out, B7P141_out, B7N4_out);
  and B7P143 (B7P143_out, B7N1_out, B7N2_out);
  and B7P144 (B7P144_out, B7P143_out, B2);
  and B7P145 (B7P145_out, B7P144_out, B7N4_out);
  or B7O146 (B7O146_out, B7P142_out, B7P145_out);
  and B7P147 (B7P147_out, B0, B7N2_out);
  and B7P148 (B7P148_out, B7P147_out, B2);
  and B7P149 (B7P149_out, B7P148_out, B7N4_out);
  or B7O150 (B7O150_out, B7O146_out, B7P149_out);
  and B7P151 (B7P151_out, B7N1_out, B1);
  and B7P152 (B7P152_out, B7P151_out, B2);
  and B7P153 (B7P153_out, B7P152_out, B7N4_out);
  or B7O154 (B7O154_out, B7O150_out, B7P153_out);
  and B7P155 (B7P155_out, B7N1_out, B7N2_out);
  and B7P156 (B7P156_out, B7P155_out, B7N3_out);
  and B7P157 (B7P157_out, B7P156_out, B3);
  or B7O158 (B7O158_out, B7O154_out, B7P157_out);
  and B7P159 (B7P159_out, B0, B7N2_out);
  and B7P160 (B7P160_out, B7P159_out, B7N3_out);
  and B7P161 (B7P161_out, B7P160_out, B3);
  or B7O162 (f, B7O158_out, B7P161_out);
  and B7P163 (B7P163_out, B7N1_out, B1);
  and B7P164 (B7P164_out, B7P163_out, B7N3_out);
  and B7P165 (B7P165_out, B7P164_out, B7N4_out);
  and B7P166 (B7P166_out, B0, B1);
  and B7P167 (B7P167_out, B7P166_out, B7N3_out);
  and B7P168 (B7P168_out, B7P167_out, B7N4_out);
  or B7O169 (B7O169_out, B7P165_out, B7P168_out);
  and B7P170 (B7P170_out, B7N1_out, B7N2_out);
  and B7P171 (B7P171_out, B7P170_out, B2);
  and B7P172 (B7P172_out, B7P171_out, B7N4_out);
  or B7O173 (B7O173_out, B7O169_out, B7P172_out);
  and B7P174 (B7P174_out, B0, B7N2_out);
  and B7P175 (B7P175_out, B7P174_out, B2);
  and B7P176 (B7P176_out, B7P175_out, B7N4_out);
  or B7O177 (B7O177_out, B7O173_out, B7P176_out);
  and B7P178 (B7P178_out, B7N1_out, B1);
  and B7P179 (B7P179_out, B7P178_out, B2);
  and B7P180 (B7P180_out, B7P179_out, B7N4_out);
  or B7O181 (B7O181_out, B7O177_out, B7P180_out);
  and B7P182 (B7P182_out, B7N1_out, B7N2_out);
  and B7P183 (B7P183_out, B7P182_out, B7N3_out);
  and B7P184 (B7P184_out, B7P183_out, B3);
  or B7O185 (B7O185_out, B7O181_out, B7P184_out);
  and B7P186 (B7P186_out, B0, B7N2_out);
  and B7P187 (B7P187_out, B7P186_out, B7N3_out);
  and B7P188 (B7P188_out, B7P187_out, B3);
  or B7O189 (g, B7O185_out, B7P188_out);
endmodule
