// Logisim project bcd_adder.circ as structural Verilog
module bcd_adder (
  input  A0,
  input  B0,
  input  A1,
  input  B1,
  input  A2,
  input  B2,
  input  A3,
  input  B3,
  input  Cin,
  input  Z,
  output S0,
  output S1,
  output S2,
  output S3,
  output Cout
);

  wire BA26_out, BA27_out, BA28_out, BA29_out, BAA1_out, BAA2_out, BAA3_out, BAA4_out, BAB1_out, BAB2_out,
       BAB3_out, BAB4_out, BAG1_out, BAG2_out, BAG3_out, BAG4_out, BAK5_out, BAL5_out, BAO1_out, BAO2_out,
       BAO3_out, BAO4_out, BB26_out, BB27_out, BB28_out, BB29_out, BG26_out, BG27_out, BG28_out, BO26_out,
       BO27_out, BO28_out, BO29_out, BX26_out, BX27_out, BX28_out, BX29_out, BXA1_out, BXA2_out, BXA3_out,
       BXA4_out, BXS1_out, BXS2_out, BXS3_out, BXS4_out;

  xor BXA1 (BXA1_out, A0, B0);
  xor BXS1 (BXS1_out, BXA1_out, Cin);
  and BAA1 (BAA1_out, A0, B0);
  and BAB1 (BAB1_out, Cin, BXA1_out);
  or BAO1 (BAO1_out, BAA1_out, BAB1_out);
  or BAG1 (BAG1_out, BAO1_out, Z);
  xor BXA2 (BXA2_out, A1, B1);
  xor BXS2 (BXS2_out, BXA2_out, BAG1_out);
  and BAA2 (BAA2_out, A1, B1);
  and BAB2 (BAB2_out, BAG1_out, BXA2_out);
  or BAO2 (BAO2_out, BAA2_out, BAB2_out);
  or BAG2 (BAG2_out, BAO2_out, Z);
  xor BXA3 (BXA3_out, A2, B2);
  xor BXS3 (BXS3_out, BXA3_out, BAG2_out);
  and BAA3 (BAA3_out, A2, B2);
  and BAB3 (BAB3_out, BAG2_out, BXA3_out);
  or BAO3 (BAO3_out, BAA3_out, BAB3_out);
  or BAG3 (BAG3_out, BAO3_out, Z);
  xor BXA4 (BXA4_out, A3, B3);
  xor BXS4 (BXS4_out, BXA4_out, BAG3_out);
  and BAA4 (BAA4_out, A3, B3);
  and BAB4 (BAB4_out, BAG3_out, BXA4_out);
  or BAO4 (BAO4_out, BAA4_out, BAB4_out);
  or BAG4 (BAG4_out, BAO4_out, Z);
  or BAJ5 (Cout, BAG4_out, BAK5_out);
  and BAK5 (BAK5_out, BAL5_out, BXS4_out);
  or BAL5 (BAL5_out, BXS3_out, BXS2_out);
  xor BX26 (BX26_out, BXS1_out, Z);
  xor BX36 (S0, BX26_out, Z);
  and BA26 (BA26_out, BXS1_out, Z);
  and BB26 (BB26_out, Z, BX26_out);
  or BO26 (BO26_out, BA26_out, BB26_out);
  or BG26 (BG26_out, BO26_out, Z);
  xor BX27 (BX27_out, BXS2_out, Cout);
  xor BX37 (S1, BX27_out, BG26_out);
  and BA27 (BA27_out, BXS2_out, Cout);
  and BB27 (BB27_out, BG26_out, BX27_out);
  or BO27 (BO27_out, BA27_out, BB27_out);
  or BG27 (BG27_out, BO27_out, Z);
  xor BX28 (BX28_out, BXS3_out, Cout);
  xor BX38 (S2, BX28_out, BG27_out);
  and BA28 (BA28_out, BXS3_out, Cout);
  and BB28 (BB28_out, BG27_out, BX28_out);
  or BO28 (BO28_out, BA28_out, BB28_out);
  or BG28 (BG28_out, BO28_out, Z);
  xor BX29 (BX29_out, BXS4_out, Z);
  xor BX39 (S3, BX29_out, BG28_out);
  and BA29 (BA29_out, BXS4_out, Z);
  and BB29 (BB29_out, BG28_out, BX29_out);
  or BO29 (BO29_out, BA29_out, BB29_out);
  // OR_Gate BG29 has open pins: in0=BO29_out, in1=Z, out=open
endmodule
