// Logisim project bcd_adder_2digit.circ as structural Verilog
module bcd_adder_2digit (
  input  A0,
  input  B0,
  input  A1,
  input  B1,
  input  A2,
  input  B2,
  input  A3,
  input  B3,
  input  A4,
  input  B4,
  input  A5,
  input  B5,
  input  A6,
  input  B6,
  input  A7,
  input  B7,
  input  Cin,
  input  Z,
  output S0,
  output S1,
  output S2,
  output S3,
  output S4,
  output S5,
  output S6,
  output S7,
  output Cout
);

  wire BA217_out, BA218_out, BB216_out, BB217_out, BB218_out, BG216_out, BG217_out, BO216_out, BO217_out,
       BO218_out, BX217_out, BX218_out, TQ1a, TQ1b, TQ1c, TQ1d, TQ1e, TQ1f, TQ1g, TQ1h, TQ1k, TQ1l, TQ1m,
       TQ1n, TQ1o, TQ1r, TQ1s, TQ1t, TQ1u, TQ1v, TQ1y, TQ1z, TQ2a, TQ2b, TQ2c, TQ2d, TQ2e, TQ2f, TQ2g, TQ2h,
       TQ2i, TQ2j, TQ2k, TQ2l, TQ2m, TQ2n, TQ3, TQ4, TQ5, TQ6, TQ9, TQ10, TQ11, TQ12, TQ13, TQ14, TQ15, TQ16,
       TQ17, TQ18, TQ19, TQ20, TQ21, TQ22, TQ25, TQ26, TQ27, TQ28, TQ29, TQa, TQb, TQc, TQd, TQg, TQh, TQi,
       TQj, TQk, TQn, TQo, TQp, TQq, TQr, TQs, TQt, TQu, TQv, TQw, TQx, TQy, TQz;

  xor BXA1 (TQ3, A0, B0);
  xor BXS1 (TQv, TQ3, Cin);
  and BAA1 (TQ4, A0, B0);
  and BAB1 (TQ5, Cin, TQ3);
  or BAO1 (TQ6, TQ4, TQ5);
  or BAG1 (TQ9, TQ6, Z);
  xor BXA2 (TQa, A1, B1);
  xor BXS2 (TQ10, TQa, TQ9);
  and BAA2 (TQb, A1, B1);
  and BAB2 (TQc, TQ9, TQa);
  or BAO2 (TQd, TQb, TQc);
  or BAG2 (TQg, TQd, Z);
  xor BXA3 (TQh, A2, B2);
  xor BXS3 (TQ16, TQh, TQg);
  and BAA3 (TQi, A2, B2);
  and BAB3 (TQj, TQg, TQh);
  or BAO3 (TQk, TQi, TQj);
  or BAG3 (TQn, TQk, Z);
  xor BXA4 (TQo, A3, B3);
  xor BXS4 (TQ1c, TQo, TQn);
  and BAA4 (TQp, A3, B3);
  and BAB4 (TQq, TQn, TQo);
  or BAO4 (TQr, TQp, TQq);
  or BAG4 (TQt, TQr, Z);
  or BAJ5 (TQ1k, TQt, TQu);
  and BAK5 (TQu, TQs, TQ1c);
  or BAL5 (TQs, TQ16, TQ10);
  xor BX26 (TQw, TQv, Z);
  xor BX36 (S0, TQw, Z);
  and BA26 (TQx, TQv, Z);
  and BB26 (TQy, Z, TQw);
  or BO26 (TQz, TQx, TQy);
  or BG26 (TQ11, TQz, Z);
  xor BX27 (TQ12, TQ10, TQ1k);
  xor BX37 (S1, TQ12, TQ11);
  and BA27 (TQ13, TQ10, TQ1k);
  and BB27 (TQ14, TQ11, TQ12);
  or BO27 (TQ15, TQ13, TQ14);
  or BG27 (TQ17, TQ15, Z);
  xor BX28 (TQ18, TQ16, TQ1k);
  xor BX38 (S2, TQ18, TQ17);
  and BA28 (TQ19, TQ16, TQ1k);
  and BB28 (TQ1a, TQ17, TQ18);
  or BO28 (TQ1b, TQ19, TQ1a);
  or BG28 (TQ1d, TQ1b, Z);
  xor BX29 (TQ1e, TQ1c, Z);
  xor BX39 (S3, TQ1e, TQ1d);
  and BA29 (TQ1f, TQ1c, Z);
  and BB29 (TQ1g, TQ1d, TQ1e);
  or BO29 (TQ1h, TQ1f, TQ1g);
  // OR_Gate BG29 has open pins: in0=TQ1h, in1=Z, out=open
  xor BXA10 (TQ1l, A4, B4);
  xor BXS10 (TQ2d, TQ1l, TQ1k);
  and BAA10 (TQ1m, A4, B4);
  and BAB10 (TQ1n, TQ1k, TQ1l);
  or BAO10 (TQ1o, TQ1m, TQ1n);
  or BAG10 (TQ1r, TQ1o, Z);
  xor BXA11 (TQ1s, A5, B5);
  xor BXS11 (TQ2i, TQ1s, TQ1r);
  and BAA11 (TQ1t, A5, B5);
  and BAB11 (TQ1u, TQ1r, TQ1s);
  or BAO11 (TQ1v, TQ1t, TQ1u);
  or BAG11 (TQ1y, TQ1v, Z);
  xor BXA12 (TQ1z, A6, B6);
  xor BXS12 (TQ2m, TQ1z, TQ1y);
  and BAA12 (TQ20, A6, B6);
  and BAB12 (TQ21, TQ1y, TQ1z);
  or BAO12 (TQ22, TQ20, TQ21);
  or BAG12 (TQ25, TQ22, Z);
  xor BXA13 (TQ26, A7, B7);
  xor BXS13 (TQ2n, TQ26, TQ25);
  and BAA13 (TQ27, A7, B7);
  and BAB13 (TQ28, TQ25, TQ26);
  or BAO13 (TQ29, TQ27, TQ28);
  or BAG13 (TQ2b, TQ29, Z);
  or BAJ14 (Cout, TQ2b, TQ2c);
  and BAK14 (TQ2c, TQ2a, TQ2n);
  or BAL14 (TQ2a, TQ2m, TQ2i);
  xor BX215 (TQ2e, TQ2d, Z);
  xor BX315 (S4, TQ2e, Z);
  and BA215 (TQ2f, TQ2d, Z);
  and BB215 (TQ2g, Z, TQ2e);
  or BO215 (TQ2h, TQ2f, TQ2g);
  or BG215 (TQ2j, TQ2h, Z);
  xor BX216 (TQ2k, TQ2i, Cout);
  xor BX316 (S5, TQ2k, TQ2j);
  and BA216 (TQ2l, TQ2i, Cout);
  and BB216 (BB216_out, TQ2j, TQ2k);
  or BO216 (BO216_out, TQ2l, BB216_out);
  or BG216 (BG216_out, BO216_out, Z);
  xor BX217 (BX217_out, TQ2m, Cout);
  xor BX317 (S6, BX217_out, BG216_out);
  and BA217 (BA217_out, TQ2m, Cout);
  and BB217 (BB217_out, BG216_out, BX217_out);
  or BO217 (BO217_out, BA217_out, BB217_out);
  or BG217 (BG217_out, BO217_out, Z);
  xor BX218 (BX218_out, TQ2n, Z);
  xor BX318 (S7, BX218_out, BG217_out);
  and BA218 (BA218_out, TQ2n, Z);
  and BB218 (BB218_out, BG217_out, BX218_out);
  or BO218 (BO218_out, BA218_out, BB218_out);
  // OR_Gate BG218 has open pins: in0=BO218_out, in1=Z, out=open

  // Other names for the same wires on the sheet: TQ0 = A0; TQ1 = B0; TQ1i = A4; TQ1j = B4; TQ1p = A5; TQ1q = B5;
  //   TQ1w = A6; TQ1x = B6; TQ2 = Cin; TQ2o = Z; TQ2p = S0; TQ2q = S4; TQ2r = S1; TQ2s = S5; TQ2t = S2; TQ2u = S6;
  //   TQ2v = S3; TQ2w = S7; TQ2x = Cout; TQ7 = A1; TQ8 = B1; TQ23 = A7; TQ24 = B7; TQe = A2; TQf = B2; TQl = A3;
  //   TQm = B3
endmodule
