// Logisim project bcd_counter.circ as structural Verilog
module bcd_counter (
  input  CLK,
  input  EN,
  input  RST,
  output Q0,
  output Q1,
  output Q2,
  output Q3
);

  wire A1_out, A2_out, A3_out, A4_out, A5_out, N1_out, O1_out;

  T_Flip_Flop U1 (.T(EN), .clk(CLK), .Q(Q0), .reset(RST));  // open: Qn, preset
  T_Flip_Flop U2 (.T(A1_out), .clk(CLK), .Q(Q1), .reset(RST));  // open: Qn, preset
  T_Flip_Flop U3 (.T(A3_out), .clk(CLK), .Q(Q2), .reset(RST));  // open: Qn, preset
  T_Flip_Flop U4 (.T(O1_out), .clk(CLK), .Q(Q3), .reset(RST));  // open: Qn, preset
  not N1 (N1_out, Q3);
  and A1 (A1_out, Q0, N1_out);
  and A2 (A2_out, Q0, Q1);
  and A3 (A3_out, A2_out, N1_out);
  and A4 (A4_out, A2_out, Q2);
  and A5 (A5_out, Q0, Q3);
  or O1 (O1_out, A4_out, A5_out);

  // Other names for the same wires on the sheet: TQ0 = EN; TQ1 = Q0; TQ2 = Q1; TQ3 = Q2; TQ4 = CLK; TQ5 = RST;
  //   TQ6 = Q3
endmodule
