// Logisim project bcd_subtractor.circ as structural Verilog
module bcd_subtractor (
  input  A0,
  input  B0,
  input  A1,
  input  B1,
  input  A2,
  input  B2,
  input  A3,
  input  B3,
  input  GND,
  input  ONE,
  output D0,
  output D1,
  output D2,
  output D3,
  output Borrow
);

  wire TQ0, TQ1a, TQ1b, TQ1c, TQ1d, TQ1f, TQ1g, TQ1h, TQ1i, TQ1j, TQ1k, TQ1l, TQ1n, TQ1o, TQ1p, TQ1q, TQ1r,
       TQ1s, TQ1t, TQ1u, TQ1v, TQ1w, TQ1x, TQ1y, TQ1z, TQ2, TQ2a, TQ2b, TQ2c, TQ2d, TQ2e, TQ2f, TQ2g, TQ2h,
       TQ2i, TQ3, TQ5, TQ6, TQ8, TQ9, TQ11, TQ18, TQ19, TQ20, TQ21, TQ22, TQ23, TQ24, TQ25, TQ26, TQ27, TQ28,
       TQ29, TQa, TQb, TQd, TQe, TQf, TQg, TQh, TQi, TQj, TQk, TQl, TQm, TQn, TQq, TQr, TQs, TQt, TQu, TQv,
       TQw, TQx, TQy, TQz;

  not N1 (TQd, B0);
  xor S12 (TQ1r, TQt, TQr);
  xor S14 (TQ23, TQ1h, TQ1g);
  xor S32 (TQ0, TQ1t, TQ1s);
  xor S34 (TQn, TQ25, TQ24);
  and B41 (TQ2h, GND, TQ2f);
  and B43 (TQj, TQe, TQf);
  xor X2 (TQ18, B2, B1);
  and A12 (TQv, A1, B1);
  and A14 (TQ1i, A3, TQ1f);
  and A32 (TQ1u, TQ1r, GND);
  and A34 (TQ26, TQ23, GND);
  or C41 (TQ2i, TQ2g, TQ2h);
  or C43 (TQl, TQh, TQj);
  or O1 (TQ9, B2, B1);
  and B12 (TQx, TQr, TQt);
  and B14 (TQ1j, TQ1g, TQ1h);
  and B32 (TQ1v, TQ1s, TQ1t);
  and B34 (TQ27, TQ24, TQ25);
  or G41 (TQ2, TQ2i, GND);
  or G43 (TQq, TQl, GND);
  xor X3 (TQa, B3, TQ9);
  or C12 (TQz, TQv, TQx);
  or C14 (TQ1k, TQ1i, TQ1j);
  or C32 (TQ1w, TQ1u, TQ1v);
  or C34 (TQ28, TQ26, TQ27);
  xor X42 (TQ3, TQ0, TQ11);
  xor X44 (TQs, TQn, GND);
  not N2 (TQ1f, TQa);
  or G12 (TQ19, TQz, GND);
  or G14 (TQ2a, TQ1k, GND);
  or G32 (TQ1y, TQ1w, GND);
  or G34 (TQ2b, TQ28, GND);
  xor S42 (D1, TQ3, TQ2);
  xor S44 (D3, TQs, TQq);
  xor X11 (TQg, A0, TQd);
  xor X13 (TQ1a, A2, TQ18);
  xor X31 (TQ1n, TQ1l, ONE);
  xor X33 (TQ1z, TQ1x, GND);
  or B2J9 (TQ11, TQ2c, TQ2d);
  and A42 (TQ5, TQ0, TQ11);
  and A44 (TQu, TQn, GND);
  xor S11 (TQ1l, TQg, GND);
  xor S13 (TQ1x, TQ1a, TQ19);
  xor S31 (TQ2e, TQ1n, GND);
  xor S33 (TQb, TQ1z, TQ1y);
  and B2K9 (TQ2d, TQ29, TQn);
  and B42 (TQ6, TQ2, TQ3);
  and B44 (TQw, TQq, TQs);
  and A11 (TQi, A0, TQd);
  and A13 (TQ1b, A2, TQ18);
  and A31 (TQ1o, TQ1l, ONE);
  and A33 (TQ20, TQ1x, GND);
  or B2L9 (TQ29, TQb, TQ0);
  or C42 (TQ8, TQ5, TQ6);
  or C44 (TQy, TQu, TQw);
  and B11 (TQk, GND, TQg);
  and B13 (TQ1c, TQ19, TQ1a);
  and B31 (TQ1p, GND, TQ1n);
  and B33 (TQ21, TQ1y, TQ1z);
  or B2T10 (TQ2c, TQ2a, TQ2b);
  or G42 (TQe, TQ8, GND);
  // OR_Gate G44 has open pins: in0=TQy, in1=GND, out=open
  or C11 (TQm, TQi, TQk);
  or C13 (TQ1d, TQ1b, TQ1c);
  or C31 (TQ1q, TQ1o, TQ1p);
  or C33 (TQ22, TQ20, TQ21);
  xor X41 (TQ2f, TQ2e, GND);
  xor X43 (TQf, TQb, TQ11);
  not NB (Borrow, TQ11);
  or G11 (TQr, TQm, GND);
  or G13 (TQ1g, TQ1d, GND);
  or G31 (TQ1s, TQ1q, GND);
  or G33 (TQ24, TQ22, GND);
  xor S41 (D0, TQ2f, GND);
  xor S43 (D2, TQf, TQe);
  xor X12 (TQt, A1, B1);
  xor X14 (TQ1h, A3, TQ1f);
  xor X32 (TQ1t, TQ1r, GND);
  xor X34 (TQ25, TQ23, GND);
  and A41 (TQ2g, TQ2e, GND);
  and A43 (TQh, TQb, TQ11);

  // Other names for the same wires on the sheet: TQ1 = B0; TQ1e = A3; TQ1m = ONE; TQ4 = B2; TQ7 = B3; TQ10 = GND;
  //   TQ12 = D0; TQ13 = D1; TQ14 = D2; TQ15 = D3; TQ16 = A2; TQ17 = Borrow; TQc = A0; TQo = A1; TQp = B1
endmodule
