// Logisim project bcd_subtractor_2digit.circ as structural Verilog
module bcd_subtractor_2digit (
  input  A0,
  input  B0,
  input  A1,
  input  B1,
  input  A2,
  input  B2,
  input  A3,
  input  B3,
  input  A4,
  input  B4,
  input  A5,
  input  B5,
  input  A6,
  input  B6,
  input  A7,
  input  B7,
  input  Bin,
  input  GND,
  output D0,
  output D1,
  output D2,
  output D3,
  output D4,
  output D5,
  output D6,
  output D7,
  output Borrow
);

  wire TQ1, TQ1a, TQ1b, TQ1d, TQ1e, TQ1f, TQ1g, TQ1h, TQ1i, TQ1j, TQ1k, TQ1l, TQ1m, TQ1n, TQ1p, TQ1q, TQ1r,
       TQ1s, TQ1t, TQ1u, TQ1v, TQ1w, TQ1x, TQ1y, TQ1z, TQ2c, TQ2e, TQ2f, TQ2g, TQ2h, TQ2i, TQ2j, TQ2k, TQ2l,
       TQ2m, TQ2n, TQ2o, TQ2p, TQ2q, TQ2r, TQ2s, TQ2t, TQ2u, TQ2v, TQ2w, TQ2x, TQ2y, TQ2z, TQ3, TQ3a, TQ3b,
       TQ3c, TQ3d, TQ3e, TQ3f, TQ3g, TQ3h, TQ3i, TQ3j, TQ3k, TQ3l, TQ3m, TQ3q, TQ3r, TQ3t, TQ3u, TQ3v, TQ3w,
       TQ3x, TQ4a, TQ4b, TQ4d, TQ4e, TQ4f, TQ4g, TQ4h, TQ4i, TQ4j, TQ4k, TQ4l, TQ4m, TQ4n, TQ4o, TQ4p, TQ4q,
       TQ4r, TQ4s, TQ4t, TQ4u, TQ4v, TQ4w, TQ4x, TQ4y, TQ4z, TQ5, TQ6, TQ7, TQ8, TQ9, TQ10, TQ11, TQ12, TQ13,
       TQ14, TQ15, TQ16, TQ17, TQ18, TQ19, TQ21, TQ22, TQ29, TQ30, TQ31, TQ32, TQ33, TQ34, TQ35, TQ36, TQ37,
       TQ38, TQ39, TQ40, TQ41, TQ42, TQ43, TQ44, TQ46, TQ47, TQ48, TQ49, TQ50, TQ51, TQa, TQc, TQd, TQe, TQf,
       TQg, TQh, TQi, TQj, TQk, TQl, TQm, TQp, TQq, TQr, TQs, TQt, TQu, TQv, TQw, TQx, TQy;

  not not_1 (TQd, B0);
  xor xor_1 (TQ29, TQs, TQq);
  xor S14 (TQ2o, TQ1i, TQ1g);
  xor X32 (TQ2e, TQ29, GND);
  xor xor_2 (TQ2q, TQ2o, GND);
  and A41 (TQ31, TQ2z, GND);
  and A43 (TQ3d, TQ3a, TQ3m);
  xor xor_3 (TQ46, B6, B5);
  and and_1 (TQ42, A5, B5);
  and A14 (TQ4g, A7, TQ4d);
  xor xor_4 (TQy, TQ4s, TQ4r);
  xor xor_5 (TQ1p, TQ5, TQ3);
  and and_2 (TQt, GND, TQp);
  and and_3 (TQ1j, TQ1d, TQ1f);
  xor X2 (TQ11, B2, B1);
  and A12 (TQu, A1, B1);
  and and_4 (TQ1k, A3, TQ1e);
  xor S32 (TQ34, TQ2e, TQ2c);
  xor S34 (TQ3g, TQ2q, TQ2p);
  and B41 (TQ32, GND, TQ30);
  and B43 (TQ3e, TQ3b, TQ3c);
  or or_1 (TQ3q, B6, B5);
  and and_5 (TQ43, TQ40, TQ41);
  and B14 (TQ4h, TQ4e, TQ4f);
  and and_6 (TQ4t, TQ4q, GND);
  and and_7 (TQ7, TQ1, GND);
  or or_2 (TQv, TQr, TQt);
  or C43 (TQ1l, TQ1h, TQ1j);
  or O1 (TQ6, B2, B1);
  and B12 (TQw, TQq, TQs);
  and and_8 (TQ1m, TQ1g, TQ1i);
  and A32 (TQ2f, TQ29, GND);
  and A34 (TQ2r, TQ2o, GND);
  or C41 (TQ33, TQ31, TQ32);
  or or_3 (TQ3f, TQ3d, TQ3e);
  xor X3 (TQ3r, B7, TQ3q);
  or C12 (TQ44, TQ42, TQ43);
  or or_4 (TQ4i, TQ4g, TQ4h);
  and B32 (TQ4u, TQ4r, TQ4s);
  and and_9 (TQ9, TQ3, TQ5);
  or or_5 (TQ10, TQv, GND);
  or or_6 (TQ1q, TQ1l, GND);
  xor xor_6 (TQ8, B3, TQ6);
  or or_7 (TQx, TQu, TQw);
  or C14 (TQ1n, TQ1k, TQ1m);
  and and_10 (TQ2g, TQ2c, TQ2e);
  and B34 (TQ2s, TQ2p, TQ2q);
  or G41 (TQ35, TQ33, GND);
  or G43 (TQ3h, TQ3f, GND);
  not N2 (TQ4d, TQ3r);
  or G12 (TQ47, TQ44, GND);
  or or_8 (TQe, TQ4i, GND);
  or C32 (TQ4v, TQ4t, TQ4u);
  or or_9 (TQa, TQ7, TQ9);
  xor xor_7 (TQ12, TQy, TQ21);
  xor X44 (TQ1s, TQ1p, GND);
  not not_2 (TQ1e, TQ8);
  xor xor_8 (TQ3u, A4, TQ3t);
  or or_10 (TQ13, TQx, GND);
  or G14 (TQ2v, TQ1n, GND);
  or or_11 (TQ2h, TQ2f, TQ2g);
  or C34 (TQ2t, TQ2r, TQ2s);
  xor X42 (TQ36, TQ34, TQ3m);
  xor xor_9 (TQ3i, TQ3g, GND);
  xor X13 (TQ48, A6, TQ46);
  not NBIN (TQ4l, TQ4j);
  or G32 (TQ4x, TQ4v, GND);
  or or_12 (TQg, TQa, GND);
  xor xor_10 (D5, TQ12, TQ10);
  xor xor_11 (D7, TQ1s, TQ1q);
  xor X11 (TQf, A0, TQd);
  xor xor_12 (TQ15, A2, TQ11);
  not not_3 (TQ1t, Bin);
  or or_13 (TQ2j, TQ2h, GND);
  or G34 (TQ2w, TQ2t, GND);
  xor S42 (D1, TQ36, TQ35);
  xor S44 (D3, TQ3i, TQ3h);
  xor S11 (TQ4k, TQ3u, GND);
  xor S13 (TQ4w, TQ48, TQ47);
  xor X31 (TQ4m, TQ4k, TQ4l);
  xor xor_13 (TQ4y, TQ4w, GND);
  or B2J22 (TQ21, TQi, TQk);
  and and_11 (TQ14, TQy, TQ21);
  and and_12 (TQ1u, TQ1p, GND);
  xor xor_14 (TQ1r, TQf, GND);
  xor xor_15 (TQ1w, TQ1r, TQ1t);
  and and_13 (TQ3v, A4, TQ3t);
  xor S31 (TQm, TQ4m, GND);
  xor xor_16 (TQ2i, TQ15, TQ13);
  xor X33 (TQ2k, TQ2i, GND);
  or B2J9 (TQ3m, TQ2x, TQ2y);
  and A42 (TQ37, TQ34, TQ3m);
  and A44 (TQ3j, TQ3g, GND);
  and and_14 (TQ49, A6, TQ46);
  xor xor_17 (TQ1b, TQ4y, TQ4x);
  and B2K22 (TQk, TQc, TQ1p);
  and and_15 (TQ16, TQ10, TQ12);
  and B44 (TQ1v, TQ1q, TQ1s);
  and A11 (TQh, A0, TQd);
  and A13 (TQ17, A2, TQ11);
  xor xor_18 (TQ2z, TQ1w, GND);
  xor S33 (TQ3a, TQ2k, TQ2j);
  and B2K9 (TQ2y, TQ2u, TQ3g);
  and B42 (TQ38, TQ35, TQ36);
  and and_16 (TQ3k, TQ3h, TQ3i);
  and and_17 (TQ3w, GND, TQ3u);
  and B13 (TQ4a, TQ47, TQ48);
  and A31 (TQ4n, TQ4k, TQ4l);
  and A33 (TQ4z, TQ4w, GND);
  or B2L22 (TQc, TQ1b, TQy);
  or C42 (TQ18, TQ14, TQ16);
  or or_14 (TQ1x, TQ1u, TQ1v);
  and B11 (TQj, GND, TQf);
  and and_18 (TQ1y, TQ1r, TQ1t);
  or or_15 (TQ3x, TQ3v, TQ3w);
  and B31 (TQ4o, GND, TQ4m);
  and and_19 (TQ19, TQ13, TQ15);
  and and_20 (TQ2l, TQ2i, GND);
  or B2L9 (TQ2u, TQ3a, TQ34);
  or or_16 (TQ39, TQ37, TQ38);
  or C44 (TQ3l, TQ3j, TQ3k);
  or or_17 (TQ4b, TQ49, TQ4a);
  and B33 (TQ50, TQ4x, TQ4y);
  or B2T22 (TQi, TQe, TQg);
  or G42 (TQ1d, TQ18, GND);
  // OR_Gate or_18 has open pins: in0=TQ1x, in1=GND, out=open
  or C11 (TQl, TQh, TQj);
  or C13 (TQ1a, TQ17, TQ19);
  and and_21 (TQ1z, GND, TQ1w);
  and and_22 (TQ2m, TQ2j, TQ2k);
  or B2T9 (TQ2x, TQ2v, TQ2w);
  or or_19 (TQ3b, TQ39, GND);
  // OR_Gate G44 has open pins: in0=TQ3l, in1=GND, out=open
  or or_20 (TQ40, TQ3x, GND);
  or G13 (TQ4e, TQ4b, GND);
  or C31 (TQ4p, TQ4n, TQ4o);
  or or_21 (TQ51, TQ4z, TQ50);
  xor X41 (TQp, TQm, GND);
  xor X43 (TQ1f, TQ1b, TQ21);
  not not_4 (Borrow, TQ21);
  or G11 (TQq, TQl, GND);
  or or_22 (TQ22, TQ1y, TQ1z);
  xor xor_19 (TQ41, A5, B5);
  or G31 (TQ4r, TQ4p, GND);
  or or_23 (TQ1g, TQ1a, GND);
  or C33 (TQ2n, TQ2l, TQ2m);
  xor xor_20 (TQ30, TQ2z, GND);
  xor xor_21 (TQ3c, TQ3a, TQ3m);
  not NB (TQ4j, TQ3m);
  xor xor_22 (TQ4f, A7, TQ4d);
  or G33 (TQ3, TQ51, GND);
  xor xor_23 (D4, TQp, GND);
  xor S43 (D6, TQ1f, TQ1d);
  xor X12 (TQs, A1, B1);
  xor X14 (TQ1i, A3, TQ1e);
  or or_24 (TQ2c, TQ22, GND);
  or or_25 (TQ2p, TQ2n, GND);
  xor S41 (D0, TQ30, GND);
  xor xor_24 (D2, TQ3c, TQ3b);
  not N1 (TQ3t, B4);
  xor S12 (TQ4q, TQ41, TQ40);
  xor xor_25 (TQ1, TQ4f, TQ4e);
  xor xor_26 (TQ4s, TQ4q, GND);
  xor X34 (TQ5, TQ1, GND);
  and and_23 (TQr, TQm, GND);
  and and_24 (TQ1h, TQ1b, TQ21);

  // Other names for the same wires on the sheet: TQ0 = B0; TQ1c = A3; TQ1o = Bin; TQ2 = B2; TQ2a = D3; TQ2b = D7;
  //   TQ2d = Borrow; TQ3n = B4; TQ3o = B6; TQ3p = B7; TQ3s = A4; TQ3y = A5; TQ3z = B5; TQ4 = B3; TQ4c = A7;
  //   TQ20 = GND; TQ23 = D0; TQ24 = D4; TQ25 = D1; TQ26 = D5; TQ27 = D2; TQ28 = D6; TQ45 = A6; TQb = A0; TQn = A1;
  //   TQo = B1; TQz = A2
endmodule
