// Logisim project bidirsreg_4bit.circ as structural Verilog
module bidirsreg_4bit (
  input  CLK,
  input  DIR,
  input  SIN,
  input  SINL,
  input  RST,
  output Q0,
  output Q1,
  output Q2,
  output Q3
);

  wire AL1_out, AL2_out, AL3_out, AL4_out, AR1_out, AR2_out, AR3_out, AR4_out, OR4_out, TQ6, TQ9, TQb, TQc;

  not N1 (TQc, DIR);
  D_Flip_Flop U1 (.D(TQ6), .clk(CLK), .Q(Q0), .reset(RST));  // open: Qn, preset
  D_Flip_Flop U2 (.D(TQ9), .clk(CLK), .Q(Q1), .reset(RST));  // open: Qn, preset
  D_Flip_Flop U3 (.D(TQb), .clk(CLK), .Q(Q2), .reset(RST));  // open: Qn, preset
  D_Flip_Flop U4 (.D(OR4_out), .clk(CLK), .Q(Q3), .reset(RST));  // open: Qn, preset
  and AR1 (AR1_out, TQc, SIN);
  and AL1 (AL1_out, DIR, Q1);
  or OR1 (TQ6, AR1_out, AL1_out);
  and AR2 (AR2_out, TQc, Q0);
  and AL2 (AL2_out, DIR, Q2);
  or OR2 (TQ9, AR2_out, AL2_out);
  and AR3 (AR3_out, TQc, Q1);
  and AL3 (AL3_out, DIR, Q3);
  or OR3 (TQb, AR3_out, AL3_out);
  and AR4 (AR4_out, TQc, Q2);
  and AL4 (AL4_out, DIR, SINL);
  or OR4 (OR4_out, AR4_out, AL4_out);

  // Other names for the same wires on the sheet: TQ0 = Q2; TQ1 = DIR; TQ2 = SINL; TQ3 = SIN; TQ4 = CLK; TQ5 = RST;
  //   TQ7 = Q3; TQ8 = Q0; TQa = Q1
endmodule
