// Logisim project bin2bcd_4bit.circ as structural Verilog
module bin2bcd_4bit (
  input  B0,
  input  B1,
  input  B2,
  input  B3,
  output T1,
  output U0,
  output U1,
  output U2,
  output U3
);

  wire A2_out, A3_out, A4_out, A5_out, A6_out, N1_out, N3_out, O2_out, TQ1, X2_out, X3_out;

  or O1 (TQ1, B2, B1);
  and A1 (T1, B3, TQ1);
  not N1 (N1_out, T1);
  xor X1 (U1, B1, T1);
  // NOT_Gate N2 has open pins: in=B1, out=open
  not N3 (N3_out, B2);
  xor X2 (X2_out, N3_out, B1);
  and A2 (A2_out, B1, N3_out);
  or O2 (O2_out, B2, A2_out);
  xor X3 (X3_out, B3, O2_out);
  and A3 (A3_out, N1_out, B2);
  and A4 (A4_out, T1, X2_out);
  or O3 (U2, A3_out, A4_out);
  and A5 (A5_out, N1_out, B3);
  and A6 (A6_out, T1, X3_out);
  or O4 (U3, A5_out, A6_out);

  assign U0 = B0;

  // Other names for the same wires on the sheet: TQ0 = U3; TQ2 = B0; TQ3 = U1; TQ4 = B1; TQ5 = B2; TQ6 = U2; TQ7 = B3;
  //   TQ8 = T1
endmodule
