// Logisim project circuit_from_json.circ as structural Verilog
module mux_4to1 (
  input  D0,
  input  S0,
  input  D1,
  input  S1,
  input  D2,
  input  D3,
  output Y
);

  wire and_1_out, and_2_out, and_3_out, and_4_out, or_1_out, or_2_out;

  not not_1 (S0, S0);
  not not_2 (D0, D0);
  and and_1 (and_1_out, D0, S0);
  and and_2 (and_2_out, D1, S0);
  and and_3 (and_3_out, D2, S0);
  and and_4 (and_4_out, D0, S0);
  or or_1 (or_1_out, and_1_out, and_2_out);
  or or_2 (or_2_out, and_3_out, and_4_out);
  or or_3 (Y, or_1_out, or_2_out);

  assign D3 = D0;
  assign S1 = D0;
endmodule
