// Logisim project comparator_3bit.circ as structural Verilog
module comparator_3bit (
  input  A0,
  input  B0,
  input  A1,
  input  B1,
  input  A2,
  input  B2,
  output GT,
  output EQ,
  output LT
);

  wire CMP1G_out, CMP2E_out, CMP2G_out, CMP2N_out, CMPA1_out, CMPA2_out, CMPE2_out, CMPG2_out, CMPO_out,
       CMPQ2_out, TQ1, TQ6, TQb, TQc, TQd;

  xnor CMP0E (TQc, A0, B0);
  not CMP0N (TQ1, B0);
  and CMP0G (TQb, A0, TQ1);
  xnor CMP1E (TQd, A1, B1);
  not CMP1N (TQ6, B1);
  and CMP1G (CMP1G_out, A1, TQ6);
  xnor CMP2E (CMP2E_out, A2, B2);
  not CMP2N (CMP2N_out, B2);
  and CMP2G (CMP2G_out, A2, CMP2N_out);
  or CMPO (CMPO_out, GT, EQ);
  not CMPL (LT, CMPO_out);
  and CMPA1 (CMPA1_out, CMPE2_out, TQb);
  or CMPG1 (GT, CMPG2_out, CMPA1_out);
  // AND_Gate CMPE1 has open pins: in0=CMPE2_out, in1=TQc, out=open
  and CMPA2 (CMPA2_out, CMP2E_out, CMP1G_out);
  or CMPG2 (CMPG2_out, CMP2G_out, CMPA2_out);
  and CMPE2 (CMPE2_out, CMP2E_out, TQd);
  // AND_Gate CMPQ1 is placed but not wired
  and CMPQ2 (CMPQ2_out, TQc, TQd);
  and CMPQ3 (EQ, CMPQ2_out, CMP2E_out);

  // Other names for the same wires on the sheet: TQ0 = GT; TQ2 = EQ; TQ3 = A0; TQ4 = LT; TQ5 = B0; TQ7 = A1; TQ8 = B1;
  //   TQ9 = A2; TQa = B2
endmodule
