// Logisim project comparator_4bit.circ as structural Verilog
module comparator_4bit (
  input  A0,
  input  B0,
  input  A1,
  input  B1,
  input  A2,
  input  B2,
  input  A3,
  input  B3,
  output GT,
  output EQ,
  output LT
);

  wire CMPA1_out, CMPA2_out, CMPA3_out, CMPE2_out, CMPE3_out, CMPG2_out, CMPG3_out, CMPO_out, CMPQ2_out,
       CMPQ3_out, TQ0, TQ3, TQ6, TQ9, TQc, TQd, TQe, TQf, TQg, TQh, TQi, TQj;

  xnor CMP0E (TQg, A0, B0);
  not CMP0N (TQ0, B0);
  and CMP0G (TQf, A0, TQ0);
  xnor CMP1E (TQh, A1, B1);
  not CMP1N (TQ3, B1);
  and CMP1G (TQe, A1, TQ3);
  xnor CMP2E (TQi, A2, B2);
  not CMP2N (TQ6, B2);
  and CMP2G (TQc, A2, TQ6);
  xnor CMP3E (TQj, A3, B3);
  not CMP3N (TQ9, B3);
  and CMP3G (TQd, A3, TQ9);
  or CMPO (CMPO_out, GT, EQ);
  not CMPL (LT, CMPO_out);
  and CMPA1 (CMPA1_out, CMPE2_out, TQf);
  or CMPG1 (GT, CMPG2_out, CMPA1_out);
  // AND_Gate CMPE1 has open pins: in0=CMPE2_out, in1=TQg, out=open
  and CMPA2 (CMPA2_out, CMPE3_out, TQe);
  or CMPG2 (CMPG2_out, CMPG3_out, CMPA2_out);
  and CMPE2 (CMPE2_out, CMPE3_out, TQh);
  and CMPA3 (CMPA3_out, TQj, TQc);
  or CMPG3 (CMPG3_out, TQd, CMPA3_out);
  and CMPE3 (CMPE3_out, TQj, TQi);
  // AND_Gate CMPQ1 is placed but not wired
  and CMPQ2 (CMPQ2_out, TQg, TQh);
  and CMPQ3 (CMPQ3_out, CMPQ2_out, TQi);
  and CMPQ4 (EQ, CMPQ3_out, TQj);

  // Other names for the same wires on the sheet: TQ1 = A0; TQ2 = B0; TQ4 = A1; TQ5 = B1; TQ7 = A2; TQ8 = B2; TQa = A3;
  //   TQb = B3; TQk = GT; TQl = EQ; TQm = LT
endmodule
