// Logisim project comparator_8bit.circ as structural Verilog
module comparator_8bit (
  input  A0,
  input  B0,
  input  A1,
  input  B1,
  input  A2,
  input  B2,
  input  A3,
  input  B3,
  input  A4,
  input  B4,
  input  A5,
  input  B5,
  input  A6,
  input  B6,
  input  A7,
  input  B7,
  output GT,
  output EQ,
  output LT
);

  wire CMP0E_out, CMP0G_out, CMP0N_out, CMP1E_out, CMP1G_out, CMP1N_out, CMP2E_out, CMP2G_out, CMP2N_out,
       CMP3E_out, CMP3G_out, CMP3N_out, CMP4E_out, CMP4G_out, CMP4N_out, CMP5E_out, CMP5G_out, CMP5N_out,
       CMP6E_out, CMP6G_out, CMP6N_out, CMP7E_out, CMP7G_out, CMP7N_out, CMPA1_out, CMPA2_out, CMPA3_out,
       CMPA4_out, CMPA5_out, CMPA6_out, CMPA7_out, CMPE2_out, CMPE3_out, CMPE4_out, CMPE5_out, CMPE6_out,
       CMPE7_out, CMPG2_out, CMPG3_out, CMPG4_out, CMPG5_out, CMPG6_out, CMPG7_out, CMPO_out, CMPQ2_out,
       CMPQ3_out, CMPQ4_out, CMPQ5_out, CMPQ6_out, CMPQ7_out;

  xnor CMP0E (CMP0E_out, A0, B0);
  not CMP0N (CMP0N_out, B0);
  and CMP0G (CMP0G_out, A0, CMP0N_out);
  xnor CMP1E (CMP1E_out, A1, B1);
  not CMP1N (CMP1N_out, B1);
  and CMP1G (CMP1G_out, A1, CMP1N_out);
  xnor CMP2E (CMP2E_out, A2, B2);
  not CMP2N (CMP2N_out, B2);
  and CMP2G (CMP2G_out, A2, CMP2N_out);
  xnor CMP3E (CMP3E_out, A3, B3);
  not CMP3N (CMP3N_out, B3);
  and CMP3G (CMP3G_out, A3, CMP3N_out);
  xnor CMP4E (CMP4E_out, A4, B4);
  not CMP4N (CMP4N_out, B4);
  and CMP4G (CMP4G_out, A4, CMP4N_out);
  xnor CMP5E (CMP5E_out, A5, B5);
  not CMP5N (CMP5N_out, B5);
  and CMP5G (CMP5G_out, A5, CMP5N_out);
  xnor CMP6E (CMP6E_out, A6, B6);
  not CMP6N (CMP6N_out, B6);
  and CMP6G (CMP6G_out, A6, CMP6N_out);
  xnor CMP7E (CMP7E_out, A7, B7);
  not CMP7N (CMP7N_out, B7);
  and CMP7G (CMP7G_out, A7, CMP7N_out);
  or CMPO (CMPO_out, GT, EQ);
  not CMPL (LT, CMPO_out);
  and CMPA1 (CMPA1_out, CMPE2_out, CMP0G_out);
  or CMPG1 (GT, CMPG2_out, CMPA1_out);
  // AND_Gate CMPE1 has open pins: in0=CMPE2_out, in1=CMP0E_out, out=open
  and CMPA2 (CMPA2_out, CMPE3_out, CMP1G_out);
  or CMPG2 (CMPG2_out, CMPG3_out, CMPA2_out);
  and CMPE2 (CMPE2_out, CMPE3_out, CMP1E_out);
  and CMPA3 (CMPA3_out, CMPE4_out, CMP2G_out);
  or CMPG3 (CMPG3_out, CMPG4_out, CMPA3_out);
  and CMPE3 (CMPE3_out, CMPE4_out, CMP2E_out);
  and CMPA4 (CMPA4_out, CMPE5_out, CMP3G_out);
  or CMPG4 (CMPG4_out, CMPG5_out, CMPA4_out);
  and CMPE4 (CMPE4_out, CMPE5_out, CMP3E_out);
  and CMPA5 (CMPA5_out, CMPE6_out, CMP4G_out);
  or CMPG5 (CMPG5_out, CMPG6_out, CMPA5_out);
  and CMPE5 (CMPE5_out, CMPE6_out, CMP4E_out);
  and CMPA6 (CMPA6_out, CMPE7_out, CMP5G_out);
  or CMPG6 (CMPG6_out, CMPG7_out, CMPA6_out);
  and CMPE6 (CMPE6_out, CMPE7_out, CMP5E_out);
  and CMPA7 (CMPA7_out, CMP7E_out, CMP6G_out);
  or CMPG7 (CMPG7_out, CMP7G_out, CMPA7_out);
  and CMPE7 (CMPE7_out, CMP7E_out, CMP6E_out);
  // AND_Gate CMPQ1 is placed but not wired
  and CMPQ2 (CMPQ2_out, CMP0E_out, CMP1E_out);
  and CMPQ3 (CMPQ3_out, CMPQ2_out, CMP2E_out);
  and CMPQ4 (CMPQ4_out, CMPQ3_out, CMP3E_out);
  and CMPQ5 (CMPQ5_out, CMPQ4_out, CMP4E_out);
  and CMPQ6 (CMPQ6_out, CMPQ5_out, CMP5E_out);
  and CMPQ7 (CMPQ7_out, CMPQ6_out, CMP6E_out);
  and CMPQ8 (EQ, CMPQ7_out, CMP7E_out);
endmodule
