// Logisim project countdown_timer.circ as structural Verilog
module countdown_timer (
  input  LOAD,
  input  RST,
  input  D0,
  input  D1,
  input  D2,
  input  D3,
  output Q0,
  output Q1,
  output Q2,
  output Q3,
  output ZERO
);

  wire CLK_out, CTDA0_out, CTDA1_out, CTDA2_out, CTDA3_out, CTDB0_out, CTDB1_out, CTDB2_out, CTDB3_out,
       CTDC2_out, CTDC3_out, CTDL_out, CTDM0_out, CTDM1_out, CTDM2_out, CTDM3_out, CTDN0_out, CTDN1_out,
       CTDN2_out, CTDN3_out, CTDX0_out, CTDX1_out, CTDX2_out, CTDX3_out, CTDZ1_out, CTDZ2_out;

  Clock CLK (.out(CLK_out));
  not CTDL (CTDL_out, LOAD);
  not CTDN0 (CTDN0_out, Q0);
  not CTDN1 (CTDN1_out, Q1);
  and CTDZ1 (CTDZ1_out, CTDN0_out, CTDN1_out);
  not CTDN2 (CTDN2_out, Q2);
  and CTDZ2 (CTDZ2_out, CTDZ1_out, CTDN2_out);
  not CTDN3 (CTDN3_out, Q3);
  and CTDZ3 (ZERO, CTDZ2_out, CTDN3_out);
  and CTDA0 (CTDA0_out, LOAD, D0);
  and CTDB0 (CTDB0_out, CTDL_out, CTDX0_out);
  or CTDM0 (CTDM0_out, CTDA0_out, CTDB0_out);
  xor CTDX0 (CTDX0_out, Q0, CTDL_out);
  D_Flip_Flop CTDF0 (.D(CTDM0_out), .clk(CLK_out), .Q(Q0), .preset(RST), .reset(RST));  // open: Qn
  and CTDA1 (CTDA1_out, LOAD, D1);
  and CTDB1 (CTDB1_out, CTDL_out, CTDX1_out);
  or CTDM1 (CTDM1_out, CTDA1_out, CTDB1_out);
  xor CTDX1 (CTDX1_out, Q1, CTDN0_out);
  D_Flip_Flop CTDF1 (.D(CTDM1_out), .clk(CLK_out), .Q(Q1), .preset(RST), .reset(RST));  // open: Qn
  and CTDA2 (CTDA2_out, LOAD, D2);
  and CTDB2 (CTDB2_out, CTDL_out, CTDX2_out);
  or CTDM2 (CTDM2_out, CTDA2_out, CTDB2_out);
  xor CTDX2 (CTDX2_out, Q2, CTDC2_out);
  D_Flip_Flop CTDF2 (.D(CTDM2_out), .clk(CLK_out), .Q(Q2), .preset(RST), .reset(RST));  // open: Qn
  and CTDA3 (CTDA3_out, LOAD, D3);
  and CTDB3 (CTDB3_out, CTDL_out, CTDX3_out);
  or CTDM3 (CTDM3_out, CTDA3_out, CTDB3_out);
  xor CTDX3 (CTDX3_out, Q3, CTDC3_out);
  D_Flip_Flop CTDF3 (.D(CTDM3_out), .clk(CLK_out), .Q(Q3), .preset(RST), .reset(RST));  // open: Qn
  and CTDC2 (CTDC2_out, CTDN0_out, CTDN1_out);
  and CTDC3 (CTDC3_out, CTDC2_out, CTDN2_out);
endmodule
