// Logisim project counter_4bit.circ as structural Verilog
module counter_4bit (
  input  ENP,
  input  ENT,
  input  nLOAD,
  input  nCLR,
  input  D0,
  input  D1,
  input  D2,
  input  D3,
  output Q0,
  output Q1,
  output Q2,
  output Q3,
  output RCO
);

  wire CLK_out;

  Clock CLK (.out(CLK_out));
  _74161 U1 (
    .pin1(nCLR), .pin2(CLK_out), .pin3(D0), .pin4(D1), .pin5(D2), .pin6(D3), .pin7(ENP), .pin15(RCO),
    .pin14(Q0), .pin13(Q1), .pin12(Q2), .pin11(Q3), .pin10(ENT), .pin9(nLOAD));
endmodule
