// Logisim project counter_8bit.circ as structural Verilog
module counter_8bit (
  input  ENP,
  input  ENT,
  input  nLOAD,
  input  nCLR,
  input  D0,
  input  D1,
  input  D2,
  input  D3,
  input  D4,
  input  D5,
  input  D6,
  input  D7,
  output Q0,
  output Q1,
  output Q2,
  output Q3,
  output Q4,
  output Q5,
  output Q6,
  output Q7,
  output RCO
);

  wire CLK_out, U1_pin15;

  Clock CLK (.out(CLK_out));
  _74161 U1 (
    .pin1(nCLR), .pin2(CLK_out), .pin3(D0), .pin4(D1), .pin5(D2), .pin6(D3), .pin7(ENP), .pin15(U1_pin15),
    .pin14(Q0), .pin13(Q1), .pin12(Q2), .pin11(Q3), .pin10(ENT), .pin9(nLOAD));
  _74161 U2 (
    .pin1(nCLR), .pin2(CLK_out), .pin3(D4), .pin4(D5), .pin5(D6), .pin6(D7), .pin7(ENP), .pin15(RCO),
    .pin14(Q4), .pin13(Q5), .pin12(Q6), .pin11(Q7), .pin10(U1_pin15), .pin9(nLOAD));
endmodule
