// Logisim project d138_allout.circ as structural Verilog
module d138_allout (
  input  A,
  input  B,
  input  C,
  input  nG2A,
  input  nG2B,
  input  G1,
  output nY0,
  output nY1,
  output nY2,
  output nY3,
  output nY4,
  output nY5,
  output nY6,
  output nY7
);

  _74138 U1 (
    .pin1(A), .pin2(B), .pin3(C), .pin4(nG2A), .pin5(nG2B), .pin6(G1), .pin7(nY7), .pin15(nY0), .pin14(nY1),
    .pin13(nY2), .pin12(nY3), .pin11(nY4), .pin10(nY5), .pin9(nY6));
endmodule
