// Logisim project d138_diag.circ as structural Verilog
module d138_diag (
  input  A,
  input  B,
  input  C,
  input  nG2A,
  input  nG2B,
  input  G1,
  output nY0
);

  _74138 U1 (
    .pin1(A), .pin2(B), .pin3(C), .pin4(nG2A), .pin5(nG2B), .pin6(G1), .pin15(nY0));  // open: pin7, pin14, pin13, pin12, pin11, pin10, pin9
endmodule
