// Logisim project debouncer.circ as structural Verilog
module debouncer (
  input  IN,
  input  RST,
  output OUT
);

  wire A1_out, A2_out, A3_out, O1_out, TQ1, U1_q, U2_q, U3_q;

  Clock CLK (.out(TQ1));
  D_Flip_Flop U1 (.D(IN), .clk(TQ1), .Q(U1_q), .reset(RST));  // open: Qn, preset
  D_Flip_Flop U2 (.D(U1_q), .clk(TQ1), .Q(U2_q), .reset(RST));  // open: Qn, preset
  D_Flip_Flop U3 (.D(U2_q), .clk(TQ1), .Q(U3_q), .reset(RST));  // open: Qn, preset
  and A1 (A1_out, U1_q, U2_q);
  and A2 (A2_out, U1_q, U3_q);
  and A3 (A3_out, U2_q, U3_q);
  or O1 (O1_out, A1_out, A2_out);
  or O2 (OUT, O1_out, A3_out);

  // Other names for the same wires on the sheet: TQ0 = OUT; TQ2 = RST; TQ3 = IN
endmodule
