// Logisim project decoder_2bit.circ as structural Verilog
module decoder_2bit (
  input  A0,
  input  A1,
  output Y0,
  output Y1,
  output Y2,
  output Y3
);

  wire TQ1, TQ3;

  not DECN1 (TQ3, A0);
  not DECN2 (TQ1, A1);
  and DEC0_1 (Y0, TQ3, TQ1);
  and DEC1_1 (Y1, A0, TQ1);
  and DEC2_1 (Y2, TQ3, A1);
  and DEC3_1 (Y3, A0, A1);

  // Other names for the same wires on the sheet: TQ0 = Y0; TQ2 = Y1; TQ4 = Y2; TQ5 = A0; TQ6 = A1; TQ7 = Y3
endmodule
