// Logisim project decoder_3bit.circ as structural Verilog
module decoder_3bit (
  input  A0,
  input  A1,
  input  A2,
  output Y0,
  output Y1,
  output Y2,
  output Y3,
  output Y4,
  output Y5,
  output Y6,
  output Y7
);

  wire DEC1_1_out, DEC2_1_out, DEC3_1_out, DEC4_1_out, DEC5_1_out, DEC6_1_out, DEC7_1_out, TQ1, TQ3, TQb, TQe;

  not DECN1 (TQ1, A0);
  not DECN2 (TQe, A1);
  not DECN3 (TQb, A2);
  and DEC0_1 (TQ3, TQ1, TQe);
  and DEC0_2 (Y0, TQ3, TQb);
  and DEC1_1 (DEC1_1_out, A0, TQe);
  and DEC1_2 (Y1, DEC1_1_out, TQb);
  and DEC2_1 (DEC2_1_out, TQ1, A1);
  and DEC2_2 (Y2, DEC2_1_out, TQb);
  and DEC3_1 (DEC3_1_out, A0, A1);
  and DEC3_2 (Y3, DEC3_1_out, TQb);
  and DEC4_1 (DEC4_1_out, TQ1, TQe);
  and DEC4_2 (Y4, DEC4_1_out, A2);
  and DEC5_1 (DEC5_1_out, A0, TQe);
  and DEC5_2 (Y5, DEC5_1_out, A2);
  and DEC6_1 (DEC6_1_out, TQ1, A1);
  and DEC6_2 (Y6, DEC6_1_out, A2);
  and DEC7_1 (DEC7_1_out, A0, A1);
  and DEC7_2 (Y7, DEC7_1_out, A2);

  // Other names for the same wires on the sheet: TQ0 = Y5; TQ2 = Y6; TQ4 = A0; TQ5 = Y0; TQ6 = A1; TQ7 = A2; TQ8 = Y7;
  //   TQ9 = Y1; TQa = Y2; TQc = Y3; TQd = Y4
endmodule
