// Logisim project decoder_4to16.circ as structural Verilog
module decoder_4to16 (
  input  A0,
  input  A1,
  input  A2,
  input  A3,
  input  nG2,
  output Y0,
  output Y1,
  output Y2,
  output Y3,
  output Y4,
  output Y5,
  output Y6,
  output Y7,
  output Y8,
  output Y9,
  output Y10,
  output Y11,
  output Y12,
  output Y13,
  output Y14,
  output Y15
);

  wire U1_pin6;

  _74138 U1 (
    .pin1(A0), .pin2(A1), .pin3(A2), .pin4(nG2), .pin5(nG2), .pin6(U1_pin6), .pin7(Y7), .pin15(Y0),
    .pin14(Y1), .pin13(Y2), .pin12(Y3), .pin11(Y4), .pin10(Y5), .pin9(Y6));
  _74138 U2 (
    .pin1(A0), .pin2(A1), .pin3(A2), .pin4(nG2), .pin5(nG2), .pin6(A3), .pin7(Y15), .pin15(Y8), .pin14(Y9),
    .pin13(Y10), .pin12(Y11), .pin11(Y12), .pin10(Y13), .pin9(Y14));
  not U3A (U1_pin6, A3);

  // Other names for the same wires on the sheet: TQ0 = A0; TQ1 = A1; TQ2 = A2; TQ3 = A3; TQ4 = nG2; TQ5 = Y0;
  //   TQ6 = Y1; TQ7 = Y2; TQ8 = Y3; TQ9 = Y4; TQa = Y5; TQb = Y6; TQc = Y7; TQd = Y8; TQe = Y9; TQf = Y10; TQg = Y11;
  //   TQh = Y12; TQi = Y13; TQj = Y14; TQk = Y15
endmodule
