// Logisim project demux_4to1.circ as structural Verilog
module demux_4to1 (
  input  DATA,
  input  S0,
  input  S1,
  output Y0,
  output Y1,
  output Y2,
  output Y3
);

  wire D0_1_out, D1_1_out, D2_1_out, D3_1_out, DN1_out, DN2_out;

  not DN1 (DN1_out, S0);
  not DN2 (DN2_out, S1);
  and D0_1 (D0_1_out, DN1_out, DN2_out);
  and G1 (Y0, DATA, D0_1_out);
  and D1_1 (D1_1_out, S0, DN2_out);
  and G2 (Y1, DATA, D1_1_out);
  and D2_1 (D2_1_out, DN1_out, S1);
  and G3 (Y2, DATA, D2_1_out);
  and D3_1 (D3_1_out, S0, S1);
  and G4 (Y3, DATA, D3_1_out);

  // Other names for the same wires on the sheet: TQ0 = Y2; TQ1 = S0; TQ2 = S1; TQ3 = DATA; TQ4 = Y3; TQ5 = Y0;
  //   TQ6 = Y1
endmodule
