// Logisim project dff.circ as structural Verilog
module dff (
  input  D,
  input  RST,
  output Q,
  output nQ
);

  wire CLK_out;

  Clock CLK (.out(CLK_out));
  D_Flip_Flop U1 (.D(D), .clk(CLK_out), .Q(Q), .Qn(nQ), .preset(RST), .reset(RST));
endmodule
