// Logisim project digital_clock.circ as structural Verilog
module digital_clock (
  input  RST,
  output Q0,
  output Q1,
  output Q2,
  output Q3,
  output Q4,
  output Q5,
  output Q6,
  output Q7,
  output Q8,
  output Q9,
  output Q10,
  output Q11,
  output Q12,
  output Q13,
  output Q18,
  output Q19,
  output Q20,
  output Q21,
  output Q22
);

  wire CLK_out, D0A1_out, D0A2_out, D0A3_out, D0M1_out, D0M2_out, D0M3_out, D0N1_out, D0N2_out, D0NW_out,
       D0O3_out, D0R2_out, D0R3_out, D0T0_out, D1A1_out, D1A2_out, D1EC_out, D1M1_out, D1M2_out, D1N1_out,
       D1NW_out, D1O2_out, D1R2_out, D1T0_out, D1TE_out, D1W_out, D2A1_out, D2A2_out, D2A3_out, D2EC_out,
       D2M1_out, D2M2_out, D2M3_out, D2N1_out, D2N2_out, D2NW_out, D2O3_out, D2R2_out, D2R3_out, D2T0_out,
       D2TE_out, D2W_out, D3A1_out, D3A2_out, D3EC_out, D3M1_out, D3M2_out, D3N1_out, D3NW_out, D3O2_out,
       D3R2_out, D3T0_out, D3TE_out, D3W_out, HA1_out, HA2_out, HA3_out, HA4_out, HM1_out, HM2_out, HM3_out,
       HM4_out, HN3_out, HNW_out, HO1_out, HO2_out, HO4_out, HR2_out, HR3_out, HR4_out, HW_out;

  Clock CLK (.out(CLK_out));
  T_Flip_Flop D0F0 (.T(D0T0_out), .clk(CLK_out), .Q(Q0), .reset(RST), .preset(RST));  // open: Qn
  T_Flip_Flop D0F1 (.T(D0M1_out), .clk(CLK_out), .Q(Q1), .reset(RST), .preset(RST));  // open: Qn
  T_Flip_Flop D0F2 (.T(D0M2_out), .clk(CLK_out), .Q(Q2), .reset(RST), .preset(RST));  // open: Qn
  T_Flip_Flop D0F3 (.T(D0O3_out), .clk(CLK_out), .Q(Q3), .reset(RST), .preset(RST));  // open: Qn
  not D0N1 (D0N1_out, Q1);
  and D0A1 (D0A1_out, Q0, D0N1_out);
  not D0N2 (D0N2_out, Q2);
  and D0A2 (D0A2_out, D0A1_out, D0N2_out);
  and D0A3 (D0A3_out, D0A2_out, Q3);
  not D0NW (D0NW_out, D0A3_out);
  or D0T0 (D0T0_out, D0NW_out, D0A3_out);
  and D0M1 (D0M1_out, Q0, D0NW_out);
  and D0R2 (D0R2_out, Q0, Q1);
  and D0M2 (D0M2_out, D0R2_out, D0NW_out);
  and D0R3 (D0R3_out, D0R2_out, Q2);
  and D0M3 (D0M3_out, D0R3_out, D0NW_out);
  or D0O3 (D0O3_out, D0M3_out, D0A3_out);
  T_Flip_Flop D1F0 (.T(D1T0_out), .clk(CLK_out), .Q(Q4), .reset(RST), .preset(RST));  // open: Qn
  T_Flip_Flop D1F1 (.T(D1M1_out), .clk(CLK_out), .Q(Q5), .reset(RST), .preset(RST));  // open: Qn
  T_Flip_Flop D1F2 (.T(D1O2_out), .clk(CLK_out), .Q(Q6), .reset(RST), .preset(RST));  // open: Qn
  not D1N1 (D1N1_out, Q5);
  and D1A1 (D1A1_out, Q4, D1N1_out);
  and D1A2 (D1A2_out, D1A1_out, Q6);
  and D1W (D1W_out, D0A3_out, D1A2_out);
  not D1NW (D1NW_out, D1W_out);
  and D1TE (D1TE_out, D0A3_out, D1NW_out);
  or D1T0 (D1T0_out, D1TE_out, D1W_out);
  and D1M1 (D1M1_out, Q4, D1TE_out);
  and D1R2 (D1R2_out, Q4, Q5);
  and D1M2 (D1M2_out, D1R2_out, D1TE_out);
  or D1O2 (D1O2_out, D1M2_out, D1W_out);
  and D1EC (D1EC_out, D0A3_out, D1W_out);
  T_Flip_Flop D2F0 (.T(D2T0_out), .clk(CLK_out), .Q(Q7), .reset(RST), .preset(RST));  // open: Qn
  T_Flip_Flop D2F1 (.T(D2M1_out), .clk(CLK_out), .Q(Q8), .reset(RST), .preset(RST));  // open: Qn
  T_Flip_Flop D2F2 (.T(D2M2_out), .clk(CLK_out), .Q(Q9), .reset(RST), .preset(RST));  // open: Qn
  T_Flip_Flop D2F3 (.T(D2O3_out), .clk(CLK_out), .Q(Q10), .reset(RST), .preset(RST));  // open: Qn
  not D2N1 (D2N1_out, Q8);
  and D2A1 (D2A1_out, Q7, D2N1_out);
  not D2N2 (D2N2_out, Q9);
  and D2A2 (D2A2_out, D2A1_out, D2N2_out);
  and D2A3 (D2A3_out, D2A2_out, Q10);
  and D2W (D2W_out, D1EC_out, D2A3_out);
  not D2NW (D2NW_out, D2W_out);
  and D2TE (D2TE_out, D1EC_out, D2NW_out);
  or D2T0 (D2T0_out, D2TE_out, D2W_out);
  and D2M1 (D2M1_out, Q7, D2TE_out);
  and D2R2 (D2R2_out, Q7, Q8);
  and D2M2 (D2M2_out, D2R2_out, D2TE_out);
  and D2R3 (D2R3_out, D2R2_out, Q9);
  and D2M3 (D2M3_out, D2R3_out, D2TE_out);
  or D2O3 (D2O3_out, D2M3_out, D2W_out);
  and D2EC (D2EC_out, D1EC_out, D2W_out);
  T_Flip_Flop D3F0 (.T(D3T0_out), .clk(CLK_out), .Q(Q11), .reset(RST), .preset(RST));  // open: Qn
  T_Flip_Flop D3F1 (.T(D3M1_out), .clk(CLK_out), .Q(Q12), .reset(RST), .preset(RST));  // open: Qn
  T_Flip_Flop D3F2 (.T(D3O2_out), .clk(CLK_out), .Q(Q13), .reset(RST), .preset(RST));  // open: Qn
  not D3N1 (D3N1_out, Q12);
  and D3A1 (D3A1_out, Q11, D3N1_out);
  and D3A2 (D3A2_out, D3A1_out, Q13);
  and D3W (D3W_out, D2EC_out, D3A2_out);
  not D3NW (D3NW_out, D3W_out);
  and D3TE (D3TE_out, D2EC_out, D3NW_out);
  or D3T0 (D3T0_out, D3TE_out, D3W_out);
  and D3M1 (D3M1_out, Q11, D3TE_out);
  and D3R2 (D3R2_out, Q11, Q12);
  and D3M2 (D3M2_out, D3R2_out, D3TE_out);
  or D3O2 (D3O2_out, D3M2_out, D3W_out);
  and D3EC (D3EC_out, D2EC_out, D3W_out);
  T_Flip_Flop DH0 (.T(D3EC_out), .clk(CLK_out), .Q(Q18), .reset(RST), .preset(RST));  // open: Qn
  T_Flip_Flop DH1 (.T(HO1_out), .clk(CLK_out), .Q(Q19), .reset(RST), .preset(RST));  // open: Qn
  T_Flip_Flop DH2 (.T(HO2_out), .clk(CLK_out), .Q(Q20), .reset(RST), .preset(RST));  // open: Qn
  T_Flip_Flop DH3 (.T(HM3_out), .clk(CLK_out), .Q(Q21), .reset(RST), .preset(RST));  // open: Qn
  T_Flip_Flop DH4 (.T(HO4_out), .clk(CLK_out), .Q(Q22), .reset(RST), .preset(RST));  // open: Qn
  and HA1 (HA1_out, Q18, Q19);
  and HA2 (HA2_out, HA1_out, Q20);
  not HN3 (HN3_out, Q21);
  and HA3 (HA3_out, HA2_out, HN3_out);
  and HA4 (HA4_out, HA3_out, Q22);
  and HW (HW_out, D3EC_out, HA4_out);
  not HNW (HNW_out, HW_out);
  and HM1 (HM1_out, Q18, HNW_out);
  or HO1 (HO1_out, HM1_out, HW_out);
  and HR2 (HR2_out, Q18, Q19);
  and HM2 (HM2_out, HR2_out, HNW_out);
  or HO2 (HO2_out, HM2_out, HW_out);
  and HR3 (HR3_out, HR2_out, Q20);
  and HM3 (HM3_out, HR3_out, HNW_out);
  and HR4 (HR4_out, HR3_out, Q21);
  and HM4 (HM4_out, HR4_out, HNW_out);
  or HO4 (HO4_out, HM4_out, HW_out);
endmodule
