// Logisim project divider_1stage.circ as structural Verilog
module divider_1stage (
  input  T,
  input  RST,
  output Q0
);

  wire CLK_out;

  Clock CLK (.out(CLK_out));
  T_Flip_Flop U1 (.T(T), .clk(CLK_out), .Q(Q0), .reset(RST), .preset(RST));  // open: Qn
endmodule
