// Logisim project divider_2stage.circ as structural Verilog
module divider_2stage (
  input  T,
  input  RST,
  output Q0,
  output Q1
);

  wire TQ2;

  Clock CLK (.out(TQ2));
  T_Flip_Flop U1 (.T(T), .clk(TQ2), .Q(Q0), .reset(RST));  // open: Qn, preset
  T_Flip_Flop U2 (.T(Q0), .clk(TQ2), .Q(Q1), .reset(RST));  // open: Qn, preset

  // Other names for the same wires on the sheet: TQ0 = T; TQ1 = Q0; TQ3 = RST; TQ4 = Q1
endmodule
