// Logisim project divider_3stage.circ as structural Verilog
module divider_3stage (
  input  CLK,
  input  T,
  input  RST,
  output Q0,
  output Q1,
  output Q2
);

  wire TQ3;

  T_Flip_Flop U1 (.T(T), .clk(CLK), .Q(Q0), .reset(RST));  // open: Qn, preset
  T_Flip_Flop U2 (.T(Q0), .clk(CLK), .Q(Q1), .reset(RST));  // open: Qn, preset
  T_Flip_Flop U3 (.T(TQ3), .clk(CLK), .Q(Q2), .reset(RST));  // open: Qn, preset
  and TA2_1 (TQ3, Q0, Q1);

  // Other names for the same wires on the sheet: TQ0 = T; TQ1 = Q0; TQ2 = Q1; TQ4 = CLK; TQ5 = RST; TQ6 = Q2
endmodule
