// Logisim project divider_4stage.circ as structural Verilog
module divider_4stage (
  input  T,
  input  RST,
  output Q0,
  output Q1,
  output Q2,
  output Q3
);

  wire TA2_1_out, TA3_1_out, TA3_2_out, TQ2;

  Clock CLK (.out(TQ2));
  T_Flip_Flop U1 (.T(T), .clk(TQ2), .Q(Q0), .reset(RST));  // open: Qn, preset
  T_Flip_Flop U2 (.T(Q0), .clk(TQ2), .Q(Q1), .reset(RST));  // open: Qn, preset
  T_Flip_Flop U3 (.T(TA2_1_out), .clk(TQ2), .Q(Q2), .reset(RST));  // open: Qn, preset
  and TA2_1 (TA2_1_out, Q0, Q1);
  T_Flip_Flop U4 (.T(TA3_2_out), .clk(TQ2), .Q(Q3), .reset(RST));  // open: Qn, preset
  and TA3_1 (TA3_1_out, Q0, Q1);
  and TA3_2 (TA3_2_out, TA3_1_out, Q2);

  // Other names for the same wires on the sheet: TQ0 = T; TQ1 = Q2; TQ3 = RST; TQ4 = Q3; TQ5 = Q0; TQ6 = Q1
endmodule
