// Logisim project divider_4x4.circ as structural Verilog
module divider_4x4 (
  input  A0,
  input  B0,
  input  A1,
  input  B1,
  input  A2,
  input  B2,
  input  A3,
  input  B3,
  input  GND,
  output Q0,
  output R0,
  output Q1,
  output R1,
  output Q2,
  output R2,
  output Q3,
  output R3
);

  wire DV0A_out, DV0B_out, DV0C_out, DV0D_out, DV0N_out, DV0O_out, DV0X_out, DV1A_out, DV1B_out, DV1C_out,
       DV1D_out, DV1N_out, DV1O_out, DV1X_out, DV2A_out, DV2B_out, DV2C_out, DV2D_out, DV2N_out, DV2O_out,
       DV2X_out, DV3A_out, DV3B_out, DV3C_out, DV3D_out, DV3N_out, DV3O_out, DV3X_out, DV4A_out, DV4B_out,
       DV4C_out, DV4N_out, DV4O_out, DV4X_out, DV9A_out, DV9B_out, DV9C_out, DV9D_out, DV9N_out, DV9O_out,
       DV9X_out, DV10A_out, DV10B_out, DV10C_out, DV10D_out, DV10N_out, DV10O_out, DV10X_out, DV11A_out,
       DV11B_out, DV11C_out, DV11D_out, DV11N_out, DV11O_out, DV11X_out, DV12A_out, DV12B_out, DV12C_out,
       DV12D_out, DV12N_out, DV12O_out, DV12X_out, DV13A_out, DV13B_out, DV13C_out, DV13N_out, DV13O_out,
       DV13X_out, DV18A_out, DV18B_out, DV18C_out, DV18D_out, DV18N_out, DV18O_out, DV18X_out, DV19A_out,
       DV19B_out, DV19C_out, DV19D_out, DV19N_out, DV19O_out, DV19X_out, DV20A_out, DV20B_out, DV20C_out,
       DV20D_out, DV20N_out, DV20O_out, DV20X_out, DV21A_out, DV21B_out, DV21C_out, DV21D_out, DV21N_out,
       DV21O_out, DV21X_out, DV22A_out, DV22B_out, DV22C_out, DV22N_out, DV22O_out, DV22X_out, DV27A_out,
       DV27B_out, DV27C_out, DV27D_out, DV27N_out, DV27O_out, DV27X_out, DV28A_out, DV28B_out, DV28C_out,
       DV28D_out, DV28N_out, DV28O_out, DV28X_out, DV29A_out, DV29B_out, DV29C_out, DV29D_out, DV29N_out,
       DV29O_out, DV29X_out, DV30A_out, DV30B_out, DV30C_out, DV30D_out, DV30N_out, DV30O_out, DV30X_out,
       DV31A_out, DV31B_out, DV31C_out, DV31N_out, DV31O_out, DV31X_out, DVM5O_out, DVM6O_out, DVM7O_out,
       DVM8O_out, DVM14O_out, DVM15O_out, DVM16O_out, DVM17O_out, DVM23O_out, DVM24O_out, DVM25O_out,
       DVM26O_out, DVM51_out, DVM52_out, DVM61_out, DVM62_out, DVM71_out, DVM72_out, DVM81_out, DVM82_out,
       DVM141_out, DVM142_out, DVM151_out, DVM152_out, DVM161_out, DVM162_out, DVM171_out, DVM172_out,
       DVM231_out, DVM232_out, DVM241_out, DVM242_out, DVM251_out, DVM252_out, DVM261_out, DVM262_out,
       DVM321_out, DVM322_out, DVM331_out, DVM332_out, DVM341_out, DVM342_out, DVM351_out, DVM352_out;

  xor DV0X (DV0X_out, A3, B0);
  xor DV0D (DV0D_out, DV0X_out, GND);
  not DV0N (DV0N_out, A3);
  or DV0O (DV0O_out, B0, GND);
  and DV0A (DV0A_out, DV0N_out, DV0O_out);
  and DV0B (DV0B_out, B0, GND);
  or DV0C (DV0C_out, DV0A_out, DV0B_out);
  xor DV1X (DV1X_out, GND, B1);
  xor DV1D (DV1D_out, DV1X_out, DV0C_out);
  not DV1N (DV1N_out, GND);
  or DV1O (DV1O_out, B1, DV0C_out);
  and DV1A (DV1A_out, DV1N_out, DV1O_out);
  and DV1B (DV1B_out, B1, DV0C_out);
  or DV1C (DV1C_out, DV1A_out, DV1B_out);
  xor DV2X (DV2X_out, GND, B2);
  xor DV2D (DV2D_out, DV2X_out, DV1C_out);
  not DV2N (DV2N_out, GND);
  or DV2O (DV2O_out, B2, DV1C_out);
  and DV2A (DV2A_out, DV2N_out, DV2O_out);
  and DV2B (DV2B_out, B2, DV1C_out);
  or DV2C (DV2C_out, DV2A_out, DV2B_out);
  xor DV3X (DV3X_out, GND, B3);
  xor DV3D (DV3D_out, DV3X_out, DV2C_out);
  not DV3N (DV3N_out, GND);
  or DV3O (DV3O_out, B3, DV2C_out);
  and DV3A (DV3A_out, DV3N_out, DV3O_out);
  and DV3B (DV3B_out, B3, DV2C_out);
  or DV3C (DV3C_out, DV3A_out, DV3B_out);
  xor DV4X (DV4X_out, GND, GND);
  // XOR_Gate DV4D has open pins: in0=DV4X_out, in1=DV3C_out, out=open
  not DV4N (DV4N_out, GND);
  or DV4O (DV4O_out, GND, DV3C_out);
  and DV4A (DV4A_out, DV4N_out, DV4O_out);
  and DV4B (DV4B_out, GND, DV3C_out);
  or DV4C (DV4C_out, DV4A_out, DV4B_out);
  not DVQ6 (Q3, DV4C_out);
  and DVM51 (DVM51_out, DV0D_out, Q3);
  and DVM52 (DVM52_out, A3, DV4C_out);
  or DVM5O (DVM5O_out, DVM51_out, DVM52_out);
  and DVM61 (DVM61_out, DV1D_out, Q3);
  and DVM62 (DVM62_out, GND, DV4C_out);
  or DVM6O (DVM6O_out, DVM61_out, DVM62_out);
  and DVM71 (DVM71_out, DV2D_out, Q3);
  and DVM72 (DVM72_out, GND, DV4C_out);
  or DVM7O (DVM7O_out, DVM71_out, DVM72_out);
  and DVM81 (DVM81_out, DV3D_out, Q3);
  and DVM82 (DVM82_out, GND, DV4C_out);
  or DVM8O (DVM8O_out, DVM81_out, DVM82_out);
  xor DV9X (DV9X_out, A2, B0);
  xor DV9D (DV9D_out, DV9X_out, GND);
  not DV9N (DV9N_out, A2);
  or DV9O (DV9O_out, B0, GND);
  and DV9A (DV9A_out, DV9N_out, DV9O_out);
  and DV9B (DV9B_out, B0, GND);
  or DV9C (DV9C_out, DV9A_out, DV9B_out);
  xor DV10X (DV10X_out, DVM5O_out, B1);
  xor DV10D (DV10D_out, DV10X_out, DV9C_out);
  not DV10N (DV10N_out, DVM5O_out);
  or DV10O (DV10O_out, B1, DV9C_out);
  and DV10A (DV10A_out, DV10N_out, DV10O_out);
  and DV10B (DV10B_out, B1, DV9C_out);
  or DV10C (DV10C_out, DV10A_out, DV10B_out);
  xor DV11X (DV11X_out, DVM6O_out, B2);
  xor DV11D (DV11D_out, DV11X_out, DV10C_out);
  not DV11N (DV11N_out, DVM6O_out);
  or DV11O (DV11O_out, B2, DV10C_out);
  and DV11A (DV11A_out, DV11N_out, DV11O_out);
  and DV11B (DV11B_out, B2, DV10C_out);
  or DV11C (DV11C_out, DV11A_out, DV11B_out);
  xor DV12X (DV12X_out, DVM7O_out, B3);
  xor DV12D (DV12D_out, DV12X_out, DV11C_out);
  not DV12N (DV12N_out, DVM7O_out);
  or DV12O (DV12O_out, B3, DV11C_out);
  and DV12A (DV12A_out, DV12N_out, DV12O_out);
  and DV12B (DV12B_out, B3, DV11C_out);
  or DV12C (DV12C_out, DV12A_out, DV12B_out);
  xor DV13X (DV13X_out, DVM8O_out, GND);
  // XOR_Gate DV13D has open pins: in0=DV13X_out, in1=DV12C_out, out=open
  not DV13N (DV13N_out, DVM8O_out);
  or DV13O (DV13O_out, GND, DV12C_out);
  and DV13A (DV13A_out, DV13N_out, DV13O_out);
  and DV13B (DV13B_out, GND, DV12C_out);
  or DV13C (DV13C_out, DV13A_out, DV13B_out);
  not DVQ15 (Q2, DV13C_out);
  and DVM141 (DVM141_out, DV9D_out, Q2);
  and DVM142 (DVM142_out, A2, DV13C_out);
  or DVM14O (DVM14O_out, DVM141_out, DVM142_out);
  and DVM151 (DVM151_out, DV10D_out, Q2);
  and DVM152 (DVM152_out, DVM5O_out, DV13C_out);
  or DVM15O (DVM15O_out, DVM151_out, DVM152_out);
  and DVM161 (DVM161_out, DV11D_out, Q2);
  and DVM162 (DVM162_out, DVM6O_out, DV13C_out);
  or DVM16O (DVM16O_out, DVM161_out, DVM162_out);
  and DVM171 (DVM171_out, DV12D_out, Q2);
  and DVM172 (DVM172_out, DVM7O_out, DV13C_out);
  or DVM17O (DVM17O_out, DVM171_out, DVM172_out);
  xor DV18X (DV18X_out, A1, B0);
  xor DV18D (DV18D_out, DV18X_out, GND);
  not DV18N (DV18N_out, A1);
  or DV18O (DV18O_out, B0, GND);
  and DV18A (DV18A_out, DV18N_out, DV18O_out);
  and DV18B (DV18B_out, B0, GND);
  or DV18C (DV18C_out, DV18A_out, DV18B_out);
  xor DV19X (DV19X_out, DVM14O_out, B1);
  xor DV19D (DV19D_out, DV19X_out, DV18C_out);
  not DV19N (DV19N_out, DVM14O_out);
  or DV19O (DV19O_out, B1, DV18C_out);
  and DV19A (DV19A_out, DV19N_out, DV19O_out);
  and DV19B (DV19B_out, B1, DV18C_out);
  or DV19C (DV19C_out, DV19A_out, DV19B_out);
  xor DV20X (DV20X_out, DVM15O_out, B2);
  xor DV20D (DV20D_out, DV20X_out, DV19C_out);
  not DV20N (DV20N_out, DVM15O_out);
  or DV20O (DV20O_out, B2, DV19C_out);
  and DV20A (DV20A_out, DV20N_out, DV20O_out);
  and DV20B (DV20B_out, B2, DV19C_out);
  or DV20C (DV20C_out, DV20A_out, DV20B_out);
  xor DV21X (DV21X_out, DVM16O_out, B3);
  xor DV21D (DV21D_out, DV21X_out, DV20C_out);
  not DV21N (DV21N_out, DVM16O_out);
  or DV21O (DV21O_out, B3, DV20C_out);
  and DV21A (DV21A_out, DV21N_out, DV21O_out);
  and DV21B (DV21B_out, B3, DV20C_out);
  or DV21C (DV21C_out, DV21A_out, DV21B_out);
  xor DV22X (DV22X_out, DVM17O_out, GND);
  // XOR_Gate DV22D has open pins: in0=DV22X_out, in1=DV21C_out, out=open
  not DV22N (DV22N_out, DVM17O_out);
  or DV22O (DV22O_out, GND, DV21C_out);
  and DV22A (DV22A_out, DV22N_out, DV22O_out);
  and DV22B (DV22B_out, GND, DV21C_out);
  or DV22C (DV22C_out, DV22A_out, DV22B_out);
  not DVQ24 (Q1, DV22C_out);
  and DVM231 (DVM231_out, DV18D_out, Q1);
  and DVM232 (DVM232_out, A1, DV22C_out);
  or DVM23O (DVM23O_out, DVM231_out, DVM232_out);
  and DVM241 (DVM241_out, DV19D_out, Q1);
  and DVM242 (DVM242_out, DVM14O_out, DV22C_out);
  or DVM24O (DVM24O_out, DVM241_out, DVM242_out);
  and DVM251 (DVM251_out, DV20D_out, Q1);
  and DVM252 (DVM252_out, DVM15O_out, DV22C_out);
  or DVM25O (DVM25O_out, DVM251_out, DVM252_out);
  and DVM261 (DVM261_out, DV21D_out, Q1);
  and DVM262 (DVM262_out, DVM16O_out, DV22C_out);
  or DVM26O (DVM26O_out, DVM261_out, DVM262_out);
  xor DV27X (DV27X_out, A0, B0);
  xor DV27D (DV27D_out, DV27X_out, GND);
  not DV27N (DV27N_out, A0);
  or DV27O (DV27O_out, B0, GND);
  and DV27A (DV27A_out, DV27N_out, DV27O_out);
  and DV27B (DV27B_out, B0, GND);
  or DV27C (DV27C_out, DV27A_out, DV27B_out);
  xor DV28X (DV28X_out, DVM23O_out, B1);
  xor DV28D (DV28D_out, DV28X_out, DV27C_out);
  not DV28N (DV28N_out, DVM23O_out);
  or DV28O (DV28O_out, B1, DV27C_out);
  and DV28A (DV28A_out, DV28N_out, DV28O_out);
  and DV28B (DV28B_out, B1, DV27C_out);
  or DV28C (DV28C_out, DV28A_out, DV28B_out);
  xor DV29X (DV29X_out, DVM24O_out, B2);
  xor DV29D (DV29D_out, DV29X_out, DV28C_out);
  not DV29N (DV29N_out, DVM24O_out);
  or DV29O (DV29O_out, B2, DV28C_out);
  and DV29A (DV29A_out, DV29N_out, DV29O_out);
  and DV29B (DV29B_out, B2, DV28C_out);
  or DV29C (DV29C_out, DV29A_out, DV29B_out);
  xor DV30X (DV30X_out, DVM25O_out, B3);
  xor DV30D (DV30D_out, DV30X_out, DV29C_out);
  not DV30N (DV30N_out, DVM25O_out);
  or DV30O (DV30O_out, B3, DV29C_out);
  and DV30A (DV30A_out, DV30N_out, DV30O_out);
  and DV30B (DV30B_out, B3, DV29C_out);
  or DV30C (DV30C_out, DV30A_out, DV30B_out);
  xor DV31X (DV31X_out, DVM26O_out, GND);
  // XOR_Gate DV31D has open pins: in0=DV31X_out, in1=DV30C_out, out=open
  not DV31N (DV31N_out, DVM26O_out);
  or DV31O (DV31O_out, GND, DV30C_out);
  and DV31A (DV31A_out, DV31N_out, DV31O_out);
  and DV31B (DV31B_out, GND, DV30C_out);
  or DV31C (DV31C_out, DV31A_out, DV31B_out);
  not DVQ33 (Q0, DV31C_out);
  and DVM321 (DVM321_out, DV27D_out, Q0);
  and DVM322 (DVM322_out, A0, DV31C_out);
  or DVM32O (R0, DVM321_out, DVM322_out);
  and DVM331 (DVM331_out, DV28D_out, Q0);
  and DVM332 (DVM332_out, DVM23O_out, DV31C_out);
  or DVM33O (R1, DVM331_out, DVM332_out);
  and DVM341 (DVM341_out, DV29D_out, Q0);
  and DVM342 (DVM342_out, DVM24O_out, DV31C_out);
  or DVM34O (R2, DVM341_out, DVM342_out);
  and DVM351 (DVM351_out, DV30D_out, Q0);
  and DVM352 (DVM352_out, DVM25O_out, DV31C_out);
  or DVM35O (R3, DVM351_out, DVM352_out);
endmodule
