// Logisim project dlatch.circ as structural Verilog
module dlatch (
  input  D,
  input  EN,
  output Q,
  output nQ
);

  wire TQ1, TQ3, TQ4;

  not DN (TQ1, D);
  nand U1 (TQ3, EN, D);
  nand U2 (TQ4, EN, TQ1);
  nand U3 (Q, TQ3, nQ);
  nand U4 (nQ, TQ4, Q);

  // Other names for the same wires on the sheet: TQ0 = D; TQ2 = EN; TQ5 = Q; TQ6 = nQ
endmodule
