// Logisim project dryer_controller.circ as structural Verilog
module dryer_controller (
  input  RST,
  input  START,
  input  TMR,
  output HEAT,
  output TUMBLE,
  output DONE
);

  wire A13_out, A14_out, A15_out, AH0_out, AH1_out, NC0_out, NC1_out, O16_out, O17_out, O19_out, O20_out,
       TQ1, TQ3, TQ4, TQ6, TQ7, TQ8, TQ9, TQa, TQc, TQd, TQe, TQf, TQg, TQh, TQi, TQj, TQk, TQl, TQn;

  Clock CLK (.out(TQ1));
  D_Flip_Flop U1 (.D(TQg), .clk(TQ1), .Q(TQf), .reset(RST));  // open: Qn, preset
  D_Flip_Flop U2 (.D(TQl), .clk(TQ1), .Q(TQk), .reset(RST));  // open: Qn, preset
  not N1 (TQ9, TQf);
  not N2 (TQ6, TQk);
  not NIstart (TQe, START);
  not NItmr (TQd, TMR);
  // AND_Gate M0 has open pins: in0=TQ9, in1=TQ6, out=open
  and A1 (TQ3, TQ9, TQ6);
  and A2 (TQ4, TQ3, TQd);
  and A3 (TQj, TQ4, START);
  and M4 (HEAT, TQf, TQ6);
  and A5 (TQ7, TQf, TQ6);
  and A6 (TQ8, TQ7, TMR);
  and A7 (TQh, TQ8, TQe);
  and M8 (TQn, TQ9, TQk);
  and A9 (TQa, TQ9, TQk);
  and A10 (TQc, TQa, TMR);
  and A11 (TQi, TQc, TQe);
  and M12 (DONE, TQf, TQk);
  and A13 (A13_out, TQf, TQk);
  and A14 (A14_out, A13_out, TQd);
  and A15 (A15_out, A14_out, TQe);
  or O16 (O16_out, TQj, TQi);
  or O17 (O17_out, TQh, A15_out);
  not NC0 (NC0_out, O17_out);
  and AH0 (AH0_out, TQf, NC0_out);
  or O18 (TQg, O16_out, AH0_out);
  or O19 (O19_out, TQh, TQi);
  or O20 (O20_out, TQj, A15_out);
  not NC1 (NC1_out, O20_out);
  and AH1 (AH1_out, TQk, NC1_out);
  or O21 (TQl, O19_out, AH1_out);
  or Ofo22 (TUMBLE, HEAT, TQn);

  // Other names for the same wires on the sheet: TQ0 = DONE; TQ2 = RST; TQ5 = START; TQb = TMR; TQm = HEAT;
  //   TQo = TUMBLE
endmodule
