// Logisim project edge_detector.circ as structural Verilog
module edge_detector (
  input  CLK,
  input  IN,
  input  RST,
  output RISE,
  output FALL
);

  wire TQ3, TQ4, TQ5;

  D_Flip_Flop U1 (.D(IN), .clk(CLK), .Q(TQ4), .reset(RST));  // open: Qn, preset
  not N1 (TQ3, TQ4);
  not N2 (TQ5, IN);
  and A1 (RISE, IN, TQ3);
  and A2 (FALL, TQ4, TQ5);

  // Other names for the same wires on the sheet: TQ0 = CLK; TQ1 = RST; TQ2 = IN; TQ6 = RISE; TQ7 = FALL
endmodule
