// Logisim project elevator_controller.circ as structural Verilog
module elevator_controller (
  input  RST,
  input  UP,
  input  DN,
  output D1,
  output D2
);

  wire A47_out, A49_out, A50_out, O52_out, O53_out, O55_out, O56_out, O57_out, O58_out, O59_out, O60_out,
       TQ0, TQ1, TQ1a, TQ1b, TQ1c, TQ1d, TQ1e, TQ1f, TQ1g, TQ2, TQ4, TQ5, TQ8, TQ9, TQ10, TQ11, TQ12, TQ13,
       TQ14, TQ15, TQ16, TQ19, TQa, TQb, TQc, TQd, TQe, TQf, TQg, TQh, TQi, TQj, TQk, TQl, TQm, TQn, TQo,
       TQp, TQq, TQr, TQs, TQt, TQu, TQv, TQw, TQx, TQy, TQz;

  Clock CLK (.out(TQ2));
  D_Flip_Flop U1 (.D(TQ1b), .clk(TQ2), .Q(TQ15), .reset(RST));  // open: Qn, preset
  D_Flip_Flop U2 (.D(TQ5), .clk(TQ2), .Q(TQ16), .reset(RST));  // open: Qn, preset
  not N1 (TQv, TQ15);
  not N2 (TQm, TQ16);
  not NIup (TQ14, UP);
  not NIdn (TQ11, DN);
  and M0 (D1, TQv, TQm);
  and A1 (TQ8, TQv, TQm);
  and A2 (TQ9, TQ8, TQ11);
  // AND_Gate A3 has open pins: in0=TQ9, in1=TQ14, out=open
  and A4 (TQa, TQv, TQm);
  and A5 (TQb, TQa, TQ11);
  and A6 (TQ19, TQb, UP);
  and A7 (TQc, TQv, TQm);
  and A8 (TQd, TQc, DN);
  // AND_Gate A9 has open pins: in0=TQd, in1=TQ14, out=open
  and A10 (TQe, TQv, TQm);
  and A11 (TQf, TQe, DN);
  and A12 (TQ1a, TQf, UP);
  // AND_Gate M13 has open pins: in0=TQ15, in1=TQm, out=open
  and A14 (TQg, TQ15, TQm);
  and A15 (TQh, TQg, TQ11);
  and A16 (TQ1c, TQh, TQ14);
  and A17 (TQi, TQ15, TQm);
  and A18 (TQj, TQi, TQ11);
  and A19 (TQ1d, TQj, UP);
  and A20 (TQk, TQ15, TQm);
  and A21 (TQl, TQk, DN);
  and A22 (TQ1e, TQl, TQ14);
  and A23 (TQn, TQ15, TQm);
  and A24 (TQo, TQn, DN);
  and A25 (TQ1f, TQo, UP);
  and M26 (D2, TQv, TQ16);
  and A27 (TQp, TQv, TQ16);
  and A28 (TQq, TQp, TQ11);
  and A29 (TQ1g, TQq, TQ14);
  and A30 (TQr, TQv, TQ16);
  and A31 (TQs, TQr, TQ11);
  and A32 (TQ0, TQs, UP);
  and A33 (TQt, TQv, TQ16);
  and A34 (TQu, TQt, DN);
  and A35 (TQ1, TQu, TQ14);
  and A36 (TQw, TQv, TQ16);
  and A37 (TQx, TQw, DN);
  and A38 (TQ4, TQx, UP);
  // AND_Gate M39 has open pins: in0=TQ15, in1=TQ16, out=open
  and A40 (TQy, TQ15, TQ16);
  and A41 (TQz, TQy, TQ11);
  // AND_Gate A42 has open pins: in0=TQz, in1=TQ14, out=open
  and A43 (TQ10, TQ15, TQ16);
  and A44 (TQ12, TQ10, TQ11);
  // AND_Gate A45 has open pins: in0=TQ12, in1=UP, out=open
  and A46 (TQ13, TQ15, TQ16);
  and A47 (A47_out, TQ13, DN);
  // AND_Gate A48 has open pins: in0=A47_out, in1=TQ14, out=open
  and A49 (A49_out, TQ15, TQ16);
  and A50 (A50_out, A49_out, DN);
  // AND_Gate A51 has open pins: in0=A50_out, in1=UP, out=open
  or O52 (O52_out, TQ19, TQ1a);
  or O53 (O53_out, O52_out, TQ1);
  or O54 (TQ1b, O53_out, TQ4);
  or O55 (O55_out, TQ1c, TQ1d);
  or O56 (O56_out, O55_out, TQ1e);
  or O57 (O57_out, O56_out, TQ1f);
  or O58 (O58_out, O57_out, TQ1g);
  or O59 (O59_out, O58_out, TQ0);
  or O60 (O60_out, O59_out, TQ1);
  or O61 (TQ5, O60_out, TQ4);

  // Other names for the same wires on the sheet: TQ3 = RST; TQ6 = D1; TQ7 = D2; TQ17 = DN; TQ18 = UP
endmodule
