// Logisim project encoder_16to4.circ as structural Verilog
module encoder_16to4 (
  input  I0,
  input  I1,
  input  I2,
  input  I3,
  input  I4,
  input  I5,
  input  I6,
  input  I7,
  input  I8,
  input  I9,
  input  I10,
  input  I11,
  input  I12,
  input  I13,
  input  I14,
  input  I15,
  input  EN,
  output Y0,
  output Y1,
  output Y2,
  output Y3,
  output GS
);

  wire TQh, TQi, TQj, TQk, TQl, TQn, TQo, TQq, TQr, TQs, TQv, U4B_out, U4C_out, U5A_out, U5B_out, U5C_out,
       U6A_out, U6B_out, U6C_out, U6D_out, U7A_out, U7B_out;

  _74148 U1 (
    .pin1(I0), .pin2(I1), .pin3(I2), .pin4(I3), .pin5(I4), .pin6(I5), .pin7(I6), .pin15(TQr), .pin14(TQo),
    .pin13(TQl), .pin11(TQi), .pin10(TQh), .pin9(I7));  // open: pin12
  _74148 U2 (
    .pin1(I8), .pin2(I9), .pin3(I10), .pin4(I11), .pin5(I12), .pin6(I13), .pin7(I14), .pin15(TQq),
    .pin14(TQn), .pin13(TQk), .pin12(TQh), .pin11(TQj), .pin10(EN), .pin9(I15));
  not U3A (Y3, TQj);
  not U3B (TQv, TQi);
  not U4A (TQs, TQq);
  not U4B (U4B_out, TQn);
  not U4C (U4C_out, TQk);
  not U5A (U5A_out, TQr);
  not U5B (U5B_out, TQo);
  not U5C (U5C_out, TQl);
  and U6A (U6A_out, TQs, Y3);
  and U6B (U6B_out, U4B_out, Y3);
  and U6C (U6C_out, U4C_out, Y3);
  and U6D (U6D_out, U5A_out, TQj);
  and U7A (U7A_out, U5B_out, TQj);
  and U7B (U7B_out, U5C_out, TQj);
  or U8A (Y2, U6A_out, U6D_out);
  or U8B (Y1, U6B_out, U7A_out);
  or U8C (Y0, U6C_out, U7B_out);
  or U8D (GS, Y3, TQv);

  // Other names for the same wires on the sheet: TQ0 = I0; TQ1 = I8; TQ2 = I1; TQ3 = I9; TQ4 = I2; TQ5 = I10;
  //   TQ6 = I3; TQ7 = I11; TQ8 = I4; TQ9 = I12; TQa = I5; TQb = I13; TQc = I6; TQd = I14; TQe = I7; TQf = I15;
  //   TQg = EN; TQm = Y0; TQp = Y1; TQt = Y2; TQu = Y3; TQw = GS
endmodule
