// Logisim project encoder_4to2.circ as structural Verilog
module encoder_4to2 (
  input  I2,
  input  I3,
  input  I1,
  input  I0,
  output Y1,
  output Y0,
  output G
);

  wire enc4_g_o2_out, enc4_n2_out, enc4_p0_out;

  or enc4_g_o1 (Y1, I2, I3);
  or enc4_g_o2 (enc4_g_o2_out, Y1, I1);
  or enc4_g_o3 (G, enc4_g_o2_out, I0);
  not enc4_n2 (enc4_n2_out, I2);
  and enc4_p0 (enc4_p0_out, I1, enc4_n2_out);
  or enc4_y0_o1 (Y0, I3, enc4_p0_out);

  // Other names for the same wires on the sheet: TQ0 = I0; TQ1 = I2; TQ2 = I1; TQ3 = I3; TQ4 = Y1; TQ5 = Y0; TQ6 = G
endmodule
