// Logisim project encoder_8to3.circ as structural Verilog
module encoder_8to3 (
  input  I6,
  input  I7,
  input  I5,
  input  I4,
  input  I3,
  input  I2,
  input  I1,
  input  I0,
  output Y2,
  output Y1,
  output Y0,
  output G
);

  wire enc_g_o1_out, enc_g_o2_out, enc_g_o3_out, enc_g_o4_out, enc_g_o5_out, enc_g_o6_out, enc_n2_out,
       enc_n3_out, enc_n6_out, enc_n23_out, enc_n45_out, enc_r23_o1_out, enc_r45_o1_out, enc_r67_o1_out,
       enc_t1a_out, enc_t1b_out, enc_t1c_out, enc_t3a_out, enc_t3b_out, enc_t5_out, enc_y0a_o1_out,
       enc_y0b_o1_out, enc_y1a_out, enc_y2_o1_out, enc_y2_o2_out;

  or enc_g_o1 (enc_g_o1_out, I6, I7);
  or enc_g_o2 (enc_g_o2_out, enc_g_o1_out, I5);
  or enc_g_o3 (enc_g_o3_out, enc_g_o2_out, I4);
  or enc_g_o4 (enc_g_o4_out, enc_g_o3_out, I3);
  or enc_g_o5 (enc_g_o5_out, enc_g_o4_out, I2);
  or enc_g_o6 (enc_g_o6_out, enc_g_o5_out, I1);
  or enc_g_o7 (G, enc_g_o6_out, I0);
  or enc_y2_o1 (enc_y2_o1_out, I4, I5);
  or enc_y2_o2 (enc_y2_o2_out, enc_y2_o1_out, I6);
  or enc_y2_o3 (Y2, enc_y2_o2_out, I7);
  or enc_r67_o1 (enc_r67_o1_out, I6, I7);
  or enc_r45_o1 (enc_r45_o1_out, I4, I5);
  not enc_n45 (enc_n45_out, enc_r45_o1_out);
  or enc_r23_o1 (enc_r23_o1_out, I3, I2);
  and enc_y1a (enc_y1a_out, enc_n45_out, enc_r23_o1_out);
  or enc_y1_o1 (Y1, enc_r67_o1_out, enc_y1a_out);
  not enc_n6 (enc_n6_out, I6);
  and enc_t5 (enc_t5_out, enc_n6_out, I5);
  and enc_t3a (enc_t3a_out, enc_n45_out, enc_n6_out);
  and enc_t3b (enc_t3b_out, enc_t3a_out, I3);
  not enc_n2 (enc_n2_out, I2);
  not enc_n3 (enc_n3_out, I3);
  and enc_n23 (enc_n23_out, enc_n2_out, enc_n3_out);
  and enc_t1a (enc_t1a_out, enc_n23_out, enc_n45_out);
  and enc_t1b (enc_t1b_out, enc_t1a_out, enc_n6_out);
  and enc_t1c (enc_t1c_out, enc_t1b_out, I1);
  or enc_y0a_o1 (enc_y0a_o1_out, I7, enc_t5_out);
  or enc_y0b_o1 (enc_y0b_o1_out, enc_y0a_o1_out, enc_t3b_out);
  or enc_y0c_o1 (Y0, enc_y0b_o1_out, enc_t1c_out);
endmodule
