// Logisim project excess3_adder.circ as structural Verilog
module excess3_adder (
  input  A0,
  input  B0,
  input  A1,
  input  B1,
  input  A2,
  input  B2,
  input  A3,
  input  B3,
  input  ONE,
  input  GND,
  output S0,
  output S1,
  output S2,
  output S3,
  output Cout
);

  wire E3A27_out, E3A28_out, E3B27_out, E3B28_out, E3G26_out, E3G27_out, E3O26_out, E3O27_out, E3O28_out,
       E3X27_out, E3X28_out, TQ2, TQ3, TQ4, TQ5, TQ8, TQ9, TQ10, TQ11, TQ12, TQ13, TQ14, TQa, TQb, TQc, TQf,
       TQg, TQh, TQi, TQj, TQm, TQn, TQo, TQp, TQq, TQr, TQt, TQu, TQv, TQw, TQx, TQy, TQz;

  xor E3X1 (TQ2, A0, B0);
  xor E3S1 (TQr, TQ2, GND);
  and E3A1 (TQ3, A0, B0);
  and E3B1 (TQ4, GND, TQ2);
  or E3O1 (TQ5, TQ3, TQ4);
  or E3G1 (TQ8, TQ5, GND);
  xor E3X2 (TQ9, A1, B1);
  xor E3S2 (TQx, TQ9, TQ8);
  and E3A2 (TQa, A1, B1);
  and E3B2 (TQb, TQ8, TQ9);
  or E3O2 (TQc, TQa, TQb);
  or E3G2 (TQf, TQc, GND);
  xor E3X3 (TQg, A2, B2);
  xor E3S3 (TQ12, TQg, TQf);
  and E3A3 (TQh, A2, B2);
  and E3B3 (TQi, TQf, TQg);
  or E3O3 (TQj, TQh, TQi);
  or E3G3 (TQm, TQj, GND);
  xor E3X4 (TQn, A3, B3);
  xor E3S4 (TQ13, TQn, TQm);
  and E3A4 (TQo, A3, B3);
  and E3B4 (TQp, TQm, TQn);
  or E3O4 (TQq, TQo, TQp);
  or E3G4 (Cout, TQq, GND);
  not E3N1 (TQ14, Cout);
  xor E3X25 (TQt, TQr, ONE);
  xor E3S25 (S0, TQt, GND);
  and E3A25 (TQu, TQr, ONE);
  and E3B25 (TQv, GND, TQt);
  or E3O25 (TQw, TQu, TQv);
  or E3G25 (TQy, TQw, GND);
  xor E3X26 (TQz, TQx, Cout);
  xor E3S26 (S1, TQz, TQy);
  and E3A26 (TQ10, TQx, Cout);
  and E3B26 (TQ11, TQy, TQz);
  or E3O26 (E3O26_out, TQ10, TQ11);
  or E3G26 (E3G26_out, E3O26_out, GND);
  xor E3X27 (E3X27_out, TQ12, TQ14);
  xor E3S27 (S2, E3X27_out, E3G26_out);
  and E3A27 (E3A27_out, TQ12, TQ14);
  and E3B27 (E3B27_out, E3G26_out, E3X27_out);
  or E3O27 (E3O27_out, E3A27_out, E3B27_out);
  or E3G27 (E3G27_out, E3O27_out, GND);
  xor E3X28 (E3X28_out, TQ13, TQ14);
  xor E3S28 (S3, E3X28_out, E3G27_out);
  and E3A28 (E3A28_out, TQ13, TQ14);
  and E3B28 (E3B28_out, E3G27_out, E3X28_out);
  or E3O28 (E3O28_out, E3A28_out, E3B28_out);
  // OR_Gate E3G28 has open pins: in0=E3O28_out, in1=GND, out=open

  // Other names for the same wires on the sheet: TQ0 = A0; TQ1 = B0; TQ1a = Cout; TQ6 = A1; TQ7 = B1; TQ15 = GND;
  //   TQ16 = S0; TQ17 = S1; TQ18 = S2; TQ19 = S3; TQd = A2; TQe = B2; TQk = A3; TQl = B3; TQs = ONE
endmodule
