// Logisim project excess3_bcd.circ as structural Verilog
module excess3_bcd (
  input  D1,
  input  D2,
  input  D4,
  input  D8,
  output E1,
  output E2,
  output E4,
  output E8
);

  wire TQ0, TQ7, TQ9;

  xor U1 (TQ0, D2, D1);
  not U2 (E2, TQ0);
  not U3 (E1, D1);
  or U4 (TQ7, D2, D1);
  xor U5 (E4, D4, TQ7);
  and U6 (TQ9, D4, TQ7);
  xor U7 (E8, D8, TQ9);

  // Other names for the same wires on the sheet: TQ1 = E2; TQ2 = E1; TQ3 = D2; TQ4 = D1; TQ5 = E4; TQ6 = D4; TQ8 = D8;
  //   TQa = E8
endmodule
