// Logisim project excess3tobcd.circ as structural Verilog
module excess3tobcd (
  input  E1,
  input  E2,
  input  E4,
  input  E8,
  output D1,
  output D2,
  output D4,
  output D8
);

  wire A1_out, A2_out, N2_out, N3_out;

  not N1 (D1, E1);
  xor X1 (D2, E2, E1);
  and A1 (A1_out, E2, E1);
  not N2 (N2_out, A1_out);
  not N3 (N3_out, E4);
  xor X2 (D4, E4, N2_out);
  and A2 (A2_out, N3_out, N2_out);
  xor X3 (D8, E8, A2_out);

  // Other names for the same wires on the sheet: TQ0 = D8; TQ1 = D1; TQ2 = D2; TQ3 = E2; TQ4 = E1; TQ5 = E4; TQ6 = D4;
  //   TQ7 = E8
endmodule
