// Logisim project flash_adc_3bit.circ as structural Verilog
module flash_adc_3bit (
  input  V6,
  input  V7,
  input  V5,
  input  V4,
  input  V3,
  input  V2,
  input  V1,
  input  V0,
  output D2,
  output D1,
  output D0,
  output GS
);

  wire TQ0, TQ1, TQ2, TQ3, TQ4, TQ5, TQ7, TQ8, TQa, TQb, TQc, TQd, TQg, TQj, TQk, TQl, TQm, TQn, TQo, TQp,
       TQs, TQt, TQu, TQv, TQw;

  or enc_g_o1 (TQ0, V6, V7);
  not enc_n45 (TQm, TQa);
  and enc_t1b (TQp, TQn, TQo);
  or enc_g_o2 (TQ1, TQ0, V5);
  or enc_r23_o1 (TQb, V3, V2);
  and enc_t1c (TQw, TQp, V1);
  and enc_y1a (TQd, TQm, TQb);
  or enc_g_o3 (TQ2, TQ1, V4);
  or enc_y0a_o1 (TQt, V7, TQs);
  or enc_g_o4 (TQ3, TQ2, V3);
  or enc_y1_o1 (D1, TQc, TQd);
  or enc_y0b_o1 (TQv, TQt, TQu);
  not enc_n6 (TQo, V6);
  or enc_g_o5 (TQ4, TQ3, V2);
  or enc_y0c_o1 (D0, TQv, TQw);
  or enc_g_o6 (TQ5, TQ4, V1);
  and enc_t5 (TQs, TQo, V5);
  and enc_t3a (TQg, TQm, TQo);
  or enc_g_o7 (GS, TQ5, V0);
  or enc_y2_o1 (TQ7, V4, V5);
  and enc_t3b (TQu, TQg, V3);
  not enc_n2 (TQj, V2);
  or enc_y2_o2 (TQ8, TQ7, V6);
  not enc_n3 (TQk, V3);
  or enc_y2_o3 (D2, TQ8, V7);
  and enc_n23 (TQl, TQj, TQk);
  or enc_r67_o1 (TQc, V6, V7);
  and enc_t1a (TQn, TQl, TQm);
  or enc_r45_o1 (TQa, V4, V5);

  // Other names for the same wires on the sheet: TQ6 = V0; TQ9 = V4; TQ10 = GS; TQe = V6; TQf = V5; TQh = V2;
  //   TQi = V3; TQq = V1; TQr = V7; TQx = D2; TQy = D1; TQz = D0
endmodule
