// Logisim project freq_meter.circ as structural Verilog
module freq_meter (
  input  SIG,
  input  RST,
  output F0,
  output F1,
  output F2,
  output F3,
  output WIN
);

  wire CLK_out, FCC0_q, FCC1_q, FCC2_q, FCC3_q, FCN0_out, FCN1_out, FCN2_out, FCW0_out, FCW1_out, FCW2_out,
       FCW3_out, FCX0_out, FCX1_out, FCX2_out, FCX3_out, FEN_out, FLA0_out, FLA1_out, FLA2_out, FLA3_out,
       FLB0_out, FLB1_out, FLB2_out, FLB3_out, FLN_out, FLR0_out, FLR1_out, FLR2_out, FLR3_out, FNL_out,
       FNW_out, FRIS_out, FSP_q, FSPN_out, FW1_out, FW2_out, FWC0_q, FWC1_q, FWC2_q, FWN_out, FWND_q,
       FWNX_out, FWX1_out, FWX2_out;

  Clock CLK (.out(CLK_out));
  and FW1 (FW1_out, FWC0_q, FWC1_q);
  and FW2 (FW2_out, FW1_out, FWC2_q);
  D_Flip_Flop FWC0 (.D(FWN_out), .clk(CLK_out), .Q(FWC0_q), .preset(RST), .reset(RST));  // open: Qn
  D_Flip_Flop FWC1 (.D(FWX1_out), .clk(CLK_out), .Q(FWC1_q), .preset(RST), .reset(RST));  // open: Qn
  D_Flip_Flop FWC2 (.D(FWX2_out), .clk(CLK_out), .Q(FWC2_q), .preset(RST), .reset(RST));  // open: Qn
  not FWN (FWN_out, FWC0_q);
  xor FWX1 (FWX1_out, FWC1_q, FWC0_q);
  xor FWX2 (FWX2_out, FWC2_q, FW1_out);
  D_Flip_Flop FWIN (.D(FWNX_out), .clk(CLK_out), .Q(WIN), .preset(RST), .reset(RST));  // open: Qn
  xor FWNX (FWNX_out, WIN, FW2_out);
  D_Flip_Flop FWND (.D(WIN), .clk(CLK_out), .Q(FWND_q), .preset(RST), .reset(RST));  // open: Qn
  D_Flip_Flop FSP (.D(SIG), .clk(CLK_out), .Q(FSP_q), .preset(RST), .reset(RST));  // open: Qn
  not FSPN (FSPN_out, FSP_q);
  and FRIS (FRIS_out, SIG, FSPN_out);
  and FEN (FEN_out, WIN, FRIS_out);
  D_Flip_Flop FCC0 (.D(FCW0_out), .clk(CLK_out), .Q(FCC0_q), .preset(RST), .reset(RST));  // open: Qn
  xor FCX0 (FCX0_out, FCC0_q, FEN_out);
  and FCW0 (FCW0_out, WIN, FCX0_out);
  and FCN0 (FCN0_out, FEN_out, FCC0_q);
  D_Flip_Flop FCC1 (.D(FCW1_out), .clk(CLK_out), .Q(FCC1_q), .preset(RST), .reset(RST));  // open: Qn
  xor FCX1 (FCX1_out, FCC1_q, FCN0_out);
  and FCW1 (FCW1_out, WIN, FCX1_out);
  and FCN1 (FCN1_out, FCN0_out, FCC1_q);
  D_Flip_Flop FCC2 (.D(FCW2_out), .clk(CLK_out), .Q(FCC2_q), .preset(RST), .reset(RST));  // open: Qn
  xor FCX2 (FCX2_out, FCC2_q, FCN1_out);
  and FCW2 (FCW2_out, WIN, FCX2_out);
  and FCN2 (FCN2_out, FCN1_out, FCC2_q);
  D_Flip_Flop FCC3 (.D(FCW3_out), .clk(CLK_out), .Q(FCC3_q), .preset(RST), .reset(RST));  // open: Qn
  xor FCX3 (FCX3_out, FCC3_q, FCN2_out);
  and FCW3 (FCW3_out, WIN, FCX3_out);
  not FNW (FNW_out, WIN);
  and FLN (FLN_out, FNW_out, FWND_q);
  not FNL (FNL_out, FLN_out);
  D_Flip_Flop FLO0 (.D(FLR0_out), .clk(CLK_out), .Q(F0), .preset(RST), .reset(RST));  // open: Qn
  and FLA0 (FLA0_out, FLN_out, FCC0_q);
  and FLB0 (FLB0_out, FNL_out, F0);
  or FLR0 (FLR0_out, FLA0_out, FLB0_out);
  D_Flip_Flop FLO1 (.D(FLR1_out), .clk(CLK_out), .Q(F1), .preset(RST), .reset(RST));  // open: Qn
  and FLA1 (FLA1_out, FLN_out, FCC1_q);
  and FLB1 (FLB1_out, FNL_out, F1);
  or FLR1 (FLR1_out, FLA1_out, FLB1_out);
  D_Flip_Flop FLO2 (.D(FLR2_out), .clk(CLK_out), .Q(F2), .preset(RST), .reset(RST));  // open: Qn
  and FLA2 (FLA2_out, FLN_out, FCC2_q);
  and FLB2 (FLB2_out, FNL_out, F2);
  or FLR2 (FLR2_out, FLA2_out, FLB2_out);
  D_Flip_Flop FLO3 (.D(FLR3_out), .clk(CLK_out), .Q(F3), .preset(RST), .reset(RST));  // open: Qn
  and FLA3 (FLA3_out, FLN_out, FCC3_q);
  and FLB3 (FLB3_out, FNL_out, F3);
  or FLR3 (FLR3_out, FLA3_out, FLB3_out);
endmodule
