// Logisim project from_json_full_adder.circ as structural Verilog
module full_adder (
  input  A,
  input  B,
  input  Cin,
  output SUM,
  output Cout
);

  wire net_a_b_carry, net_ab_carry, net_ab_xor;

  xor xor_1 (net_ab_xor, A, B);
  and and_1 (net_a_b_carry, A, B);
  xor xor_2 (Cout, net_ab_xor, B);
  and and_2 (net_ab_carry, net_ab_xor, B);
  or or_1 (Cout, net_ab_carry, net_a_b_carry);

  assign Cin = B;
  assign SUM = Cout;

  // Other names for the same wires on the sheet: net_a = A; net_b = B; net_cin = B; net_cout = Cout; net_sum = Cout
endmodule
