// Logisim project from_json_mux_4to1.circ as structural Verilog
module mux_4to1 (
  input  D0,
  input  S0,
  input  D1,
  input  S1,
  input  D2,
  input  D3,
  output Y
);

  wire n7, n8, n9, n10, n11, n12, n13, n14, n15, n16, n17, n18;

  not not_1 (n7, S0);
  not not_2 (n8, S1);
  and and_1 (n9, D0, n8);
  and and_2 (n11, D1, n8);
  and and_3 (n13, D2, S1);
  and and_4 (n15, D3, S1);
  and and_5 (n10, n9, n7);
  and and_6 (n12, n11, S0);
  and and_7 (n14, n13, n7);
  and and_8 (n16, n15, S0);
  or or_1 (n17, n10, n12);
  or or_2 (n18, n14, n16);
  or or_3 (Y, n17, n18);

  // Other names for the same wires on the sheet: n1 = D0; n2 = D1; n3 = D2; n4 = D3; n5 = S0; n6 = S1; n19 = Y
endmodule
