// Logisim project from_json_nand_xor3.circ as structural Verilog
module nand_xor3 (
  input  A,
  input  B,
  input  C,
  output Y
);

  wire n1_out, n2_out, n3_out, n4_out, n5_out, n6_out, xab_out;

  nand nand_1 (n1_out, A, B);
  nand nand_2 (n2_out, A, n1_out);
  nand nand_3 (n3_out, B, n1_out);
  nand nand_4 (xab_out, n2_out, n3_out);
  nand nand_5 (n4_out, xab_out, C);
  nand nand_6 (n5_out, xab_out, n4_out);
  nand nand_7 (n6_out, C, n4_out);
  nand nand_8 (Y, n5_out, n6_out);
endmodule
