// Logisim project fsmseq101.circ as structural Verilog
module fsmseq101 (
  input  CLK,
  input  RST,
  input  X,
  output F
);

  wire TQ2, TQ3, TQ4, TQ5, TQ6, TQ7, TQ8, TQ9, TQa, TQb, TQc, TQd, TQe, TQg, TQh, TQi, TQj, TQk, TQl, TQm,
       TQn, TQo, TQp, TQq;

  D_Flip_Flop U1 (.D(TQl), .clk(CLK), .Q(TQc), .reset(RST));  // open: Qn, preset
  and A7 (TQm, TQ4, TQb);
  and A19 (TQj, TQe, X);
  and A8 (TQ6, TQc, TQ5);
  or O20 (TQi, TQg, TQh);
  D_Flip_Flop U2 (.D(TQq), .clk(CLK), .Q(TQd), .reset(RST));  // open: Qn, preset
  and A9 (TQh, TQ6, X);
  or O21 (TQk, TQi, TQj);
  not N1 (TQ8, TQc);
  // AND_Gate M10 has open pins: in0=TQ8, in1=TQd, out=open
  or O22 (TQl, TQk, TQp);
  not N2 (TQ5, TQd);
  not NIx (TQb, X);
  and A11 (TQ7, TQ8, TQd);
  or O23 (TQo, TQm, TQn);
  // AND_Gate M0 has open pins: in0=TQ8, in1=TQ5, out=open
  // AND_Gate A12 has open pins: in0=TQ7, in1=TQb, out=open
  or O24 (TQq, TQo, TQp);
  and A1 (TQ2, TQ8, TQ5);
  and A13 (TQ9, TQ8, TQd);
  // AND_Gate A2 has open pins: in0=TQ2, in1=TQb, out=open
  and A14 (TQp, TQ9, X);
  and A3 (TQ3, TQ8, TQ5);
  and M15 (F, TQc, TQd);
  and A4 (TQg, TQ3, X);
  and A16 (TQa, TQc, TQd);
  // AND_Gate M5 has open pins: in0=TQc, in1=TQ5, out=open
  and A17 (TQn, TQa, TQb);
  and A6 (TQ4, TQc, TQ5);
  and A18 (TQe, TQc, TQd);

  // Other names for the same wires on the sheet: TQ0 = CLK; TQ1 = RST; TQf = X; TQr = F
endmodule
