// Logisim project full_adder.circ as structural Verilog
module full_adder (
  input  A,
  input  B,
  input  Cin,
  output SUM,
  output Cout
);

  wire and_1_out, and_2_out;

  xor xor_1 (A, A, B);
  and and_1 (and_1_out, A, B);
  xor xor_2 (Cout, A, A);
  and and_2 (and_2_out, A, A);
  or or_1 (Cout, and_1_out, and_2_out);

  assign Cin = A;
  assign SUM = Cout;
endmodule
