// Logisim project generic_fsm.circ as structural Verilog
module generic_fsm (
  input  RST,
  input  A,
  input  B,
  output Z
);

  wire O53_out, O54_out, O55_out, O56_out, O57_out, O59_out, O60_out, O61_out, O62_out, O63_out, O64_out,
       TQ0, TQ1, TQ1a, TQ1b, TQ1c, TQ1d, TQ1f, TQ1h, TQ1i, TQ1j, TQ1k, TQ1l, TQ1m, TQ1n, TQ2, TQ4, TQ5, TQ6,
       TQ7, TQ8, TQ9, TQ10, TQ11, TQ12, TQ13, TQ14, TQ15, TQ16, TQ17, TQ18, TQ19, TQa, TQb, TQc, TQd, TQf,
       TQg, TQh, TQi, TQj, TQk, TQl, TQm, TQn, TQo, TQp, TQq, TQr, TQs, TQt, TQu, TQv, TQw, TQx, TQy, TQz;

  Clock CLK (.out(TQ2));
  D_Flip_Flop U1 (.D(TQ1m), .clk(TQ2), .Q(TQ1b), .reset(RST));  // open: Qn, preset
  D_Flip_Flop U2 (.D(TQa), .clk(TQ2), .Q(TQ1c), .reset(RST));  // open: Qn, preset
  not N1 (TQ10, TQ1b);
  not N2 (TQr, TQ1c);
  not NIa (TQ16, A);
  not NIb (TQ1a, B);
  // AND_Gate M0 has open pins: in0=TQ10, in1=TQr, out=open
  and A1 (TQ9, TQ10, TQr);
  and A2 (TQc, TQ9, TQ16);
  // AND_Gate A3 has open pins: in0=TQc, in1=TQ1a, out=open
  and A4 (TQf, TQ10, TQr);
  and A5 (TQg, TQf, A);
  and A6 (TQ1h, TQg, TQ1a);
  and A7 (TQh, TQ10, TQr);
  and A8 (TQi, TQh, TQ16);
  // AND_Gate A9 has open pins: in0=TQi, in1=B, out=open
  and A10 (TQj, TQ10, TQr);
  and A11 (TQk, TQj, A);
  // AND_Gate A12 has open pins: in0=TQk, in1=B, out=open
  // AND_Gate M13 has open pins: in0=TQ1b, in1=TQr, out=open
  and A14 (TQl, TQ1b, TQr);
  and A15 (TQm, TQl, TQ16);
  and A16 (TQ1i, TQm, TQ1a);
  and A17 (TQn, TQ1b, TQr);
  and A18 (TQo, TQn, A);
  and A19 (TQ1n, TQo, TQ1a);
  and A20 (TQp, TQ1b, TQr);
  and A21 (TQq, TQp, TQ16);
  // AND_Gate A22 has open pins: in0=TQq, in1=B, out=open
  and A23 (TQs, TQ1b, TQr);
  and A24 (TQt, TQs, A);
  and A25 (TQ1k, TQt, B);
  and M26 (TQb, TQ10, TQ1c);
  and A27 (TQu, TQ10, TQ1c);
  and A28 (TQv, TQu, TQ16);
  and A29 (TQ0, TQv, TQ1a);
  and A30 (TQw, TQ10, TQ1c);
  and A31 (TQx, TQw, A);
  and A32 (TQ5, TQx, TQ1a);
  and A33 (TQy, TQ10, TQ1c);
  and A34 (TQz, TQy, TQ16);
  and A35 (TQ1l, TQz, B);
  and A36 (TQ11, TQ10, TQ1c);
  and A37 (TQ12, TQ11, A);
  and A38 (TQ1, TQ12, B);
  and M39 (TQd, TQ1b, TQ1c);
  and A40 (TQ13, TQ1b, TQ1c);
  and A41 (TQ14, TQ13, TQ16);
  and A42 (TQ6, TQ14, TQ1a);
  and A43 (TQ15, TQ1b, TQ1c);
  and A44 (TQ17, TQ15, TQ16);
  and A45 (TQ4, TQ17, B);
  and A46 (TQ18, TQ1b, TQ1c);
  and A47 (TQ19, TQ18, A);
  and A48 (TQ7, TQ19, TQ1a);
  and A49 (TQ1d, TQ1b, TQ1c);
  and A50 (TQ1f, TQ1d, A);
  and A51 (TQ8, TQ1f, B);
  or O52 (TQ1j, TQ1h, TQ1i);
  or O53 (O53_out, TQ1j, TQ1k);
  or O54 (O54_out, O53_out, TQ1l);
  or O55 (O55_out, O54_out, TQ5);
  or O56 (O56_out, O55_out, TQ6);
  or O57 (O57_out, O56_out, TQ7);
  or O58 (TQ1m, O57_out, TQ8);
  or O59 (O59_out, TQ1n, TQ0);
  or O60 (O60_out, O59_out, TQ1);
  or O61 (O61_out, O60_out, TQ4);
  or O62 (O62_out, O61_out, TQ5);
  or O63 (O63_out, O62_out, TQ6);
  or O64 (O64_out, O63_out, TQ7);
  or O65 (TQa, O64_out, TQ8);
  or Ofo66 (Z, TQb, TQd);

  // Other names for the same wires on the sheet: TQ1e = A; TQ1g = B; TQ3 = RST; TQe = Z
endmodule
