// Logisim project gray_4bit.circ as structural Verilog
module gray_4bit (
  input  B0,
  input  B1,
  input  B2,
  input  B3,
  output G0,
  output G1,
  output G2,
  output G3
);

  xor U1 (G0, B0, B1);
  xor U2 (G1, B1, B2);
  xor U3 (G2, B2, B3);

  assign G3 = B3;

  // Other names for the same wires on the sheet: TQ0 = B0; TQ1 = G0; TQ2 = B1; TQ3 = G1; TQ4 = B2; TQ5 = G2; TQ6 = B3
endmodule
