// Logisim project graycnt_2bit_test.circ as structural Verilog
module graycnt_2bit_test (
  input  CLK,
  input  RST,
  output G0,
  output Q0,
  output G1,
  output Q1
);

  wire TQ2, TQ3;

  D_Flip_Flop U1 (.D(TQ2), .clk(CLK), .Q(Q0), .reset(RST));  // open: Qn, preset
  D_Flip_Flop U2 (.D(TQ3), .clk(CLK), .Q(G1), .reset(RST));  // open: Qn, preset
  not N1 (TQ2, Q0);
  xor X2 (TQ3, G1, Q0);
  xor G3 (G0, Q0, G1);

  assign Q1 = G1;

  // Other names for the same wires on the sheet: TQ0 = CLK; TQ1 = RST; TQ4 = G0; TQ5 = Q0; TQ6 = G1
endmodule
