// Logisim project graycnt_3bit.circ as structural Verilog
module graycnt_3bit (
  input  CLK,
  input  RST,
  output G0,
  output Q0,
  output G1,
  output Q1,
  output G2,
  output Q2
);

  wire TQ0, TQ2, TQ6, TQ7;

  D_Flip_Flop U1 (.D(TQ0), .clk(CLK), .Q(Q0), .reset(RST));  // open: Qn, preset
  D_Flip_Flop U2 (.D(TQ2), .clk(CLK), .Q(Q1), .reset(RST));  // open: Qn, preset
  D_Flip_Flop U3 (.D(TQ7), .clk(CLK), .Q(G2), .reset(RST));  // open: Qn, preset
  not N1 (TQ0, Q0);
  xor X2 (TQ2, Q1, Q0);
  and A3 (TQ6, Q0, Q1);
  xor X4 (TQ7, G2, TQ6);
  xor UG1 (G0, Q0, Q1);
  xor UG2 (G1, Q1, G2);

  assign Q2 = G2;

  // Other names for the same wires on the sheet: TQ1 = Q0; TQ3 = Q1; TQ4 = CLK; TQ5 = RST; TQ8 = G2; TQ9 = G0;
  //   TQa = G1
endmodule
