// Logisim project graycnt_3bit_test.circ as structural Verilog
module graycnt_3bit_test (
  input  RST,
  output G0,
  output Q0,
  output G1,
  output Q1,
  output G2,
  output Q2
);

  wire A3_out, CLK_out, N1_out, X2_out, X4_out;

  Clock CLK (.out(CLK_out));
  D_Flip_Flop U1 (.D(N1_out), .clk(CLK_out), .Q(Q0), .preset(RST), .reset(RST));  // open: Qn
  D_Flip_Flop U2 (.D(X2_out), .clk(CLK_out), .Q(Q1), .preset(RST), .reset(RST));  // open: Qn
  D_Flip_Flop U3 (.D(X4_out), .clk(CLK_out), .Q(G2), .preset(RST), .reset(RST));  // open: Qn
  not N1 (N1_out, Q0);
  xor X2 (X2_out, Q1, Q0);
  and A3 (A3_out, Q0, Q1);
  xor X4 (X4_out, G2, A3_out);
  xor G5 (G0, Q0, Q1);
  xor G6 (G1, Q1, G2);

  assign Q2 = G2;
endmodule
