// Logisim project graycnt_4bit_test.circ as structural Verilog
module graycnt_4bit_test (
  input  CLK,
  input  RST,
  output G0,
  output Q0,
  output G1,
  output Q1,
  output G2,
  output Q2,
  output G3,
  output Q3
);

  wire A3_out, A5_out, TQ6, TQ7, X4_out, X6_out;

  D_Flip_Flop U1 (.D(TQ6), .clk(CLK), .Q(Q0), .reset(RST));  // open: Qn, preset
  D_Flip_Flop U2 (.D(TQ7), .clk(CLK), .Q(Q1), .reset(RST));  // open: Qn, preset
  D_Flip_Flop U3 (.D(X4_out), .clk(CLK), .Q(Q2), .reset(RST));  // open: Qn, preset
  D_Flip_Flop U4 (.D(X6_out), .clk(CLK), .Q(G3), .reset(RST));  // open: Qn, preset
  not N1 (TQ6, Q0);
  xor X2 (TQ7, Q1, Q0);
  and A3 (A3_out, Q0, Q1);
  xor X4 (X4_out, Q2, A3_out);
  and A5 (A5_out, A3_out, Q2);
  xor X6 (X6_out, G3, A5_out);
  xor G7 (G0, Q0, Q1);
  xor G8 (G1, Q1, Q2);
  xor G9 (G2, Q2, G3);

  assign Q3 = G3;

  // Other names for the same wires on the sheet: TQ0 = Q0; TQ1 = Q1; TQ2 = Q2; TQ3 = G3; TQ4 = CLK; TQ5 = RST;
  //   TQ8 = G0; TQ9 = G1; TQa = G2
endmodule
