// Logisim project jk_flipflop.circ as structural Verilog
module jk_flipflop (
  input  J,
  input  K,
  input  CLK,
  input  CLR,
  input  PRE,
  output Q,
  output nQ
);

  J_K_Flip_Flop JK (.J(J), .K(K), .clk(CLK), .Q(Q), .Qn(nQ), .preset(PRE), .reset(CLK));

  assign CLR = CLK;
endmodule
