// Logisim project johnson_4stage.circ as structural Verilog
module johnson_4stage (
  input  CLK,
  input  RST,
  output Q0,
  output Q1,
  output Q2,
  output Q3
);

  wire JN_out;

  not JN (JN_out, Q3);
  D_Flip_Flop U1 (.D(JN_out), .clk(CLK), .Q(Q0), .reset(RST));  // open: Qn, preset
  D_Flip_Flop U2 (.D(Q0), .clk(CLK), .Q(Q1), .reset(RST));  // open: Qn, preset
  D_Flip_Flop U3 (.D(Q1), .clk(CLK), .Q(Q2), .reset(RST));  // open: Qn, preset
  D_Flip_Flop U4 (.D(Q2), .clk(CLK), .Q(Q3), .reset(RST));  // open: Qn, preset

  // Other names for the same wires on the sheet: TQ0 = Q3; TQ1 = Q0; TQ2 = Q1; TQ3 = Q2; TQ4 = CLK; TQ5 = RST
endmodule
