// Logisim project layout_reserved_area_router_fixture.circ as structural Verilog
module layout_reserved_area_router_fixture (
  input  A,
  output Y
);

  not N1 (Y, A);

  // Other names for the same wires on the sheet: n1 = A; n2 = Y
endmodule
