// Logisim project lfsr_4bit.circ as structural Verilog
module lfsr_4bit (
  input  CLK,
  input  SEED,
  input  RST,
  output Q0,
  output Q1,
  output Q2,
  output Q3
);

  wire TQ4, TQ6;

  D_Flip_Flop U1 (.D(TQ6), .clk(CLK), .Q(Q0), .reset(RST));  // open: Qn, preset
  D_Flip_Flop U2 (.D(Q0), .clk(CLK), .Q(Q1), .reset(RST));  // open: Qn, preset
  D_Flip_Flop U3 (.D(Q1), .clk(CLK), .Q(Q2), .reset(RST));  // open: Qn, preset
  D_Flip_Flop U4 (.D(Q2), .clk(CLK), .Q(Q3), .reset(RST));  // open: Qn, preset
  xor X1 (TQ4, Q3, Q2);
  or O1 (TQ6, SEED, TQ4);

  // Other names for the same wires on the sheet: TQ0 = Q2; TQ1 = CLK; TQ2 = RST; TQ3 = SEED; TQ5 = Q3; TQ7 = Q0;
  //   TQ8 = Q1
endmodule
