// Logisim project logic_f_a.circ as structural Verilog
module logic_f_a (
  input  A,
  output F
);

  wire n2;

  not not_1 (n2, A);
  not not_2 (F, n2);

  // Other names for the same wires on the sheet: n1 = A; n3 = F
endmodule
