// Logisim project logic_f_a0b0a1b1a2b2a3b3_not_and_xor.circ as structural Verilog
module logic_f_a0b0a1b1a2b2a3b3_not_and_xor (
  input  A0,
  input  B0,
  input  A1,
  input  B1,
  input  A2,
  input  B2,
  input  A3,
  input  B3,
  output F
);

  wire n9, n10, n11, n12, n13, n14, n15, n16, n17, n18;

  xor xor_1 (n9, A0, B0);
  xor xor_2 (n10, A1, B1);
  xor xor_3 (n13, A2, B2);
  xor xor_4 (n16, A3, B3);
  not not_1 (n11, n9);
  not not_2 (n12, n10);
  not not_3 (n15, n13);
  not not_4 (n18, n16);
  and and_1 (n14, n11, n12);
  and and_2 (n17, n14, n15);
  and and_3 (F, n17, n18);

  // Other names for the same wires on the sheet: n1 = A0; n2 = B0; n3 = A1; n4 = B1; n5 = A2; n6 = B2; n7 = A3;
  //   n8 = B3; n19 = F
endmodule
