// Logisim project logic_f_ab.circ as structural Verilog
module logic_f_ab (
  input  A,
  input  B,
  output F
);

  wire n1;

  not not_1 (n1, B);
  and and_1 (F, A, n1);

  // Other names for the same wires on the sheet: n2 = A; n3 = B; n4 = F
endmodule
