// Logisim project logic_f_ab_not_xor.circ as structural Verilog
module logic_f_ab_not_xor (
  input  A,
  input  B,
  output F
);

  wire n3;

  xor xor_1 (n3, A, B);
  not not_1 (F, n3);

  // Other names for the same wires on the sheet: n1 = A; n2 = B; n4 = F
endmodule
