// Logisim project logic_f_ab_xor.circ as structural Verilog
module logic_f_ab_xor (
  input  A,
  input  B,
  output F
);

  xor xor_1 (F, A, B);

  // Other names for the same wires on the sheet: n1 = A; n2 = B; n3 = F
endmodule
