// Logisim project logic_f_abc.circ as structural Verilog
module logic_f_abc (
  input  A,
  input  B,
  input  C,
  output F
);

  wire n1, n2, n3, n4, n5, n6, n7, n8, n9, n10;

  not not_1 (n1, A);
  not not_2 (n4, A);
  and and_1 (n6, A, B);
  not not_3 (n2, B);
  and and_2 (n5, n4, B);
  and and_3 (n10, n6, C);
  and and_4 (n3, n1, n2);
  and and_5 (n8, n5, C);
  and and_6 (n7, n3, C);
  or or_1 (n9, n7, n8);
  or or_2 (F, n9, n10);

  // Other names for the same wires on the sheet: n11 = A; n12 = B; n13 = C; n14 = F
endmodule
