// Logisim project logic_f_abc_xor.circ as structural Verilog
module logic_f_abc_xor (
  input  A,
  input  B,
  input  C,
  output F
);

  wire n4;

  xor xor_1 (n4, A, B);
  xor xor_2 (F, n4, C);

  // Other names for the same wires on the sheet: n1 = A; n2 = B; n3 = C; n5 = F
endmodule
