// Logisim project logic_f_abcd.circ as structural Verilog
module logic_f_abcd (
  input  A,
  input  B,
  input  C,
  input  D,
  output F
);

  wire n5, n6, n7, n8, n9, n10, n11, n12, n13, n14, n15, n16, n17, n18, n19, n20, n21, n22, n23, n24, n25,
       n26, n27, n28, n29, n30, n31, n32, n33, n34, n35, n36, n37, n38, n39, n40, n41, n42, n43;

  not not_1 (n5, A);
  not not_2 (n11, A);
  not not_3 (n16, A);
  not not_4 (n20, A);
  and and_1 (n27, A, B);
  and and_2 (n30, A, B);
  not not_5 (n6, B);
  not not_6 (n12, B);
  and and_3 (n17, n16, B);
  and and_4 (n21, n20, B);
  not not_7 (n23, B);
  and and_5 (n31, n30, C);
  and and_6 (n7, n5, n6);
  not not_8 (n8, C);
  and and_7 (n13, n11, n12);
  not not_9 (n18, C);
  and and_8 (n22, n21, C);
  and and_9 (n24, A, n23);
  not not_10 (n28, C);
  and and_10 (n43, n31, D);
  and and_11 (n9, n7, n8);
  not not_11 (n10, D);
  and and_12 (n14, n13, C);
  not not_12 (n15, D);
  and and_13 (n19, n17, n18);
  and and_14 (n37, n22, D);
  and and_15 (n25, n24, C);
  not not_13 (n26, D);
  and and_16 (n29, n27, n28);
  and and_17 (n32, n9, n10);
  and and_18 (n33, n14, n15);
  and and_19 (n35, n19, D);
  and and_20 (n39, n25, n26);
  and and_21 (n41, n29, D);
  or or_1 (n34, n32, n33);
  or or_2 (n36, n34, n35);
  or or_3 (n38, n36, n37);
  or or_4 (n40, n38, n39);
  or or_5 (n42, n40, n41);
  or or_6 (F, n42, n43);

  // Other names for the same wires on the sheet: n1 = A; n2 = B; n3 = C; n4 = D; n44 = F
endmodule
