// Logisim project logic_f_s0s1d0d2d1d3.circ as structural Verilog
module logic_f_s0s1d0d2d1d3 (
  input  S0,
  input  D0,
  input  S1,
  input  D2,
  input  D1,
  input  D3,
  output F
);

  wire n7, n8, n9, n10, n11, n12, n13, n14, n15, n16, n17, n18;

  not not_1 (n7, S0);
  not not_2 (n8, S1);
  and and_1 (n16, D3, S0);
  and and_2 (n9, n7, n8);
  and and_3 (n10, n7, D2);
  and and_4 (n13, n8, D1);
  and and_5 (n18, n16, S1);
  and and_6 (n11, n9, D0);
  and and_7 (n12, n10, S1);
  and and_8 (n15, n13, S0);
  or or_1 (n14, n11, n12);
  or or_2 (n17, n14, n15);
  or or_3 (F, n17, n18);

  // Other names for the same wires on the sheet: n1 = S0; n2 = S1; n3 = D0; n4 = D2; n5 = D1; n6 = D3; n19 = F
endmodule
