// Logisim project logic_multi_d_bout_ab_xor.circ as structural Verilog
module logic_multi_d_bout_ab_xor (
  input  A,
  input  B,
  output D,
  output BOUT
);

  wire n3;

  xor xor_1 (D, A, B);
  not not_1 (n3, A);
  and and_1 (BOUT, n3, B);

  // Other names for the same wires on the sheet: n1 = A; n2 = B; n4 = D; n5 = BOUT
endmodule
