// Logisim project logic_multi_f_gt_f_eq_f_lt_ba_not_xor.circ as structural Verilog
module logic_multi_f_gt_f_eq_f_lt_ba_not_xor (
  input  B,
  input  A,
  output F_GT,
  output F_EQ,
  output F_LT
);

  wire n3, n4, n5;

  not not_1 (n3, B);
  xor xor_1 (n4, A, B);
  not not_2 (n5, A);
  and and_1 (F_GT, n3, A);
  not not_3 (F_EQ, n4);
  and and_2 (F_LT, n5, B);

  // Other names for the same wires on the sheet: n1 = B; n2 = A; n6 = F_GT; n7 = F_EQ; n8 = F_LT
endmodule
