// Logisim project logic_multi_sum_carry_ab_multi.circ as structural Verilog
module logic_multi_sum_carry_ab_multi (
  input  A,
  input  B,
  output SUM,
  output CARRY
);

  xor xor_1 (SUM, A, B);
  and and_1 (CARRY, A, B);

  // Other names for the same wires on the sheet: n1 = A; n2 = B; n3 = SUM; n4 = CARRY
endmodule
