// Logisim project logic_multi_sum_carry_ab_multi_ttl.circ as structural Verilog
module logic_multi_sum_carry_ab_multi_ttl (
  input  A,
  input  B,
  output SUM,
  output CARRY
);

  xor U1A (SUM, A, B);
  and U2A (CARRY, A, B);

  // Other names for the same wires on the sheet: n1 = A; n2 = B; n3 = SUM; n4 = CARRY
endmodule
