// Logisim project logic_multi_sum_carry_ab_xor_ttl_dip_subckt.circ as structural Verilog
module logic_multi_sum_carry_ab_xor_ttl_dip_subckt (
  input  A,
  input  B,
  output SUM,
  output CARRY
);

  wire GND;

  U1_7486 U1_7486 (
    ._1_net_a(A), ._14_VCC(A), ._13_unused(SUM), ._7_GND(GND), ._8_unused(GND), ._3_net_i1(A));  // open: _2_net_b, _12_unused, _4_unused, _11_unused, _5_unused, _10_unused, _6_unused, _9_unused
  U2_7408 U2_7408 (
    ._1_net_a(A), ._14_VCC(A), ._13_unused(CARRY), ._7_GND(GND), ._8_unused(GND), ._3_net_i2(A));  // open: _2_net_b, _12_unused, _4_unused, _11_unused, _5_unused, _10_unused, _6_unused, _9_unused

  assign B = A;

  // Other names for the same wires on the sheet: n1 = A; n2 = A; VCC = A; n3 = SUM; n4 = CARRY

  // Notes on the sheet:
  //   1:net_a
  //   2:net_b
  //   3:net_i1
  //   7:GND
  //   U1 7486
  //   14:VCC
  //   1:net_a
  //   2:net_b
  //   3:net_i2
  //   7:GND
  //   U2 7408
  //   14:VCC
endmodule

module U1_7486 (
  input  _1_net_a,
  input  _14_VCC,
  input  _2_net_b,
  input  _13_unused,
  input  _12_unused,
  input  _4_unused,
  input  _11_unused,
  input  _5_unused,
  input  _10_unused,
  input  _6_unused,
  input  _9_unused,
  input  _7_GND,
  input  _8_unused,
  output _3_net_i1
);

  xor XOR0 (_3_net_i1, _1_net_a, _2_net_b);

  // Notes on the sheet:
  //   U1 7486
endmodule

module U2_7408 (
  input  _1_net_a,
  input  _14_VCC,
  input  _2_net_b,
  input  _13_unused,
  input  _12_unused,
  input  _4_unused,
  input  _11_unused,
  input  _5_unused,
  input  _10_unused,
  input  _6_unused,
  input  _9_unused,
  input  _7_GND,
  input  _8_unused,
  output _3_net_i2
);

  and AND0 (_3_net_i2, _1_net_a, _2_net_b);

  // Notes on the sheet:
  //   U2 7408
endmodule
