// Logisim project logic_multi_sum_carry_abcin_multi.circ as structural Verilog
module logic_multi_sum_carry_abcin_multi (
  input  A,
  input  B,
  input  Cin,
  output SUM,
  output CARRY
);

  wire n4, n5, n6;

  xor xor_1 (n4, A, B);
  and and_1 (n6, A, B);
  xor xor_2 (SUM, n4, Cin);
  and and_2 (n5, n4, Cin);
  or or_1 (CARRY, n5, n6);

  // Other names for the same wires on the sheet: n1 = A; n2 = B; n3 = Cin; n7 = SUM; n8 = CARRY
endmodule
