// Logisim project logic_multi_sum_carry_abcin_xor_and_xor_or_ttl.circ as structural Verilog
module logic_multi_sum_carry_abcin_xor_and_xor_or_ttl (
  input  A,
  input  B,
  input  Cin,
  output SUM,
  output CARRY
);

  wire n4, n5, n6;

  xor U1A (n4, A, B);
  and U2B (n6, A, B);
  xor U1B (SUM, n4, Cin);
  and U2A (n5, n4, Cin);
  or U3A (CARRY, n5, n6);

  // Other names for the same wires on the sheet: n1 = A; n2 = B; n3 = Cin; n7 = SUM; n8 = CARRY
endmodule
