// Logisim project logic_multi_sum_cout_abcin_xor_and_xor_or.circ as structural Verilog
module logic_multi_sum_cout_abcin_xor_and_xor_or (
  input  A,
  input  B,
  input  Cin,
  output SUM,
  output Cout
);

  wire n4, n5, n6;

  xor xor_1 (n4, A, B);
  and and_1 (n5, A, B);
  xor xor_2 (SUM, n4, Cin);
  and and_2 (n6, Cin, n4);
  or or_1 (Cout, n5, n6);

  // Other names for the same wires on the sheet: n1 = A; n2 = B; n3 = Cin; n7 = SUM; n8 = Cout
endmodule
