// Logisim project logic_multi_sum_cout_abcin_xor_and_xor_or_7400.circ as structural Verilog
module logic_multi_sum_cout_abcin_xor_and_xor_or_7400 (
  input  A,
  input  B,
  input  Cin,
  output SUM,
  output Cout
);

  wire n4, n5, n6, n7, n8, n9, n10, n11, n12, n13, n14;

  nand U1A (n4, A, B);
  nand U1B (n5, A, n4);
  nand U1C (n6, B, n4);
  nand U3C (n12, n4, n4);
  nand U1D (n7, n5, n6);
  nand U3D (n14, n12, n12);
  nand U2A (n8, n7, Cin);
  nand U2B (n9, n7, n8);
  nand U2C (n10, Cin, n8);
  nand U3A (n11, n8, n8);
  nand U2D (SUM, n9, n10);
  nand U3B (n13, n11, n11);
  nand U4A (Cout, n13, n14);

  // Other names for the same wires on the sheet: n1 = A; n2 = B; n3 = Cin; n15 = SUM; n16 = Cout
endmodule
