// Logisim project logic_multi_sum_cout_abcin_xor_and_xor_or_ttl_dip_subckt.circ as structural Verilog
module logic_multi_sum_cout_abcin_xor_and_xor_or_ttl_dip_subckt (
  input  A,
  input  B,
  input  Cin,
  output SUM,
  output Cout
);

  wire n4, n5, n6;

  // U1_7486 U1_7486: pin names not known; wires that end beside it: B, n4, n4, Cin, SUM
  // U2_7408 U2_7408: pin names not known; wires that end beside it: Cin, n5, A, B, n6
  // U3_7432 U3_7432: pin names not known; wires that end beside it: n6, Cout

  // Other names for the same wires on the sheet: n1 = A; n2 = B; n3 = Cin; n7 = SUM; n8 = Cout

  // Notes on the sheet:
  //   1:net_a
  //   2:net_b
  //   3:net_i1
  //   4:net_i1
  //   5:net_cin
  //   6:net_i4
  //   7:GND
  //   U1 7486
  //   14:VCC
  //   1:net_i1
  //   2:net_cin
  //   3:net_i2
  //   4:net_a
  //   5:net_b
  //   6:net_i3
  //   7:GND
  //   U2 7408
  //   14:VCC
  //   1:net_i2
  //   2:net_i3
  //   3:net_i5
  //   7:GND
  //   U3 7432
  //   14:VCC
endmodule

module U1_7486 (
  input  _1_net_a,
  input  _14_VCC,
  input  _2_net_b,
  input  _13_unused,
  input  _12_unused,
  input  _4_net_i1,
  input  _11_unused,
  input  _5_net_cin,
  input  _10_unused,
  input  _9_unused,
  input  _7_GND,
  input  _8_unused,
  output _3_net_i1,
  output _6_net_i4
);

  xor XOR0 (_3_net_i1, _1_net_a, _2_net_b);
  xor XOR1 (_6_net_i4, _4_net_i1, _4_net_i1);

  assign _5_net_cin = _4_net_i1;

  // Notes on the sheet:
  //   U1 7486
endmodule

module U2_7408 (
  input  _1_net_i1,
  input  _14_VCC,
  input  _2_net_cin,
  input  _13_unused,
  input  _12_unused,
  input  _4_net_a,
  input  _11_unused,
  input  _5_net_b,
  input  _10_unused,
  input  _9_unused,
  input  _7_GND,
  input  _8_unused,
  output _3_net_i2,
  output _6_net_i3
);

  and AND0 (_3_net_i2, _1_net_i1, _2_net_cin);
  and AND1 (_6_net_i3, _4_net_a, _4_net_a);

  assign _5_net_b = _4_net_a;

  // Notes on the sheet:
  //   U2 7408
endmodule

module U3_7432 (
  input  _1_net_i2,
  input  _14_VCC,
  input  _2_net_i3,
  input  _13_unused,
  input  _12_unused,
  input  _4_unused,
  input  _11_unused,
  input  _5_unused,
  input  _10_unused,
  input  _6_unused,
  input  _9_unused,
  input  _7_GND,
  input  _8_unused,
  output _3_net_i5
);

  or OR0 (_3_net_i5, _1_net_i2, _2_net_i3);

  // Notes on the sheet:
  //   U3 7432
endmodule
