// Logisim project logic_multi_x_y_z_abc_xor.circ as structural Verilog
module logic_multi_x_y_z_abc_xor (
  input  A,
  input  B,
  input  C,
  output X,
  output Y,
  output Z
);

  wire n4;

  and and_1 (X, A, B);
  xor xor_1 (n4, A, B);
  xor xor_2 (Z, n4, C);

  assign Y = X;

  // Other names for the same wires on the sheet: n1 = A; n2 = B; n3 = C; n5 = X; n6 = Z
endmodule
