// Logisim project logic_n_ab.circ as structural Verilog
module logic_n_ab (
  input  A,
  input  B,
  output N
);

  nand nand_1 (N, A, B);

  // Other names for the same wires on the sheet: n1 = A; n2 = B; n3 = N
endmodule
