// Logisim project logic_p_ab.circ as structural Verilog
module logic_p_ab (
  input  A,
  input  B,
  output P
);

  and and_1 (P, A, B);

  // Other names for the same wires on the sheet: n1 = A; n2 = B; n3 = P
endmodule
