// Logisim project logic_p_abc.circ as structural Verilog
module logic_p_abc (
  input  B,
  input  C,
  input  A,
  output P
);

  wire n1;

  and and_1 (n1, B, C);
  xor xor_1 (P, A, n1);

  // Other names for the same wires on the sheet: n2 = A; n3 = B; n4 = C; n5 = P
endmodule
