// Logisim project logic_r_ab.circ as structural Verilog
module logic_r_ab (
  input  A,
  input  B,
  output R
);

  nor nor_1 (R, A, B);

  // Other names for the same wires on the sheet: n1 = A; n2 = B; n3 = R
endmodule
