// Logisim project logic_x_abc.circ as structural Verilog
module logic_x_abc (
  input  A,
  input  B,
  input  C,
  output X
);

  wire n1;

  xor xor_1 (n1, A, B);
  xor xor_2 (X, n1, C);

  // Other names for the same wires on the sheet: n2 = A; n3 = B; n4 = C; n5 = X
endmodule
