// Logisim project logic_y_a_not_7404.circ as structural Verilog
module logic_y_a_not_7404 (
  input  A,
  output Y
);

  not U1A (Y, A);

  // Other names for the same wires on the sheet: n1 = A; n2 = Y
endmodule
