// Logisim project logic_y_ab.circ as structural Verilog
module logic_y_ab (
  input  A,
  input  B,
  output Y
);

  and and_1 (Y, A, B);

  // Other names for the same wires on the sheet: n1 = A; n2 = B; n3 = Y
endmodule
