// Logisim project logic_y_ab_and_7408.circ as structural Verilog
module logic_y_ab_and_7408 (
  input  A,
  input  B,
  output Y
);

  and U1A (Y, A, B);

  // Other names for the same wires on the sheet: n1 = A; n2 = B; n3 = Y
endmodule
