// Logisim project logic_y_ab_nand.circ as structural Verilog
module logic_y_ab_nand (
  input  A,
  input  B,
  output Y
);

  nand nand_1 (Y, A, B);

  // Other names for the same wires on the sheet: n1 = A; n2 = B; n3 = Y
endmodule
