// Logisim project logic_y_ab_nor.circ as structural Verilog
module logic_y_ab_nor (
  input  A,
  input  B,
  output Y
);

  nor nor_1 (Y, A, B);

  // Other names for the same wires on the sheet: n1 = A; n2 = B; n3 = Y
endmodule
