// Logisim project logic_y_ab_xor_7400.circ as structural Verilog
module logic_y_ab_xor_7400 (
  input  A,
  input  B,
  output Y
);

  wire n3, n4, n5;

  nand U1A (n3, A, B);
  nand U1B (n4, A, n3);
  nand U1C (n5, B, n3);
  nand U1D (Y, n4, n5);

  // Other names for the same wires on the sheet: n1 = A; n2 = B; n6 = Y
endmodule
