// Logisim project logic_y_ab_xor_7486.circ as structural Verilog
module logic_y_ab_xor_7486 (
  input  A,
  input  B,
  output Y
);

  xor U1A (Y, A, B);

  // Other names for the same wires on the sheet: n1 = A; n2 = B; n3 = Y
endmodule
