// Logisim project logic_y_ab_xor_nand_only.circ as structural Verilog
module logic_y_ab_xor_nand_only (
  input  A,
  input  B,
  output Y
);

  wire n3, n4, n5;

  nand nand_1 (n3, A, B);
  nand nand_2 (n4, A, n3);
  nand nand_3 (n5, B, n3);
  nand nand_4 (Y, n4, n5);

  // Other names for the same wires on the sheet: n1 = A; n2 = B; n6 = Y
endmodule
