// Logisim project logic_y_abc_and_xor.circ as structural Verilog
module logic_y_abc_and_xor (
  input  B,
  input  C,
  input  A,
  output Y
);

  wire n1;

  and and_1 (n1, B, C);
  xor xor_1 (Y, A, n1);

  // Other names for the same wires on the sheet: n2 = A; n3 = B; n4 = C; n5 = Y
endmodule
