// Logisim project logic_y_abc_xor.circ as structural Verilog
module logic_y_abc_xor (
  input  A,
  input  B,
  input  C,
  output Y
);

  wire n1;

  xor xor_1 (n1, A, B);
  xor xor_2 (Y, n1, C);

  // Other names for the same wires on the sheet: n2 = A; n3 = B; n4 = C; n5 = Y
endmodule
