// Logisim project logic_y_abcdef.circ as structural Verilog
module logic_y_abcdef (
  input  A,
  input  B,
  input  C,
  input  D,
  input  E,
  input  F,
  output Y
);

  wire n7, n8, n9, n10;

  and and_1 (n7, A, B);
  and and_2 (n8, C, D);
  and and_3 (n10, E, F);
  or or_1 (n9, n7, n8);
  or or_2 (Y, n9, n10);

  // Other names for the same wires on the sheet: n1 = A; n2 = B; n3 = C; n4 = D; n5 = E; n6 = F; n11 = Y
endmodule
