// Logisim project logic_y_ba.circ as structural Verilog
module logic_y_ba (
  input  B,
  input  A,
  output Y
);

  wire n3;

  not not_1 (n3, B);
  and and_1 (Y, n3, A);

  // Other names for the same wires on the sheet: n1 = B; n2 = A; n4 = Y
endmodule
