// Logisim project mac_4bit.circ as structural Verilog
module mac_4bit (
  input  RST,
  input  GND,
  input  A0,
  input  A1,
  input  A2,
  input  A3,
  input  B0,
  input  B1,
  input  B2,
  input  B3,
  output Q0,
  output Q1,
  output Q2,
  output Q3,
  output Q4,
  output Q5,
  output Q6,
  output Q7
);

  wire CLK_out, MACA17_out, MACA18_out, MACA19_out, MACA20_out, MACA21_out, MACA22_out, MACA23_out,
       MACA24_out, MACA25_out, MACA26_out, MACA27_out, MACA28_out, MACA29_out, MACA30_out, MACA31_out,
       MACA32_out, MACA33_out, MACA34_out, MACB17_out, MACB18_out, MACB19_out, MACB20_out, MACB21_out,
       MACB22_out, MACB23_out, MACB24_out, MACB25_out, MACB26_out, MACB27_out, MACB28_out, MACB29_out,
       MACB30_out, MACB31_out, MACB32_out, MACB33_out, MACB34_out, MACG17_out, MACG18_out, MACG19_out,
       MACG20_out, MACG22_out, MACG23_out, MACG24_out, MACG25_out, MACG26_out, MACG28_out, MACG29_out,
       MACG30_out, MACG31_out, MACG32_out, MACG33_out, MACH35_out, MACH36_out, MACH37_out, MACH38_out,
       MACH39_out, MACH40_out, MACH41_out, MACH42_out, MACI35_out, MACI36_out, MACI37_out, MACI38_out,
       MACI39_out, MACI40_out, MACI41_out, MACI42_out, MACJ35_out, MACJ36_out, MACJ37_out, MACJ38_out,
       MACJ39_out, MACJ40_out, MACJ41_out, MACJ42_out, MACK35_out, MACK36_out, MACK37_out, MACK38_out,
       MACK39_out, MACK40_out, MACK41_out, MACO17_out, MACO18_out, MACO19_out, MACO20_out, MACO21_out,
       MACO22_out, MACO23_out, MACO24_out, MACO25_out, MACO26_out, MACO27_out, MACO28_out, MACO29_out,
       MACO30_out, MACO31_out, MACO32_out, MACO33_out, MACO34_out, MACP1_out, MACP2_out, MACP3_out,
       MACP4_out, MACP5_out, MACP6_out, MACP7_out, MACP8_out, MACP9_out, MACP10_out, MACP11_out, MACP12_out,
       MACP13_out, MACP14_out, MACP15_out, MACP16_out, MACS17_out, MACS18_out, MACS19_out, MACS20_out,
       MACS21_out, MACS22_out, MACS23_out, MACS24_out, MACS25_out, MACS26_out, MACS27_out, MACS28_out,
       MACS29_out, MACS30_out, MACS31_out, MACS32_out, MACT35_out, MACT36_out, MACT37_out, MACT38_out,
       MACT39_out, MACT40_out, MACT41_out, MACT42_out, MACX17_out, MACX18_out, MACX19_out, MACX20_out,
       MACX21_out, MACX22_out, MACX23_out, MACX24_out, MACX25_out, MACX26_out, MACX27_out, MACX28_out,
       MACX29_out, MACX30_out, MACX31_out, MACX32_out, MACX33_out, MACX34_out, MACY35_out, MACY36_out,
       MACY37_out, MACY38_out, MACY39_out, MACY40_out, MACY41_out, MACY42_out;

  Clock CLK (.out(CLK_out));
  D_Flip_Flop U1 (.D(MACT35_out), .clk(CLK_out), .Q(Q0), .preset(RST), .reset(RST));  // open: Qn
  D_Flip_Flop U2 (.D(MACT36_out), .clk(CLK_out), .Q(Q1), .preset(RST), .reset(RST));  // open: Qn
  D_Flip_Flop U3 (.D(MACT37_out), .clk(CLK_out), .Q(Q2), .preset(RST), .reset(RST));  // open: Qn
  D_Flip_Flop U4 (.D(MACT38_out), .clk(CLK_out), .Q(Q3), .preset(RST), .reset(RST));  // open: Qn
  D_Flip_Flop U5 (.D(MACT39_out), .clk(CLK_out), .Q(Q4), .preset(RST), .reset(RST));  // open: Qn
  D_Flip_Flop U6 (.D(MACT40_out), .clk(CLK_out), .Q(Q5), .preset(RST), .reset(RST));  // open: Qn
  D_Flip_Flop U7 (.D(MACT41_out), .clk(CLK_out), .Q(Q6), .preset(RST), .reset(RST));  // open: Qn
  D_Flip_Flop U8 (.D(MACT42_out), .clk(CLK_out), .Q(Q7), .preset(RST), .reset(RST));  // open: Qn
  and MACP1 (MACP1_out, A0, B0);
  and MACP2 (MACP2_out, A1, B0);
  and MACP3 (MACP3_out, A2, B0);
  and MACP4 (MACP4_out, A3, B0);
  and MACP5 (MACP5_out, A0, B1);
  and MACP6 (MACP6_out, A1, B1);
  and MACP7 (MACP7_out, A2, B1);
  and MACP8 (MACP8_out, A3, B1);
  and MACP9 (MACP9_out, A0, B2);
  and MACP10 (MACP10_out, A1, B2);
  and MACP11 (MACP11_out, A2, B2);
  and MACP12 (MACP12_out, A3, B2);
  and MACP13 (MACP13_out, A0, B3);
  and MACP14 (MACP14_out, A1, B3);
  and MACP15 (MACP15_out, A2, B3);
  and MACP16 (MACP16_out, A3, B3);
  xor MACX17 (MACX17_out, MACP2_out, MACP5_out);
  xor MACS17 (MACS17_out, MACX17_out, GND);
  and MACA17 (MACA17_out, MACP2_out, MACP5_out);
  and MACB17 (MACB17_out, GND, MACX17_out);
  or MACO17 (MACO17_out, MACA17_out, MACB17_out);
  or MACG17 (MACG17_out, MACO17_out, GND);
  xor MACX18 (MACX18_out, MACP3_out, MACP6_out);
  xor MACS18 (MACS18_out, MACX18_out, MACG17_out);
  and MACA18 (MACA18_out, MACP3_out, MACP6_out);
  and MACB18 (MACB18_out, MACG17_out, MACX18_out);
  or MACO18 (MACO18_out, MACA18_out, MACB18_out);
  or MACG18 (MACG18_out, MACO18_out, GND);
  xor MACX19 (MACX19_out, MACP4_out, MACP7_out);
  xor MACS19 (MACS19_out, MACX19_out, MACG18_out);
  and MACA19 (MACA19_out, MACP4_out, MACP7_out);
  and MACB19 (MACB19_out, MACG18_out, MACX19_out);
  or MACO19 (MACO19_out, MACA19_out, MACB19_out);
  or MACG19 (MACG19_out, MACO19_out, GND);
  xor MACX20 (MACX20_out, GND, MACP8_out);
  xor MACS20 (MACS20_out, MACX20_out, MACG19_out);
  and MACA20 (MACA20_out, GND, MACP8_out);
  and MACB20 (MACB20_out, MACG19_out, MACX20_out);
  or MACO20 (MACO20_out, MACA20_out, MACB20_out);
  or MACG20 (MACG20_out, MACO20_out, GND);
  xor MACX21 (MACX21_out, GND, GND);
  xor MACS21 (MACS21_out, MACX21_out, MACG20_out);
  and MACA21 (MACA21_out, GND, GND);
  and MACB21 (MACB21_out, MACG20_out, MACX21_out);
  or MACO21 (MACO21_out, MACA21_out, MACB21_out);
  // OR_Gate MACG21 has open pins: in0=MACO21_out, in1=GND, out=open
  xor MACX22 (MACX22_out, MACS18_out, MACP9_out);
  xor MACS22 (MACS22_out, MACX22_out, GND);
  and MACA22 (MACA22_out, MACS18_out, MACP9_out);
  and MACB22 (MACB22_out, GND, MACX22_out);
  or MACO22 (MACO22_out, MACA22_out, MACB22_out);
  or MACG22 (MACG22_out, MACO22_out, GND);
  xor MACX23 (MACX23_out, MACS19_out, MACP10_out);
  xor MACS23 (MACS23_out, MACX23_out, MACG22_out);
  and MACA23 (MACA23_out, MACS19_out, MACP10_out);
  and MACB23 (MACB23_out, MACG22_out, MACX23_out);
  or MACO23 (MACO23_out, MACA23_out, MACB23_out);
  or MACG23 (MACG23_out, MACO23_out, GND);
  xor MACX24 (MACX24_out, MACS20_out, MACP11_out);
  xor MACS24 (MACS24_out, MACX24_out, MACG23_out);
  and MACA24 (MACA24_out, MACS20_out, MACP11_out);
  and MACB24 (MACB24_out, MACG23_out, MACX24_out);
  or MACO24 (MACO24_out, MACA24_out, MACB24_out);
  or MACG24 (MACG24_out, MACO24_out, GND);
  xor MACX25 (MACX25_out, MACS21_out, MACP12_out);
  xor MACS25 (MACS25_out, MACX25_out, MACG24_out);
  and MACA25 (MACA25_out, MACS21_out, MACP12_out);
  and MACB25 (MACB25_out, MACG24_out, MACX25_out);
  or MACO25 (MACO25_out, MACA25_out, MACB25_out);
  or MACG25 (MACG25_out, MACO25_out, GND);
  xor MACX26 (MACX26_out, GND, GND);
  xor MACS26 (MACS26_out, MACX26_out, MACG25_out);
  and MACA26 (MACA26_out, GND, GND);
  and MACB26 (MACB26_out, MACG25_out, MACX26_out);
  or MACO26 (MACO26_out, MACA26_out, MACB26_out);
  or MACG26 (MACG26_out, MACO26_out, GND);
  xor MACX27 (MACX27_out, GND, GND);
  xor MACS27 (MACS27_out, MACX27_out, MACG26_out);
  and MACA27 (MACA27_out, GND, GND);
  and MACB27 (MACB27_out, MACG26_out, MACX27_out);
  or MACO27 (MACO27_out, MACA27_out, MACB27_out);
  // OR_Gate MACG27 has open pins: in0=MACO27_out, in1=GND, out=open
  xor MACX28 (MACX28_out, MACS23_out, MACP13_out);
  xor MACS28 (MACS28_out, MACX28_out, GND);
  and MACA28 (MACA28_out, MACS23_out, MACP13_out);
  and MACB28 (MACB28_out, GND, MACX28_out);
  or MACO28 (MACO28_out, MACA28_out, MACB28_out);
  or MACG28 (MACG28_out, MACO28_out, GND);
  xor MACX29 (MACX29_out, MACS24_out, MACP14_out);
  xor MACS29 (MACS29_out, MACX29_out, MACG28_out);
  and MACA29 (MACA29_out, MACS24_out, MACP14_out);
  and MACB29 (MACB29_out, MACG28_out, MACX29_out);
  or MACO29 (MACO29_out, MACA29_out, MACB29_out);
  or MACG29 (MACG29_out, MACO29_out, GND);
  xor MACX30 (MACX30_out, MACS25_out, MACP15_out);
  xor MACS30 (MACS30_out, MACX30_out, MACG29_out);
  and MACA30 (MACA30_out, MACS25_out, MACP15_out);
  and MACB30 (MACB30_out, MACG29_out, MACX30_out);
  or MACO30 (MACO30_out, MACA30_out, MACB30_out);
  or MACG30 (MACG30_out, MACO30_out, GND);
  xor MACX31 (MACX31_out, MACS26_out, MACP16_out);
  xor MACS31 (MACS31_out, MACX31_out, MACG30_out);
  and MACA31 (MACA31_out, MACS26_out, MACP16_out);
  and MACB31 (MACB31_out, MACG30_out, MACX31_out);
  or MACO31 (MACO31_out, MACA31_out, MACB31_out);
  or MACG31 (MACG31_out, MACO31_out, GND);
  xor MACX32 (MACX32_out, MACS27_out, GND);
  xor MACS32 (MACS32_out, MACX32_out, MACG31_out);
  and MACA32 (MACA32_out, MACS27_out, GND);
  and MACB32 (MACB32_out, MACG31_out, MACX32_out);
  or MACO32 (MACO32_out, MACA32_out, MACB32_out);
  or MACG32 (MACG32_out, MACO32_out, GND);
  xor MACX33 (MACX33_out, GND, GND);
  // XOR_Gate MACS33 has open pins: in0=MACX33_out, in1=MACG32_out, out=open
  and MACA33 (MACA33_out, GND, GND);
  and MACB33 (MACB33_out, MACG32_out, MACX33_out);
  or MACO33 (MACO33_out, MACA33_out, MACB33_out);
  or MACG33 (MACG33_out, MACO33_out, GND);
  xor MACX34 (MACX34_out, GND, GND);
  // XOR_Gate MACS34 has open pins: in0=MACX34_out, in1=MACG33_out, out=open
  and MACA34 (MACA34_out, GND, GND);
  and MACB34 (MACB34_out, MACG33_out, MACX34_out);
  or MACO34 (MACO34_out, MACA34_out, MACB34_out);
  // OR_Gate MACG34 has open pins: in0=MACO34_out, in1=GND, out=open
  xor MACY35 (MACY35_out, MACP1_out, Q0);
  xor MACT35 (MACT35_out, MACY35_out, GND);
  and MACH35 (MACH35_out, MACP1_out, Q0);
  and MACI35 (MACI35_out, GND, MACY35_out);
  or MACJ35 (MACJ35_out, MACH35_out, MACI35_out);
  or MACK35 (MACK35_out, MACJ35_out, GND);
  xor MACY36 (MACY36_out, MACS17_out, Q1);
  xor MACT36 (MACT36_out, MACY36_out, MACK35_out);
  and MACH36 (MACH36_out, MACS17_out, Q1);
  and MACI36 (MACI36_out, MACK35_out, MACY36_out);
  or MACJ36 (MACJ36_out, MACH36_out, MACI36_out);
  or MACK36 (MACK36_out, MACJ36_out, GND);
  xor MACY37 (MACY37_out, MACS22_out, Q2);
  xor MACT37 (MACT37_out, MACY37_out, MACK36_out);
  and MACH37 (MACH37_out, MACS22_out, Q2);
  and MACI37 (MACI37_out, MACK36_out, MACY37_out);
  or MACJ37 (MACJ37_out, MACH37_out, MACI37_out);
  or MACK37 (MACK37_out, MACJ37_out, GND);
  xor MACY38 (MACY38_out, MACS28_out, Q3);
  xor MACT38 (MACT38_out, MACY38_out, MACK37_out);
  and MACH38 (MACH38_out, MACS28_out, Q3);
  and MACI38 (MACI38_out, MACK37_out, MACY38_out);
  or MACJ38 (MACJ38_out, MACH38_out, MACI38_out);
  or MACK38 (MACK38_out, MACJ38_out, GND);
  xor MACY39 (MACY39_out, MACS29_out, Q4);
  xor MACT39 (MACT39_out, MACY39_out, MACK38_out);
  and MACH39 (MACH39_out, MACS29_out, Q4);
  and MACI39 (MACI39_out, MACK38_out, MACY39_out);
  or MACJ39 (MACJ39_out, MACH39_out, MACI39_out);
  or MACK39 (MACK39_out, MACJ39_out, GND);
  xor MACY40 (MACY40_out, MACS30_out, Q5);
  xor MACT40 (MACT40_out, MACY40_out, MACK39_out);
  and MACH40 (MACH40_out, MACS30_out, Q5);
  and MACI40 (MACI40_out, MACK39_out, MACY40_out);
  or MACJ40 (MACJ40_out, MACH40_out, MACI40_out);
  or MACK40 (MACK40_out, MACJ40_out, GND);
  xor MACY41 (MACY41_out, MACS31_out, Q6);
  xor MACT41 (MACT41_out, MACY41_out, MACK40_out);
  and MACH41 (MACH41_out, MACS31_out, Q6);
  and MACI41 (MACI41_out, MACK40_out, MACY41_out);
  or MACJ41 (MACJ41_out, MACH41_out, MACI41_out);
  or MACK41 (MACK41_out, MACJ41_out, GND);
  xor MACY42 (MACY42_out, MACS32_out, Q7);
  xor MACT42 (MACT42_out, MACY42_out, MACK41_out);
  and MACH42 (MACH42_out, MACS32_out, Q7);
  and MACI42 (MACI42_out, MACK41_out, MACY42_out);
  or MACJ42 (MACJ42_out, MACH42_out, MACI42_out);
  // OR_Gate MACK42 has open pins: in0=MACJ42_out, in1=GND, out=open
endmodule
