// Logisim project mod100_counter.circ as structural Verilog
module mod100_counter (
  input  RST,
  output Q0,
  output Q1,
  output Q2,
  output Q3,
  output Q4,
  output Q5,
  output Q6,
  output TC
);

  wire NR2_out, NR3_out, NR4_out, NR5_out, NR6_out, TM1_out, TM5_out, TM6_out, TQ1, TQ3, TQ4, TQ6, TQ7, TQ9,
       TQb, TQc, TQd, TQe, TQf, TQg, TQh, TQi, TQj, TQk, TQm;

  Clock CLK (.out(TQ7));
  T_Flip_Flop U1 (.T(TQe), .clk(TQ7), .Q(Q0), .reset(RST));  // open: Qn, preset
  T_Flip_Flop U2 (.T(TQf), .clk(TQ7), .Q(Q1), .reset(RST));  // open: Qn, preset
  T_Flip_Flop U3 (.T(TQg), .clk(TQ7), .Q(Q2), .reset(RST));  // open: Qn, preset
  T_Flip_Flop U4 (.T(TQh), .clk(TQ7), .Q(Q3), .reset(RST));  // open: Qn, preset
  T_Flip_Flop U5 (.T(TQi), .clk(TQ7), .Q(Q4), .reset(RST));  // open: Qn, preset
  T_Flip_Flop U6 (.T(TQj), .clk(TQ7), .Q(Q5), .reset(RST));  // open: Qn, preset
  T_Flip_Flop U7 (.T(TQm), .clk(TQ7), .Q(Q6), .reset(RST));  // open: Qn, preset
  and AT2 (TQ1, Q0, Q1);
  not N3 (TQ3, Q2);
  and AT3 (TQ4, TQ1, TQ3);
  not N4 (TQ6, Q3);
  and AT4 (TQ9, TQ4, TQ6);
  not N5 (TQb, Q4);
  and AT5 (TQc, TQ9, TQb);
  and AT6 (TQd, TQc, Q5);
  and AT7 (TC, TQd, Q6);
  not NA (TQk, TC);
  or T0 (TQe, TQk, TC);
  and TM1 (TM1_out, Q0, TQk);
  or TO1 (TQf, TM1_out, TC);
  and NR2 (NR2_out, Q0, Q1);
  and TM2 (TQg, NR2_out, TQk);
  and NR3 (NR3_out, NR2_out, Q2);
  and TM3 (TQh, NR3_out, TQk);
  and NR4 (NR4_out, NR3_out, Q3);
  and TM4 (TQi, NR4_out, TQk);
  and NR5 (NR5_out, NR4_out, Q4);
  and TM5 (TM5_out, NR5_out, TQk);
  or TO5 (TQj, TM5_out, TC);
  and NR6 (NR6_out, NR5_out, Q5);
  and TM6 (TM6_out, NR6_out, TQk);
  or TO6 (TQm, TM6_out, TC);

  // Other names for the same wires on the sheet: TQ0 = Q3; TQ2 = Q4; TQ5 = Q5; TQ8 = RST; TQa = Q6; TQl = TC;
  //   TQn = Q0; TQo = Q1; TQp = Q2
endmodule
