// Logisim project mod10_counter.circ as structural Verilog
module mod10_counter (
  input  CLK,
  input  RST,
  output Q0,
  output Q1,
  output Q2,
  output Q3,
  output TC
);

  wire AT2_out, AT3_out, N2_out, N3_out, NA_out, NR2_out, NR3_out, TM3_out, TO3_out, TQ5, TQ6, TQ7;

  T_Flip_Flop U1 (.T(TQ5), .clk(CLK), .Q(Q0), .reset(RST));  // open: Qn, preset
  T_Flip_Flop U2 (.T(TQ6), .clk(CLK), .Q(Q1), .reset(RST));  // open: Qn, preset
  T_Flip_Flop U3 (.T(TQ7), .clk(CLK), .Q(Q2), .reset(RST));  // open: Qn, preset
  T_Flip_Flop U4 (.T(TO3_out), .clk(CLK), .Q(Q3), .reset(RST));  // open: Qn, preset
  not N2 (N2_out, Q1);
  and AT2 (AT2_out, Q0, N2_out);
  not N3 (N3_out, Q2);
  and AT3 (AT3_out, AT2_out, N3_out);
  and AT4 (TC, AT3_out, Q3);
  not NA (NA_out, TC);
  or T0 (TQ5, NA_out, TC);
  and TM1 (TQ6, Q0, NA_out);
  and NR2 (NR2_out, Q0, Q1);
  and TM2 (TQ7, NR2_out, NA_out);
  and NR3 (NR3_out, NR2_out, Q2);
  and TM3 (TM3_out, NR3_out, NA_out);
  or TO3 (TO3_out, TM3_out, TC);

  // Other names for the same wires on the sheet: TQ0 = Q1; TQ1 = Q2; TQ2 = CLK; TQ3 = RST; TQ4 = Q3; TQ8 = TC;
  //   TQ9 = Q0
endmodule
