// Logisim project mod128_counter.circ as structural Verilog
module mod128_counter (
  input  RST,
  output Q0,
  output Q1,
  output Q2,
  output Q3,
  output Q4,
  output Q5,
  output Q6,
  output TC
);

  wire NR2_out, NR3_out, NR4_out, NR5_out, NR6_out, TM2_out, TM3_out, TM4_out, TM5_out, TM6_out, TQ1, TQ3,
       TQ4, TQ6, TQ7, TQ9, TQc, TQd, TQe, TQf, TQg, TQh, TQi, TQj, TQl;

  Clock CLK (.out(TQ9));
  T_Flip_Flop U1 (.T(TQc), .clk(TQ9), .Q(Q0), .reset(RST));  // open: Qn, preset
  T_Flip_Flop U2 (.T(TQe), .clk(TQ9), .Q(Q1), .reset(RST));  // open: Qn, preset
  T_Flip_Flop U3 (.T(TQf), .clk(TQ9), .Q(Q2), .reset(RST));  // open: Qn, preset
  T_Flip_Flop U4 (.T(TQg), .clk(TQ9), .Q(Q3), .reset(RST));  // open: Qn, preset
  T_Flip_Flop U5 (.T(TQh), .clk(TQ9), .Q(Q4), .reset(RST));  // open: Qn, preset
  T_Flip_Flop U6 (.T(TQi), .clk(TQ9), .Q(Q5), .reset(RST));  // open: Qn, preset
  T_Flip_Flop U7 (.T(TQl), .clk(TQ9), .Q(Q6), .reset(RST));  // open: Qn, preset
  and AT2 (TQ1, Q0, Q1);
  and AT3 (TQ3, TQ1, Q2);
  and AT4 (TQ4, TQ3, Q3);
  and AT5 (TQ6, TQ4, Q4);
  and AT6 (TQ7, TQ6, Q5);
  and AT7 (TC, TQ7, Q6);
  not NA (TQj, TC);
  or T0 (TQc, TQj, TC);
  and TM1 (TQd, Q0, TQj);
  or TO1 (TQe, TQd, TC);
  and NR2 (NR2_out, Q0, Q1);
  and TM2 (TM2_out, NR2_out, TQj);
  or TO2 (TQf, TM2_out, TC);
  and NR3 (NR3_out, NR2_out, Q2);
  and TM3 (TM3_out, NR3_out, TQj);
  or TO3 (TQg, TM3_out, TC);
  and NR4 (NR4_out, NR3_out, Q3);
  and TM4 (TM4_out, NR4_out, TQj);
  or TO4 (TQh, TM4_out, TC);
  and NR5 (NR5_out, NR4_out, Q4);
  and TM5 (TM5_out, NR5_out, TQj);
  or TO5 (TQi, TM5_out, TC);
  and NR6 (NR6_out, NR5_out, Q5);
  and TM6 (TM6_out, NR6_out, TQj);
  or TO6 (TQl, TM6_out, TC);

  // Other names for the same wires on the sheet: TQ0 = Q2; TQ2 = Q3; TQ5 = Q4; TQ8 = Q5; TQa = RST; TQb = Q6;
  //   TQk = TC; TQm = Q0; TQn = Q1
endmodule
