// Logisim project mod5_counter.circ as structural Verilog
module mod5_counter (
  input  CLK,
  input  RST,
  output Q0,
  output Q1,
  output Q2,
  output Q3
);

  wire AT2_out, AT3_out, AT4_out, N1_out, N2_out, N4_out, NR2_out, NR3_out, TM2_out, TM3_out, TQ4, TQ5, TQ6;

  T_Flip_Flop U1 (.T(TQ6), .clk(CLK), .Q(Q0), .reset(RST));  // open: Qn, preset
  T_Flip_Flop U2 (.T(TQ4), .clk(CLK), .Q(Q1), .reset(RST));  // open: Qn, preset
  T_Flip_Flop U3 (.T(TQ5), .clk(CLK), .Q(Q2), .reset(RST));  // open: Qn, preset
  T_Flip_Flop U4 (.T(TM3_out), .clk(CLK), .Q(Q3), .reset(RST));  // open: Qn, preset
  not N1 (N1_out, Q0);
  not N2 (N2_out, Q1);
  and AT2 (AT2_out, N1_out, N2_out);
  and AT3 (AT3_out, AT2_out, Q2);
  not N4 (N4_out, Q3);
  and AT4 (AT4_out, AT3_out, N4_out);
  not NA (TQ6, AT4_out);
  and TM1 (TQ4, Q0, TQ6);
  and NR2 (NR2_out, Q0, Q1);
  and TM2 (TM2_out, NR2_out, TQ6);
  or TO2 (TQ5, TM2_out, AT4_out);
  and NR3 (NR3_out, NR2_out, Q2);
  and TM3 (TM3_out, NR3_out, TQ6);

  // Other names for the same wires on the sheet: TQ0 = Q2; TQ1 = CLK; TQ2 = RST; TQ3 = Q3; TQ7 = Q0; TQ8 = Q1
endmodule
