// Logisim project mod60_counter.circ as structural Verilog
module mod60_counter (
  input  RST,
  output Q0,
  output Q1,
  output Q2,
  output Q3,
  output Q4,
  output Q5,
  output TC
);

  wire NA_out, NR2_out, NR3_out, NR4_out, NR5_out, TM1_out, TM3_out, TM4_out, TM5_out, TQ1, TQ2, TQ3, TQ4,
       TQ5, TQ6, TQ7, TQ8, TQ9, TQa, TQc, TQi;

  Clock CLK (.out(TQi));
  T_Flip_Flop U1 (.T(TQ6), .clk(TQi), .Q(Q0), .reset(RST));  // open: Qn, preset
  T_Flip_Flop U2 (.T(TQ7), .clk(TQi), .Q(Q1), .reset(RST));  // open: Qn, preset
  T_Flip_Flop U3 (.T(TQ8), .clk(TQi), .Q(Q2), .reset(RST));  // open: Qn, preset
  T_Flip_Flop U4 (.T(TQ9), .clk(TQi), .Q(Q3), .reset(RST));  // open: Qn, preset
  T_Flip_Flop U5 (.T(TQa), .clk(TQi), .Q(Q4), .reset(RST));  // open: Qn, preset
  T_Flip_Flop U6 (.T(TQc), .clk(TQi), .Q(Q5), .reset(RST));  // open: Qn, preset
  and AT2 (TQ1, Q0, Q1);
  not N3 (TQ2, Q2);
  and AT3 (TQ3, TQ1, TQ2);
  and AT4 (TQ4, TQ3, Q3);
  and AT5 (TQ5, TQ4, Q4);
  and AT6 (TC, TQ5, Q5);
  not NA (NA_out, TC);
  or T0 (TQ6, NA_out, TC);
  and TM1 (TM1_out, Q0, NA_out);
  or TO1 (TQ7, TM1_out, TC);
  and NR2 (NR2_out, Q0, Q1);
  and TM2 (TQ8, NR2_out, NA_out);
  and NR3 (NR3_out, NR2_out, Q2);
  and TM3 (TM3_out, NR3_out, NA_out);
  or TO3 (TQ9, TM3_out, TC);
  and NR4 (NR4_out, NR3_out, Q3);
  and TM4 (TM4_out, NR4_out, NA_out);
  or TO4 (TQa, TM4_out, TC);
  and NR5 (NR5_out, NR4_out, Q4);
  and TM5 (TM5_out, NR5_out, NA_out);
  or TO5 (TQc, TM5_out, TC);

  // Other names for the same wires on the sheet: TQ0 = Q5; TQb = TC; TQd = Q0; TQe = Q1; TQf = Q2; TQg = Q3; TQh = Q4;
  //   TQj = RST
endmodule
