// Logisim project mod6_counter.circ as structural Verilog
module mod6_counter (
  input  CLK,
  input  RST,
  output Q0,
  output Q1,
  output Q2,
  output Q3,
  output TC
);

  wire AT2_out, AT3_out, N2_out, N4_out, NA_out, NR2_out, NR3_out, TM2_out, TM3_out, TQ5, TQ6, TQ8;

  T_Flip_Flop U1 (.T(TQ5), .clk(CLK), .Q(Q0), .reset(RST));  // open: Qn, preset
  T_Flip_Flop U2 (.T(TQ6), .clk(CLK), .Q(Q1), .reset(RST));  // open: Qn, preset
  T_Flip_Flop U3 (.T(TQ8), .clk(CLK), .Q(Q2), .reset(RST));  // open: Qn, preset
  T_Flip_Flop U4 (.T(TM3_out), .clk(CLK), .Q(Q3), .reset(RST));  // open: Qn, preset
  not N2 (N2_out, Q1);
  and AT2 (AT2_out, Q0, N2_out);
  and AT3 (AT3_out, AT2_out, Q2);
  not N4 (N4_out, Q3);
  and AT4 (TC, AT3_out, N4_out);
  not NA (NA_out, TC);
  or T0 (TQ5, NA_out, TC);
  and TM1 (TQ6, Q0, NA_out);
  and NR2 (NR2_out, Q0, Q1);
  and TM2 (TM2_out, NR2_out, NA_out);
  or TO2 (TQ8, TM2_out, TC);
  and NR3 (NR3_out, NR2_out, Q2);
  and TM3 (TM3_out, NR3_out, NA_out);

  // Other names for the same wires on the sheet: TQ0 = Q1; TQ1 = Q2; TQ2 = CLK; TQ3 = RST; TQ4 = Q3; TQ7 = TC;
  //   TQ9 = Q0
endmodule
