// Logisim project mod7_counter.circ as structural Verilog
module mod7_counter (
  input  CLK,
  input  RST,
  output Q0,
  output Q1,
  output Q2,
  output Q3
);

  wire AT2_out, AT3_out, AT4_out, N1_out, N4_out, NR2_out, NR3_out, TM1_out, TM2_out, TM3_out, TQ5, TQ6, TQ7;

  T_Flip_Flop U1 (.T(TQ7), .clk(CLK), .Q(Q0), .reset(RST));  // open: Qn, preset
  T_Flip_Flop U2 (.T(TQ5), .clk(CLK), .Q(Q1), .reset(RST));  // open: Qn, preset
  T_Flip_Flop U3 (.T(TQ6), .clk(CLK), .Q(Q2), .reset(RST));  // open: Qn, preset
  T_Flip_Flop U4 (.T(TM3_out), .clk(CLK), .Q(Q3), .reset(RST));  // open: Qn, preset
  not N1 (N1_out, Q0);
  and AT2 (AT2_out, N1_out, Q1);
  and AT3 (AT3_out, AT2_out, Q2);
  not N4 (N4_out, Q3);
  and AT4 (AT4_out, AT3_out, N4_out);
  not NA (TQ7, AT4_out);
  and TM1 (TM1_out, Q0, TQ7);
  or TO1 (TQ5, TM1_out, AT4_out);
  and NR2 (NR2_out, Q0, Q1);
  and TM2 (TM2_out, NR2_out, TQ7);
  or TO2 (TQ6, TM2_out, AT4_out);
  and NR3 (NR3_out, NR2_out, Q2);
  and TM3 (TM3_out, NR3_out, TQ7);

  // Other names for the same wires on the sheet: TQ0 = Q1; TQ1 = Q2; TQ2 = CLK; TQ3 = RST; TQ4 = Q3; TQ8 = Q0
endmodule
