// Logisim project multiplier_2x2.circ as structural Verilog
module multiplier_2x2 (
  input  A0,
  input  A1,
  input  B0,
  input  B1,
  input  GND,
  output P0,
  output P1,
  output P2,
  output P3
);

  wire TQ4, TQ5, TQ6, TQ7, TQ8, TQ9, TQa, TQb, TQc, TQd, TQe, TQf, TQg, TQh, TQi, TQj, TQk;

  and MULP1 (P0, A0, B0);
  and MULA6 (TQd, GND, TQa);
  and MULP2 (TQ4, A1, B0);
  and MULB6 (TQe, TQb, TQc);
  and MULP3 (TQ5, A0, B1);
  or MULO6 (TQf, TQd, TQe);
  and MULP4 (TQa, A1, B1);
  or MULG6 (TQg, TQf, GND);
  xor MULX5 (TQ6, TQ4, TQ5);
  xor MULX7 (TQh, GND, GND);
  xor MULS5 (P1, TQ6, GND);
  xor MULS7 (P3, TQh, TQg);
  and MULA5 (TQ7, TQ4, TQ5);
  and MULA7 (TQi, GND, GND);
  and MULB5 (TQ8, GND, TQ6);
  and MULB7 (TQj, TQg, TQh);
  or MULO5 (TQ9, TQ7, TQ8);
  or MULO7 (TQk, TQi, TQj);
  or MULG5 (TQb, TQ9, GND);
  // OR_Gate MULG7 has open pins: in0=TQk, in1=GND, out=open
  xor MULX6 (TQc, GND, TQa);
  xor MULS6 (P2, TQc, TQb);

  // Other names for the same wires on the sheet: TQ0 = B0; TQ1 = A0; TQ2 = A1; TQ3 = B1; TQl = GND; TQm = P0;
  //   TQn = P1; TQo = P2; TQp = P3
endmodule
