// Logisim project multiplier_4x4.circ as structural Verilog
module multiplier_4x4 (
  input  A0,
  input  A1,
  input  A2,
  input  A3,
  input  B0,
  input  B1,
  input  B2,
  input  B3,
  input  GND,
  output P0,
  output P1,
  output P2,
  output P3,
  output P4,
  output P5,
  output P6,
  output P7
);

  wire MULA17_out, MULA18_out, MULA19_out, MULA20_out, MULA21_out, MULA22_out, MULA23_out, MULA24_out,
       MULA25_out, MULA26_out, MULA27_out, MULA28_out, MULA29_out, MULA30_out, MULA31_out, MULA32_out,
       MULA33_out, MULA34_out, MULB17_out, MULB18_out, MULB19_out, MULB20_out, MULB21_out, MULB22_out,
       MULB23_out, MULB24_out, MULB25_out, MULB26_out, MULB27_out, MULB28_out, MULB29_out, MULB30_out,
       MULB31_out, MULB32_out, MULB33_out, MULB34_out, MULG17_out, MULG18_out, MULG19_out, MULG20_out,
       MULG22_out, MULG23_out, MULG24_out, MULG25_out, MULG26_out, MULG28_out, MULG29_out, MULG30_out,
       MULG31_out, MULG32_out, MULG33_out, MULO17_out, MULO18_out, MULO19_out, MULO20_out, MULO21_out,
       MULO22_out, MULO23_out, MULO24_out, MULO25_out, MULO26_out, MULO27_out, MULO28_out, MULO29_out,
       MULO30_out, MULO31_out, MULO32_out, MULO33_out, MULO34_out, MULP2_out, MULP3_out, MULP4_out,
       MULP5_out, MULP6_out, MULP7_out, MULP8_out, MULP9_out, MULP10_out, MULP11_out, MULP12_out, MULP13_out,
       MULP14_out, MULP15_out, MULP16_out, MULS18_out, MULS19_out, MULS20_out, MULS21_out, MULS23_out,
       MULS24_out, MULS25_out, MULS26_out, MULS27_out, MULX17_out, MULX18_out, MULX19_out, MULX20_out,
       MULX21_out, MULX22_out, MULX23_out, MULX24_out, MULX25_out, MULX26_out, MULX27_out, MULX28_out,
       MULX29_out, MULX30_out, MULX31_out, MULX32_out, MULX33_out, MULX34_out;

  and MULP1 (P0, A0, B0);
  and MULP2 (MULP2_out, A1, B0);
  and MULP3 (MULP3_out, A2, B0);
  and MULP4 (MULP4_out, A3, B0);
  and MULP5 (MULP5_out, A0, B1);
  and MULP6 (MULP6_out, A1, B1);
  and MULP7 (MULP7_out, A2, B1);
  and MULP8 (MULP8_out, A3, B1);
  and MULP9 (MULP9_out, A0, B2);
  and MULP10 (MULP10_out, A1, B2);
  and MULP11 (MULP11_out, A2, B2);
  and MULP12 (MULP12_out, A3, B2);
  and MULP13 (MULP13_out, A0, B3);
  and MULP14 (MULP14_out, A1, B3);
  and MULP15 (MULP15_out, A2, B3);
  and MULP16 (MULP16_out, A3, B3);
  xor MULX17 (MULX17_out, MULP2_out, MULP5_out);
  xor MULS17 (P1, MULX17_out, GND);
  and MULA17 (MULA17_out, MULP2_out, MULP5_out);
  and MULB17 (MULB17_out, GND, MULX17_out);
  or MULO17 (MULO17_out, MULA17_out, MULB17_out);
  buf MULG17 (MULG17_out, MULO17_out);  // OR_Gate
  xor MULX18 (MULX18_out, MULP3_out, MULP6_out);
  xor MULS18 (MULS18_out, MULX18_out, MULG17_out);
  and MULA18 (MULA18_out, MULP3_out, MULP6_out);
  and MULB18 (MULB18_out, MULG17_out, MULX18_out);
  or MULO18 (MULO18_out, MULA18_out, MULB18_out);
  buf MULG18 (MULG18_out, MULO18_out);  // OR_Gate
  xor MULX19 (MULX19_out, MULP4_out, MULP7_out);
  xor MULS19 (MULS19_out, MULX19_out, MULG18_out);
  and MULA19 (MULA19_out, MULP4_out, MULP7_out);
  and MULB19 (MULB19_out, MULG18_out, MULX19_out);
  or MULO19 (MULO19_out, MULA19_out, MULB19_out);
  buf MULG19 (MULG19_out, MULO19_out);  // OR_Gate
  xor MULX20 (MULX20_out, GND, MULP8_out);
  xor MULS20 (MULS20_out, MULX20_out, MULG19_out);
  and MULA20 (MULA20_out, GND, MULP8_out);
  and MULB20 (MULB20_out, MULG19_out, MULX20_out);
  or MULO20 (MULO20_out, MULA20_out, MULB20_out);
  buf MULG20 (MULG20_out, MULO20_out);  // OR_Gate
  xor MULX21 (MULX21_out, GND, GND);
  xor MULS21 (MULS21_out, MULX21_out, MULG20_out);
  and MULA21 (MULA21_out, GND, GND);
  and MULB21 (MULB21_out, MULG20_out, MULX21_out);
  or MULO21 (MULO21_out, MULA21_out, MULB21_out);
  // OR_Gate MULG21 has open pins: in0=MULO21_out, out=open
  xor MULX22 (MULX22_out, MULS18_out, MULP9_out);
  xor MULS22 (P2, MULX22_out, GND);
  and MULA22 (MULA22_out, MULS18_out, MULP9_out);
  and MULB22 (MULB22_out, GND, MULX22_out);
  or MULO22 (MULO22_out, MULA22_out, MULB22_out);
  buf MULG22 (MULG22_out, MULO22_out);  // OR_Gate
  xor MULX23 (MULX23_out, MULS19_out, MULP10_out);
  xor MULS23 (MULS23_out, MULX23_out, MULG22_out);
  and MULA23 (MULA23_out, MULS19_out, MULP10_out);
  and MULB23 (MULB23_out, MULG22_out, MULX23_out);
  or MULO23 (MULO23_out, MULA23_out, MULB23_out);
  buf MULG23 (MULG23_out, MULO23_out);  // OR_Gate
  xor MULX24 (MULX24_out, MULS20_out, MULP11_out);
  xor MULS24 (MULS24_out, MULX24_out, MULG23_out);
  and MULA24 (MULA24_out, MULS20_out, MULP11_out);
  and MULB24 (MULB24_out, MULG23_out, MULX24_out);
  or MULO24 (MULO24_out, MULA24_out, MULB24_out);
  buf MULG24 (MULG24_out, MULO24_out);  // OR_Gate
  xor MULX25 (MULX25_out, MULS21_out, MULP12_out);
  xor MULS25 (MULS25_out, MULX25_out, MULG24_out);
  and MULA25 (MULA25_out, MULS21_out, MULP12_out);
  and MULB25 (MULB25_out, MULG24_out, MULX25_out);
  or MULO25 (MULO25_out, MULA25_out, MULB25_out);
  buf MULG25 (MULG25_out, MULO25_out);  // OR_Gate
  xor MULX26 (MULX26_out, GND, GND);
  xor MULS26 (MULS26_out, MULX26_out, MULG25_out);
  and MULA26 (MULA26_out, GND, GND);
  and MULB26 (MULB26_out, MULG25_out, MULX26_out);
  or MULO26 (MULO26_out, MULA26_out, MULB26_out);
  buf MULG26 (MULG26_out, MULO26_out);  // OR_Gate
  xor MULX27 (MULX27_out, GND, GND);
  xor MULS27 (MULS27_out, MULX27_out, MULG26_out);
  and MULA27 (MULA27_out, GND, GND);
  and MULB27 (MULB27_out, MULG26_out, MULX27_out);
  or MULO27 (MULO27_out, MULA27_out, MULB27_out);
  // OR_Gate MULG27 has open pins: in0=MULO27_out, out=open
  xor MULX28 (MULX28_out, MULS23_out, MULP13_out);
  xor MULS28 (P3, MULX28_out, GND);
  and MULA28 (MULA28_out, MULS23_out, MULP13_out);
  and MULB28 (MULB28_out, GND, MULX28_out);
  or MULO28 (MULO28_out, MULA28_out, MULB28_out);
  buf MULG28 (MULG28_out, MULO28_out);  // OR_Gate
  xor MULX29 (MULX29_out, MULS24_out, MULP14_out);
  xor MULS29 (P4, MULX29_out, MULG28_out);
  and MULA29 (MULA29_out, MULS24_out, MULP14_out);
  and MULB29 (MULB29_out, MULG28_out, MULX29_out);
  or MULO29 (MULO29_out, MULA29_out, MULB29_out);
  buf MULG29 (MULG29_out, MULO29_out);  // OR_Gate
  xor MULX30 (MULX30_out, MULS25_out, MULP15_out);
  xor MULS30 (P5, MULX30_out, MULG29_out);
  and MULA30 (MULA30_out, MULS25_out, MULP15_out);
  and MULB30 (MULB30_out, MULG29_out, MULX30_out);
  or MULO30 (MULO30_out, MULA30_out, MULB30_out);
  buf MULG30 (MULG30_out, MULO30_out);  // OR_Gate
  xor MULX31 (MULX31_out, MULS26_out, MULP16_out);
  xor MULS31 (P6, MULX31_out, MULG30_out);
  and MULA31 (MULA31_out, MULS26_out, MULP16_out);
  and MULB31 (MULB31_out, MULG30_out, MULX31_out);
  or MULO31 (MULO31_out, MULA31_out, MULB31_out);
  buf MULG31 (MULG31_out, MULO31_out);  // OR_Gate
  xor MULX32 (MULX32_out, MULS27_out, GND);
  xor MULS32 (P7, MULX32_out, MULG31_out);
  and MULA32 (MULA32_out, MULS27_out, GND);
  and MULB32 (MULB32_out, MULG31_out, MULX32_out);
  or MULO32 (MULO32_out, MULA32_out, MULB32_out);
  buf MULG32 (MULG32_out, MULO32_out);  // OR_Gate
  xor MULX33 (MULX33_out, GND, GND);
  // XOR_Gate MULS33 has open pins: in0=MULX33_out, in1=MULG32_out, out=open
  and MULA33 (MULA33_out, GND, GND);
  and MULB33 (MULB33_out, MULG32_out, MULX33_out);
  or MULO33 (MULO33_out, MULA33_out, MULB33_out);
  buf MULG33 (MULG33_out, MULO33_out);  // OR_Gate
  xor MULX34 (MULX34_out, GND, GND);
  // XOR_Gate MULS34 has open pins: in0=MULX34_out, in1=MULG33_out, out=open
  and MULA34 (MULA34_out, GND, GND);
  and MULB34 (MULB34_out, MULG33_out, MULX34_out);
  or MULO34 (MULO34_out, MULA34_out, MULB34_out);
  // OR_Gate MULG34 has open pins: in0=MULO34_out, out=open
endmodule
