// Logisim project multiplier_8x8.circ as structural Verilog
module multiplier_8x8 (
  input  A0,
  input  A1,
  input  A2,
  input  A3,
  input  A4,
  input  A5,
  input  A6,
  input  A7,
  input  B0,
  input  B1,
  input  B2,
  input  B3,
  input  B4,
  input  B5,
  input  B6,
  input  B7,
  input  GND,
  output P0,
  output P1,
  output P2,
  output P3,
  output P4,
  output P5,
  output P6,
  output P7,
  output P8,
  output P9,
  output P10,
  output P11,
  output P12,
  output P13,
  output P14,
  output P15
);

  wire MULA147_out, MULA148_out, MULB146_out, MULB147_out, MULB148_out, MULG146_out, MULG147_out,
       MULO146_out, MULO147_out, MULO148_out, MULX147_out, MULX148_out, TQ0, TQ1, TQ1a, TQ1b, TQ1c, TQ1d,
       TQ2, TQ2a, TQ2b, TQ2c, TQ2d, TQ2e, TQ2f, TQ2g, TQ2h, TQ2i, TQ2j, TQ2k, TQ2l, TQ2m, TQ2n, TQ2o, TQ2p,
       TQ2q, TQ2r, TQ2s, TQ2t, TQ2u, TQ2v, TQ2w, TQ2x, TQ2y, TQ2z, TQ3, TQ3a, TQ3b, TQ3c, TQ3d, TQ3e, TQ3f,
       TQ3g, TQ3h, TQ3i, TQ3j, TQ3k, TQ3l, TQ3m, TQ3n, TQ3o, TQ3p, TQ3q, TQ3r, TQ3s, TQ3t, TQ3u, TQ3v, TQ3w,
       TQ3x, TQ3y, TQ3z, TQ4, TQ4a, TQ4b, TQ4c, TQ4d, TQ4e, TQ4f, TQ4g, TQ4h, TQ4i, TQ4j, TQ4k, TQ4l, TQ4m,
       TQ4n, TQ4o, TQ4p, TQ4q, TQ4r, TQ4s, TQ4t, TQ4u, TQ4v, TQ4w, TQ4x, TQ4y, TQ4z, TQ5, TQ5a, TQ5b, TQ5c,
       TQ5d, TQ5e, TQ5f, TQ5g, TQ5h, TQ5i, TQ5j, TQ5k, TQ5l, TQ5m, TQ5n, TQ5o, TQ5p, TQ5q, TQ5r, TQ5s, TQ5t,
       TQ5u, TQ5v, TQ5w, TQ5x, TQ5y, TQ5z, TQ6, TQ6a, TQ6b, TQ6c, TQ6d, TQ6e, TQ6f, TQ6g, TQ6h, TQ6i, TQ6j,
       TQ6k, TQ6l, TQ6m, TQ6n, TQ6o, TQ6p, TQ6q, TQ6r, TQ6s, TQ6t, TQ6u, TQ6v, TQ6w, TQ6x, TQ6y, TQ6z, TQ7,
       TQ7a, TQ7b, TQ7c, TQ7d, TQ7e, TQ7f, TQ7g, TQ7h, TQ7i, TQ7j, TQ7k, TQ7l, TQ7m, TQ7n, TQ7o, TQ7p, TQ7q,
       TQ7r, TQ7s, TQ7t, TQ7u, TQ7v, TQ7w, TQ7x, TQ7y, TQ7z, TQ8, TQ8a, TQ8b, TQ8c, TQ8d, TQ8e, TQ8f, TQ8g,
       TQ8h, TQ8i, TQ8j, TQ8k, TQ8l, TQ8m, TQ8n, TQ8o, TQ8p, TQ8q, TQ8r, TQ8s, TQ8t, TQ8u, TQ8v, TQ8w, TQ8x,
       TQ8y, TQ8z, TQ9, TQ9a, TQ9b, TQ9c, TQ9d, TQ9e, TQ9f, TQ9g, TQ9h, TQ9i, TQ9j, TQ9k, TQ9l, TQ9m, TQ9n,
       TQ9o, TQ9p, TQ9q, TQ9r, TQ9s, TQ9t, TQ9u, TQ9v, TQ9w, TQ9x, TQ9y, TQ9z, TQ10, TQ11, TQ13, TQ14, TQ15,
       TQ16, TQ17, TQ18, TQ26, TQ27, TQ28, TQ29, TQ30, TQ31, TQ32, TQ33, TQ34, TQ35, TQ36, TQ37, TQ38, TQ39,
       TQ40, TQ41, TQ42, TQ43, TQ44, TQ45, TQ46, TQ47, TQ48, TQ49, TQ50, TQ51, TQ52, TQ53, TQ54, TQ55, TQ56,
       TQ57, TQ58, TQ59, TQ60, TQ61, TQ62, TQ63, TQ64, TQ65, TQ66, TQ67, TQ68, TQ69, TQ70, TQ71, TQ72, TQ73,
       TQ74, TQ75, TQ76, TQ77, TQ78, TQ79, TQ80, TQ81, TQ82, TQ83, TQ84, TQ85, TQ86, TQ87, TQ88, TQ89, TQ90,
       TQ91, TQ92, TQ93, TQ94, TQ95, TQ96, TQ97, TQ98, TQ99, TQa0, TQa1, TQa2, TQa3, TQa4, TQa5, TQa6, TQa7,
       TQa8, TQa9, TQaa, TQab, TQac, TQad, TQae, TQaf, TQag, TQah, TQai, TQaj, TQak, TQal, TQam, TQan, TQao,
       TQap, TQaq, TQar, TQas, TQat, TQau, TQav, TQaw, TQax, TQay, TQaz, TQb, TQb0, TQb1, TQb2, TQb3, TQb4,
       TQb5, TQb6, TQb7, TQb8, TQb9, TQba, TQbb, TQbc, TQbd, TQbe, TQbf, TQbg, TQbh, TQbi, TQbj, TQbk, TQbl,
       TQbm, TQbn, TQbo, TQbp, TQbq, TQbr, TQbs, TQbt, TQbu, TQbv, TQbw, TQbx, TQby, TQbz, TQc, TQc0, TQc1,
       TQc2, TQc3, TQc4, TQc5, TQc6, TQc7, TQc8, TQc9, TQca, TQcb, TQcc, TQcd, TQce, TQcf, TQcg, TQch, TQci,
       TQcj, TQck, TQcl, TQcm, TQcn, TQco, TQcp, TQcq, TQcr, TQcs, TQct, TQcu, TQcv, TQcw, TQcx, TQcy, TQcz,
       TQd, TQd0, TQd1, TQd2, TQd3, TQd4, TQd5, TQd6, TQd7, TQd8, TQd9, TQda, TQdb, TQdc, TQdd, TQde, TQdf,
       TQdg, TQdh, TQdi, TQdj, TQdk, TQdl, TQdm, TQdn, TQdo, TQdp, TQdq, TQdr, TQds, TQdt, TQdu, TQdv, TQdw,
       TQdx, TQdy, TQdz, TQe, TQe0, TQe1, TQe2, TQe3, TQe4, TQe5, TQe6, TQe7, TQe8, TQe9, TQea, TQeb, TQec,
       TQed, TQee, TQef, TQeg, TQeh, TQei, TQej, TQek, TQel, TQem, TQen, TQeo, TQep, TQeq, TQer, TQes, TQet,
       TQeu, TQev, TQew, TQex, TQey, TQez, TQf, TQf0, TQf1, TQf2, TQf3, TQf4, TQf5, TQf6, TQf7, TQf8, TQf9,
       TQfa, TQfb, TQfc, TQfd, TQfe, TQff, TQfg, TQfh, TQfi, TQfj, TQg, TQh, TQj, TQk, TQl, TQm, TQn, TQo,
       TQp, TQq, TQr, TQt, TQu, TQv, TQw, TQx, TQy, TQz;

  and MULP1 (P0, A0, B0);
  and MULP2 (TQ26, A1, B0);
  and MULP3 (TQ2c, A2, B0);
  and MULP4 (TQ2j, A3, B0);
  and MULP5 (TQ2q, A4, B0);
  and MULP6 (TQ2x, A5, B0);
  and MULP7 (TQ34, A6, B0);
  and MULP8 (TQ3b, A7, B0);
  and MULP9 (TQ27, A0, B1);
  and MULP10 (TQ2d, A1, B1);
  and MULP11 (TQ2k, A2, B1);
  and MULP12 (TQ2r, A3, B1);
  and MULP13 (TQ2y, A4, B1);
  and MULP14 (TQ35, A5, B1);
  and MULP15 (TQ3c, A6, B1);
  and MULP16 (TQ3i, A7, B1);
  and MULP17 (TQ3u, A0, B2);
  and MULP18 (TQ40, A1, B2);
  and MULP19 (TQ47, A2, B2);
  and MULP20 (TQ4e, A3, B2);
  and MULP21 (TQ4l, A4, B2);
  and MULP22 (TQ4s, A5, B2);
  and MULP23 (TQ4z, A6, B2);
  and MULP24 (TQ56, A7, B2);
  and MULP25 (TQ5n, A0, B3);
  and MULP26 (TQ5t, A1, B3);
  and MULP27 (TQ60, A2, B3);
  and MULP28 (TQ67, A3, B3);
  and MULP29 (TQ6e, A4, B3);
  and MULP30 (TQ6l, A5, B3);
  and MULP31 (TQ6s, A6, B3);
  and MULP32 (TQ6z, A7, B3);
  and MULP33 (TQ7m, A0, B4);
  and MULP34 (TQ7s, A1, B4);
  and MULP35 (TQ7z, A2, B4);
  and MULP36 (TQ86, A3, B4);
  and MULP37 (TQ8d, A4, B4);
  and MULP38 (TQ8k, A5, B4);
  and MULP39 (TQ8r, A6, B4);
  and MULP40 (TQ8y, A7, B4);
  and MULP41 (TQ9r, A0, B5);
  and MULP42 (TQ9x, A1, B5);
  and MULP43 (TQa4, A2, B5);
  and MULP44 (TQab, A3, B5);
  and MULP45 (TQai, A4, B5);
  and MULP46 (TQap, A5, B5);
  and MULP47 (TQaw, A6, B5);
  and MULP48 (TQb3, A7, B5);
  and MULP49 (TQc2, A0, B6);
  and MULP50 (TQc8, A1, B6);
  and MULP51 (TQcf, A2, B6);
  and MULP52 (TQcm, A3, B6);
  and MULP53 (TQct, A4, B6);
  and MULP54 (TQd0, A5, B6);
  and MULP55 (TQd7, A6, B6);
  and MULP56 (TQde, A7, B6);
  and MULP57 (TQej, A0, B7);
  and MULP58 (TQep, A1, B7);
  and MULP59 (TQew, A2, B7);
  and MULP60 (TQf3, A3, B7);
  and MULP61 (TQfa, A4, B7);
  and MULP62 (TQfh, A5, B7);
  and MULP63 (TQ4, A6, B7);
  and MULP64 (TQc, A7, B7);
  xor MULX65 (TQ28, TQ26, TQ27);
  xor MULS65 (P1, TQ28, GND);
  and MULA65 (TQ29, TQ26, TQ27);
  and MULB65 (TQ2a, GND, TQ28);
  or MULO65 (TQ2b, TQ29, TQ2a);
  or MULG65 (TQ2e, TQ2b, GND);
  xor MULX66 (TQ2f, TQ2c, TQ2d);
  xor MULS66 (TQ3t, TQ2f, TQ2e);
  and MULA66 (TQ2g, TQ2c, TQ2d);
  and MULB66 (TQ2h, TQ2e, TQ2f);
  or MULO66 (TQ2i, TQ2g, TQ2h);
  or MULG66 (TQ2l, TQ2i, GND);
  xor MULX67 (TQ2m, TQ2j, TQ2k);
  xor MULS67 (TQ3z, TQ2m, TQ2l);
  and MULA67 (TQ2n, TQ2j, TQ2k);
  and MULB67 (TQ2o, TQ2l, TQ2m);
  or MULO67 (TQ2p, TQ2n, TQ2o);
  or MULG67 (TQ2s, TQ2p, GND);
  xor MULX68 (TQ2t, TQ2q, TQ2r);
  xor MULS68 (TQ46, TQ2t, TQ2s);
  and MULA68 (TQ2u, TQ2q, TQ2r);
  and MULB68 (TQ2v, TQ2s, TQ2t);
  or MULO68 (TQ2w, TQ2u, TQ2v);
  or MULG68 (TQ2z, TQ2w, GND);
  xor MULX69 (TQ30, TQ2x, TQ2y);
  xor MULS69 (TQ4d, TQ30, TQ2z);
  and MULA69 (TQ31, TQ2x, TQ2y);
  and MULB69 (TQ32, TQ2z, TQ30);
  or MULO69 (TQ33, TQ31, TQ32);
  or MULG69 (TQ36, TQ33, GND);
  xor MULX70 (TQ37, TQ34, TQ35);
  xor MULS70 (TQ4k, TQ37, TQ36);
  and MULA70 (TQ38, TQ34, TQ35);
  and MULB70 (TQ39, TQ36, TQ37);
  or MULO70 (TQ3a, TQ38, TQ39);
  or MULG70 (TQ3d, TQ3a, GND);
  xor MULX71 (TQ3e, TQ3b, TQ3c);
  xor MULS71 (TQ4r, TQ3e, TQ3d);
  and MULA71 (TQ3f, TQ3b, TQ3c);
  and MULB71 (TQ3g, TQ3d, TQ3e);
  or MULO71 (TQ3h, TQ3f, TQ3g);
  or MULG71 (TQ3j, TQ3h, GND);
  xor MULX72 (TQ3k, GND, TQ3i);
  xor MULS72 (TQ4y, TQ3k, TQ3j);
  and MULA72 (TQ3l, GND, TQ3i);
  and MULB72 (TQ3m, TQ3j, TQ3k);
  or MULO72 (TQ3n, TQ3l, TQ3m);
  or MULG72 (TQ3o, TQ3n, GND);
  xor MULX73 (TQ3p, GND, GND);
  xor MULS73 (TQ55, TQ3p, TQ3o);
  and MULA73 (TQ3q, GND, GND);
  and MULB73 (TQ3r, TQ3o, TQ3p);
  or MULO73 (TQ3s, TQ3q, TQ3r);
  // OR_Gate MULG73 has open pins: in0=TQ3s, in1=GND, out=open
  xor MULX74 (TQ3v, TQ3t, TQ3u);
  xor MULS74 (P2, TQ3v, GND);
  and MULA74 (TQ3w, TQ3t, TQ3u);
  and MULB74 (TQ3x, GND, TQ3v);
  or MULO74 (TQ3y, TQ3w, TQ3x);
  or MULG74 (TQ41, TQ3y, GND);
  xor MULX75 (TQ42, TQ3z, TQ40);
  xor MULS75 (TQ5m, TQ42, TQ41);
  and MULA75 (TQ43, TQ3z, TQ40);
  and MULB75 (TQ44, TQ41, TQ42);
  or MULO75 (TQ45, TQ43, TQ44);
  or MULG75 (TQ48, TQ45, GND);
  xor MULX76 (TQ49, TQ46, TQ47);
  xor MULS76 (TQ5s, TQ49, TQ48);
  and MULA76 (TQ4a, TQ46, TQ47);
  and MULB76 (TQ4b, TQ48, TQ49);
  or MULO76 (TQ4c, TQ4a, TQ4b);
  or MULG76 (TQ4f, TQ4c, GND);
  xor MULX77 (TQ4g, TQ4d, TQ4e);
  xor MULS77 (TQ5z, TQ4g, TQ4f);
  and MULA77 (TQ4h, TQ4d, TQ4e);
  and MULB77 (TQ4i, TQ4f, TQ4g);
  or MULO77 (TQ4j, TQ4h, TQ4i);
  or MULG77 (TQ4m, TQ4j, GND);
  xor MULX78 (TQ4n, TQ4k, TQ4l);
  xor MULS78 (TQ66, TQ4n, TQ4m);
  and MULA78 (TQ4o, TQ4k, TQ4l);
  and MULB78 (TQ4p, TQ4m, TQ4n);
  or MULO78 (TQ4q, TQ4o, TQ4p);
  or MULG78 (TQ4t, TQ4q, GND);
  xor MULX79 (TQ4u, TQ4r, TQ4s);
  xor MULS79 (TQ6d, TQ4u, TQ4t);
  and MULA79 (TQ4v, TQ4r, TQ4s);
  and MULB79 (TQ4w, TQ4t, TQ4u);
  or MULO79 (TQ4x, TQ4v, TQ4w);
  or MULG79 (TQ50, TQ4x, GND);
  xor MULX80 (TQ51, TQ4y, TQ4z);
  xor MULS80 (TQ6k, TQ51, TQ50);
  and MULA80 (TQ52, TQ4y, TQ4z);
  and MULB80 (TQ53, TQ50, TQ51);
  or MULO80 (TQ54, TQ52, TQ53);
  or MULG80 (TQ57, TQ54, GND);
  xor MULX81 (TQ58, TQ55, TQ56);
  xor MULS81 (TQ6r, TQ58, TQ57);
  and MULA81 (TQ59, TQ55, TQ56);
  and MULB81 (TQ5a, TQ57, TQ58);
  or MULO81 (TQ5b, TQ59, TQ5a);
  or MULG81 (TQ5c, TQ5b, GND);
  xor MULX82 (TQ5d, GND, GND);
  xor MULS82 (TQ6y, TQ5d, TQ5c);
  and MULA82 (TQ5e, GND, GND);
  and MULB82 (TQ5f, TQ5c, TQ5d);
  or MULO82 (TQ5g, TQ5e, TQ5f);
  or MULG82 (TQ5h, TQ5g, GND);
  xor MULX83 (TQ5i, GND, GND);
  xor MULS83 (TQ75, TQ5i, TQ5h);
  and MULA83 (TQ5j, GND, GND);
  and MULB83 (TQ5k, TQ5h, TQ5i);
  or MULO83 (TQ5l, TQ5j, TQ5k);
  // OR_Gate MULG83 has open pins: in0=TQ5l, in1=GND, out=open
  xor MULX84 (TQ5o, TQ5m, TQ5n);
  xor MULS84 (P3, TQ5o, GND);
  and MULA84 (TQ5p, TQ5m, TQ5n);
  and MULB84 (TQ5q, GND, TQ5o);
  or MULO84 (TQ5r, TQ5p, TQ5q);
  or MULG84 (TQ5u, TQ5r, GND);
  xor MULX85 (TQ5v, TQ5s, TQ5t);
  xor MULS85 (TQ7l, TQ5v, TQ5u);
  and MULA85 (TQ5w, TQ5s, TQ5t);
  and MULB85 (TQ5x, TQ5u, TQ5v);
  or MULO85 (TQ5y, TQ5w, TQ5x);
  or MULG85 (TQ61, TQ5y, GND);
  xor MULX86 (TQ62, TQ5z, TQ60);
  xor MULS86 (TQ7r, TQ62, TQ61);
  and MULA86 (TQ63, TQ5z, TQ60);
  and MULB86 (TQ64, TQ61, TQ62);
  or MULO86 (TQ65, TQ63, TQ64);
  or MULG86 (TQ68, TQ65, GND);
  xor MULX87 (TQ69, TQ66, TQ67);
  xor MULS87 (TQ7y, TQ69, TQ68);
  and MULA87 (TQ6a, TQ66, TQ67);
  and MULB87 (TQ6b, TQ68, TQ69);
  or MULO87 (TQ6c, TQ6a, TQ6b);
  or MULG87 (TQ6f, TQ6c, GND);
  xor MULX88 (TQ6g, TQ6d, TQ6e);
  xor MULS88 (TQ85, TQ6g, TQ6f);
  and MULA88 (TQ6h, TQ6d, TQ6e);
  and MULB88 (TQ6i, TQ6f, TQ6g);
  or MULO88 (TQ6j, TQ6h, TQ6i);
  or MULG88 (TQ6m, TQ6j, GND);
  xor MULX89 (TQ6n, TQ6k, TQ6l);
  xor MULS89 (TQ8c, TQ6n, TQ6m);
  and MULA89 (TQ6o, TQ6k, TQ6l);
  and MULB89 (TQ6p, TQ6m, TQ6n);
  or MULO89 (TQ6q, TQ6o, TQ6p);
  or MULG89 (TQ6t, TQ6q, GND);
  xor MULX90 (TQ6u, TQ6r, TQ6s);
  xor MULS90 (TQ8j, TQ6u, TQ6t);
  and MULA90 (TQ6v, TQ6r, TQ6s);
  and MULB90 (TQ6w, TQ6t, TQ6u);
  or MULO90 (TQ6x, TQ6v, TQ6w);
  or MULG90 (TQ70, TQ6x, GND);
  xor MULX91 (TQ71, TQ6y, TQ6z);
  xor MULS91 (TQ8q, TQ71, TQ70);
  and MULA91 (TQ72, TQ6y, TQ6z);
  and MULB91 (TQ73, TQ70, TQ71);
  or MULO91 (TQ74, TQ72, TQ73);
  or MULG91 (TQ76, TQ74, GND);
  xor MULX92 (TQ77, TQ75, GND);
  xor MULS92 (TQ8x, TQ77, TQ76);
  and MULA92 (TQ78, TQ75, GND);
  and MULB92 (TQ79, TQ76, TQ77);
  or MULO92 (TQ7a, TQ78, TQ79);
  or MULG92 (TQ7b, TQ7a, GND);
  xor MULX93 (TQ7c, GND, GND);
  xor MULS93 (TQ94, TQ7c, TQ7b);
  and MULA93 (TQ7d, GND, GND);
  and MULB93 (TQ7e, TQ7b, TQ7c);
  or MULO93 (TQ7f, TQ7d, TQ7e);
  or MULG93 (TQ7g, TQ7f, GND);
  xor MULX94 (TQ7h, GND, GND);
  xor MULS94 (TQ9a, TQ7h, TQ7g);
  and MULA94 (TQ7i, GND, GND);
  and MULB94 (TQ7j, TQ7g, TQ7h);
  or MULO94 (TQ7k, TQ7i, TQ7j);
  // OR_Gate MULG94 has open pins: in0=TQ7k, in1=GND, out=open
  xor MULX95 (TQ7n, TQ7l, TQ7m);
  xor MULS95 (P4, TQ7n, GND);
  and MULA95 (TQ7o, TQ7l, TQ7m);
  and MULB95 (TQ7p, GND, TQ7n);
  or MULO95 (TQ7q, TQ7o, TQ7p);
  or MULG95 (TQ7t, TQ7q, GND);
  xor MULX96 (TQ7u, TQ7r, TQ7s);
  xor MULS96 (TQ9q, TQ7u, TQ7t);
  and MULA96 (TQ7v, TQ7r, TQ7s);
  and MULB96 (TQ7w, TQ7t, TQ7u);
  or MULO96 (TQ7x, TQ7v, TQ7w);
  or MULG96 (TQ80, TQ7x, GND);
  xor MULX97 (TQ81, TQ7y, TQ7z);
  xor MULS97 (TQ9w, TQ81, TQ80);
  and MULA97 (TQ82, TQ7y, TQ7z);
  and MULB97 (TQ83, TQ80, TQ81);
  or MULO97 (TQ84, TQ82, TQ83);
  or MULG97 (TQ87, TQ84, GND);
  xor MULX98 (TQ88, TQ85, TQ86);
  xor MULS98 (TQa3, TQ88, TQ87);
  and MULA98 (TQ89, TQ85, TQ86);
  and MULB98 (TQ8a, TQ87, TQ88);
  or MULO98 (TQ8b, TQ89, TQ8a);
  or MULG98 (TQ8e, TQ8b, GND);
  xor MULX99 (TQ8f, TQ8c, TQ8d);
  xor MULS99 (TQaa, TQ8f, TQ8e);
  and MULA99 (TQ8g, TQ8c, TQ8d);
  and MULB99 (TQ8h, TQ8e, TQ8f);
  or MULO99 (TQ8i, TQ8g, TQ8h);
  or MULG99 (TQ8l, TQ8i, GND);
  xor MULX100 (TQ8m, TQ8j, TQ8k);
  xor MULS100 (TQah, TQ8m, TQ8l);
  and MULA100 (TQ8n, TQ8j, TQ8k);
  and MULB100 (TQ8o, TQ8l, TQ8m);
  or MULO100 (TQ8p, TQ8n, TQ8o);
  or MULG100 (TQ8s, TQ8p, GND);
  xor MULX101 (TQ8t, TQ8q, TQ8r);
  xor MULS101 (TQao, TQ8t, TQ8s);
  and MULA101 (TQ8u, TQ8q, TQ8r);
  and MULB101 (TQ8v, TQ8s, TQ8t);
  or MULO101 (TQ8w, TQ8u, TQ8v);
  or MULG101 (TQ8z, TQ8w, GND);
  xor MULX102 (TQ90, TQ8x, TQ8y);
  xor MULS102 (TQav, TQ90, TQ8z);
  and MULA102 (TQ91, TQ8x, TQ8y);
  and MULB102 (TQ92, TQ8z, TQ90);
  or MULO102 (TQ93, TQ91, TQ92);
  or MULG102 (TQ95, TQ93, GND);
  xor MULX103 (TQ96, TQ94, GND);
  xor MULS103 (TQb2, TQ96, TQ95);
  and MULA103 (TQ97, TQ94, GND);
  and MULB103 (TQ98, TQ95, TQ96);
  or MULO103 (TQ99, TQ97, TQ98);
  or MULG103 (TQ9b, TQ99, GND);
  xor MULX104 (TQ9c, TQ9a, GND);
  xor MULS104 (TQb9, TQ9c, TQ9b);
  and MULA104 (TQ9d, TQ9a, GND);
  and MULB104 (TQ9e, TQ9b, TQ9c);
  or MULO104 (TQ9f, TQ9d, TQ9e);
  or MULG104 (TQ9g, TQ9f, GND);
  xor MULX105 (TQ9h, GND, GND);
  xor MULS105 (TQbf, TQ9h, TQ9g);
  and MULA105 (TQ9i, GND, GND);
  and MULB105 (TQ9j, TQ9g, TQ9h);
  or MULO105 (TQ9k, TQ9i, TQ9j);
  or MULG105 (TQ9l, TQ9k, GND);
  xor MULX106 (TQ9m, GND, GND);
  xor MULS106 (TQbl, TQ9m, TQ9l);
  and MULA106 (TQ9n, GND, GND);
  and MULB106 (TQ9o, TQ9l, TQ9m);
  or MULO106 (TQ9p, TQ9n, TQ9o);
  // OR_Gate MULG106 has open pins: in0=TQ9p, in1=GND, out=open
  xor MULX107 (TQ9s, TQ9q, TQ9r);
  xor MULS107 (P5, TQ9s, GND);
  and MULA107 (TQ9t, TQ9q, TQ9r);
  and MULB107 (TQ9u, GND, TQ9s);
  or MULO107 (TQ9v, TQ9t, TQ9u);
  or MULG107 (TQ9y, TQ9v, GND);
  xor MULX108 (TQ9z, TQ9w, TQ9x);
  xor MULS108 (TQc1, TQ9z, TQ9y);
  and MULA108 (TQa0, TQ9w, TQ9x);
  and MULB108 (TQa1, TQ9y, TQ9z);
  or MULO108 (TQa2, TQa0, TQa1);
  or MULG108 (TQa5, TQa2, GND);
  xor MULX109 (TQa6, TQa3, TQa4);
  xor MULS109 (TQc7, TQa6, TQa5);
  and MULA109 (TQa7, TQa3, TQa4);
  and MULB109 (TQa8, TQa5, TQa6);
  or MULO109 (TQa9, TQa7, TQa8);
  or MULG109 (TQac, TQa9, GND);
  xor MULX110 (TQad, TQaa, TQab);
  xor MULS110 (TQce, TQad, TQac);
  and MULA110 (TQae, TQaa, TQab);
  and MULB110 (TQaf, TQac, TQad);
  or MULO110 (TQag, TQae, TQaf);
  or MULG110 (TQaj, TQag, GND);
  xor MULX111 (TQak, TQah, TQai);
  xor MULS111 (TQcl, TQak, TQaj);
  and MULA111 (TQal, TQah, TQai);
  and MULB111 (TQam, TQaj, TQak);
  or MULO111 (TQan, TQal, TQam);
  or MULG111 (TQaq, TQan, GND);
  xor MULX112 (TQar, TQao, TQap);
  xor MULS112 (TQcs, TQar, TQaq);
  and MULA112 (TQas, TQao, TQap);
  and MULB112 (TQat, TQaq, TQar);
  or MULO112 (TQau, TQas, TQat);
  or MULG112 (TQax, TQau, GND);
  xor MULX113 (TQay, TQav, TQaw);
  xor MULS113 (TQcz, TQay, TQax);
  and MULA113 (TQaz, TQav, TQaw);
  and MULB113 (TQb0, TQax, TQay);
  or MULO113 (TQb1, TQaz, TQb0);
  or MULG113 (TQb4, TQb1, GND);
  xor MULX114 (TQb5, TQb2, TQb3);
  xor MULS114 (TQd6, TQb5, TQb4);
  and MULA114 (TQb6, TQb2, TQb3);
  and MULB114 (TQb7, TQb4, TQb5);
  or MULO114 (TQb8, TQb6, TQb7);
  or MULG114 (TQba, TQb8, GND);
  xor MULX115 (TQbb, TQb9, GND);
  xor MULS115 (TQdd, TQbb, TQba);
  and MULA115 (TQbc, TQb9, GND);
  and MULB115 (TQbd, TQba, TQbb);
  or MULO115 (TQbe, TQbc, TQbd);
  or MULG115 (TQbg, TQbe, GND);
  xor MULX116 (TQbh, TQbf, GND);
  xor MULS116 (TQdk, TQbh, TQbg);
  and MULA116 (TQbi, TQbf, GND);
  and MULB116 (TQbj, TQbg, TQbh);
  or MULO116 (TQbk, TQbi, TQbj);
  or MULG116 (TQbm, TQbk, GND);
  xor MULX117 (TQbn, TQbl, GND);
  xor MULS117 (TQdq, TQbn, TQbm);
  and MULA117 (TQbo, TQbl, GND);
  and MULB117 (TQbp, TQbm, TQbn);
  or MULO117 (TQbq, TQbo, TQbp);
  or MULG117 (TQbr, TQbq, GND);
  xor MULX118 (TQbs, GND, GND);
  xor MULS118 (TQdw, TQbs, TQbr);
  and MULA118 (TQbt, GND, GND);
  and MULB118 (TQbu, TQbr, TQbs);
  or MULO118 (TQbv, TQbt, TQbu);
  or MULG118 (TQbw, TQbv, GND);
  xor MULX119 (TQbx, GND, GND);
  xor MULS119 (TQe2, TQbx, TQbw);
  and MULA119 (TQby, GND, GND);
  and MULB119 (TQbz, TQbw, TQbx);
  or MULO119 (TQc0, TQby, TQbz);
  // OR_Gate MULG119 has open pins: in0=TQc0, in1=GND, out=open
  xor MULX120 (TQc3, TQc1, TQc2);
  xor MULS120 (P6, TQc3, GND);
  and MULA120 (TQc4, TQc1, TQc2);
  and MULB120 (TQc5, GND, TQc3);
  or MULO120 (TQc6, TQc4, TQc5);
  or MULG120 (TQc9, TQc6, GND);
  xor MULX121 (TQca, TQc7, TQc8);
  xor MULS121 (TQei, TQca, TQc9);
  and MULA121 (TQcb, TQc7, TQc8);
  and MULB121 (TQcc, TQc9, TQca);
  or MULO121 (TQcd, TQcb, TQcc);
  or MULG121 (TQcg, TQcd, GND);
  xor MULX122 (TQch, TQce, TQcf);
  xor MULS122 (TQeo, TQch, TQcg);
  and MULA122 (TQci, TQce, TQcf);
  and MULB122 (TQcj, TQcg, TQch);
  or MULO122 (TQck, TQci, TQcj);
  or MULG122 (TQcn, TQck, GND);
  xor MULX123 (TQco, TQcl, TQcm);
  xor MULS123 (TQev, TQco, TQcn);
  and MULA123 (TQcp, TQcl, TQcm);
  and MULB123 (TQcq, TQcn, TQco);
  or MULO123 (TQcr, TQcp, TQcq);
  or MULG123 (TQcu, TQcr, GND);
  xor MULX124 (TQcv, TQcs, TQct);
  xor MULS124 (TQf2, TQcv, TQcu);
  and MULA124 (TQcw, TQcs, TQct);
  and MULB124 (TQcx, TQcu, TQcv);
  or MULO124 (TQcy, TQcw, TQcx);
  or MULG124 (TQd1, TQcy, GND);
  xor MULX125 (TQd2, TQcz, TQd0);
  xor MULS125 (TQf9, TQd2, TQd1);
  and MULA125 (TQd3, TQcz, TQd0);
  and MULB125 (TQd4, TQd1, TQd2);
  or MULO125 (TQd5, TQd3, TQd4);
  or MULG125 (TQd8, TQd5, GND);
  xor MULX126 (TQd9, TQd6, TQd7);
  xor MULS126 (TQfg, TQd9, TQd8);
  and MULA126 (TQda, TQd6, TQd7);
  and MULB126 (TQdb, TQd8, TQd9);
  or MULO126 (TQdc, TQda, TQdb);
  or MULG126 (TQdf, TQdc, GND);
  xor MULX127 (TQdg, TQdd, TQde);
  xor MULS127 (TQ3, TQdg, TQdf);
  and MULA127 (TQdh, TQdd, TQde);
  and MULB127 (TQdi, TQdf, TQdg);
  or MULO127 (TQdj, TQdh, TQdi);
  or MULG127 (TQdl, TQdj, GND);
  xor MULX128 (TQdm, TQdk, GND);
  xor MULS128 (TQb, TQdm, TQdl);
  and MULA128 (TQdn, TQdk, GND);
  and MULB128 (TQdo, TQdl, TQdm);
  or MULO128 (TQdp, TQdn, TQdo);
  or MULG128 (TQdr, TQdp, GND);
  xor MULX129 (TQds, TQdq, GND);
  xor MULS129 (TQj, TQds, TQdr);
  and MULA129 (TQdt, TQdq, GND);
  and MULB129 (TQdu, TQdr, TQds);
  or MULO129 (TQdv, TQdt, TQdu);
  or MULG129 (TQdx, TQdv, GND);
  xor MULX130 (TQdy, TQdw, GND);
  xor MULS130 (TQp, TQdy, TQdx);
  and MULA130 (TQdz, TQdw, GND);
  and MULB130 (TQe0, TQdx, TQdy);
  or MULO130 (TQe1, TQdz, TQe0);
  or MULG130 (TQe3, TQe1, GND);
  xor MULX131 (TQe4, TQe2, GND);
  xor MULS131 (TQw, TQe4, TQe3);
  and MULA131 (TQe5, TQe2, GND);
  and MULB131 (TQe6, TQe3, TQe4);
  or MULO131 (TQe7, TQe5, TQe6);
  or MULG131 (TQe8, TQe7, GND);
  xor MULX132 (TQe9, GND, GND);
  xor MULS132 (TQ13, TQe9, TQe8);
  and MULA132 (TQea, GND, GND);
  and MULB132 (TQeb, TQe8, TQe9);
  or MULO132 (TQec, TQea, TQeb);
  or MULG132 (TQed, TQec, GND);
  xor MULX133 (TQee, GND, GND);
  xor MULS133 (TQ1a, TQee, TQed);
  and MULA133 (TQef, GND, GND);
  and MULB133 (TQeg, TQed, TQee);
  or MULO133 (TQeh, TQef, TQeg);
  // OR_Gate MULG133 has open pins: in0=TQeh, in1=GND, out=open
  xor MULX134 (TQek, TQei, TQej);
  xor MULS134 (P7, TQek, GND);
  and MULA134 (TQel, TQei, TQej);
  and MULB134 (TQem, GND, TQek);
  or MULO134 (TQen, TQel, TQem);
  or MULG134 (TQeq, TQen, GND);
  xor MULX135 (TQer, TQeo, TQep);
  xor MULS135 (P8, TQer, TQeq);
  and MULA135 (TQes, TQeo, TQep);
  and MULB135 (TQet, TQeq, TQer);
  or MULO135 (TQeu, TQes, TQet);
  or MULG135 (TQex, TQeu, GND);
  xor MULX136 (TQey, TQev, TQew);
  xor MULS136 (P9, TQey, TQex);
  and MULA136 (TQez, TQev, TQew);
  and MULB136 (TQf0, TQex, TQey);
  or MULO136 (TQf1, TQez, TQf0);
  or MULG136 (TQf4, TQf1, GND);
  xor MULX137 (TQf5, TQf2, TQf3);
  xor MULS137 (P10, TQf5, TQf4);
  and MULA137 (TQf6, TQf2, TQf3);
  and MULB137 (TQf7, TQf4, TQf5);
  or MULO137 (TQf8, TQf6, TQf7);
  or MULG137 (TQfb, TQf8, GND);
  xor MULX138 (TQfc, TQf9, TQfa);
  xor MULS138 (P11, TQfc, TQfb);
  and MULA138 (TQfd, TQf9, TQfa);
  and MULB138 (TQfe, TQfb, TQfc);
  or MULO138 (TQff, TQfd, TQfe);
  or MULG138 (TQfi, TQff, GND);
  xor MULX139 (TQfj, TQfg, TQfh);
  xor MULS139 (P12, TQfj, TQfi);
  and MULA139 (TQ0, TQfg, TQfh);
  and MULB139 (TQ1, TQfi, TQfj);
  or MULO139 (TQ2, TQ0, TQ1);
  or MULG139 (TQ5, TQ2, GND);
  xor MULX140 (TQ6, TQ3, TQ4);
  xor MULS140 (P13, TQ6, TQ5);
  and MULA140 (TQ7, TQ3, TQ4);
  and MULB140 (TQ8, TQ5, TQ6);
  or MULO140 (TQ9, TQ7, TQ8);
  or MULG140 (TQd, TQ9, GND);
  xor MULX141 (TQe, TQb, TQc);
  xor MULS141 (P14, TQe, TQd);
  and MULA141 (TQf, TQb, TQc);
  and MULB141 (TQg, TQd, TQe);
  or MULO141 (TQh, TQf, TQg);
  or MULG141 (TQk, TQh, GND);
  xor MULX142 (TQl, TQj, GND);
  xor MULS142 (P15, TQl, TQk);
  and MULA142 (TQm, TQj, GND);
  and MULB142 (TQn, TQk, TQl);
  or MULO142 (TQo, TQm, TQn);
  or MULG142 (TQq, TQo, GND);
  xor MULX143 (TQr, TQp, GND);
  // XOR_Gate MULS143 has open pins: in0=TQr, in1=TQq, out=open
  and MULA143 (TQt, TQp, GND);
  and MULB143 (TQu, TQq, TQr);
  or MULO143 (TQv, TQt, TQu);
  or MULG143 (TQx, TQv, GND);
  xor MULX144 (TQy, TQw, GND);
  // XOR_Gate MULS144 has open pins: in0=TQy, in1=TQx, out=open
  and MULA144 (TQz, TQw, GND);
  and MULB144 (TQ10, TQx, TQy);
  or MULO144 (TQ11, TQz, TQ10);
  or MULG144 (TQ14, TQ11, GND);
  xor MULX145 (TQ15, TQ13, GND);
  // XOR_Gate MULS145 has open pins: in0=TQ15, in1=TQ14, out=open
  and MULA145 (TQ16, TQ13, GND);
  and MULB145 (TQ17, TQ14, TQ15);
  or MULO145 (TQ18, TQ16, TQ17);
  or MULG145 (TQ1b, TQ18, GND);
  xor MULX146 (TQ1c, TQ1a, GND);
  // XOR_Gate MULS146 has open pins: in0=TQ1c, in1=TQ1b, out=open
  and MULA146 (TQ1d, TQ1a, GND);
  and MULB146 (MULB146_out, TQ1b, TQ1c);
  or MULO146 (MULO146_out, TQ1d, MULB146_out);
  or MULG146 (MULG146_out, MULO146_out, GND);
  xor MULX147 (MULX147_out, GND, GND);
  // XOR_Gate MULS147 has open pins: in0=MULX147_out, in1=MULG146_out, out=open
  and MULA147 (MULA147_out, GND, GND);
  and MULB147 (MULB147_out, MULG146_out, MULX147_out);
  or MULO147 (MULO147_out, MULA147_out, MULB147_out);
  or MULG147 (MULG147_out, MULO147_out, GND);
  xor MULX148 (MULX148_out, GND, GND);
  // XOR_Gate MULS148 has open pins: in0=MULX148_out, in1=MULG147_out, out=open
  and MULA148 (MULA148_out, GND, GND);
  and MULB148 (MULB148_out, MULG147_out, MULX148_out);
  or MULO148 (MULO148_out, MULA148_out, MULB148_out);
  // OR_Gate MULG148 has open pins: in0=MULO148_out, in1=GND, out=open

  // Other names for the same wires on the sheet: TQ1e = B5; TQ1f = GND; TQ1g = B6; TQ1h = P0; TQ1i = A0; TQ1j = P1;
  //   TQ1k = P2; TQ1l = A1; TQ1m = P3; TQ1n = P4; TQ1o = A2; TQ1p = P5; TQ1q = P6; TQ1r = A3; TQ1s = P7; TQ1t = P8;
  //   TQ1u = A4; TQ1v = P9; TQ1w = P10; TQ1x = A5; TQ1y = P11; TQ1z = P12; TQ12 = B3; TQ19 = B4; TQ20 = A6;
  //   TQ21 = P13; TQ22 = P14; TQ23 = A7; TQ24 = P15; TQ25 = B7; TQa = B0; TQi = B1; TQs = B2
endmodule
