// Logisim project mux_4to1.circ as structural Verilog
module mux_4to1 (
  input  D0,
  input  D1,
  input  D2,
  input  D3,
  input  S0,
  input  S1,
  output Y
);

  wire MUX0D_out, MUX0S1_out, MUX1D_out, MUX1S1_out, MUX2D_out, MUX2S1_out, MUX3D_out, MUX3S1_out, MUXN1_out,
       MUXN2_out, MUXO1_out, MUXO2_out;

  and MUX0D (MUX0D_out, D0, MUX0S1_out);
  and MUX0S1 (MUX0S1_out, MUXN1_out, MUXN2_out);
  and MUX1D (MUX1D_out, D1, MUX1S1_out);
  and MUX1S1 (MUX1S1_out, S0, MUXN2_out);
  and MUX2D (MUX2D_out, D2, MUX2S1_out);
  and MUX2S1 (MUX2S1_out, MUXN1_out, S1);
  and MUX3D (MUX3D_out, D3, MUX3S1_out);
  and MUX3S1 (MUX3S1_out, S0, S1);
  or MUXO1 (MUXO1_out, MUX0D_out, MUX1D_out);
  or MUXO2 (MUXO2_out, MUXO1_out, MUX2D_out);
  or MUXO3 (Y, MUXO2_out, MUX3D_out);
  not MUXN1 (MUXN1_out, S0);
  not MUXN2 (MUXN2_out, S1);

  // Other names for the same wires on the sheet: TQ0 = S0; TQ1 = S1; TQ2 = D0; TQ3 = D1; TQ4 = D2; TQ5 = D3; TQ6 = Y
endmodule
