// Logisim project mux_8to1.circ as structural Verilog
module mux_8to1 (
  input  D0,
  input  D1,
  input  D2,
  input  D3,
  input  D4,
  input  D5,
  input  D6,
  input  D7,
  input  S0,
  input  S1,
  input  S2,
  output Y
);

  wire MUX0D_out, MUX0S1_out, MUX0S2_out, MUX1D_out, MUX1S1_out, MUX1S2_out, MUX2D_out, MUX2S1_out,
       MUX2S2_out, MUX3D_out, MUX3S1_out, MUX3S2_out, MUX4D_out, MUX4S1_out, MUX4S2_out, MUX5D_out,
       MUX5S1_out, MUX5S2_out, MUX6D_out, MUX6S1_out, MUX6S2_out, MUX7D_out, MUX7S1_out, MUX7S2_out,
       MUXN1_out, MUXN2_out, MUXN3_out, MUXO1_out, MUXO2_out, MUXO3_out, MUXO4_out, MUXO5_out, MUXO6_out;

  and MUX0D (MUX0D_out, D0, MUX0S2_out);
  and MUX0S1 (MUX0S1_out, MUXN1_out, MUXN2_out);
  and MUX0S2 (MUX0S2_out, MUX0S1_out, MUXN3_out);
  and MUX1D (MUX1D_out, D1, MUX1S2_out);
  and MUX1S1 (MUX1S1_out, S0, MUXN2_out);
  and MUX1S2 (MUX1S2_out, MUX1S1_out, MUXN3_out);
  and MUX2D (MUX2D_out, D2, MUX2S2_out);
  and MUX2S1 (MUX2S1_out, MUXN1_out, S1);
  and MUX2S2 (MUX2S2_out, MUX2S1_out, MUXN3_out);
  and MUX3D (MUX3D_out, D3, MUX3S2_out);
  and MUX3S1 (MUX3S1_out, S0, S1);
  and MUX3S2 (MUX3S2_out, MUX3S1_out, MUXN3_out);
  and MUX4D (MUX4D_out, D4, MUX4S2_out);
  and MUX4S1 (MUX4S1_out, MUXN1_out, MUXN2_out);
  and MUX4S2 (MUX4S2_out, MUX4S1_out, S2);
  and MUX5D (MUX5D_out, D5, MUX5S2_out);
  and MUX5S1 (MUX5S1_out, S0, MUXN2_out);
  and MUX5S2 (MUX5S2_out, MUX5S1_out, S2);
  and MUX6D (MUX6D_out, D6, MUX6S2_out);
  and MUX6S1 (MUX6S1_out, MUXN1_out, S1);
  and MUX6S2 (MUX6S2_out, MUX6S1_out, S2);
  and MUX7D (MUX7D_out, D7, MUX7S2_out);
  and MUX7S1 (MUX7S1_out, S0, S1);
  and MUX7S2 (MUX7S2_out, MUX7S1_out, S2);
  or MUXO1 (MUXO1_out, MUX0D_out, MUX1D_out);
  or MUXO2 (MUXO2_out, MUXO1_out, MUX2D_out);
  or MUXO3 (MUXO3_out, MUXO2_out, MUX3D_out);
  or MUXO4 (MUXO4_out, MUXO3_out, MUX4D_out);
  or MUXO5 (MUXO5_out, MUXO4_out, MUX5D_out);
  or MUXO6 (MUXO6_out, MUXO5_out, MUX6D_out);
  or MUXO7 (Y, MUXO6_out, MUX7D_out);
  not MUXN1 (MUXN1_out, S0);
  not MUXN2 (MUXN2_out, S1);
  not MUXN3 (MUXN3_out, S2);
endmodule
