// Logisim project nand_xor3.circ as structural Verilog
module nand_xor3 (
  input  A,
  input  B,
  input  C,
  output Y
);

  wire n3, n4, n5, n6, n8, n9, n10;

  nand nand_1 (n3, A, B);
  nand nand_2 (n4, A, n3);
  nand nand_3 (n5, B, n3);
  nand nand_4 (n6, n4, n5);
  nand nand_5 (n8, n6, C);
  nand nand_6 (n9, n6, n8);
  nand nand_7 (n10, C, n8);
  nand nand_8 (Y, n9, n10);

  // Other names for the same wires on the sheet: n1 = A; n2 = B; n7 = C; n11 = Y
endmodule
