// Logisim project nine_complement.circ as structural Verilog
module nine_complement (
  input  D1,
  input  D2,
  input  D4,
  input  D8,
  output C1,
  output C2,
  output C4,
  output C8
);

  wire TQ6, TQ7;

  not N1 (C1, D1);
  xor X2 (C4, D4, D2);
  or O1 (TQ6, D4, D2);
  xor X3 (TQ7, D8, TQ6);
  not N2 (C8, TQ7);

  assign C2 = D2;

  // Other names for the same wires on the sheet: TQ0 = D1; TQ1 = C1; TQ2 = C4; TQ3 = D4; TQ4 = D2; TQ5 = D8; TQ8 = C8
endmodule
