// Logisim project oneshot_4clk.circ as structural Verilog
module oneshot_4clk (
  input  TRIG,
  input  RST,
  input  GND,
  output PULSE
);

  wire A1_out, CLK_out, DM4_1_out, EA2_out, EA3_out, KA_out, N1_out, ND_out, NO2_out, OR1_out, U1_q, UC1_q,
       UC2_q, X2_out, X3_out;

  Clock CLK (.out(CLK_out));
  D_Flip_Flop U1 (.D(TRIG), .clk(CLK_out), .Q(U1_q), .preset(RST), .reset(RST));  // open: Qn
  not N1 (N1_out, U1_q);
  and A1 (A1_out, TRIG, N1_out);
  D_Flip_Flop U2 (.D(OR1_out), .clk(CLK_out), .Q(PULSE), .preset(RST), .reset(RST));  // open: Qn
  D_Flip_Flop UC1 (.D(EA2_out), .clk(CLK_out), .Q(UC1_q), .preset(RST), .reset(RST));  // open: Qn
  xor X2 (X2_out, UC1_q, NO2_out);
  and EA2 (EA2_out, X2_out, PULSE);
  not NO2 (NO2_out, GND);
  D_Flip_Flop UC2 (.D(EA3_out), .clk(CLK_out), .Q(UC2_q), .preset(RST), .reset(RST));  // open: Qn
  xor X3 (X3_out, UC2_q, UC1_q);
  and EA3 (EA3_out, X3_out, PULSE);
  and DM4_1 (DM4_1_out, UC1_q, UC2_q);
  not ND (ND_out, DM4_1_out);
  and KA (KA_out, PULSE, ND_out);
  or OR1 (OR1_out, A1_out, KA_out);
endmodule
