// Logisim project parity_8bit.circ as structural Verilog
module parity_8bit (
  input  D0,
  input  D1,
  input  D2,
  input  D3,
  input  D4,
  input  D5,
  input  D6,
  input  D7,
  output P
);

  wire PAR1_out, PAR2_out, PAR3_out, PAR4_out, PAR5_out, PAR6_out;

  xor PAR1 (PAR1_out, D0, D1);
  xor PAR2 (PAR2_out, PAR1_out, D2);
  xor PAR3 (PAR3_out, PAR2_out, D3);
  xor PAR4 (PAR4_out, PAR3_out, D4);
  xor PAR5 (PAR5_out, PAR4_out, D5);
  xor PAR6 (PAR6_out, PAR5_out, D6);
  xor PAR7 (P, PAR6_out, D7);

  // Other names for the same wires on the sheet: TQ0 = D0; TQ1 = D1; TQ2 = D2; TQ3 = D3; TQ4 = D4; TQ5 = D5; TQ6 = D6;
  //   TQ7 = D7; TQ8 = P
endmodule
