// Logisim project pingpong_machine.circ as structural Verilog
module pingpong_machine (
  input  RST,
  input  L,
  input  R,
  input  MISS,
  output LL,
  output RL,
  output BL,
  output BR
);

  wire AH2_out, NC2_out, O107_out, O108_out, O109_out, O110_out, O111_out, O112_out, O113_out, O114_out,
       O115_out, O116_out, O117_out, TQ0, TQ1, TQ1a, TQ1b, TQ1c, TQ1d, TQ1e, TQ1f, TQ1g, TQ1h, TQ1i, TQ1j,
       TQ1k, TQ1l, TQ1m, TQ1n, TQ1o, TQ1q, TQ1r, TQ1s, TQ1t, TQ1u, TQ1w, TQ1x, TQ1y, TQ1z, TQ2, TQ2a, TQ2b,
       TQ2c, TQ2d, TQ2e, TQ2f, TQ2g, TQ2h, TQ2i, TQ2j, TQ2k, TQ2l, TQ2m, TQ2n, TQ2o, TQ2p, TQ2q, TQ2r, TQ2s,
       TQ2t, TQ2u, TQ2v, TQ2w, TQ2x, TQ2y, TQ2z, TQ3, TQ3a, TQ3b, TQ3c, TQ3d, TQ3e, TQ3f, TQ3g, TQ9, TQ10,
       TQ11, TQ12, TQ13, TQ14, TQ15, TQ16, TQ17, TQ18, TQ19, TQ20, TQ21, TQ22, TQ23, TQ24, TQ25, TQ27, TQ28,
       TQ29, TQ30, TQ31, TQ32, TQ33, TQ34, TQ35, TQ36, TQ37, TQ38, TQ39, TQa, TQb, TQc, TQd, TQe, TQf, TQg,
       TQh, TQi, TQj, TQk, TQl, TQm, TQn, TQo, TQp, TQq, TQr, TQs, TQt, TQu, TQv, TQw, TQx, TQy, TQz;

  Clock CLK (.out(TQ2));
  D_Flip_Flop U1 (.D(TQ2m), .clk(TQ2), .Q(TQ2i), .reset(RST));  // open: Qn, preset
  D_Flip_Flop U2 (.D(TQ32), .clk(TQ2), .Q(TQ2y), .reset(RST));  // open: Qn, preset
  D_Flip_Flop U3 (.D(TQ3), .clk(TQ2), .Q(TQ0), .reset(RST));  // open: Qn, preset
  not N1 (TQ1y, TQ2i);
  not N2 (TQ1z, TQ2y);
  not N3 (TQ1e, TQ0);
  not NIl (TQ22, L);
  not NIr (TQ24, R);
  not NImiss (TQ1x, MISS);
  and M0 (TQ9, TQ1y, TQ1z);
  // AND_Gate M1 has open pins: in0=TQ9, in1=TQ1e, out=open
  and A2 (TQa, TQ1y, TQ1z);
  and A3 (TQb, TQa, TQ1e);
  and A4 (TQc, TQb, L);
  and A5 (TQd, TQc, TQ24);
  and A6 (TQ33, TQd, TQ1x);
  and A7 (TQe, TQ1y, TQ1z);
  and A8 (TQf, TQe, TQ1e);
  and A9 (TQg, TQf, TQ22);
  and A10 (TQh, TQg, R);
  and A11 (TQ36, TQh, TQ1x);
  and M12 (TQi, TQ2i, TQ1z);
  and M13 (BR, TQi, TQ1e);
  and A14 (TQj, TQ2i, TQ1z);
  and A15 (TQk, TQj, TQ1e);
  and A16 (TQl, TQk, TQ22);
  and A17 (TQm, TQl, R);
  and A18 (TQ37, TQm, TQ1x);
  and A19 (TQn, TQ2i, TQ1z);
  and A20 (TQo, TQn, TQ1e);
  and A21 (TQp, TQo, TQ22);
  and A22 (TQq, TQp, TQ24);
  and A23 (TQ38, TQq, MISS);
  and M24 (TQr, TQ1y, TQ2y);
  and M25 (BL, TQr, TQ1e);
  and A26 (TQs, TQ1y, TQ2y);
  and A27 (TQt, TQs, TQ1e);
  and A28 (TQu, TQt, L);
  and A29 (TQv, TQu, TQ24);
  and A30 (TQ34, TQv, TQ1x);
  and A31 (TQw, TQ1y, TQ2y);
  and A32 (TQx, TQw, TQ1e);
  and A33 (TQy, TQx, TQ22);
  and A34 (TQz, TQy, TQ24);
  and A35 (TQ1, TQz, MISS);
  and M36 (TQ10, TQ2i, TQ2y);
  and M37 (LL, TQ10, TQ1e);
  and A38 (TQ11, TQ2i, TQ2y);
  and A39 (TQ12, TQ11, TQ1e);
  and A40 (TQ13, TQ12, TQ22);
  and A41 (TQ14, TQ13, TQ24);
  and A42 (TQ39, TQ14, TQ1x);
  and A43 (TQ15, TQ2i, TQ2y);
  and A44 (TQ16, TQ15, TQ1e);
  and A45 (TQ17, TQ16, L);
  and A46 (TQ18, TQ17, TQ24);
  and A47 (TQ3a, TQ18, TQ1x);
  and A48 (TQ19, TQ2i, TQ2y);
  and A49 (TQ1a, TQ19, TQ1e);
  and A50 (TQ1b, TQ1a, TQ22);
  and A51 (TQ1c, TQ1b, R);
  and A52 (TQ3b, TQ1c, TQ1x);
  and A53 (TQ1d, TQ2i, TQ2y);
  and A54 (TQ1f, TQ1d, TQ1e);
  and A55 (TQ1g, TQ1f, TQ22);
  and A56 (TQ1h, TQ1g, TQ24);
  and A57 (TQ3c, TQ1h, MISS);
  and M58 (TQ1i, TQ1y, TQ1z);
  and M59 (RL, TQ1i, TQ0);
  and A60 (TQ1j, TQ1y, TQ1z);
  and A61 (TQ1k, TQ1j, TQ0);
  and A62 (TQ1l, TQ1k, TQ22);
  and A63 (TQ1m, TQ1l, TQ24);
  and A64 (TQ3d, TQ1m, TQ1x);
  and A65 (TQ1n, TQ1y, TQ1z);
  and A66 (TQ1o, TQ1n, TQ0);
  and A67 (TQ1q, TQ1o, L);
  and A68 (TQ1r, TQ1q, TQ24);
  and A69 (TQ3e, TQ1r, TQ1x);
  and A70 (TQ1s, TQ1y, TQ1z);
  and A71 (TQ1t, TQ1s, TQ0);
  and A72 (TQ1u, TQ1t, TQ22);
  and A73 (TQ1w, TQ1u, R);
  and A74 (TQ3f, TQ1w, TQ1x);
  and A75 (TQ20, TQ1y, TQ1z);
  and A76 (TQ21, TQ20, TQ0);
  and A77 (TQ23, TQ21, TQ22);
  and A78 (TQ25, TQ23, TQ24);
  and A79 (TQ3g, TQ25, MISS);
  or O80 (TQ27, TQ33, TQ34);
  or O81 (TQ2k, TQ27, TQ38);
  or O82 (TQ28, TQ36, TQ37);
  or O83 (TQ29, TQ28, TQ1);
  or O84 (TQ2a, TQ29, TQ39);
  or O85 (TQ2b, TQ2a, TQ3a);
  or O86 (TQ2c, TQ2b, TQ3b);
  or O87 (TQ2d, TQ2c, TQ3c);
  or O88 (TQ2e, TQ2d, TQ3d);
  or O89 (TQ2f, TQ2e, TQ3e);
  or O90 (TQ2g, TQ2f, TQ3f);
  or O91 (TQ2h, TQ2g, TQ3g);
  not NC0 (TQ2j, TQ2h);
  and AH0 (TQ2l, TQ2i, TQ2j);
  or O92 (TQ2m, TQ2k, TQ2l);
  or O93 (TQ2n, TQ36, TQ37);
  or O94 (TQ30, TQ2n, TQ38);
  or O95 (TQ2o, TQ33, TQ34);
  or O96 (TQ2p, TQ2o, TQ1);
  or O97 (TQ2q, TQ2p, TQ39);
  or O98 (TQ2r, TQ2q, TQ3a);
  or O99 (TQ2s, TQ2r, TQ3b);
  or O100 (TQ2t, TQ2s, TQ3c);
  or O101 (TQ2u, TQ2t, TQ3d);
  or O102 (TQ2v, TQ2u, TQ3e);
  or O103 (TQ2w, TQ2v, TQ3f);
  or O104 (TQ2x, TQ2w, TQ3g);
  not NC1 (TQ2z, TQ2x);
  and AH1 (TQ31, TQ2y, TQ2z);
  or O105 (TQ32, TQ30, TQ31);
  or O106 (TQ35, TQ33, TQ34);
  or O107 (O107_out, TQ35, TQ36);
  or O108 (O108_out, O107_out, TQ37);
  or O109 (O109_out, O108_out, TQ38);
  or O110 (O110_out, O109_out, TQ39);
  or O111 (O111_out, O110_out, TQ3a);
  or O112 (O112_out, O111_out, TQ3b);
  or O113 (O113_out, O112_out, TQ3c);
  or O114 (O114_out, O113_out, TQ3d);
  or O115 (O115_out, O114_out, TQ3e);
  or O116 (O116_out, O115_out, TQ3f);
  or O117 (O117_out, O116_out, TQ3g);
  not NC2 (NC2_out, O117_out);
  and AH2 (AH2_out, TQ0, NC2_out);
  or O118 (TQ3, TQ1, AH2_out);

  // Other names for the same wires on the sheet: TQ1p = L; TQ1v = R; TQ4 = RST; TQ5 = LL; TQ6 = RL; TQ7 = BL;
  //   TQ8 = BR; TQ26 = MISS
endmodule
