// Logisim project piso_4bit.circ as structural Verilog
module piso_4bit (
  input  CLK,
  input  LOAD,
  input  RST,
  input  SI,
  input  D0,
  input  D1,
  input  D2,
  input  D3,
  output SO,
  output Q0,
  output Q1,
  output Q2,
  output Q3
);

  wire PISOA2_out, PISOA3_out, PISOB1_out, PISOB2_out, PISOB3_out, PISOM1_out, PISOM2_out, PISOM3_out, TQ1,
       TQ2, TQ3, TQ5, TQb;

  not PISOL (TQb, LOAD);
  and PISOA0 (TQ1, LOAD, D0);
  and PISOB0 (TQ2, TQb, Q1);
  or PISOM0 (TQ3, TQ1, TQ2);
  D_Flip_Flop PISO1 (.D(TQ3), .clk(CLK), .Q(Q0), .reset(RST));  // open: Qn, preset
  and PISOA1 (TQ5, LOAD, D1);
  and PISOB1 (PISOB1_out, TQb, Q2);
  or PISOM1 (PISOM1_out, TQ5, PISOB1_out);
  D_Flip_Flop PISO2 (.D(PISOM1_out), .clk(CLK), .Q(Q1), .reset(RST));  // open: Qn, preset
  and PISOA2 (PISOA2_out, LOAD, D2);
  and PISOB2 (PISOB2_out, TQb, Q3);
  or PISOM2 (PISOM2_out, PISOA2_out, PISOB2_out);
  D_Flip_Flop PISO3 (.D(PISOM2_out), .clk(CLK), .Q(Q2), .reset(RST));  // open: Qn, preset
  and PISOA3 (PISOA3_out, LOAD, D3);
  and PISOB3 (PISOB3_out, TQb, SI);
  or PISOM3 (PISOM3_out, PISOA3_out, PISOB3_out);
  D_Flip_Flop PISO4 (.D(PISOM3_out), .clk(CLK), .Q(Q3), .reset(RST));  // open: Qn, preset

  assign SO = Q0;

  // Other names for the same wires on the sheet: TQ0 = D0; TQ4 = D1; TQ6 = Q1; TQ7 = D2; TQ8 = Q2; TQ9 = LOAD;
  //   TQa = D3; TQc = SI; TQd = CLK; TQe = RST; TQf = Q3; TQg = Q0
endmodule
