// Logisim project ram_chip.circ as structural Verilog
module ram_chip (
  input  [7:0] ADR,
  input  [7:0] DIN,
  input  STR,
  input  CLR,
  output [7:0] DOUT
);

  wire TQ5;

  Clock CLK (.out(TQ5));
  RAM RAM1 (.addr(ADR), .we(CLR), .oe(STR), .clk(TQ5), .din(DOUT), .dout(DIN));
  // Pins of 1 and 8 bits meet at DOUT
  // Pins of 1 and 8 bits meet at ADR
  // Pins of 1 and 8 bits meet at DIN

  // Other names for the same wires on the sheet: TQ0[7:0] = ADR; TQ1[7:0] = DIN; TQ2[7:0] = DOUT; TQ3 = STR;
  //   TQ4 = CLR
endmodule
