// Logisim project register_4bit.circ as structural Verilog
module register_4bit (
  input  CLK,
  input  RST,
  input  D0,
  input  D1,
  input  D2,
  input  D3,
  output Q0,
  output Q1,
  output Q2,
  output Q3
);

  D_Flip_Flop U1 (.D(D0), .clk(CLK), .Q(Q0), .reset(RST));  // open: Qn, preset
  D_Flip_Flop U2 (.D(D1), .clk(CLK), .Q(Q1), .reset(RST));  // open: Qn, preset
  D_Flip_Flop U3 (.D(D2), .clk(CLK), .Q(Q2), .reset(RST));  // open: Qn, preset
  D_Flip_Flop U4 (.D(D3), .clk(CLK), .Q(Q3), .reset(RST));  // open: Qn, preset

  // Other names for the same wires on the sheet: TQ0 = D0; TQ1 = Q0; TQ2 = D1; TQ3 = Q1; TQ4 = D2; TQ5 = Q2; TQ6 = D3;
  //   TQ7 = CLK; TQ8 = RST; TQ9 = Q3
endmodule
