// Logisim project ring_counter.circ as structural Verilog
module ring_counter (
  input  CLK,
  input  SEED,
  input  RST,
  output Q0,
  output Q1,
  output Q2,
  output Q3
);

  wire O1_out;

  D_Flip_Flop U1 (.D(O1_out), .clk(CLK), .Q(Q0), .reset(RST));  // open: Qn, preset
  D_Flip_Flop U2 (.D(Q0), .clk(CLK), .Q(Q1), .reset(RST));  // open: Qn, preset
  D_Flip_Flop U3 (.D(Q1), .clk(CLK), .Q(Q2), .reset(RST));  // open: Qn, preset
  D_Flip_Flop U4 (.D(Q2), .clk(CLK), .Q(Q3), .reset(RST));  // open: Qn, preset
  or O1 (O1_out, SEED, Q3);

  // Other names for the same wires on the sheet: TQ0 = RST; TQ1 = SEED; TQ2 = Q3; TQ3 = Q0; TQ4 = Q1; TQ5 = Q2;
  //   TQ6 = CLK
endmodule
