// Logisim project rom_chip.circ as structural Verilog
module rom_chip (
  input  [7:0] ADR,
  output [7:0] DOUT
);

  ROM ROM1 (.addr(ADR), .data(DOUT));
  // Pins of 1 and 8 bits meet at DOUT
  // Pins of 1 and 8 bits meet at ADR

  // Other names for the same wires on the sheet: TQ0[7:0] = ADR; TQ1[7:0] = DOUT
endmodule
