// Logisim project rotate_shifter_4bit_right.circ as structural Verilog
module rotate_shifter_4bit_right (
  input  D0,
  input  D1,
  input  D2,
  input  D3,
  input  SH0,
  input  SH1,
  output Y0,
  output Y1,
  output Y2,
  output Y3
);

  wire MO31_out, MO32_out, MO42_out, MO43_out, SA34_out, SA36_out, SA38_out, SA40_out, SB30_out, SB35_out,
       SB37_out, SB39_out, SB41_out, TQ0, TQ1, TQ2, TQ3, TQ4, TQ5, TQ6, TQ7, TQ8, TQ9, TQb, TQc, TQd, TQe,
       TQf, TQg, TQh, TQi, TQj, TQk, TQm, TQn, TQo, TQp, TQq, TQr, TQs, TQw, TQy;

  not NS1 (TQy, SH0);
  not NS2 (TQw, SH1);
  and SA1 (TQ0, D0, TQy);
  and SB2 (TQ4, TQ0, TQw);
  and SA3 (TQ1, D1, SH0);
  and SB4 (TQ5, TQ1, TQw);
  and SA5 (TQ2, D2, TQy);
  and SB6 (TQ7, TQ2, SH1);
  and SA7 (TQ3, D3, SH0);
  and SB8 (TQ9, TQ3, SH1);
  or MO9 (TQ6, TQ4, TQ5);
  or MO10 (TQ8, TQ6, TQ7);
  or MO11 (Y0, TQ8, TQ9);
  and SA12 (TQb, D1, TQy);
  and SB13 (TQf, TQb, TQw);
  and SA14 (TQc, D2, SH0);
  and SB15 (TQg, TQc, TQw);
  and SA16 (TQd, D3, TQy);
  and SB17 (TQi, TQd, SH1);
  and SA18 (TQe, D0, SH0);
  and SB19 (TQk, TQe, SH1);
  or MO20 (TQh, TQf, TQg);
  or MO21 (TQj, TQh, TQi);
  or MO22 (Y1, TQj, TQk);
  and SA23 (TQm, D2, TQy);
  and SB24 (TQq, TQm, TQw);
  and SA25 (TQn, D3, SH0);
  and SB26 (TQr, TQn, TQw);
  and SA27 (TQo, D0, TQy);
  and SB28 (TQs, TQo, SH1);
  and SA29 (TQp, D1, SH0);
  and SB30 (SB30_out, TQp, SH1);
  or MO31 (MO31_out, TQq, TQr);
  or MO32 (MO32_out, MO31_out, TQs);
  or MO33 (Y2, MO32_out, SB30_out);
  and SA34 (SA34_out, D3, TQy);
  and SB35 (SB35_out, SA34_out, TQw);
  and SA36 (SA36_out, D0, SH0);
  and SB37 (SB37_out, SA36_out, TQw);
  and SA38 (SA38_out, D1, TQy);
  and SB39 (SB39_out, SA38_out, SH1);
  and SA40 (SA40_out, D2, SH0);
  and SB41 (SB41_out, SA40_out, SH1);
  or MO42 (MO42_out, SB35_out, SB37_out);
  or MO43 (MO43_out, MO42_out, SB39_out);
  or MO44 (Y3, MO43_out, SB41_out);

  // Other names for the same wires on the sheet: TQ10 = SH0; TQ11 = SH1; TQ12 = Y3; TQa = Y0; TQl = Y1; TQt = Y2;
  //   TQu = D3; TQv = D0; TQx = D1; TQz = D2
endmodule
