// Logisim project sar_4bit.circ as structural Verilog
module sar_4bit (
  input  D0,
  input  D1,
  input  D2,
  input  D3,
  input  SH0,
  input  SH1,
  output Y0,
  output Y1,
  output Y2,
  output Y3
);

  wire MO31_out, MO32_out, MO42_out, MO43_out, SA34_out, SA36_out, SA38_out, SA40_out, SB30_out, SB35_out,
       SB37_out, SB39_out, SB41_out, TQ1, TQ2, TQ3, TQ4, TQ5, TQ6, TQ7, TQ8, TQ9, TQa, TQd, TQe, TQf, TQg,
       TQh, TQi, TQj, TQk, TQl, TQm, TQp, TQq, TQr, TQs, TQt, TQu, TQv, TQx, TQy;

  not NS1 (TQy, SH0);
  not NS2 (TQx, SH1);
  and SA1 (TQ1, D0, TQy);
  and SB2 (TQ5, TQ1, TQx);
  and SA3 (TQ2, D1, SH0);
  and SB4 (TQ6, TQ2, TQx);
  and SA5 (TQ3, D2, TQy);
  and SB6 (TQ8, TQ3, SH1);
  and SA7 (TQ4, D3, SH0);
  and SB8 (TQa, TQ4, SH1);
  or MO9 (TQ7, TQ5, TQ6);
  or MO10 (TQ9, TQ7, TQ8);
  or MO11 (Y0, TQ9, TQa);
  and SA12 (TQd, D1, TQy);
  and SB13 (TQh, TQd, TQx);
  and SA14 (TQe, D2, SH0);
  and SB15 (TQi, TQe, TQx);
  and SA16 (TQf, D3, TQy);
  and SB17 (TQk, TQf, SH1);
  and SA18 (TQg, D3, SH0);
  and SB19 (TQm, TQg, SH1);
  or MO20 (TQj, TQh, TQi);
  or MO21 (TQl, TQj, TQk);
  or MO22 (Y1, TQl, TQm);
  and SA23 (TQp, D2, TQy);
  and SB24 (TQt, TQp, TQx);
  and SA25 (TQq, D3, SH0);
  and SB26 (TQu, TQq, TQx);
  and SA27 (TQr, D3, TQy);
  and SB28 (TQv, TQr, SH1);
  and SA29 (TQs, D3, SH0);
  and SB30 (SB30_out, TQs, SH1);
  or MO31 (MO31_out, TQt, TQu);
  or MO32 (MO32_out, MO31_out, TQv);
  or MO33 (Y2, MO32_out, SB30_out);
  and SA34 (SA34_out, D3, TQy);
  and SB35 (SB35_out, SA34_out, TQx);
  and SA36 (SA36_out, D3, SH0);
  and SB37 (SB37_out, SA36_out, TQx);
  and SA38 (SA38_out, D3, TQy);
  and SB39 (SB39_out, SA38_out, SH1);
  and SA40 (SA40_out, D3, SH0);
  and SB41 (SB41_out, SA40_out, SH1);
  or MO42 (MO42_out, SB35_out, SB37_out);
  or MO43 (MO43_out, MO42_out, SB39_out);
  or MO44 (Y3, MO43_out, SB41_out);

  // Other names for the same wires on the sheet: TQ0 = D0; TQ10 = SH0; TQ11 = SH1; TQ12 = Y3; TQb = Y0; TQc = D1;
  //   TQn = Y1; TQo = D2; TQw = Y2; TQz = D3
endmodule
