// Logisim project satadd_4bit.circ as structural Verilog
module satadd_4bit (
  input  A0,
  input  B0,
  input  A1,
  input  B1,
  input  A2,
  input  B2,
  input  A3,
  input  B3,
  input  GND,
  output S0,
  output S1,
  output S2,
  output S3
);

  wire SAA3_out, SAA4_out, SAB3_out, SAB4_out, SAG3_out, SAG4_out, SAO3_out, SAO4_out, SAS3_out, SAS4_out,
       SAX4_out, TQ2, TQ3, TQ4, TQ5, TQ8, TQ9, TQa, TQb, TQc, TQf, TQg, TQk, TQm;

  xor SAX1 (TQ2, A0, B0);
  xor SAS1 (TQk, TQ2, GND);
  and SAA1 (TQ3, A0, B0);
  and SAB1 (TQ4, GND, TQ2);
  or SAO1 (TQ5, TQ3, TQ4);
  or SAG1 (TQ8, TQ5, GND);
  xor SAX2 (TQ9, A1, B1);
  xor SAS2 (TQm, TQ9, TQ8);
  and SAA2 (TQa, A1, B1);
  and SAB2 (TQb, TQ8, TQ9);
  or SAO2 (TQc, TQa, TQb);
  or SAG2 (TQf, TQc, GND);
  xor SAX3 (TQg, A2, B2);
  xor SAS3 (SAS3_out, TQg, TQf);
  and SAA3 (SAA3_out, A2, B2);
  and SAB3 (SAB3_out, TQf, TQg);
  or SAO3 (SAO3_out, SAA3_out, SAB3_out);
  or SAG3 (SAG3_out, SAO3_out, GND);
  xor SAX4 (SAX4_out, A3, B3);
  xor SAS4 (SAS4_out, SAX4_out, SAG3_out);
  and SAA4 (SAA4_out, A3, B3);
  and SAB4 (SAB4_out, SAG3_out, SAX4_out);
  or SAO4 (SAO4_out, SAA4_out, SAB4_out);
  or SAG4 (SAG4_out, SAO4_out, GND);
  or SAU5 (S0, TQk, SAG4_out);
  or SAU6 (S1, TQm, SAG4_out);
  or SAU7 (S2, SAS3_out, SAG4_out);
  or SAU8 (S3, SAS4_out, SAG4_out);

  // Other names for the same wires on the sheet: TQ0 = A0; TQ1 = B0; TQ6 = A1; TQ7 = B1; TQd = A2; TQe = B2; TQh = A3;
  //   TQi = B3; TQj = GND; TQl = S0; TQn = S1; TQo = S2; TQp = S3
endmodule
