// Logisim project seqdet_101.circ as structural Verilog
module seqdet_101 (
  input  CLK,
  input  X,
  input  RST,
  output F
);

  wire A1_out, A2_out, A3_out, N1_out, N2_out, O1_out, U1_q, U2_q;

  D_Flip_Flop U1 (.D(X), .clk(CLK), .Q(U1_q), .reset(RST));  // open: Qn, preset
  D_Flip_Flop U2 (.D(O1_out), .clk(CLK), .Q(U2_q), .reset(RST));  // open: Qn, preset
  not N1 (N1_out, X);
  not N2 (N2_out, U1_q);
  and A1 (A1_out, U1_q, N1_out);
  and A2 (A2_out, N2_out, X);
  and A3 (A3_out, U2_q, A2_out);
  or O1 (O1_out, A1_out, A3_out);
  and A4 (F, U2_q, U1_q);

  // Other names for the same wires on the sheet: TQ0 = CLK; TQ1 = RST; TQ2 = X; TQ3 = F
endmodule
