// Logisim project seqdet_1101.circ as structural Verilog
module seqdet_1101 (
  input  CLK,
  input  X,
  input  RST,
  output F
);

  wire TQ0, TQ1, TQ2, TQ3, TQ4, TQ5, TQ6, TQ7, TQ8, TQ9, TQa, TQb, TQc, TQd, TQe, TQg, TQh, TQi, TQj, TQk,
       TQl, TQm;

  D_Flip_Flop U1 (.D(TQ6), .clk(CLK), .Q(TQd), .reset(RST));  // open: Qn, preset
  and A8 (TQh, TQe, X);
  and A9 (TQi, TQg, TQh);
  D_Flip_Flop U2 (.D(TQb), .clk(CLK), .Q(TQc), .reset(RST));  // open: Qn, preset
  and A10 (TQl, TQj, TQk);
  D_Flip_Flop U3 (.D(TQi), .clk(CLK), .Q(TQj), .reset(RST));  // open: Qn, preset
  and A11 (F, TQl, TQm);
  not N1 (TQm, TQd);
  not N4 (TQ3, X);
  not N2 (TQk, TQc);
  and B1 (TQ0, TQk, TQm);
  not N3 (TQg, TQj);
  and B2 (TQ4, TQ0, X);
  and A3 (TQ7, TQk, TQd);
  and B3 (TQ1, TQg, TQc);
  and A4 (TQ8, TQ7, X);
  and B4 (TQ2, TQ1, TQm);
  and A5 (TQ9, TQc, TQm);
  and B5 (TQ5, TQ2, TQ3);
  or O1 (TQa, TQ8, TQ9);
  or O2 (TQ6, TQ4, TQ5);
  and A6 (TQb, TQg, TQa);
  and A7 (TQe, TQc, TQd);

  // Other names for the same wires on the sheet: TQf = X; TQn = F; TQo = CLK; TQp = RST
endmodule
