// Logisim project shiftreg_4bit.circ as structural Verilog
module shiftreg_4bit (
  input  CLK,
  input  DIN,
  input  RST,
  output Q0,
  output Q1,
  output Q2,
  output Q3
);

  D_Flip_Flop U1 (.D(DIN), .clk(CLK), .Q(Q0), .preset(RST), .reset(RST));  // open: Qn
  D_Flip_Flop U2 (.D(Q0), .clk(CLK), .Q(Q1), .preset(RST), .reset(RST));  // open: Qn
  D_Flip_Flop U3 (.D(Q1), .clk(CLK), .Q(Q2), .preset(RST), .reset(RST));  // open: Qn
  D_Flip_Flop U4 (.D(Q2), .clk(CLK), .Q(Q3), .preset(RST), .reset(RST));  // open: Qn
endmodule
