// Logisim project signmag_4bit.circ as structural Verilog
module signmag_4bit (
  input  A0,
  input  A1,
  input  A2,
  input  A3,
  output B0,
  output B1,
  output B2,
  output B3
);

  wire CA2_out, NS_out, SA0_out, SA1_out, SA2_out, ST0_out, ST1_out, ST2_out, TQ2, TQ4, TQ5, TQ6, TQ7,
       TX1_out, TX2_out;

  not N1 (TQ4, A0);
  not N2 (TQ2, A1);
  not N3 (TQ5, A2);
  not N4 (TQ7, A3);
  and CA1 (TQ6, TQ2, TQ4);
  xor TX1 (TX1_out, TQ2, TQ4);
  and CA2 (CA2_out, TQ5, TQ6);
  xor TX2 (TX2_out, TQ5, TQ6);
  // AND_Gate CA3 has open pins: in0=TQ7, in1=CA2_out, out=open
  // XOR_Gate TX3 has open pins: in0=TQ7, in1=CA2_out, out=open
  not NS (NS_out, A3);
  and ST0 (ST0_out, A3, A0);
  and SA0 (SA0_out, NS_out, A0);
  or OR0 (B0, ST0_out, SA0_out);
  and ST1 (ST1_out, A3, TX1_out);
  and SA1 (SA1_out, NS_out, A1);
  or OR1 (B1, ST1_out, SA1_out);
  and ST2 (ST2_out, A3, TX2_out);
  and SA2 (SA2_out, NS_out, A2);
  or OR2 (B2, ST2_out, SA2_out);

  assign B3 = A3;

  // Other names for the same wires on the sheet: TQ0 = A2; TQ1 = B2; TQ3 = A3; TQ8 = A0; TQ9 = B0; TQa = A1; TQb = B1
endmodule
