// Logisim project squarer_4bit.circ as structural Verilog
module squarer_4bit (
  input  A0,
  input  A1,
  input  A2,
  input  A3,
  input  GND,
  output P0,
  output P1,
  output P2,
  output P3,
  output P4,
  output P5,
  output P6,
  output P7
);

  wire SQA17_out, SQA18_out, SQA19_out, SQA20_out, SQA21_out, SQA22_out, SQA23_out, SQA24_out, SQA25_out,
       SQA26_out, SQA27_out, SQA28_out, SQA29_out, SQA30_out, SQA31_out, SQA32_out, SQA33_out, SQA34_out,
       SQB17_out, SQB18_out, SQB19_out, SQB20_out, SQB21_out, SQB22_out, SQB23_out, SQB24_out, SQB25_out,
       SQB26_out, SQB27_out, SQB28_out, SQB29_out, SQB30_out, SQB31_out, SQB32_out, SQB33_out, SQB34_out,
       SQG17_out, SQG18_out, SQG19_out, SQG20_out, SQG22_out, SQG23_out, SQG24_out, SQG25_out, SQG26_out,
       SQG28_out, SQG29_out, SQG30_out, SQG31_out, SQG32_out, SQG33_out, SQO17_out, SQO18_out, SQO19_out,
       SQO20_out, SQO21_out, SQO22_out, SQO23_out, SQO24_out, SQO25_out, SQO26_out, SQO27_out, SQO28_out,
       SQO29_out, SQO30_out, SQO31_out, SQO32_out, SQO33_out, SQO34_out, SQP2_out, SQP3_out, SQP4_out,
       SQP5_out, SQP6_out, SQP7_out, SQP8_out, SQP9_out, SQP10_out, SQP11_out, SQP12_out, SQP13_out,
       SQP14_out, SQP15_out, SQP16_out, SQS18_out, SQS19_out, SQS20_out, SQS21_out, SQS23_out, SQS24_out,
       SQS25_out, SQS26_out, SQS27_out, SQX17_out, SQX18_out, SQX19_out, SQX20_out, SQX21_out, SQX22_out,
       SQX23_out, SQX24_out, SQX25_out, SQX26_out, SQX27_out, SQX28_out, SQX29_out, SQX30_out, SQX31_out,
       SQX32_out, SQX33_out, SQX34_out;

  and SQP1 (P0, A0, A0);
  and SQP2 (SQP2_out, A1, A0);
  and SQP3 (SQP3_out, A2, A0);
  and SQP4 (SQP4_out, A3, A0);
  and SQP5 (SQP5_out, A0, A1);
  and SQP6 (SQP6_out, A1, A1);
  and SQP7 (SQP7_out, A2, A1);
  and SQP8 (SQP8_out, A3, A1);
  and SQP9 (SQP9_out, A0, A2);
  and SQP10 (SQP10_out, A1, A2);
  and SQP11 (SQP11_out, A2, A2);
  and SQP12 (SQP12_out, A3, A2);
  and SQP13 (SQP13_out, A0, A3);
  and SQP14 (SQP14_out, A1, A3);
  and SQP15 (SQP15_out, A2, A3);
  and SQP16 (SQP16_out, A3, A3);
  xor SQX17 (SQX17_out, SQP2_out, SQP5_out);
  xor SQS17 (P1, SQX17_out, GND);
  and SQA17 (SQA17_out, SQP2_out, SQP5_out);
  and SQB17 (SQB17_out, GND, SQX17_out);
  or SQO17 (SQO17_out, SQA17_out, SQB17_out);
  or SQG17 (SQG17_out, SQO17_out, GND);
  xor SQX18 (SQX18_out, SQP3_out, SQP6_out);
  xor SQS18 (SQS18_out, SQX18_out, SQG17_out);
  and SQA18 (SQA18_out, SQP3_out, SQP6_out);
  and SQB18 (SQB18_out, SQG17_out, SQX18_out);
  or SQO18 (SQO18_out, SQA18_out, SQB18_out);
  or SQG18 (SQG18_out, SQO18_out, GND);
  xor SQX19 (SQX19_out, SQP4_out, SQP7_out);
  xor SQS19 (SQS19_out, SQX19_out, SQG18_out);
  and SQA19 (SQA19_out, SQP4_out, SQP7_out);
  and SQB19 (SQB19_out, SQG18_out, SQX19_out);
  or SQO19 (SQO19_out, SQA19_out, SQB19_out);
  or SQG19 (SQG19_out, SQO19_out, GND);
  xor SQX20 (SQX20_out, GND, SQP8_out);
  xor SQS20 (SQS20_out, SQX20_out, SQG19_out);
  and SQA20 (SQA20_out, GND, SQP8_out);
  and SQB20 (SQB20_out, SQG19_out, SQX20_out);
  or SQO20 (SQO20_out, SQA20_out, SQB20_out);
  or SQG20 (SQG20_out, SQO20_out, GND);
  xor SQX21 (SQX21_out, GND, GND);
  xor SQS21 (SQS21_out, SQX21_out, SQG20_out);
  and SQA21 (SQA21_out, GND, GND);
  and SQB21 (SQB21_out, SQG20_out, SQX21_out);
  or SQO21 (SQO21_out, SQA21_out, SQB21_out);
  // OR_Gate SQG21 has open pins: in0=SQO21_out, in1=GND, out=open
  xor SQX22 (SQX22_out, SQS18_out, SQP9_out);
  xor SQS22 (P2, SQX22_out, GND);
  and SQA22 (SQA22_out, SQS18_out, SQP9_out);
  and SQB22 (SQB22_out, GND, SQX22_out);
  or SQO22 (SQO22_out, SQA22_out, SQB22_out);
  or SQG22 (SQG22_out, SQO22_out, GND);
  xor SQX23 (SQX23_out, SQS19_out, SQP10_out);
  xor SQS23 (SQS23_out, SQX23_out, SQG22_out);
  and SQA23 (SQA23_out, SQS19_out, SQP10_out);
  and SQB23 (SQB23_out, SQG22_out, SQX23_out);
  or SQO23 (SQO23_out, SQA23_out, SQB23_out);
  or SQG23 (SQG23_out, SQO23_out, GND);
  xor SQX24 (SQX24_out, SQS20_out, SQP11_out);
  xor SQS24 (SQS24_out, SQX24_out, SQG23_out);
  and SQA24 (SQA24_out, SQS20_out, SQP11_out);
  and SQB24 (SQB24_out, SQG23_out, SQX24_out);
  or SQO24 (SQO24_out, SQA24_out, SQB24_out);
  or SQG24 (SQG24_out, SQO24_out, GND);
  xor SQX25 (SQX25_out, SQS21_out, SQP12_out);
  xor SQS25 (SQS25_out, SQX25_out, SQG24_out);
  and SQA25 (SQA25_out, SQS21_out, SQP12_out);
  and SQB25 (SQB25_out, SQG24_out, SQX25_out);
  or SQO25 (SQO25_out, SQA25_out, SQB25_out);
  or SQG25 (SQG25_out, SQO25_out, GND);
  xor SQX26 (SQX26_out, GND, GND);
  xor SQS26 (SQS26_out, SQX26_out, SQG25_out);
  and SQA26 (SQA26_out, GND, GND);
  and SQB26 (SQB26_out, SQG25_out, SQX26_out);
  or SQO26 (SQO26_out, SQA26_out, SQB26_out);
  or SQG26 (SQG26_out, SQO26_out, GND);
  xor SQX27 (SQX27_out, GND, GND);
  xor SQS27 (SQS27_out, SQX27_out, SQG26_out);
  and SQA27 (SQA27_out, GND, GND);
  and SQB27 (SQB27_out, SQG26_out, SQX27_out);
  or SQO27 (SQO27_out, SQA27_out, SQB27_out);
  // OR_Gate SQG27 has open pins: in0=SQO27_out, in1=GND, out=open
  xor SQX28 (SQX28_out, SQS23_out, SQP13_out);
  xor SQS28 (P3, SQX28_out, GND);
  and SQA28 (SQA28_out, SQS23_out, SQP13_out);
  and SQB28 (SQB28_out, GND, SQX28_out);
  or SQO28 (SQO28_out, SQA28_out, SQB28_out);
  or SQG28 (SQG28_out, SQO28_out, GND);
  xor SQX29 (SQX29_out, SQS24_out, SQP14_out);
  xor SQS29 (P4, SQX29_out, SQG28_out);
  and SQA29 (SQA29_out, SQS24_out, SQP14_out);
  and SQB29 (SQB29_out, SQG28_out, SQX29_out);
  or SQO29 (SQO29_out, SQA29_out, SQB29_out);
  or SQG29 (SQG29_out, SQO29_out, GND);
  xor SQX30 (SQX30_out, SQS25_out, SQP15_out);
  xor SQS30 (P5, SQX30_out, SQG29_out);
  and SQA30 (SQA30_out, SQS25_out, SQP15_out);
  and SQB30 (SQB30_out, SQG29_out, SQX30_out);
  or SQO30 (SQO30_out, SQA30_out, SQB30_out);
  or SQG30 (SQG30_out, SQO30_out, GND);
  xor SQX31 (SQX31_out, SQS26_out, SQP16_out);
  xor SQS31 (P6, SQX31_out, SQG30_out);
  and SQA31 (SQA31_out, SQS26_out, SQP16_out);
  and SQB31 (SQB31_out, SQG30_out, SQX31_out);
  or SQO31 (SQO31_out, SQA31_out, SQB31_out);
  or SQG31 (SQG31_out, SQO31_out, GND);
  xor SQX32 (SQX32_out, SQS27_out, GND);
  xor SQS32 (P7, SQX32_out, SQG31_out);
  and SQA32 (SQA32_out, SQS27_out, GND);
  and SQB32 (SQB32_out, SQG31_out, SQX32_out);
  or SQO32 (SQO32_out, SQA32_out, SQB32_out);
  or SQG32 (SQG32_out, SQO32_out, GND);
  xor SQX33 (SQX33_out, GND, GND);
  // XOR_Gate SQS33 has open pins: in0=SQX33_out, in1=SQG32_out, out=open
  and SQA33 (SQA33_out, GND, GND);
  and SQB33 (SQB33_out, SQG32_out, SQX33_out);
  or SQO33 (SQO33_out, SQA33_out, SQB33_out);
  or SQG33 (SQG33_out, SQO33_out, GND);
  xor SQX34 (SQX34_out, GND, GND);
  // XOR_Gate SQS34 has open pins: in0=SQX34_out, in1=SQG33_out, out=open
  and SQA34 (SQA34_out, GND, GND);
  and SQB34 (SQB34_out, SQG33_out, SQX34_out);
  or SQO34 (SQO34_out, SQA34_out, SQB34_out);
  // OR_Gate SQG34 has open pins: in0=SQO34_out, in1=GND, out=open
endmodule
