// Logisim project srlatch.circ as structural Verilog
module srlatch (
  input  S,
  input  R,
  output Q,
  output nQ
);

  nand U1 (Q, S, nQ);
  nand U2 (nQ, R, Q);

  // Other names for the same wires on the sheet: TQ0 = S; TQ1 = R; TQ2 = Q; TQ3 = nQ
endmodule
