// Logisim project stepper_motor.circ as structural Verilog
module stepper_motor (
  input  RST,
  input  EN,
  input  DIR,
  output P0,
  output P1,
  output P2,
  output P3
);

  wire O52_out, O53_out, O54_out, O55_out, O56_out, O57_out, O59_out, O60_out, O61_out, O62_out, O63_out,
       O64_out, TQ0, TQ1, TQ1a, TQ1b, TQ1c, TQ1d, TQ1e, TQ1g, TQ1i, TQ1j, TQ1k, TQ1l, TQ1m, TQ1n, TQ2, TQ4,
       TQ5, TQ6, TQ7, TQ8, TQ9, TQ10, TQ11, TQ12, TQ13, TQ14, TQ15, TQ16, TQ17, TQ18, TQ19, TQa, TQc, TQg,
       TQh, TQi, TQj, TQk, TQl, TQm, TQn, TQo, TQp, TQq, TQr, TQs, TQt, TQu, TQv, TQw, TQx, TQy, TQz;

  Clock CLK (.out(TQ2));
  D_Flip_Flop U1 (.D(TQ1m), .clk(TQ2), .Q(TQ1c), .reset(RST));  // open: Qn, preset
  D_Flip_Flop U2 (.D(TQa), .clk(TQ2), .Q(TQ1d), .reset(RST));  // open: Qn, preset
  not N1 (TQ11, TQ1c);
  not N2 (TQs, TQ1d);
  not NIen (TQ18, EN);
  not NIdir (TQ1a, DIR);
  and M0 (P0, TQ11, TQs);
  and A1 (TQ9, TQ11, TQs);
  and A2 (TQc, TQ9, TQ1a);
  // AND_Gate A3 has open pins: in0=TQc, in1=TQ18, out=open
  and A4 (TQg, TQ11, TQs);
  and A5 (TQh, TQg, DIR);
  // AND_Gate A6 has open pins: in0=TQh, in1=TQ18, out=open
  and A7 (TQi, TQ11, TQs);
  and A8 (TQj, TQi, TQ1a);
  and A9 (TQ1n, TQj, EN);
  and A10 (TQk, TQ11, TQs);
  and A11 (TQl, TQk, DIR);
  and A12 (TQ1i, TQl, EN);
  and M13 (P1, TQ1c, TQs);
  and A14 (TQm, TQ1c, TQs);
  and A15 (TQn, TQm, TQ1a);
  and A16 (TQ1j, TQn, TQ18);
  and A17 (TQo, TQ1c, TQs);
  and A18 (TQp, TQo, DIR);
  and A19 (TQ1k, TQp, TQ18);
  and A20 (TQq, TQ1c, TQs);
  and A21 (TQr, TQq, TQ1a);
  // AND_Gate A22 has open pins: in0=TQr, in1=EN, out=open
  and A23 (TQt, TQ1c, TQs);
  and A24 (TQu, TQt, DIR);
  and A25 (TQ5, TQu, EN);
  and M26 (P2, TQ11, TQ1d);
  and A27 (TQv, TQ11, TQ1d);
  and A28 (TQw, TQv, TQ1a);
  and A29 (TQ6, TQw, TQ18);
  and A30 (TQx, TQ11, TQ1d);
  and A31 (TQy, TQx, DIR);
  and A32 (TQ7, TQy, TQ18);
  and A33 (TQz, TQ11, TQ1d);
  and A34 (TQ10, TQz, TQ1a);
  and A35 (TQ1l, TQ10, EN);
  and A36 (TQ12, TQ11, TQ1d);
  and A37 (TQ13, TQ12, DIR);
  and A38 (TQ0, TQ13, EN);
  and M39 (P3, TQ1c, TQ1d);
  and A40 (TQ14, TQ1c, TQ1d);
  and A41 (TQ15, TQ14, TQ1a);
  and A42 (TQ1, TQ15, TQ18);
  and A43 (TQ16, TQ1c, TQ1d);
  and A44 (TQ17, TQ16, DIR);
  and A45 (TQ4, TQ17, TQ18);
  and A46 (TQ19, TQ1c, TQ1d);
  and A47 (TQ1b, TQ19, TQ1a);
  and A48 (TQ8, TQ1b, EN);
  and A49 (TQ1e, TQ1c, TQ1d);
  and A50 (TQ1g, TQ1e, DIR);
  // AND_Gate A51 has open pins: in0=TQ1g, in1=EN, out=open
  or O52 (O52_out, TQ1n, TQ0);
  or O53 (O53_out, O52_out, TQ1);
  or O54 (O54_out, O53_out, TQ4);
  or O55 (O55_out, O54_out, TQ1i);
  or O56 (O56_out, O55_out, TQ1j);
  or O57 (O57_out, O56_out, TQ1k);
  or O58 (TQ1m, O57_out, TQ1l);
  or O59 (O59_out, TQ1n, TQ0);
  or O60 (O60_out, O59_out, TQ1);
  or O61 (O61_out, O60_out, TQ4);
  or O62 (O62_out, O61_out, TQ5);
  or O63 (O63_out, O62_out, TQ6);
  or O64 (O64_out, O63_out, TQ7);
  or O65 (TQa, O64_out, TQ8);

  // Other names for the same wires on the sheet: TQ1f = DIR; TQ1h = EN; TQ3 = RST; TQb = P0; TQd = P1; TQe = P2;
  //   TQf = P3
endmodule
