// Logisim project stopwatch.circ as structural Verilog
module stopwatch (
  input  RUN,
  input  RST,
  output Q0,
  output Q1,
  output Q2,
  output Q3,
  output Q4,
  output Q5,
  output Q6
);

  wire CLK_out, SWNA_out, SWNR2_out, SWNR3_out, SWNT_out, SWT0_out, SWTA1_out, SWTA2_out, SWTC_out, SWTE_out,
       SWTM1_out, SWTM2_out, SWTN1_out, SWTNR2_out, SWTO2_out, SWTW_out, SWUA1_out, SWUA2_out, SWUA3_out,
       SWUC_out, SWUM1_out, SWUM2_out, SWUM3_out, SWUN1_out, SWUN2_out, SWUO3_out, SWUW_out;

  Clock CLK (.out(CLK_out));
  // NOT_Gate SWRN has open pins: in=RUN, out=open
  T_Flip_Flop SWUF0 (.T(SWT0_out), .clk(CLK_out), .Q(Q0), .reset(RST), .preset(RST));  // open: Qn
  T_Flip_Flop SWUF1 (.T(SWUM1_out), .clk(CLK_out), .Q(Q1), .reset(RST), .preset(RST));  // open: Qn
  T_Flip_Flop SWUF2 (.T(SWUM2_out), .clk(CLK_out), .Q(Q2), .reset(RST), .preset(RST));  // open: Qn
  T_Flip_Flop SWUF3 (.T(SWUO3_out), .clk(CLK_out), .Q(Q3), .reset(RST), .preset(RST));  // open: Qn
  T_Flip_Flop SWTF0 (.T(SWTE_out), .clk(CLK_out), .Q(Q4), .reset(RST), .preset(RST));  // open: Qn
  T_Flip_Flop SWTF1 (.T(SWTM1_out), .clk(CLK_out), .Q(Q5), .reset(RST), .preset(RST));  // open: Qn
  T_Flip_Flop SWTF2 (.T(SWTO2_out), .clk(CLK_out), .Q(Q6), .reset(RST), .preset(RST));  // open: Qn
  not SWUN1 (SWUN1_out, Q1);
  and SWUA1 (SWUA1_out, Q0, SWUN1_out);
  not SWUN2 (SWUN2_out, Q2);
  and SWUA2 (SWUA2_out, SWUA1_out, SWUN2_out);
  and SWUA3 (SWUA3_out, SWUA2_out, Q3);
  not SWNA (SWNA_out, SWUA3_out);
  and SWUC (SWUC_out, SWNA_out, RUN);
  and SWUW (SWUW_out, SWUA3_out, RUN);
  or SWT0 (SWT0_out, SWUC_out, SWUW_out);
  and SWUM1 (SWUM1_out, Q0, SWUC_out);
  and SWNR2 (SWNR2_out, Q0, Q1);
  and SWUM2 (SWUM2_out, SWNR2_out, SWUC_out);
  and SWNR3 (SWNR3_out, SWNR2_out, Q2);
  and SWUM3 (SWUM3_out, SWNR3_out, SWUC_out);
  or SWUO3 (SWUO3_out, SWUM3_out, SWUW_out);
  and SWTE (SWTE_out, RUN, SWUA3_out);
  not SWTN1 (SWTN1_out, Q5);
  and SWTA1 (SWTA1_out, Q4, SWTN1_out);
  and SWTA2 (SWTA2_out, SWTA1_out, Q6);
  not SWNT (SWNT_out, SWTA2_out);
  and SWTW (SWTW_out, SWTE_out, SWTA2_out);
  and SWTC (SWTC_out, SWTE_out, SWNT_out);
  and SWTM1 (SWTM1_out, Q4, SWTC_out);
  and SWTNR2 (SWTNR2_out, Q4, Q5);
  and SWTM2 (SWTM2_out, SWTNR2_out, SWTC_out);
  or SWTO2 (SWTO2_out, SWTM2_out, SWTW_out);
endmodule
