// Logisim project subtractor_1bit.circ as structural Verilog
module subtractor_1bit (
  input  A0,
  input  B0,
  input  Bin,
  output D0,
  output Bout
);

  wire SUB0A_out, SUB0B_out, SUB0N_out, SUB0O_out, SUB0X_out;

  xor SUB0X (SUB0X_out, A0, B0);
  xor SUB0D (D0, SUB0X_out, Bin);
  not SUB0N (SUB0N_out, A0);
  or SUB0O (SUB0O_out, B0, Bin);
  and SUB0A (SUB0A_out, SUB0N_out, SUB0O_out);
  and SUB0B (SUB0B_out, B0, Bin);
  or SUB0C (Bout, SUB0A_out, SUB0B_out);

  // Other names for the same wires on the sheet: TQ0 = A0; TQ1 = B0; TQ2 = D0; TQ3 = Bin; TQ4 = Bout
endmodule
