// Logisim project subtractor_4bit.circ as structural Verilog
module subtractor_4bit (
  input  A0,
  input  B0,
  input  A1,
  input  B1,
  input  A2,
  input  B2,
  input  A3,
  input  B3,
  input  Bin,
  output D0,
  output D1,
  output D2,
  output D3,
  output Bout
);

  wire SUB0A_out, SUB0B_out, SUB0C_out, SUB0N_out, SUB0O_out, SUB0X_out, SUB1A_out, SUB1B_out, SUB1C_out,
       SUB1N_out, SUB1O_out, SUB1X_out, SUB2A_out, SUB2B_out, SUB2C_out, SUB2N_out, SUB2O_out, SUB2X_out,
       SUB3A_out, SUB3B_out, SUB3N_out, SUB3O_out, SUB3X_out;

  xor SUB0X (SUB0X_out, A0, B0);
  xor SUB0D (D0, SUB0X_out, Bin);
  not SUB0N (SUB0N_out, A0);
  or SUB0O (SUB0O_out, B0, Bin);
  and SUB0A (SUB0A_out, SUB0N_out, SUB0O_out);
  and SUB0B (SUB0B_out, B0, Bin);
  or SUB0C (SUB0C_out, SUB0A_out, SUB0B_out);
  xor SUB1X (SUB1X_out, A1, B1);
  xor SUB1D (D1, SUB1X_out, SUB0C_out);
  not SUB1N (SUB1N_out, A1);
  or SUB1O (SUB1O_out, B1, SUB0C_out);
  and SUB1A (SUB1A_out, SUB1N_out, SUB1O_out);
  and SUB1B (SUB1B_out, B1, SUB0C_out);
  or SUB1C (SUB1C_out, SUB1A_out, SUB1B_out);
  xor SUB2X (SUB2X_out, A2, B2);
  xor SUB2D (D2, SUB2X_out, SUB1C_out);
  not SUB2N (SUB2N_out, A2);
  or SUB2O (SUB2O_out, B2, SUB1C_out);
  and SUB2A (SUB2A_out, SUB2N_out, SUB2O_out);
  and SUB2B (SUB2B_out, B2, SUB1C_out);
  or SUB2C (SUB2C_out, SUB2A_out, SUB2B_out);
  xor SUB3X (SUB3X_out, A3, B3);
  xor SUB3D (D3, SUB3X_out, SUB2C_out);
  not SUB3N (SUB3N_out, A3);
  or SUB3O (SUB3O_out, B3, SUB2C_out);
  and SUB3A (SUB3A_out, SUB3N_out, SUB3O_out);
  and SUB3B (SUB3B_out, B3, SUB2C_out);
  or SUB3C (Bout, SUB3A_out, SUB3B_out);
endmodule
