// Logisim project subtractor_8bit.circ as structural Verilog
module subtractor_8bit (
  input  A0,
  input  B0,
  input  A1,
  input  B1,
  input  A2,
  input  B2,
  input  A3,
  input  B3,
  input  A4,
  input  B4,
  input  A5,
  input  B5,
  input  A6,
  input  B6,
  input  A7,
  input  B7,
  input  Bin,
  output D0,
  output D1,
  output D2,
  output D3,
  output D4,
  output D5,
  output D6,
  output D7,
  output Bout
);

  wire SUB0A_out, SUB0B_out, SUB0C_out, SUB0N_out, SUB0O_out, SUB0X_out, SUB1A_out, SUB1B_out, SUB1C_out,
       SUB1N_out, SUB1O_out, SUB1X_out, SUB2A_out, SUB2B_out, SUB2C_out, SUB2N_out, SUB2O_out, SUB2X_out,
       SUB3A_out, SUB3B_out, SUB3C_out, SUB3N_out, SUB3O_out, SUB3X_out, SUB4A_out, SUB4B_out, SUB4C_out,
       SUB4N_out, SUB4O_out, SUB4X_out, SUB5A_out, SUB5B_out, SUB5C_out, SUB5N_out, SUB5O_out, SUB5X_out,
       SUB6A_out, SUB6B_out, SUB6C_out, SUB6N_out, SUB6O_out, SUB6X_out, SUB7A_out, SUB7B_out, SUB7N_out,
       SUB7O_out, SUB7X_out;

  xor SUB0X (SUB0X_out, A0, B0);
  xor SUB0D (D0, SUB0X_out, Bin);
  not SUB0N (SUB0N_out, A0);
  or SUB0O (SUB0O_out, B0, Bin);
  and SUB0A (SUB0A_out, SUB0N_out, SUB0O_out);
  and SUB0B (SUB0B_out, B0, Bin);
  or SUB0C (SUB0C_out, SUB0A_out, SUB0B_out);
  xor SUB1X (SUB1X_out, A1, B1);
  xor SUB1D (D1, SUB1X_out, SUB0C_out);
  not SUB1N (SUB1N_out, A1);
  or SUB1O (SUB1O_out, B1, SUB0C_out);
  and SUB1A (SUB1A_out, SUB1N_out, SUB1O_out);
  and SUB1B (SUB1B_out, B1, SUB0C_out);
  or SUB1C (SUB1C_out, SUB1A_out, SUB1B_out);
  xor SUB2X (SUB2X_out, A2, B2);
  xor SUB2D (D2, SUB2X_out, SUB1C_out);
  not SUB2N (SUB2N_out, A2);
  or SUB2O (SUB2O_out, B2, SUB1C_out);
  and SUB2A (SUB2A_out, SUB2N_out, SUB2O_out);
  and SUB2B (SUB2B_out, B2, SUB1C_out);
  or SUB2C (SUB2C_out, SUB2A_out, SUB2B_out);
  xor SUB3X (SUB3X_out, A3, B3);
  xor SUB3D (D3, SUB3X_out, SUB2C_out);
  not SUB3N (SUB3N_out, A3);
  or SUB3O (SUB3O_out, B3, SUB2C_out);
  and SUB3A (SUB3A_out, SUB3N_out, SUB3O_out);
  and SUB3B (SUB3B_out, B3, SUB2C_out);
  or SUB3C (SUB3C_out, SUB3A_out, SUB3B_out);
  xor SUB4X (SUB4X_out, A4, B4);
  xor SUB4D (D4, SUB4X_out, SUB3C_out);
  not SUB4N (SUB4N_out, A4);
  or SUB4O (SUB4O_out, B4, SUB3C_out);
  and SUB4A (SUB4A_out, SUB4N_out, SUB4O_out);
  and SUB4B (SUB4B_out, B4, SUB3C_out);
  or SUB4C (SUB4C_out, SUB4A_out, SUB4B_out);
  xor SUB5X (SUB5X_out, A5, B5);
  xor SUB5D (D5, SUB5X_out, SUB4C_out);
  not SUB5N (SUB5N_out, A5);
  or SUB5O (SUB5O_out, B5, SUB4C_out);
  and SUB5A (SUB5A_out, SUB5N_out, SUB5O_out);
  and SUB5B (SUB5B_out, B5, SUB4C_out);
  or SUB5C (SUB5C_out, SUB5A_out, SUB5B_out);
  xor SUB6X (SUB6X_out, A6, B6);
  xor SUB6D (D6, SUB6X_out, SUB5C_out);
  not SUB6N (SUB6N_out, A6);
  or SUB6O (SUB6O_out, B6, SUB5C_out);
  and SUB6A (SUB6A_out, SUB6N_out, SUB6O_out);
  and SUB6B (SUB6B_out, B6, SUB5C_out);
  or SUB6C (SUB6C_out, SUB6A_out, SUB6B_out);
  xor SUB7X (SUB7X_out, A7, B7);
  xor SUB7D (D7, SUB7X_out, SUB6C_out);
  not SUB7N (SUB7N_out, A7);
  or SUB7O (SUB7O_out, B7, SUB6C_out);
  and SUB7A (SUB7A_out, SUB7N_out, SUB7O_out);
  and SUB7B (SUB7B_out, B7, SUB6C_out);
  or SUB7C (Bout, SUB7A_out, SUB7B_out);
endmodule
