// Logisim project tff.circ as structural Verilog
module tff (
  input  T,
  input  RST,
  output Q,
  output nQ
);

  wire CLK_out;

  Clock CLK (.out(CLK_out));
  T_Flip_Flop U1 (.T(T), .clk(CLK_out), .Q(Q), .Qn(nQ), .reset(RST), .preset(RST));
endmodule
