// Logisim project traffic_light.circ as structural Verilog
module traffic_light (
  input  CLK,
  input  EN,
  input  RST,
  output RED,
  output YELLOW,
  output GREEN
);

  wire N2_out, U1_q, U2_q;

  T_Flip_Flop U1 (.T(EN), .clk(CLK), .Q(U1_q), .reset(RST));  // open: Qn, preset
  T_Flip_Flop U2 (.T(U1_q), .clk(CLK), .Q(U2_q), .reset(RST));  // open: Qn, preset
  not N1 (GREEN, U2_q);
  not N2 (N2_out, U1_q);
  and R1 (RED, U2_q, U1_q);
  and Y1 (YELLOW, U2_q, N2_out);

  // Other names for the same wires on the sheet: TQ0 = EN; TQ1 = CLK; TQ2 = RST; TQ3 = GREEN; TQ4 = RED; TQ5 = YELLOW
endmodule
