// Logisim project tristate_buffer.circ as structural Verilog
module tristate_buffer (
  input  A,
  input  nG,
  output Y
);

  _74125 U1 (.pin1(nG), .pin2(A), .pin3(Y));  // open: pin4, pin5, pin6, pin13, pin12, pin11, pin10, pin9, pin8

  // Other names for the same wires on the sheet: TQ0 = nG; TQ1 = A; TQ2 = Y
endmodule
