// Logisim project ttl_7402.circ as structural Verilog
module ttl_7402 (
  input  pin2,
  input  pin3,
  input  pin5,
  input  pin6,
  input  pin8,
  input  pin9,
  input  pin11,
  input  pin12,
  output pin1,
  output pin4,
  output pin10,
  output pin13
);

  _7402 u_7402_1 (
    .pin1(pin2), .pin2(pin2), .pin3(pin2), .pin4(pin2), .pin5(pin2), .pin6(pin2), .pin13(pin2), .pin12(pin2),
    .pin11(pin2), .pin10(pin2), .pin9(pin2), .pin8(pin2));

  assign pin1 = pin2;
  assign pin3 = pin2;
  assign pin4 = pin2;
  assign pin5 = pin2;
  assign pin6 = pin2;
  assign pin8 = pin2;
  assign pin9 = pin2;
  assign pin10 = pin2;
  assign pin11 = pin2;
  assign pin12 = pin2;
  assign pin13 = pin2;
endmodule
