// Logisim project ttl_74138.circ as structural Verilog
module ttl_74138 (
  input  A,
  input  B,
  input  C,
  input  nG2A_Enable,
  input  nG2B_Enable,
  input  G1_Enable,
  output nY7,
  output nY6,
  output nY5,
  output nY4,
  output nY3,
  output nY2,
  output nY1,
  output nY0
);

  _74138 u_74138_1 (
    .pin1(A), .pin2(A), .pin3(A), .pin4(A), .pin5(A), .pin6(A), .pin7(nY0), .pin15(nY0), .pin14(nY0),
    .pin13(nY0), .pin12(nY0), .pin11(nY0), .pin10(nY0), .pin9(nY0));

  assign B = A;
  assign C = A;
  assign G1_Enable = A;
  assign nG2A_Enable = A;
  assign nG2B_Enable = A;
  assign nY1 = nY0;
  assign nY2 = nY0;
  assign nY3 = nY0;
  assign nY4 = nY0;
  assign nY5 = nY0;
  assign nY6 = nY0;
  assign nY7 = nY0;
endmodule
