// Logisim project ttl_74139.circ as structural Verilog
module ttl_74139 (
  input  _1nG_Enable,
  input  _1A,
  input  _1B,
  input  _2B,
  input  _2A,
  input  _2nG_Enable,
  output _1nY0,
  output _1nY1,
  output _1nY2,
  output _1nY3,
  output _2nY3,
  output _2nY2,
  output _2nY1,
  output _2nY0
);

  _74139 u_74139_1 (
    .pin1(_1A), .pin2(_1A), .pin3(_1A), .pin4(_1nY0), .pin5(_1nY0), .pin6(_1nY0), .pin7(_1nY0), .pin15(_1A),
    .pin14(_1A), .pin13(_1A), .pin12(_1nY0), .pin11(_1nY0), .pin10(_1nY0), .pin9(_1nY0));

  assign _1B = _1A;
  assign _1nG_Enable = _1A;
  assign _1nY1 = _1nY0;
  assign _1nY2 = _1nY0;
  assign _1nY3 = _1nY0;
  assign _2A = _1A;
  assign _2B = _1A;
  assign _2nG_Enable = _1A;
  assign _2nY0 = _1nY0;
  assign _2nY1 = _1nY0;
  assign _2nY2 = _1nY0;
  assign _2nY3 = _1nY0;
endmodule
