// Logisim project ttl_74151.circ as structural Verilog
module ttl_74151 (
  input  D3,
  input  D2,
  input  D1,
  input  D0,
  input  nG,
  input  C,
  input  B,
  input  A,
  input  D7,
  input  D6,
  input  D5,
  input  D4,
  output Y,
  output W
);

  _74151 u_74151_1 (
    .pin1(A), .pin2(A), .pin3(A), .pin4(A), .pin5(A), .pin6(A), .pin7(A), .pin15(A), .pin14(A), .pin13(A),
    .pin12(A), .pin11(A), .pin10(A), .pin9(A));

  assign B = A;
  assign C = A;
  assign D0 = A;
  assign D1 = A;
  assign D2 = A;
  assign D3 = A;
  assign D4 = A;
  assign D5 = A;
  assign D6 = A;
  assign D7 = A;
  assign nG = A;
  assign W = A;
  assign Y = A;
endmodule
