// Logisim project ttl_74151_macro.circ as structural Verilog
module ttl_74151_macro (
  input  D0,
  input  S0,
  input  D1,
  input  S1,
  input  D2,
  input  S2,
  input  D3,
  input  nG,
  input  D4,
  input  D5,
  input  D6,
  input  D7,
  output Y,
  output nW
);

  wire a0_to_b, a1_to_b, a2_to_b, a3_to_b, a4_to_b, a5_to_b, a6_to_b, a7_to_b, b0_to_c, b1_to_c, b2_to_c,
       b3_to_c, b4_to_c, b5_to_c, b6_to_c, b7_to_c, c0_to_d, c1_to_d, c2_to_d, c3_to_d, c4_to_d, c5_to_d,
       c6_to_d, c7_to_d, en_fanout, ns0_fanout, ns1_fanout, ns2_fanout, or01_to_03, or03_to_y, or23_to_03,
       or45_to_47, or47_to_y, or67_to_47, t0_to_or01, t1_to_or01, t2_to_or23, t3_to_or23, t4_to_or45,
       t5_to_or45, t6_to_or67, t7_to_or67;

  not not_1 (ns0_fanout, S0);
  not not_2 (ns1_fanout, S1);
  not not_3 (ns2_fanout, S2);
  not not_4 (en_fanout, nG);
  and and_1 (a0_to_b, D0, en_fanout);
  and and_2 (a1_to_b, D1, en_fanout);
  and and_3 (a2_to_b, D2, en_fanout);
  and and_4 (a3_to_b, D3, en_fanout);
  and and_5 (a4_to_b, D4, en_fanout);
  and and_6 (a5_to_b, D5, en_fanout);
  and and_7 (a6_to_b, D6, en_fanout);
  and and_8 (a7_to_b, D7, en_fanout);
  and and_9 (b0_to_c, ns0_fanout, a0_to_b);
  and and_10 (b1_to_c, S0, a1_to_b);
  and and_11 (b2_to_c, ns0_fanout, a2_to_b);
  and and_12 (b3_to_c, S0, a3_to_b);
  and and_13 (b4_to_c, ns0_fanout, a4_to_b);
  and and_14 (b5_to_c, S0, a5_to_b);
  and and_15 (b6_to_c, ns0_fanout, a6_to_b);
  and and_16 (b7_to_c, S0, a7_to_b);
  and and_17 (c0_to_d, ns1_fanout, b0_to_c);
  and and_18 (c1_to_d, ns1_fanout, b1_to_c);
  and and_19 (c2_to_d, S1, b2_to_c);
  and and_20 (c3_to_d, S1, b3_to_c);
  and and_21 (c4_to_d, ns1_fanout, b4_to_c);
  and and_22 (c5_to_d, ns1_fanout, b5_to_c);
  and and_23 (c6_to_d, S1, b6_to_c);
  and and_24 (c7_to_d, S1, b7_to_c);
  and and_25 (t0_to_or01, ns2_fanout, c0_to_d);
  and and_26 (t1_to_or01, ns2_fanout, c1_to_d);
  and and_27 (t2_to_or23, ns2_fanout, c2_to_d);
  and and_28 (t3_to_or23, ns2_fanout, c3_to_d);
  and and_29 (t4_to_or45, S2, c4_to_d);
  and and_30 (t5_to_or45, S2, c5_to_d);
  and and_31 (t6_to_or67, S2, c6_to_d);
  and and_32 (t7_to_or67, S2, c7_to_d);
  or or_1 (or01_to_03, t0_to_or01, t1_to_or01);
  or or_2 (or23_to_03, t2_to_or23, t3_to_or23);
  or or_3 (or45_to_47, t4_to_or45, t5_to_or45);
  or or_4 (or67_to_47, t6_to_or67, t7_to_or67);
  or or_5 (or03_to_y, or01_to_03, or23_to_03);
  or or_6 (or47_to_y, or45_to_47, or67_to_47);
  or or_7 (Y, or03_to_y, or47_to_y);
  not not_5 (nW, Y);

  // Other names for the same wires on the sheet: s0_fanout = S0; s1_fanout = S1; s2_fanout = S2
endmodule
