// Logisim project ttl_74151_native.circ as structural Verilog
module ttl_74151_native (
  input  D0,
  output Y
);

  _74151 u_74151_1 (
    .pin1(D0), .pin2(D0), .pin3(D0), .pin4(D0), .pin5(D0), .pin6(D0), .pin7(D0));  // open: pin15, pin14, pin13, pin12, pin11, pin10, pin9

  assign Y = D0;
endmodule
