// Logisim project ttl_74153.circ as structural Verilog
module ttl_74153 (
  input  n1E,
  input  S1,
  input  _1D3,
  input  _1D2,
  input  _1D1,
  input  _1D0,
  input  _2D0,
  input  _2D1,
  input  _2D2,
  input  _2D3,
  input  S0,
  input  n2E,
  output _1Y,
  output _2Y
);

  _74153 u_74153_1 (
    .pin1(_1D0), .pin2(_1D0), .pin3(_1D0), .pin4(_1D0), .pin5(_1D0), .pin6(_1D0), .pin7(_1Y), .pin15(_1D0),
    .pin14(_1D0), .pin13(_1D0), .pin12(_1D0), .pin11(_1D0), .pin10(_1D0), .pin9(_1Y));

  assign _1D1 = _1D0;
  assign _1D2 = _1D0;
  assign _1D3 = _1D0;
  assign _2D0 = _1D0;
  assign _2D1 = _1D0;
  assign _2D2 = _1D0;
  assign _2D3 = _1D0;
  assign _2Y = _1Y;
  assign n1E = _1D0;
  assign n2E = _1D0;
  assign S0 = _1D0;
  assign S1 = _1D0;
endmodule
