// Logisim project ttl_74158.circ as structural Verilog
module ttl_74158 (
  input  SELECT,
  input  _1A,
  input  _1B,
  input  _2A,
  input  _2B,
  input  _3B,
  input  _3A,
  input  _4B,
  input  _4A,
  input  nSTROBE,
  output _1Y,
  output _2Y,
  output _3Y,
  output _4Y
);

  _74158 u_74158_1 (
    .pin1(_1A), .pin2(_1A), .pin3(_1A), .pin4(_1A), .pin5(_1A), .pin6(_1A), .pin7(_1A), .pin15(_1A),
    .pin14(_1A), .pin13(_1A), .pin12(_1A), .pin11(_1A), .pin10(_1A), .pin9(_1A));

  assign _1B = _1A;
  assign _1Y = _1A;
  assign _2A = _1A;
  assign _2B = _1A;
  assign _2Y = _1A;
  assign _3A = _1A;
  assign _3B = _1A;
  assign _3Y = _1A;
  assign _4A = _1A;
  assign _4B = _1A;
  assign _4Y = _1A;
  assign nSTROBE = _1A;
  assign SELECT = _1A;
endmodule
