// Logisim project ttl_74160.circ as structural Verilog
module ttl_74160 (
  input  MR_CLR,
  input  CP_CLK,
  input  D0_A,
  input  D1_B,
  input  D2_C,
  input  D3_D,
  input  CE_ENP,
  input  PE_LOAD,
  input  CET_ENT,
  output Q3_QD,
  output Q2_QC,
  output A1_QB,
  output A0_QA,
  output TC_RC0
);

  _74160 u_74160_1 (
    .pin1(CE_ENP), .pin2(CP_CLK), .pin3(D0_A), .pin4(D1_B), .pin5(D2_C), .pin6(D3_D), .pin7(CE_ENP),
    .pin15(CP_CLK), .pin14(D0_A), .pin13(D1_B), .pin12(D2_C), .pin11(D3_D), .pin10(CE_ENP), .pin9(PE_LOAD));

  assign A0_QA = D0_A;
  assign A1_QB = D1_B;
  assign CET_ENT = CE_ENP;
  assign MR_CLR = CE_ENP;
  assign Q2_QC = D2_C;
  assign Q3_QD = D3_D;
  assign TC_RC0 = CP_CLK;
endmodule
