// Logisim project ttl_74160_macro.circ as structural Verilog
module ttl_74160_macro (
  input  [3:0] D_3_0,
  input  CLK,
  input  CLR,
  input  LOAD,
  input  UP,
  input  EN,
  output [3:0] Q_3_0,
  output TC
);

  // _74160_core 74160_core_1: pin names not known; wires that end beside it: D_3_0, CLK, CLR, LOAD, UP, EN, Q_3_0, TC
endmodule

module _74160_core (
  input  CLR,
  input  LOAD,
  input  UP_1,
  input  EN,
  input  CLK,
  input  [3:0] D_3_0,
  output TC,
  output [3:0] Q_3_0
);

  Counter #(.max('h9), .width(4)) CTR_DIV10 (
    .clr(CLR), .load(LOAD), .up(UP_1), .count(EN), .clk(CLK), .D(D_3_0), .carry(TC), .Q(Q_3_0));
endmodule
