// Logisim project ttl_74161.circ as structural Verilog
module ttl_74161 (
  input  MR_CLR,
  input  CP_CLK,
  input  D0_A,
  input  D1_B,
  input  D2_C,
  input  D3_D,
  input  CE_ENP,
  input  PE_LOAD,
  input  CET_ENT,
  output Q3_QD,
  output Q2_QC,
  output A1_QB,
  output A0_QA,
  output TC_RC0
);

  _74161 u_74161_1 (
    .pin1(CE_ENP), .pin2(CE_ENP), .pin3(CE_ENP), .pin4(CE_ENP), .pin5(CE_ENP), .pin6(CE_ENP), .pin7(CE_ENP),
    .pin15(CE_ENP), .pin14(CE_ENP), .pin13(CE_ENP), .pin12(CE_ENP), .pin11(CE_ENP), .pin10(CE_ENP),
    .pin9(CE_ENP));

  assign A0_QA = CE_ENP;
  assign A1_QB = CE_ENP;
  assign CET_ENT = CE_ENP;
  assign CP_CLK = CE_ENP;
  assign D0_A = CE_ENP;
  assign D1_B = CE_ENP;
  assign D2_C = CE_ENP;
  assign D3_D = CE_ENP;
  assign MR_CLR = CE_ENP;
  assign PE_LOAD = CE_ENP;
  assign Q2_QC = CE_ENP;
  assign Q3_QD = CE_ENP;
  assign TC_RC0 = CE_ENP;
endmodule
