// Logisim project ttl_74164.circ as structural Verilog
module ttl_74164 (
  input  A,
  input  B,
  input  Clock,
  input  Clear,
  output QA,
  output QB,
  output QC,
  output QD,
  output QE,
  output QF,
  output QG,
  output QH
);

  _74164 u_74164_1 (
    .pin1(A), .pin2(A), .pin3(Clear), .pin4(Clear), .pin5(Clear), .pin6(Clear), .pin13(Clear), .pin12(Clear),
    .pin11(Clear), .pin10(Clear), .pin9(Clear), .pin8(Clear));

  assign B = A;
  assign Clock = Clear;
  assign QA = Clear;
  assign QB = Clear;
  assign QC = Clear;
  assign QD = Clear;
  assign QE = Clear;
  assign QF = Clear;
  assign QG = Clear;
  assign QH = Clear;
endmodule
