// Logisim project ttl_74165.circ as structural Verilog
module ttl_74165 (
  input  Shift_Load,
  input  Clock,
  input  P4,
  input  P5,
  input  P6,
  input  P7,
  input  Serial_Input,
  input  P0,
  input  P1,
  input  P2,
  input  P3,
  input  Clock_Inhibit,
  output Q7n,
  output Q7
);

  _74165 u_74165_1 (
    .pin1(Clock), .pin2(Clock), .pin3(Clock), .pin4(Clock), .pin5(Clock), .pin6(Clock), .pin7(Q7),
    .pin15(Clock), .pin14(Clock), .pin13(Clock), .pin12(Clock), .pin11(Clock), .pin10(Clock), .pin9(Q7));

  assign Clock_Inhibit = Clock;
  assign P0 = Clock;
  assign P1 = Clock;
  assign P2 = Clock;
  assign P3 = Clock;
  assign P4 = Clock;
  assign P5 = Clock;
  assign P6 = Clock;
  assign P7 = Clock;
  assign Q7n = Q7;
  assign Serial_Input = Clock;
  assign Shift_Load = Clock;
endmodule
