// Logisim project ttl_74166.circ as structural Verilog
module ttl_74166 (
  input  Serial_Input,
  input  P0,
  input  P1,
  input  P2,
  input  P3,
  input  Clock_Inhibit,
  input  Clock,
  input  Clear,
  input  P4,
  input  P5,
  input  P6,
  input  P7,
  input  Shift_Load,
  output Q7
);

  _74166 u_74166_1 (
    .pin1(Clear), .pin2(Clear), .pin3(Clear), .pin4(Clear), .pin5(Clear), .pin6(Clear), .pin7(Clear),
    .pin15(Clear), .pin14(Clear), .pin13(Clear), .pin12(Clear), .pin11(Clear), .pin10(Clear), .pin9(Clear));

  assign Clock = Clear;
  assign Clock_Inhibit = Clear;
  assign P0 = Clear;
  assign P1 = Clear;
  assign P2 = Clear;
  assign P3 = Clear;
  assign P4 = Clear;
  assign P5 = Clear;
  assign P6 = Clear;
  assign P7 = Clear;
  assign Q7 = Clear;
  assign Serial_Input = Clear;
  assign Shift_Load = Clear;
endmodule
