// Logisim project ttl_74175.circ as structural Verilog
module ttl_74175 (
  input  nCLR,
  input  D1,
  input  D2,
  input  CLK,
  input  D3,
  input  D4,
  output Q1,
  output nQ1,
  output nQ2,
  output Q2,
  output Q3,
  output nQ3,
  output nQ4,
  output Q4
);

  _74175 u_74175_1 (
    .pin1(CLK), .pin2(CLK), .pin3(CLK), .pin4(CLK), .pin5(CLK), .pin6(CLK), .pin7(CLK), .pin15(CLK),
    .pin14(CLK), .pin13(CLK), .pin12(CLK), .pin11(CLK), .pin10(CLK), .pin9(CLK));

  assign D1 = CLK;
  assign D2 = CLK;
  assign D3 = CLK;
  assign D4 = CLK;
  assign nCLR = CLK;
  assign nQ1 = CLK;
  assign nQ2 = CLK;
  assign nQ3 = CLK;
  assign nQ4 = CLK;
  assign Q1 = CLK;
  assign Q2 = CLK;
  assign Q3 = CLK;
  assign Q4 = CLK;
endmodule
