// Logisim project ttl_74181.circ as structural Verilog
module ttl_74181 (
  input  B0,
  input  A0,
  input  S3,
  input  S2,
  input  S1,
  input  S0,
  input  nCi,
  input  M,
  input  B3,
  input  A3,
  input  B2,
  input  A2,
  input  B1,
  input  A1,
  output F0,
  output F1,
  output F2,
  output F3,
  output A_B,
  output Pn,
  output Co,
  output Gn
);

  // _74181 74181_1: pin names not known; wires that end beside it: A0, A_B, A0, A_B

  assign A1 = A0;
  assign A2 = A0;
  assign A3 = A0;
  assign B0 = A0;
  assign B1 = A0;
  assign B2 = A0;
  assign B3 = A0;
  assign Co = A_B;
  assign F0 = A_B;
  assign F1 = A_B;
  assign F2 = A_B;
  assign F3 = A_B;
  assign Gn = A_B;
  assign M = A0;
  assign nCi = A0;
  assign Pn = A_B;
  assign S0 = A0;
  assign S1 = A0;
  assign S2 = A0;
  assign S3 = A0;
endmodule
