// Logisim project ttl_74182.circ as structural Verilog
module ttl_74182 (
  input  G1,
  input  P1,
  input  G0,
  input  P0,
  input  G3,
  input  P3,
  input  Cn,
  input  G2,
  input  P2,
  output P,
  output Cnz,
  output G,
  output Cny,
  output Cnx
);

  _74182 u_74182_1 (
    .pin1(Cn), .pin2(Cn), .pin3(Cn), .pin4(Cn), .pin5(Cn), .pin6(Cn), .pin7(Cnx), .pin15(Cn), .pin14(Cn),
    .pin13(Cn), .pin12(Cnx), .pin11(Cnx), .pin10(Cnx), .pin9(Cnx));

  assign Cny = Cnx;
  assign Cnz = Cnx;
  assign G = Cnx;
  assign G0 = Cn;
  assign G1 = Cn;
  assign G2 = Cn;
  assign G3 = Cn;
  assign P = Cnx;
  assign P0 = Cn;
  assign P1 = Cn;
  assign P2 = Cn;
  assign P3 = Cn;
endmodule
