// Logisim project ttl_74193.circ as structural Verilog
module ttl_74193 (
  input  Data_Input_B,
  input  Count_Down,
  input  Count_Up,
  input  Data_Input_D,
  input  Data_Input_C,
  input  Load,
  input  Clear,
  input  Data_Input_A,
  output Data_Output_B,
  output Data_Output_A,
  output Data_Output_C,
  output Data_Output_D,
  output Carry,
  output Borrow
);

  _74193 u_74193_1 (
    .pin1(Clear), .pin2(Clear), .pin3(Clear), .pin4(Clear), .pin5(Clear), .pin6(Clear), .pin7(Clear),
    .pin15(Clear), .pin14(Clear), .pin13(Clear), .pin12(Clear), .pin11(Clear), .pin10(Clear), .pin9(Clear));

  assign Borrow = Clear;
  assign Carry = Clear;
  assign Count_Down = Clear;
  assign Count_Up = Clear;
  assign Data_Input_A = Clear;
  assign Data_Input_B = Clear;
  assign Data_Input_C = Clear;
  assign Data_Input_D = Clear;
  assign Data_Output_A = Clear;
  assign Data_Output_B = Clear;
  assign Data_Output_C = Clear;
  assign Data_Output_D = Clear;
  assign Load = Clear;
endmodule
