// Logisim project ttl_74194.circ as structural Verilog
module ttl_74194 (
  input  nCLR,
  input  SR,
  input  A,
  input  B,
  input  C,
  input  D,
  input  SL,
  input  S0,
  input  S1,
  input  CLK,
  output QD,
  output QC,
  output QB,
  output QA
);

  _74194 u_74194_1 (
    .pin1(A), .pin2(A), .pin3(A), .pin4(A), .pin5(A), .pin6(A), .pin7(A), .pin15(A), .pin14(A), .pin13(A),
    .pin12(A), .pin11(A), .pin10(A), .pin9(A));

  assign B = A;
  assign C = A;
  assign CLK = A;
  assign D = A;
  assign nCLR = A;
  assign QA = A;
  assign QB = A;
  assign QC = A;
  assign QD = A;
  assign S0 = A;
  assign S1 = A;
  assign SL = A;
  assign SR = A;
endmodule
