// Logisim project ttl_7421.circ as structural Verilog
module ttl_7421 (
  input  A0,
  input  B0,
  input  C0,
  input  D0,
  input  D1,
  input  C1,
  input  B1,
  input  A1,
  output Y0,
  output Y1
);

  // _7421 7421_1: pin names not known; wires that end beside it: A0, A0, A0, A0, A0, A0, A0, A0, Y0, Y0

  assign A1 = A0;
  assign B0 = A0;
  assign B1 = A0;
  assign C0 = A0;
  assign C1 = A0;
  assign D0 = A0;
  assign D1 = A0;
  assign Y1 = Y0;
endmodule
