// Logisim project ttl_74240.circ as structural Verilog
module ttl_74240 (
  input  n1G,
  input  _1A1,
  input  _1A2,
  input  _1A3,
  input  _1A4,
  input  _2A1,
  input  _2A2,
  input  _2A3,
  input  _2A4,
  input  n2G,
  output n2Y4,
  output n2Y3,
  output n2Y2,
  output n2Y1,
  output n1Y4,
  output n1Y3,
  output n1Y2,
  output n1Y1
);

  _74240 u_74240_1 (
    .pin1(_1A1), .pin2(_1A1), .pin3(_1A1), .pin4(_1A1), .pin5(_1A1), .pin6(_1A1), .pin7(_1A1), .pin8(_1A1),
    .pin9(_1A1), .pin19(_1A1), .pin18(_1A1), .pin17(_1A1), .pin16(_1A1), .pin15(_1A1), .pin14(_1A1),
    .pin13(_1A1), .pin12(_1A1), .pin11(_1A1));

  assign _1A2 = _1A1;
  assign _1A3 = _1A1;
  assign _1A4 = _1A1;
  assign _2A1 = _1A1;
  assign _2A2 = _1A1;
  assign _2A3 = _1A1;
  assign _2A4 = _1A1;
  assign n1G = _1A1;
  assign n1Y1 = _1A1;
  assign n1Y2 = _1A1;
  assign n1Y3 = _1A1;
  assign n1Y4 = _1A1;
  assign n2G = _1A1;
  assign n2Y1 = _1A1;
  assign n2Y2 = _1A1;
  assign n2Y3 = _1A1;
  assign n2Y4 = _1A1;
endmodule
