// Logisim project ttl_74245.circ as structural Verilog
module ttl_74245 (
  input  DIR,
  input  A1,
  input  A2,
  input  A3,
  input  A4,
  input  A5,
  input  A6,
  input  A7,
  input  A8,
  input  B8,
  input  B7,
  input  B6,
  input  B5,
  input  B4,
  input  B3,
  input  B2,
  input  B1,
  input  nOE
);

  _74245 u_74245_1 (
    .pin1(A1), .pin2(A1), .pin3(A1), .pin4(A1), .pin5(A1), .pin6(A1), .pin7(A1), .pin8(A1), .pin9(A1),
    .pin19(A1), .pin18(A1), .pin17(A1), .pin16(A1), .pin15(A1), .pin14(A1), .pin13(A1), .pin12(A1), .pin11(A1));

  assign A2 = A1;
  assign A3 = A1;
  assign A4 = A1;
  assign A5 = A1;
  assign A6 = A1;
  assign A7 = A1;
  assign A8 = A1;
  assign B1 = A1;
  assign B2 = A1;
  assign B3 = A1;
  assign B4 = A1;
  assign B5 = A1;
  assign B6 = A1;
  assign B7 = A1;
  assign B8 = A1;
  assign DIR = A1;
  assign nOE = A1;
endmodule
