// Logisim project ttl_74283.circ as structural Verilog
module ttl_74283 (
  input  B2,
  input  A2,
  input  A1,
  input  B1,
  input  CIN,
  input  B4,
  input  A4,
  input  A3,
  input  B3,
  output _2,
  output _1,
  output C4,
  output _4,
  output _3
);

  _74283 u_74283_1 (
    .pin1(A1), .pin2(A1), .pin3(A1), .pin4(A1), .pin5(A1), .pin6(A1), .pin7(A1), .pin15(A1), .pin14(A1),
    .pin13(A1), .pin12(A1), .pin11(A1), .pin10(A1), .pin9(A1));

  assign _1 = A1;
  assign _2 = A1;
  assign _3 = A1;
  assign _4 = A1;
  assign A2 = A1;
  assign A3 = A1;
  assign A4 = A1;
  assign B1 = A1;
  assign B2 = A1;
  assign B3 = A1;
  assign B4 = A1;
  assign C4 = A1;
  assign CIN = A1;
endmodule
