// Logisim project ttl_74299.circ as structural Verilog
module ttl_74299 (
  input  S0,
  input  nOE1,
  input  nOE2,
  input  nCLR,
  input  SR,
  input  CLK,
  input  SL,
  input  S1,
  output IOG,
  output IOE,
  output IOC,
  output IOA,
  output QA,
  output IOB,
  output IOD,
  output IOF,
  output IOH,
  output QH
);

  _74299 u_74299_1 (
    .pin1(CLK), .pin2(CLK), .pin3(CLK), .pin4(CLK), .pin5(CLK), .pin6(CLK), .pin7(CLK), .pin8(CLK),
    .pin9(CLK), .pin19(CLK), .pin18(CLK), .pin17(CLK), .pin16(CLK), .pin15(CLK), .pin14(CLK), .pin13(CLK),
    .pin12(CLK), .pin11(CLK));

  assign IOA = CLK;
  assign IOB = CLK;
  assign IOC = CLK;
  assign IOD = CLK;
  assign IOE = CLK;
  assign IOF = CLK;
  assign IOG = CLK;
  assign IOH = CLK;
  assign nCLR = CLK;
  assign nOE1 = CLK;
  assign nOE2 = CLK;
  assign QA = CLK;
  assign QH = CLK;
  assign S0 = CLK;
  assign S1 = CLK;
  assign SL = CLK;
  assign SR = CLK;
endmodule
