// Logisim project ttl_7430.circ as structural Verilog
module ttl_7430 (
  input  A,
  input  B,
  input  C,
  input  D,
  input  E,
  input  F,
  input  G,
  input  H,
  output Y
);

  // _7430 7430_1: pin names not known; wires that end beside it: A, A, A, A, A, A, A, A, Y

  assign B = A;
  assign C = A;
  assign D = A;
  assign E = A;
  assign F = A;
  assign G = A;
  assign H = A;
endmodule
