// Logisim project ttl_74377.circ as structural Verilog
module ttl_74377 (
  input  nCLKen,
  input  D1,
  input  D2,
  input  D3,
  input  D4,
  input  CLK,
  input  D5,
  input  D6,
  input  D7,
  input  D8,
  output Q1,
  output Q2,
  output Q3,
  output Q4,
  output Q5,
  output Q6,
  output Q7,
  output Q8
);

  _74377 u_74377_1 (
    .pin1(CLK), .pin2(CLK), .pin3(CLK), .pin4(CLK), .pin5(CLK), .pin6(CLK), .pin7(CLK), .pin8(CLK),
    .pin9(CLK), .pin19(CLK), .pin18(CLK), .pin17(CLK), .pin16(CLK), .pin15(CLK), .pin14(CLK), .pin13(CLK),
    .pin12(CLK), .pin11(CLK));

  assign D1 = CLK;
  assign D2 = CLK;
  assign D3 = CLK;
  assign D4 = CLK;
  assign D5 = CLK;
  assign D6 = CLK;
  assign D7 = CLK;
  assign D8 = CLK;
  assign nCLKen = CLK;
  assign Q1 = CLK;
  assign Q2 = CLK;
  assign Q3 = CLK;
  assign Q4 = CLK;
  assign Q5 = CLK;
  assign Q6 = CLK;
  assign Q7 = CLK;
  assign Q8 = CLK;
endmodule
