// Logisim project ttl_74381.circ as structural Verilog
module ttl_74381 (
  input  A1,
  input  B1,
  input  A0,
  input  B0,
  input  S0,
  input  S1,
  input  S2,
  input  Ci,
  input  B3,
  input  A3,
  input  B2,
  input  A2,
  output F0,
  output F1,
  output F2,
  output F3,
  output Gn,
  output Pn
);

  // _74381 74381_1: pin names not known; wires that end beside it: A0, F0, A0, F0

  assign A1 = A0;
  assign A2 = A0;
  assign A3 = A0;
  assign B0 = A0;
  assign B1 = A0;
  assign B2 = A0;
  assign B3 = A0;
  assign Ci = A0;
  assign F1 = F0;
  assign F2 = F0;
  assign F3 = F0;
  assign Gn = F0;
  assign Pn = F0;
  assign S0 = A0;
  assign S1 = A0;
  assign S2 = A0;
endmodule
