// Logisim project ttl_7444.circ as structural Verilog
module ttl_7444 (
  input  D,
  input  C,
  input  B,
  input  A,
  output O0,
  output O1,
  output O2,
  output O3,
  output O4,
  output O5,
  output O6,
  output O7,
  output O8,
  output O9
);

  _7444 u_7444_1 (
    .pin1(O0), .pin2(O0), .pin3(O0), .pin4(O0), .pin5(O0), .pin6(O0), .pin7(O0), .pin15(A), .pin14(A),
    .pin13(A), .pin12(A), .pin11(O0), .pin10(O0), .pin9(O0));

  assign B = A;
  assign C = A;
  assign D = A;
  assign O1 = O0;
  assign O2 = O0;
  assign O3 = O0;
  assign O4 = O0;
  assign O5 = O0;
  assign O6 = O0;
  assign O7 = O0;
  assign O8 = O0;
  assign O9 = O0;
endmodule
