// Logisim project ttl_7447.circ as structural Verilog
module ttl_7447 (
  input  B,
  input  C,
  input  LT,
  input  BI,
  input  RBI,
  input  D,
  input  A,
  output e,
  output out_9,
  output out_10,
  output out_11,
  output out_12,
  output g,
  output f
);

  _7447 u_7447_1 (
    .pin1(A), .pin2(A), .pin3(A), .pin4(A), .pin5(A), .pin6(A), .pin7(A), .pin15(e), .pin14(e), .pin13(e),
    .pin12(e), .pin11(e), .pin10(e), .pin9(e));

  assign B = A;
  assign BI = A;
  assign C = A;
  assign D = A;
  assign f = e;
  assign g = e;
  assign LT = A;
  assign out_9 = e;
  assign out_10 = e;
  assign out_11 = e;
  assign out_12 = e;
  assign RBI = A;
endmodule
