// Logisim project ttl_7451.circ as structural Verilog
module ttl_7451 (
  input  A1,
  input  A2,
  input  B2,
  input  C2,
  input  D2,
  input  C1,
  input  D1,
  input  B1,
  output Y2,
  output Y1
);

  // _7451 7451_1: pin names not known; wires that end beside it: A1, A1, A1, A1, A1, A1, A1, A1, Y1, Y1

  assign A2 = A1;
  assign B1 = A1;
  assign B2 = A1;
  assign C1 = A1;
  assign C2 = A1;
  assign D1 = A1;
  assign D2 = A1;
  assign Y2 = Y1;
endmodule
