// Logisim project ttl_7454.circ as structural Verilog
module ttl_7454 (
  input  A,
  input  C,
  input  D,
  input  E,
  input  F,
  input  G,
  input  H,
  input  B,
  output Y
);

  // _7454 7454_1: pin names not known; wires that end beside it: A, A, A, A, A, A, A, A, Y

  assign B = A;
  assign C = A;
  assign D = A;
  assign E = A;
  assign F = A;
  assign G = A;
  assign H = A;
endmodule
