// Logisim project ttl_74541.circ as structural Verilog
module ttl_74541 (
  input  nOE1,
  input  A1,
  input  A2,
  input  A3,
  input  A4,
  input  A5,
  input  A6,
  input  A7,
  input  A8,
  input  nOE2,
  output Y8,
  output Y7,
  output Y6,
  output Y5,
  output Y4,
  output Y3,
  output Y2,
  output Y1
);

  _74541 u_74541_1 (
    .pin1(A1), .pin2(A1), .pin3(A1), .pin4(A1), .pin5(A1), .pin6(A1), .pin7(A1), .pin8(A1), .pin9(A1),
    .pin19(A1), .pin18(Y1), .pin17(Y1), .pin16(Y1), .pin15(Y1), .pin14(Y1), .pin13(Y1), .pin12(Y1), .pin11(Y1));

  assign A2 = A1;
  assign A3 = A1;
  assign A4 = A1;
  assign A5 = A1;
  assign A6 = A1;
  assign A7 = A1;
  assign A8 = A1;
  assign nOE1 = A1;
  assign nOE2 = A1;
  assign Y2 = Y1;
  assign Y3 = Y1;
  assign Y4 = Y1;
  assign Y5 = Y1;
  assign Y6 = Y1;
  assign Y7 = Y1;
  assign Y8 = Y1;
endmodule
