// Logisim project ttl_7458.circ as structural Verilog
module ttl_7458 (
  input  A0,
  input  A1,
  input  B1,
  input  C1,
  input  D1,
  input  D0,
  input  E0,
  input  F0,
  input  B0,
  input  C0,
  output Y1,
  output Y0
);

  _7458 u_7458_1 (
    .pin1(A0), .pin2(A0), .pin3(A0), .pin4(A0), .pin5(A0), .pin6(Y0), .pin13(A0), .pin12(A0), .pin11(A0),
    .pin10(A0), .pin9(A0), .pin8(Y0));

  assign A1 = A0;
  assign B0 = A0;
  assign B1 = A0;
  assign C0 = A0;
  assign C1 = A0;
  assign D0 = A0;
  assign D1 = A0;
  assign E0 = A0;
  assign F0 = A0;
  assign Y1 = Y0;
endmodule
