// Logisim project ttl_7464.circ as structural Verilog
module ttl_7464 (
  input  A,
  input  E,
  input  F,
  input  G,
  input  H,
  input  I,
  input  J,
  input  K,
  input  B,
  input  C,
  input  D,
  output Y
);

  _7464 u_7464_1 (
    .pin13(A), .pin12(A), .pin11(A), .pin10(A), .pin9(A), .pin8(Y));  // open: pin1, pin2, pin3, pin4, pin5, pin6

  assign B = A;
  assign C = A;
  assign D = A;
  assign E = A;
  assign F = A;
  assign G = A;
  assign H = A;
  assign I = A;
  assign J = A;
  assign K = A;
endmodule
