// Logisim project ttl_74670.circ as structural Verilog
module ttl_74670 (
  input  D2,
  input  D3,
  input  D4,
  input  RA1,
  input  RA0,
  input  nOE,
  input  nWE,
  input  WA1,
  input  WA0,
  input  D1,
  output Q4,
  output Q3,
  output Q2,
  output Q1
);

  _74670 u_74670_1 (
    .pin1(D1), .pin2(D1), .pin3(D1), .pin4(D1), .pin5(D1), .pin6(Q1), .pin7(Q1), .pin15(D1), .pin14(D1),
    .pin13(D1), .pin12(D1), .pin11(D1), .pin10(Q1), .pin9(Q1));

  assign D2 = D1;
  assign D3 = D1;
  assign D4 = D1;
  assign nOE = D1;
  assign nWE = D1;
  assign Q2 = Q1;
  assign Q3 = Q1;
  assign Q4 = Q1;
  assign RA0 = D1;
  assign RA1 = D1;
  assign WA0 = D1;
  assign WA1 = D1;
endmodule
