// Logisim project ttl_747266.circ as structural Verilog
module ttl_747266 (
  input  pin1,
  input  pin2,
  input  pin4,
  input  pin5,
  input  pin9,
  input  pin10,
  input  pin12,
  input  pin13,
  output pin3,
  output pin6,
  output pin8,
  output pin11
);

  _747266 u_747266_1 (
    .pin1(pin1), .pin2(pin1), .pin3(pin1), .pin4(pin1), .pin5(pin1), .pin6(pin1), .pin13(pin1), .pin12(pin1),
    .pin11(pin1), .pin10(pin1), .pin9(pin1), .pin8(pin1));

  assign pin2 = pin1;
  assign pin3 = pin1;
  assign pin4 = pin1;
  assign pin5 = pin1;
  assign pin6 = pin1;
  assign pin8 = pin1;
  assign pin9 = pin1;
  assign pin10 = pin1;
  assign pin11 = pin1;
  assign pin12 = pin1;
  assign pin13 = pin1;
endmodule
