// Logisim project ttl_7474.circ as structural Verilog
module ttl_7474 (
  input  nCLR1,
  input  D1,
  input  CLK1,
  input  nPRE1,
  input  nPRE2,
  input  CLK2,
  input  D2,
  input  nCLR2,
  output Q1,
  output nQ1,
  output nQ2,
  output Q2
);

  _7474 u_7474_1 (
    .pin1(CLK1), .pin2(CLK1), .pin3(CLK1), .pin4(CLK1), .pin5(nQ1), .pin6(nQ1), .pin13(CLK1), .pin12(CLK1),
    .pin11(CLK1), .pin10(CLK1), .pin9(nQ1), .pin8(nQ1));

  assign CLK2 = CLK1;
  assign D1 = CLK1;
  assign D2 = CLK1;
  assign nCLR1 = CLK1;
  assign nCLR2 = CLK1;
  assign nPRE1 = CLK1;
  assign nPRE2 = CLK1;
  assign nQ2 = nQ1;
  assign Q1 = nQ1;
  assign Q2 = nQ1;
endmodule
