// Logisim project ttl_7485.circ as structural Verilog
module ttl_7485 (
  input  B3,
  input  in_2,
  input  in_3,
  input  in_4,
  input  B0,
  input  A0,
  input  B1,
  input  A1,
  input  A2,
  input  B2,
  input  A3,
  output out_12,
  output A_B,
  output out_14
);

  _7485 u_7485_1 (
    .pin1(A0), .pin2(A0), .pin3(A0), .pin4(A0), .pin5(A_B), .pin6(A_B), .pin7(A_B), .pin15(A0), .pin14(A0),
    .pin13(A0), .pin12(A0), .pin11(A0), .pin10(A0), .pin9(A0));

  assign A1 = A0;
  assign A2 = A0;
  assign A3 = A0;
  assign B0 = A0;
  assign B1 = A0;
  assign B2 = A0;
  assign B3 = A0;
  assign in_2 = A0;
  assign in_3 = A0;
  assign in_4 = A0;
  assign out_12 = A_B;
  assign out_14 = A_B;
endmodule
