// Logisim project ttl_7487.circ as structural Verilog
module ttl_7487 (
  input  C,
  input  A1,
  input  A2,
  input  B,
  input  A3,
  input  A4,
  output Y1,
  output Y2,
  output Y3,
  output Y4
);

  // _7487 7487_1: pin names not known; wires that end beside it: A1, A1, A1, A1, A1, A1, A1, A1, A1, A1

  assign A2 = A1;
  assign A3 = A1;
  assign A4 = A1;
  assign B = A1;
  assign C = A1;
  assign Y1 = A1;
  assign Y2 = A1;
  assign Y3 = A1;
  assign Y4 = A1;
endmodule
