// Logisim project two_bit_ripple_adder.circ as structural Verilog
module two_bit_ripple_adder (
  input  [1:0] A_1_0,
  input  [1:0] S_1_0,
  input  [1:0] B_1_0,
  output Cin,
  output Cout
);

  wire [1:1] adder_1_out;

  Adder #(.width(2)) adder_1 (.a(A_1_0), .b(B_1_0), .out({adder_1_out[1], Cin}), .cin(S_1_0[0]), .cout(Cout));
  // Pins of 1 and 2 bits meet at {adder_1_out[1], Cin}
  // Pins of 1 and 2 bits meet at S_1_0
endmodule
