// Logisim project twoscomp_4bit.circ as structural Verilog
module twoscomp_4bit (
  input  A0,
  input  A1,
  input  A2,
  input  A3,
  output B0,
  output B1,
  output B2,
  output B3
);

  wire TQ0, TQ2, TQ7, TQ8, TQa, TQb;

  not N1 (TQ8, A0);
  not N2 (TQ7, A1);
  not N3 (TQa, A2);
  not N4 (TQ0, A3);
  and CA1 (TQb, TQ7, TQ8);
  xor XB1 (B1, TQ7, TQ8);
  and CA2 (TQ2, TQa, TQb);
  xor XB2 (B2, TQa, TQb);
  // AND_Gate CA3 has open pins: in0=TQ0, in1=TQ2, out=open
  xor XB3 (B3, TQ0, TQ2);

  assign B0 = A0;

  // Other names for the same wires on the sheet: TQ1 = A1; TQ3 = A2; TQ4 = B3; TQ5 = A3; TQ6 = A0; TQ9 = B1; TQc = B2
endmodule
