// Logisim project updown_counter_4bit.circ as structural Verilog
module updown_counter_4bit (
  input  CLK,
  input  UD,
  input  EN,
  input  RST,
  output Q0,
  output Q1,
  output Q2,
  output Q3
);

  wire AD2_out, AD3_out, AU2_out, AU3_out, N4_out, TD2_out, TD3_out, TO3_out, TQ5, TQ8, TQ9, TQa, TQb,
       TU2_out, TU3_out;

  not N1 (TQb, UD);
  T_Flip_Flop U1 (.T(EN), .clk(CLK), .Q(Q0), .reset(RST));  // open: Qn, preset
  not N2 (TQ8, Q0);
  T_Flip_Flop U2 (.T(TQ5), .clk(CLK), .Q(Q1), .reset(RST));  // open: Qn, preset
  not N3 (TQ9, Q1);
  T_Flip_Flop U3 (.T(TQa), .clk(CLK), .Q(Q2), .reset(RST));  // open: Qn, preset
  not N4 (N4_out, Q2);
  T_Flip_Flop U4 (.T(TO3_out), .clk(CLK), .Q(Q3), .reset(RST));  // open: Qn, preset
  xor X1 (TQ5, Q0, UD);
  and AU2 (AU2_out, Q0, Q1);
  and AD2 (AD2_out, TQ8, TQ9);
  and TU2 (TU2_out, TQb, AU2_out);
  and TD2 (TD2_out, UD, AD2_out);
  or TO2 (TQa, TU2_out, TD2_out);
  and AU3 (AU3_out, AU2_out, Q2);
  and AD3 (AD3_out, AD2_out, N4_out);
  and TU3 (TU3_out, TQb, AU3_out);
  and TD3 (TD3_out, UD, AD3_out);
  or TO3 (TO3_out, TU3_out, TD3_out);

  // Other names for the same wires on the sheet: TQ0 = Q0; TQ1 = Q1; TQ2 = EN; TQ3 = Q2; TQ4 = CLK; TQ6 = RST;
  //   TQ7 = Q3; TQc = UD
endmodule
