// Logisim project vending_machine.circ as structural Verilog
module vending_machine (
  input  RST,
  input  A,
  input  B,
  output DONE
);

  wire TQ0, TQ1, TQ1a, TQ1b, TQ1c, TQ1d, TQ1e, TQ1f, TQ1g, TQ1h, TQ1i, TQ1j, TQ1k, TQ1l, TQ1m, TQ1n, TQ1o,
       TQ1p, TQ1q, TQ1r, TQ1s, TQ1t, TQ1u, TQ1v, TQ1w, TQ1x, TQ1y, TQ1z, TQ2, TQ2a, TQ2b, TQ2d, TQ2f, TQ2g,
       TQ2h, TQ2i, TQ2j, TQ2k, TQ2l, TQ2m, TQ2n, TQ2o, TQ2p, TQ2q, TQ2r, TQ2s, TQ2t, TQ2u, TQ2v, TQ2w, TQ2x,
       TQ2y, TQ2z, TQ3, TQ3a, TQ3b, TQ3c, TQ3d, TQ3e, TQ3f, TQ3g, TQ3h, TQ3i, TQ3j, TQ3k, TQ3l, TQ3m, TQ3n,
       TQ3o, TQ3p, TQ3q, TQ3r, TQ3s, TQ3t, TQ3u, TQ3v, TQ3w, TQ3x, TQ4, TQ5, TQ6, TQ8, TQ9, TQ10, TQ11, TQ12,
       TQ13, TQ14, TQ15, TQ16, TQ17, TQ18, TQ19, TQ20, TQ21, TQ22, TQ23, TQ24, TQ25, TQ26, TQ27, TQ28, TQ29,
       TQ30, TQ31, TQ32, TQ33, TQ34, TQ35, TQ36, TQ37, TQ38, TQ39, TQa, TQb, TQc, TQd, TQe, TQf, TQg, TQh,
       TQi, TQj, TQk, TQl, TQm, TQn, TQo, TQp, TQr, TQs, TQt, TQu, TQv, TQw, TQx, TQy, TQz;

  Clock CLK (.out(TQ5));
  D_Flip_Flop U1 (.D(TQ2x), .clk(TQ5), .Q(TQ2t), .reset(RST));  // open: Qn, preset
  and A4 (TQr, TQo, TQ22);
  and A16 (TQz, TQ2t, TQ29);
  and M28 (TQ18, TQ28, TQ3c);
  and A40 (TQ1h, TQ1g, B);
  and A52 (TQ1p, TQ2t, TQ3c);
  and A64 (TQ1z, TQ1y, TQ22);
  and A76 (TQ2d, TQ2b, B);
  or O88 (TQ2o, TQ2n, TQ4);
  or O98 (TQ3e, TQ31, TQ3u);
  and AH1 (TQ3f, TQ3c, TQ3d);
  or O120 (TQ6, TQ3, TQ4);
  and A5 (TQ3j, TQr, A);
  and A17 (TQ10, TQz, TQ1t);
  // AND_Gate M29 has open pins: in0=TQ18, in1=TQ1t, out=open
  and A41 (TQ3i, TQ1h, A);
  and A53 (TQ1q, TQ1p, TQ1t);
  and A65 (TQ8, TQ1z, TQ27);
  and A77 (TQe, TQ2d, A);
  or O89 (TQ2p, TQ2o, TQ8);
  or O99 (TQ32, TQ3j, TQ3h);
  or O109 (TQ3g, TQ3e, TQ3f);
  or O121 (TQ9, TQ6, TQ8);
  D_Flip_Flop U2 (.D(TQ3g), .clk(TQ5), .Q(TQ3c), .reset(RST));  // open: Qn, preset
  and A6 (TQs, TQ28, TQ29);
  and A18 (TQ11, TQ10, TQ22);
  and A30 (TQ19, TQ28, TQ3c);
  and M42 (TQ1i, TQ2t, TQ3c);
  and A54 (TQ1r, TQ1q, B);
  and A66 (TQ20, TQ28, TQ29);
  or O78 (TQ2f, TQ3j, TQ3q);
  or O90 (TQ2q, TQ2p, TQa);
  or O100 (TQ33, TQ32, TQ3i);
  or O110 (TQj, TQ3h, TQ3i);
  or O122 (TQb, TQ9, TQa);
  D_Flip_Flop U3 (.D(TQm), .clk(TQ5), .Q(TQh), .reset(RST));  // open: Qn, preset
  and A7 (TQt, TQs, TQ1t);
  and A19 (TQ3o, TQ11, A);
  and A31 (TQ1a, TQ19, TQ1t);
  and M43 (TQn, TQ1i, TQ1t);
  and A55 (TQ2, TQ1r, TQ27);
  and A67 (TQ21, TQ20, TQh);
  or O79 (TQ2g, TQ2f, TQ3s);
  or O91 (TQ2r, TQ2q, TQc);
  or O101 (TQ34, TQ33, TQ3w);
  or O111 (TQ3l, TQ3j, TQ3k);
  or O123 (TQd, TQb, TQc);
  not N1 (TQ28, TQ2t);
  and A8 (TQu, TQt, B);
  and A20 (TQ12, TQ2t, TQ29);
  and A32 (TQ1b, TQ1a, TQ22);
  and A44 (TQ1j, TQ2t, TQ3c);
  and A56 (TQ1s, TQ2t, TQ3c);
  and A68 (TQ23, TQ21, TQ22);
  or O80 (TQ2v, TQ2g, TQ3u);
  or O92 (TQ2s, TQ2r, TQe);
  or O102 (TQ35, TQ34, TQ0);
  or O112 (TQ3n, TQ3l, TQ3m);
  or O124 (TQf, TQd, TQe);
  not N2 (TQ29, TQ3c);
  and A9 (TQ3k, TQu, TQ27);
  and A21 (TQ13, TQ12, TQ1t);
  and A33 (TQ3u, TQ1b, A);
  and A45 (TQ1k, TQ1j, TQ1t);
  and A57 (TQ1u, TQ1s, TQ1t);
  and A69 (TQa, TQ23, A);
  or O81 (TQ2h, TQ3k, TQ3m);
  not NC0 (TQ2u, TQ2s);
  or O103 (TQ36, TQ35, TQ2);
  or O113 (TQ3p, TQ3n, TQ3o);
  not NC2 (TQi, TQf);
  not N3 (TQ1t, TQh);
  and AH0 (TQ2w, TQ2t, TQ2u);
  and AH2 (TQk, TQh, TQi);
  not NIa (TQ27, A);
  and A10 (TQv, TQ28, TQ29);
  and A22 (TQ14, TQ13, B);
  and A34 (TQ1c, TQ28, TQ3c);
  and A46 (TQ1l, TQ1k, TQ22);
  and A58 (TQ1v, TQ1u, B);
  and A70 (TQ24, TQ28, TQ29);
  or O82 (TQ2i, TQ2h, TQ3o);
  or O104 (TQ37, TQ36, TQ4);
  or O114 (TQ3r, TQ3p, TQ3q);
  and A11 (TQw, TQv, TQ1t);
  and A23 (TQ3q, TQ14, TQ27);
  and A35 (TQ1d, TQ1c, TQ1t);
  and A47 (TQ3w, TQ1l, TQ27);
  and A59 (TQ4, TQ1v, A);
  and A71 (TQ25, TQ24, TQh);
  or O83 (TQ2j, TQ2i, TQ3h);
  or O93 (TQ2x, TQ2v, TQ2w);
  or O105 (TQ38, TQ37, TQ8);
  or O115 (TQ3t, TQ3r, TQ3s);
  or O125 (TQm, TQj, TQk);
  not NIb (TQ22, B);
  or O94 (TQ2y, TQ3k, TQ3m);
  or Ofo126 (DONE, TQn, TQp);
  and M0 (TQg, TQ28, TQ29);
  and A12 (TQx, TQw, B);
  and A24 (TQ15, TQ2t, TQ29);
  and A36 (TQ1e, TQ1d, B);
  and A48 (TQ1m, TQ2t, TQ3c);
  and M60 (TQ1w, TQ28, TQ29);
  and A72 (TQ26, TQ25, B);
  or O84 (TQ2k, TQ2j, TQ3i);
  or O106 (TQ39, TQ38, TQa);
  or O116 (TQ3v, TQ3t, TQ3u);
  // AND_Gate M1 has open pins: in0=TQg, in1=TQ1t, out=open
  and A13 (TQ3m, TQx, A);
  and A25 (TQ16, TQ15, TQ1t);
  and A37 (TQ3h, TQ1e, TQ27);
  and A49 (TQ1n, TQ1m, TQ1t);
  and M61 (TQp, TQ1w, TQh);
  and A73 (TQc, TQ26, TQ27);
  or O85 (TQ2l, TQ2k, TQ3w);
  or O95 (TQ2z, TQ2y, TQ3o);
  or O107 (TQ3a, TQ39, TQc);
  or O117 (TQ3x, TQ3v, TQ3w);
  or O96 (TQ30, TQ2z, TQ3q);
  and A2 (TQl, TQ28, TQ29);
  and M14 (TQy, TQ2t, TQ29);
  and A26 (TQ17, TQ16, B);
  and A38 (TQ1f, TQ28, TQ3c);
  and A50 (TQ1o, TQ1n, TQ22);
  and A62 (TQ1x, TQ28, TQ29);
  and A74 (TQ2a, TQ28, TQ29);
  or O86 (TQ2m, TQ2l, TQ0);
  or O108 (TQ3b, TQ3a, TQe);
  or O118 (TQ1, TQ3x, TQ0);
  and A3 (TQo, TQl, TQ1t);
  // AND_Gate M15 has open pins: in0=TQy, in1=TQ1t, out=open
  and A27 (TQ3s, TQ17, A);
  and A39 (TQ1g, TQ1f, TQ1t);
  and A51 (TQ0, TQ1o, A);
  and A63 (TQ1y, TQ1x, TQh);
  and A75 (TQ2b, TQ2a, TQh);
  or O87 (TQ2n, TQ2m, TQ2);
  or O97 (TQ31, TQ30, TQ3s);
  not NC1 (TQ3d, TQ3b);
  or O119 (TQ3, TQ1, TQ2);

  // Other names for the same wires on the sheet: TQ2c = B; TQ2e = A; TQ7 = RST; TQq = DONE
endmodule
