// Logisim project water_level_controller.circ as structural Verilog
module water_level_controller (
  input  CLK,
  input  RST,
  input  LOW,
  input  FULL,
  output PUMPIN,
  output PUMPOUT
);

  wire TQ2, TQ3, TQ5, TQ6, TQ8, TQ9, TQa, TQb, TQc, TQd, TQe, TQf, TQg, TQh, TQi, TQj, TQk, TQl, TQm, TQn,
       TQo, TQp, TQq, TQr, TQs, TQt, TQu, TQv, TQx, TQy;

  D_Flip_Flop U1 (.D(TQl), .clk(CLK), .Q(TQh), .reset(RST));  // open: Qn, preset
  and A6 (TQ8, TQ6, FULL);
  not NC0 (TQi, TQg);
  and A7 (TQm, TQ8, TQf);
  and AH0 (TQk, TQh, TQi);
  D_Flip_Flop U2 (.D(TQv), .clk(CLK), .Q(TQr), .reset(RST));  // open: Qn, preset
  or O18 (TQl, TQj, TQk);
  and M8 (TQx, TQ9, TQr);
  not N1 (TQ9, TQh);
  and A9 (TQa, TQ9, TQr);
  or O19 (TQt, TQm, TQn);
  not N2 (TQ5, TQr);
  or O20 (TQq, TQo, TQp);
  not NIlow (TQf, LOW);
  and A10 (TQb, TQa, TQd);
  not NIfull (TQd, FULL);
  and A11 (TQn, TQb, TQf);
  not NC1 (TQs, TQq);
  and M0 (PUMPIN, TQ9, TQ5);
  and AH1 (TQu, TQr, TQs);
  and M12 (TQy, TQh, TQr);
  and A1 (TQ2, TQ9, TQ5);
  and A13 (TQc, TQh, TQr);
  or O21 (TQv, TQt, TQu);
  and A2 (TQ3, TQ2, TQd);
  or Ofo22 (PUMPOUT, TQx, TQy);
  and A14 (TQe, TQc, TQd);
  and A3 (TQo, TQ3, LOW);
  and A15 (TQp, TQe, TQf);
  // AND_Gate M4 has open pins: in0=TQh, in1=TQ5, out=open
  or O16 (TQj, TQo, TQn);
  and A5 (TQ6, TQh, TQ5);
  or O17 (TQg, TQm, TQp);

  // Other names for the same wires on the sheet: TQ0 = CLK; TQ1 = RST; TQ4 = LOW; TQ7 = FULL; TQw = PUMPIN;
  //   TQz = PUMPOUT
endmodule
