// Logisim project ttl_74161_native.circ as structural Verilog
module ttl_74161_native (
  input  ENT,
  input  nLOAD,
  input  nCLR,
  input  CLK,
  input  A,
  input  B,
  input  C,
  input  D,
  input  ENP,
  output RCO,
  output QA,
  output QB,
  output QC,
  output QD
);

  _74161 u_74161_1 (
    .pin1(nCLR), .pin2(CLK), .pin3(A), .pin4(B), .pin5(C), .pin6(D), .pin7(ENP), .pin15(RCO), .pin14(QA),
    .pin13(QB), .pin12(QC), .pin11(QD), .pin10(ENT), .pin9(nLOAD));
endmodule
